// Logisim project MCU.circ as structural Verilog: 8 circuits, main circuit MCU v2
module MCU_v2 (
  input  [4:0] KBD_command,
  input  [10:0] KBD_energy_increment,
  input  KBD_Ready,
  input  [31:0] Field_cache_Datai_1,
  input  [31:0] Field_cache_DataI_2,
  input  Reset,
  input  CLK,
  input  MISO,
  input  SPI_busy,
  output Request_KBD,
  output Request_KBD_energy,
  output [7:0] Cell_CSC,
  output [7:0] Cell_CSR,
  output Task_CS,
  output People_CS,
  output [1:0] Field_cache_select,
  output [2:0] Table_CSC,
  output [5:0] Table_CSR,
  output Field_cache_wr,
  output Wait_CDM,
  output SPI_clock,
  output MOSI,
  output Wrong_action,
  output CDM_8_wrong_action,
  output [7:0] Debug_out,
  output Waiting_IO,
  output SPI_communication_in_progress,
  output Basic_controller_wrong_action,
  output Pointer_critical_error
);

  wire and_1_out, and_3_out, and_4_out, and_5_out, and_6_out, and_7_out, and_8_out, and_9_out, and_10_out,
       and_11_out, and_12_out, and_13_out, and_14_out, and_16_out, and_17_out, and_18_out, and_19_out,
       and_20_out, and_21_out, and_22_out, and_23_out, and_24_out, and_25_out,
       basic_controller_1_cache_field_wr, basic_controller_1_call_cdm, basic_controller_1_check_speciality,
       basic_controller_1_cmd_overwrite, basic_controller_1_enter, basic_controller_1_kbd_cahce_overwrite,
       basic_controller_1_pc_active, basic_controller_1_pc_allow_nearby, basic_controller_1_pc_free_mode,
       basic_controller_1_req_kbd, basic_controller_1_req_kbd_num, cdm_8_1_data_code_prime,
       cdm_8_1_load_st_prime, cdm_8_1_mem, comparator_1_eq, d_ff_1_q, Data, decoder_1_out0, decoder_2_out0,
       decoder_2_out1, decoder_2_out2, decoder_2_out3, decoder_2_out4, decoder_2_out5, decoder_2_out6,
       decoder_2_out7, io_dmx_1_bc_control, io_dmx_1_cell_csc, io_dmx_1_cell_csr, io_dmx_1_debug_output,
       io_dmx_1_is_io, io_dmx_1_rom_page_control_control, io_dmx_1_spi_kbd_control,
       io_dmx_1_table__csc__csr____task_cs, io_dmx_1_universal_io_1, io_dmx_1_universal_io_2, merge,
       move_checker_1_is_wrong, multiplexer_1_out, not_1_out, not_2_out, not_3_out, not_4_out, not_5_out,
       not_6_out, not_7_out, not_8_out, not_9_out, not_10_out, or_2_out, or_3_out, or_5_out, or_6_out,
       or_8_out, or_9_out, or_10_out, or_13_out, or_16_out, or_17_out, pointer_controller_1_ready,
       spi_module_master_1_communication_end, spi_module_master_1_input_transanction_end,
       spi_module_master_1_output_transanction_end, wait_BC;
  wire [1:0] basic_controller_1_cache_field_sel, multiplexer_2_out;
  wire [2:0] register_2_q;
  wire [4:0] basic_controller_1_kbd_command_2;
  wire [6:0] demultiplexer_2_out0, demultiplexer_2_out1, register_8_q;
  wire [7:0] basic_controller_1_spi_control, cdm_8_1_addr, cdm_8_1_data_out, cdm_8_1_pc, cdm_8_1_ps,
       cdm_8_1_r0, cdm_8_1_r1, cdm_8_1_r2, cdm_8_1_r3, cdm_8_1_sp, controlled_buffer_1_out,
       controlled_buffer_2_out, controlled_buffer_4_out, controlled_buffer_9_out, controlled_buffer_10_out,
       controlled_buffer_12_out, controlled_buffer_13_out, controlled_buffer_16_out,
       controlled_buffer_18_out, controlled_buffer_23_out, controlled_buffer_24_out,
       controlled_buffer_25_out, controlled_buffer_26_out, controlled_buffer_30_out, or_4_out, or_7_out,
       pointer_controller_1_csc, pointer_controller_1_csr, pull_resistor_3_node, register_1_q, register_3_q,
       register_5_q, register_6_q, register_7_q, register_9_q, register_10_q;
  wire [7:2] pull_resistor_1_node;
  wire [7:3] controlled_buffer_5_out, register_2_q_2;
  wire [7:7] register_8_q_2;
  wire [15:0] spi_module_master_1_recv_data;

  // Probe on cdm_8_1_pc
  // Probe on cdm_8_1_r0
  // Probe on cdm_8_1_r0
  // Probe on cdm_8_1_r0
  // Probe on cdm_8_1_ps[6:4]
  // Probe on cdm_8_1_ps[7]
  // Probe on cdm_8_1_r1
  // Probe on cdm_8_1_r0
  // Probe on cdm_8_1_ps[3]
  // Probe on cdm_8_1_ps[2]
  // Probe on cdm_8_1_r1
  // Probe on cdm_8_1_r1
  // Probe on cdm_8_1_r1
  // Probe on cdm_8_1_ps[1]
  // Probe on cdm_8_1_ps[0]
  // Probe on cdm_8_1_r2
  // Probe on cdm_8_1_r2
  // Probe on cdm_8_1_r2
  // Probe on cdm_8_1_r2
  // Probe on cdm_8_1_sp
  // Probe on cdm_8_1_r3
  // Probe on cdm_8_1_r3
  // Probe on cdm_8_1_r3
  and and_1 (and_1_out, CLK, ~wait_BC, ~Waiting_IO);  // AND_Gate
  and and_2 (Wait_CDM, ~wait_BC, ~Waiting_IO);  // AND_Gate
  // Probe on cdm_8_1_r3
  not not_1 (not_1_out, and_3_out);
  assign controlled_buffer_1_out = not_1_out ? controlled_buffer_2_out : 8'bz;  // Controlled_Buffer controlled_buffer_1
  Comparator #(.mode("unsigned")) comparator_1 (.a(cdm_8_1_pc), .b({8{1'b0}}), .eq(comparator_1_eq));  // open: gt, lt
  Decoder #(.disabled(0)) decoder_1 (
    .out0(decoder_1_out0), .out1(Data), .sel(cdm_8_1_data_code_prime), .en(cdm_8_1_mem));
  CdM_8 cdm_8_1 (
    .data_code_prime(cdm_8_1_data_code_prime), .R0(cdm_8_1_r0), .R1(cdm_8_1_r1), .mem(cdm_8_1_mem),
    .R2(cdm_8_1_r2), .load_st_prime(cdm_8_1_load_st_prime), .R3(cdm_8_1_r3), .addr(cdm_8_1_addr),
    .PC(cdm_8_1_pc), .SP(cdm_8_1_sp), .data_out(cdm_8_1_data_out), .data_in(controlled_buffer_4_out),
    .PS(cdm_8_1_ps), .clk(and_1_out), .rset(Reset));  // open: page, IAck, IRQ, vector, shadow
  and and_3 (and_3_out, io_dmx_1_rom_page_control_control, cdm_8_1_load_st_prime);
  assign controlled_buffer_2_out = and_3_out ? register_1_q : 8'bz;  // Controlled_Buffer controlled_buffer_2
  Register #(.trigger("falling")) register_1 (
    .D(controlled_buffer_1_out), .en(io_dmx_1_rom_page_control_control), .Q(register_1_q), .clk(CLK),
    .clr(Reset));
  Decoder #(.select(3), .disabled(0)) decoder_2 (
    .out0(decoder_2_out0), .out1(decoder_2_out1), .out2(decoder_2_out2), .out3(decoder_2_out3),
    .out4(decoder_2_out4), .out5(decoder_2_out5), .out6(decoder_2_out6), .out7(decoder_2_out7),
    .sel(register_2_q), .en(decoder_1_out0));
  assign controlled_buffer_2_out = not_2_out ? cdm_8_1_data_out : 8'bz;  // Controlled_Buffer controlled_buffer_3
  not not_2 (not_2_out, cdm_8_1_load_st_prime);
  assign controlled_buffer_4_out = cdm_8_1_load_st_prime ? controlled_buffer_2_out : 8'bz;  // Controlled_Buffer controlled_buffer_4
  Register register_2 (
    .D(register_1_q), .en(1'b1), .Q({register_2_q_2, register_2_q}), .clk(comparator_1_eq), .clr(Reset));
  and and_4 (and_4_out, ~io_dmx_1_is_io, Data);  // AND_Gate
  IO_dmx io_dmx_1 (
    .Address(cdm_8_1_addr), .Is_IO(io_dmx_1_is_io), .Cell_CSC(io_dmx_1_cell_csc),
    .Cell_CSR(io_dmx_1_cell_csr), .Table__CSC__CSR____Task_CS(io_dmx_1_table__csc__csr____task_cs),
    .SPI_KBD_control(io_dmx_1_spi_kbd_control), .Universal_IO_1(io_dmx_1_universal_io_1),
    .Universal_IO_2(io_dmx_1_universal_io_2), .Debug_output(io_dmx_1_debug_output), .Selected(Data),
    .BC_control(io_dmx_1_bc_control), .ROM_page_control_control(io_dmx_1_rom_page_control_control));
  or or_1 (Wrong_action, CDM_8_wrong_action, Basic_controller_wrong_action);
  ROM rom_1 (.addr(cdm_8_1_addr), .data(controlled_buffer_2_out), .sel(decoder_2_out0));
  ROM rom_2 (.addr(cdm_8_1_addr), .data(controlled_buffer_2_out), .sel(decoder_2_out1));
  ROM rom_3 (.addr(cdm_8_1_addr), .data(controlled_buffer_2_out), .sel(decoder_2_out2));
  ROM rom_4 (.addr(cdm_8_1_addr), .data(controlled_buffer_2_out), .sel(decoder_2_out3));
  ROM rom_5 (.addr(cdm_8_1_addr), .data(controlled_buffer_2_out), .sel(decoder_2_out4));
  ROM rom_6 (.addr(cdm_8_1_addr), .data(controlled_buffer_2_out), .sel(decoder_2_out5));
  ROM rom_7 (.addr(cdm_8_1_addr), .data(controlled_buffer_2_out), .sel(decoder_2_out6));
  ROM rom_8 (.addr(cdm_8_1_addr), .data(controlled_buffer_2_out), .sel(decoder_2_out7));
  RAM ram_1 (
    .addr(cdm_8_1_addr), .data(controlled_buffer_2_out), .sel(and_4_out), .clk(CLK),
    .ld(cdm_8_1_load_st_prime), .clr(Reset));
  Pull_Resistor pull_resistor_1 (.node({pull_resistor_1_node, People_CS, Task_CS}));
  not not_3 (not_3_out, register_3_q[7]);
  Register #(.trigger("falling")) register_3 (
    .D(controlled_buffer_2_out), .en(io_dmx_1_table__csc__csr____task_cs), .Q(register_3_q), .clk(CLK),
    .clr(Reset));
  assign {controlled_buffer_5_out, Table_CSC} = not_3_out ? register_3_q : 8'bz;  // Controlled_Buffer controlled_buffer_5
  Register #(.trigger("falling")) register_4 (
    .D(controlled_buffer_2_out), .en(io_dmx_1_debug_output), .Q({CDM_8_wrong_action, Debug_out[6:0]}),
    .clk(CLK), .clr(Reset));
  assign {pull_resistor_1_node, People_CS, Task_CS} = register_3_q[7] ? register_3_q : 8'bz;  // Controlled_Buffer controlled_buffer_6
  Pull_Resistor pull_resistor_2 (.node({controlled_buffer_5_out, Table_CSC}));
  and and_5 (and_5_out, cdm_8_1_load_st_prime, io_dmx_1_cell_csc);
  and and_6 (and_6_out, cdm_8_1_load_st_prime, io_dmx_1_cell_csr);
  Demultiplexer #(.width(3), .disabled(0), .enable("false")) demultiplexer_1 (
    .out0(Table_CSR[2:0]), .out1(Table_CSR[5:3]), .in(controlled_buffer_5_out[5:3]),
    .sel(controlled_buffer_5_out[6]));
  assign controlled_buffer_2_out = and_5_out ? controlled_buffer_25_out : 8'bz;  // Controlled_Buffer controlled_buffer_7
  assign controlled_buffer_2_out = and_6_out ? controlled_buffer_26_out : 8'bz;  // Controlled_Buffer controlled_buffer_8
  not not_4 (not_4_out, and_5_out);
  Register #(.trigger("falling")) register_5 (
    .D(controlled_buffer_9_out), .en(io_dmx_1_cell_csc), .Q(register_5_q), .clk(CLK), .clr(Reset));
  assign controlled_buffer_9_out = not_4_out ? controlled_buffer_2_out : 8'bz;  // Controlled_Buffer controlled_buffer_9
  not not_5 (not_5_out, and_6_out);
  assign controlled_buffer_10_out = not_5_out ? controlled_buffer_2_out : 8'bz;  // Controlled_Buffer controlled_buffer_10
  Register #(.trigger("falling")) register_6 (
    .D(controlled_buffer_10_out), .en(io_dmx_1_cell_csr), .Q(register_6_q), .clk(CLK), .clr(Reset));
  Pull_Resistor pull_resistor_3 (.node(pull_resistor_3_node));
  and and_7 (and_7_out, io_dmx_1_is_io, cdm_8_1_load_st_prime, io_dmx_1_universal_io_1);
  and and_8 (and_8_out, io_dmx_1_is_io, ~cdm_8_1_load_st_prime, io_dmx_1_universal_io_1);  // AND_Gate
  or or_2 (or_2_out, io_dmx_1_universal_io_1, and_18_out, or_17_out);
  and and_9 (and_9_out, io_dmx_1_is_io, io_dmx_1_universal_io_2, cdm_8_1_load_st_prime);
  and and_10 (and_10_out, io_dmx_1_is_io, ~cdm_8_1_load_st_prime, io_dmx_1_universal_io_2);  // AND_Gate
  or or_3 (or_3_out, io_dmx_1_universal_io_2, and_18_out, or_17_out);
  Multiplexer #(.disabled(0), .enable("false")) multiplexer_1 (
    .in0(register_7_q[6]), .in1(basic_controller_1_cache_field_wr), .out(multiplexer_1_out),
    .sel(basic_controller_1_kbd_cahce_overwrite));
  assign or_4_out = pull_resistor_3_node | {register_7_q[7:3], wait_BC, register_7_q[1:0]};  // OR_Gate or_4, 8 bits wide
  and and_11 (and_11_out, wait_BC, basic_controller_1_call_cdm);
  and and_12 (and_12_out, io_dmx_1_bc_control, cdm_8_1_load_st_prime);
  assign controlled_buffer_2_out = and_12_out ? or_4_out : 8'bz;  // Controlled_Buffer controlled_buffer_11
  and and_13 (and_13_out, wait_BC, basic_controller_1_enter);
  and and_14 (and_14_out, io_dmx_1_bc_control, ~cdm_8_1_load_st_prime);  // AND_Gate
  assign controlled_buffer_12_out = and_14_out ? controlled_buffer_2_out : 8'bz;  // Controlled_Buffer controlled_buffer_12
  Register #(.trigger("falling")) register_7 (
    .D(controlled_buffer_12_out), .en(or_5_out), .Q({register_7_q[7:3], wait_BC, register_7_q[1:0]}),
    .clk(CLK), .clr(Reset));
  or or_5 (or_5_out, and_13_out, and_11_out, io_dmx_1_bc_control);
  assign controlled_buffer_13_out = wait_BC ? basic_controller_1_spi_control : 8'bz;  // Controlled_Buffer controlled_buffer_13
  assign controlled_buffer_13_out = io_dmx_1_spi_kbd_control ? controlled_buffer_2_out : 8'bz;  // Controlled_Buffer controlled_buffer_14
  Register #(.trigger("falling")) register_8 (
    .D(controlled_buffer_13_out), .en(or_6_out), .Q({register_8_q_2[7], register_8_q}), .clk(CLK),
    .clr(or_10_out));
  or or_6 (or_6_out, io_dmx_1_spi_kbd_control, wait_BC);
  assign controlled_buffer_2_out = and_7_out ? register_9_q : 8'bz;  // Controlled_Buffer controlled_buffer_15
  Register #(.trigger("falling")) register_9 (
    .D(controlled_buffer_16_out), .en(or_2_out), .Q(register_9_q), .clk(CLK), .clr(Reset));
  assign controlled_buffer_16_out = and_8_out ? controlled_buffer_2_out : 8'bz;  // Controlled_Buffer controlled_buffer_16
  assign controlled_buffer_2_out = and_9_out ? register_10_q : 8'bz;  // Controlled_Buffer controlled_buffer_17
  assign controlled_buffer_18_out = and_10_out ? controlled_buffer_2_out : 8'bz;  // Controlled_Buffer controlled_buffer_18
  Register #(.trigger("falling")) register_10 (
    .D(controlled_buffer_18_out), .en(or_3_out), .Q(register_10_q), .clk(CLK), .clr(Reset));
  Multiplexer #(.width(2), .disabled(0), .enable("false")) multiplexer_2 (
    .in0(register_7_q[5:4]), .in1(basic_controller_1_cache_field_sel), .out(multiplexer_2_out),
    .sel(basic_controller_1_kbd_cahce_overwrite));
  assign controlled_buffer_16_out = and_16_out ? or_7_out : 8'bz;  // Controlled_Buffer controlled_buffer_19
  assign controlled_buffer_16_out = not_6_out ? controlled_buffer_30_out : 8'bz;  // Controlled_Buffer controlled_buffer_20
  assign controlled_buffer_12_out = basic_controller_1_enter ? {register_7_q[7:4], 4'b0000} : 8'bz;  // Controlled_Buffer controlled_buffer_21
  assign controlled_buffer_12_out = basic_controller_1_call_cdm ? {register_7_q[7:4], 4'b0001} : 8'bz;  // Controlled_Buffer controlled_buffer_22
  and and_15 (Field_cache_wr, multiplexer_1_out, CLK);
  assign or_7_out = register_9_q | controlled_buffer_30_out;  // OR_Gate or_7, 8 bits wide
  and and_16 (and_16_out, wait_BC, merge);
  not not_6 (not_6_out, and_16_out);
  not not_7 (not_7_out, register_7_q[7]);
  and and_17 (and_17_out, not_7_out, register_7_q[7]);
  basic_controller basic_controller_1 (
    .PC_ready(pointer_controller_1_ready), .Active(wait_BC), .Is_special(pull_resistor_3_node[1]),
    .Call_CDM(basic_controller_1_call_cdm), .Mode(register_7_q[1:0]), .Wrong_move(move_checker_1_is_wrong),
    .CLK(CLK), .SPI_in(register_9_q[1:0]), .PC_active(basic_controller_1_pc_active),
    .Check_speciality(basic_controller_1_check_speciality), .PC_free_mode(basic_controller_1_pc_free_mode),
    .SPI_done(spi_module_master_1_communication_end), .SPI_control(basic_controller_1_spi_control),
    .Enter(basic_controller_1_enter), .Req_KBD(basic_controller_1_req_kbd),
    .Req_KBD_num(basic_controller_1_req_kbd_num), .KBD_command(basic_controller_1_kbd_command_2),
    .KBD_ready(KBD_Ready), .Error(Basic_controller_wrong_action),
    .KBD_command_2(basic_controller_1_kbd_command_2), .Cache_field_sel(basic_controller_1_cache_field_sel),
    .Cache_field_wr(basic_controller_1_cache_field_wr), .PC_allow_nearby(basic_controller_1_pc_allow_nearby),
    .KBD_cahce_overwrite(basic_controller_1_kbd_cahce_overwrite),
    .cmd_overwrite(basic_controller_1_cmd_overwrite));
  and and_18 (and_18_out, spi_module_master_1_communication_end, demultiplexer_2_out0[6]);
  or or_8 (or_8_out, Reset, and_17_out);
  Multiplexer #(.width(2), .disabled(0), .enable("false")) multiplexer_3 (
    .in0(multiplexer_2_out), .in1(2'b11), .out(Field_cache_select), .sel(basic_controller_1_check_speciality));
  assign controlled_buffer_23_out = and_17_out ? register_5_q : 8'bz;  // Controlled_Buffer controlled_buffer_23
  assign controlled_buffer_24_out = and_17_out ? register_6_q : 8'bz;  // Controlled_Buffer controlled_buffer_24
  assign controlled_buffer_25_out = register_7_q[3] ? register_5_q : 8'bz;  // Controlled_Buffer controlled_buffer_25
  assign controlled_buffer_26_out = register_7_q[3] ? register_6_q : 8'bz;  // Controlled_Buffer controlled_buffer_26
  not not_8 (not_8_out, register_7_q[3]);
  pointer_controller pointer_controller_1 (
    .Active(basic_controller_1_pc_active), .CLK(CLK), .RST(or_8_out), .Field_state_1(Field_cache_Datai_1),
    .Field_state_2(Field_cache_DataI_2), .Free_mode(basic_controller_1_pc_free_mode),
    .CSC(pointer_controller_1_csc), .CSR(pointer_controller_1_csr), .Err(Pointer_critical_error),
    .Ready(pointer_controller_1_ready), .KBD_command(basic_controller_1_kbd_command_2),
    .Allow_nearby(basic_controller_1_pc_allow_nearby), .RST_CSC(controlled_buffer_23_out),
    .RST_CSR(controlled_buffer_24_out));
  assign controlled_buffer_25_out = not_8_out ? pointer_controller_1_csc : 8'bz;  // Controlled_Buffer controlled_buffer_27
  assign controlled_buffer_26_out = not_8_out ? pointer_controller_1_csr : 8'bz;  // Controlled_Buffer controlled_buffer_28
  move_checker move_checker_1 (
    .CSC(controlled_buffer_25_out), .CSR(controlled_buffer_26_out), .Is_wrong(move_checker_1_is_wrong),
    .KBD_command(basic_controller_1_kbd_command_2));
  position_checker position_checker_1 (
    .CSc(controlled_buffer_25_out), .CSR(controlled_buffer_26_out), .Field_input_1(Field_cache_Datai_1),
    .Field_input_2(Field_cache_DataI_2), .Out__all(pull_resistor_3_node[1]),
    .Out__either(pull_resistor_3_node[2]));
  Multiplexer #(.width(8), .disabled(0), .enable("false")) multiplexer_4 (
    .in0(controlled_buffer_25_out), .in1({8{1'b0}}), .out(Cell_CSC), .sel(or_9_out));
  Multiplexer #(.width(8), .disabled(0), .enable("false")) multiplexer_5 (
    .in0(controlled_buffer_26_out), .in1({8{1'b0}}), .out(Cell_CSR), .sel(or_9_out));
  or or_9 (or_9_out, Reset, basic_controller_1_enter, and_19_out, basic_controller_1_check_speciality);
  not not_9 (not_9_out, spi_module_master_1_input_transanction_end);
  Demultiplexer #(.width(7), .disabled(0), .enable("false")) demultiplexer_2 (
    .out0(demultiplexer_2_out0), .out1(demultiplexer_2_out1), .in(register_8_q), .sel(register_8_q_2[7]));
  or or_10 (or_10_out, and_20_out, Reset);
  and and_19 (and_19_out, spi_module_master_1_input_transanction_end, not_9_out, ~register_8_q[2], ~register_8_q[1]);  // AND_Gate
  and and_20 (and_20_out, Waiting_IO, or_13_out, and_21_out);
  or or_11 (Request_KBD, basic_controller_1_req_kbd, register_8_q_2[7]);
  and and_21 (and_21_out, ~CLK, d_ff_1_q);  // AND_Gate
  D_Flip_Flop d_ff_1 (.clk(CLK), .D(CLK), .Q(d_ff_1_q), .reset(and_21_out));  // open: Qn, preset, en
  or or_12 (Waiting_IO, Request_KBD, SPI_communication_in_progress);
  not not_10 (not_10_out, basic_controller_1_kbd_cahce_overwrite);
  or or_13 (or_13_out, or_17_out, spi_module_master_1_communication_end);
  assign basic_controller_1_kbd_command_2 = not_10_out ? KBD_command : 5'bz;  // Controlled_Buffer controlled_buffer_29
  or or_14 (SPI_communication_in_progress, demultiplexer_2_out0[6], demultiplexer_2_out0[5], demultiplexer_2_out0[4], demultiplexer_2_out0[3], demultiplexer_2_out0[2], demultiplexer_2_out0[1], demultiplexer_2_out0[0]);
  or or_15 (Request_KBD_energy, basic_controller_1_req_kbd_num, and_22_out);
  and and_22 (and_22_out, demultiplexer_2_out1[0], register_8_q_2[7]);
  Pull_Resistor pull_resistor_4 (.node(SPI_busy));
  D_Flip_Flop d_ff_2 (.clk(CLK), .D(Request_KBD_energy), .Q(merge), .reset(Reset));  // open: Qn, preset, en
  assign {controlled_buffer_18_out, controlled_buffer_30_out} = or_17_out ? {KBD_energy_increment, basic_controller_1_kbd_command_2} : 16'bz;  // Controlled_Buffer controlled_buffer_30
  assign {controlled_buffer_18_out, controlled_buffer_30_out} = spi_module_master_1_communication_end ? spi_module_master_1_recv_data : 16'bz;  // Controlled_Buffer controlled_buffer_31
  and and_23 (and_23_out, CLK, SPI_communication_in_progress, ~SPI_busy);  // AND_Gate
  LED led_1 (.in(spi_module_master_1_input_transanction_end));
  or or_16 (or_16_out, Request_KBD, merge);
  and and_24 (and_24_out, or_16_out, KBD_Ready);
  and and_25 (and_25_out, ~SPI_communication_in_progress, basic_controller_1_cmd_overwrite);  // AND_Gate
  or or_17 (or_17_out, and_25_out, and_24_out);
  SPI_module__master spi_module_master_1 (
    .In_clock(and_23_out), .MISO(MISO), .CLK(SPI_clock), .MOSI(MOSI),
    .Output_transanction_end(spi_module_master_1_output_transanction_end),
    .Input_transanction_end(spi_module_master_1_input_transanction_end),
    .Control_command({register_8_q_2[7], register_8_q}), .Send_command(register_9_q[4:0]),
    .Send_energy({register_10_q, register_9_q[7:5]}), .Recv_data(spi_module_master_1_recv_data),
    .Communication_end(spi_module_master_1_communication_end));
  Pull_Resistor pull_resistor_5 (.node(MISO));
  LED led_2 (.in(spi_module_master_1_communication_end));
  LED led_3 (.in(spi_module_master_1_output_transanction_end));

  assign Debug_out[7] = CDM_8_wrong_action;

  // Other names for the same wires on the sheet: BC_err = Basic_controller_wrong_action;
  //   PC_err = Pointer_critical_error; wait_IO = Waiting_IO; wait_KBD = Request_KBD;
  //   wait_SPI = SPI_communication_in_progress

  // Notes on the sheet:
  //   contents of rom_1 (hex, n*v repeats v):
  //   c8 0 0 e0 6 d7 cc f7 d0 1 d1 1 d6 15 d0 1 d1 2 d6 15 d4 3a c2 d3 f7 be ad cb 0 c2 d6 25 ad c0 ee 0
  //   d7 c9 0 b5 d2 4 19 d7
  //   contents of rom_2 (hex, n*v repeats v):
  //   d7 d0 f9 d1 1 a1 d0 fe d1 ff a1 8c a1 d0 f8 d1 8 a1 d0 38 d6 bb d0 fd d1 83 a1 d0 fb d1 10 a1 d0 fc
  //   d1 c a1 d6 c2 d0 fd 35 a1 d3 2 8b d6 ca d0 30 d6 bb d0 f8 d1 4 a1 d6 ca d0 38 d6 bb d0 f8 f e0 54 d1
  //   ff b5 3a a9 d1 fe b5 8e a9 d2 50 d1 40 ee 58 d2 60 d1 80 a2 d0 fa a1 8c d1 b a1 d0 fc d1 d a1 d6 ca
  //   d0 38 d6 bb d0 fb d1 e8 a1 88 35 a1 d0 fc d1 4 a1 f e1 2d d0 f9 d1 2 a1 30 b1 d0 ff b2 a1 d0 2 a2 d0
  //   1 b1 d0 fe b2 a1 d0 3 a2 d0 f8 d1 80 a1 d0 f8 35 a1 d0 1f d1 f a1 d0 2f a1 ee d2 c1 c0 d0 38 d6 bb
  //   c4 d1 fb a4 c4 d1 c 51 d0 fc a1 d0 fb b0 d7 d1 6 51 d0 fc a1 d7 d1 fe d0 0 a4 8d a4 d7 d0 f8 d1 8 a1
  //   35 a1 d7 c5 d0 f7 a1 ee
  //   contents of rom_3 (hex, n*v repeats v):
  //   d7 d0 4 d3 10 a3 d6 d8 d0 f8 d1 8 a1 d6 c4 b0 0 e0 20 d1 1 d6 75 d0 1 d1 4 d6 ad d3 4 bf d1 2 d6 75
  //   d0 1 d1 3 d6 ad d6 d8 d0 f8 d1 8 a1 d1 c d6 75 d0 fe d1 ff a1 8c a1 d2 4 b8 d1 8 54 d6 a6 d0 3 d6 89
  //   d0 f8 d1 8 a1 b0 d1 2 71 e1 55 ee e0 d6 c4 b0 d1 f 71 e0 6c d6 d8 d3 4 bf d1 3 d6 75 d0 1 d1 6 d6 ad
  //   d2 4 bb d0 30 63 ab ee 6 c 90 90 54 d1 fb a4 d2 fd d1 82 a9 d0 fc d1 c a1 35 a9 d7 d1 4 51 d0 f8 a1
  //   b0 d7 c1 c0 d0 38 d6 a6 c4 d1 fb a4 c4 d1 c 51 d0 fc a1 d0 fb b0 d7 d1 6 51 d0 fc a1 d7 3a c2 d3 f7
  //   be ad cb 0 c2 d6 bd ad c0 ee 0 d7 c9 0 b5 d2 4 19 d7 d0 10 4c e0 cd d0 1f ee cf d0 2f d7 d6 c4 c0 b0
  //   14 c5 a4 d7 d1 fe d0 0 a4 8d a4 d7 c5 d0 f7 a1 ee
  //   contents of rom_4 (hex, n*v repeats v):
  //   d7 d0 4 b3 d6 69 d0 f8 d1 80 a1 d0 30 d6 99 d0 1 5c d6 7c d1 1 41 e0 67 d0 fb b1 c1 88 b1 c1 d0 1 d1
  //   40 d6 84 d0 fb b0 d1 3 71 e1 37 d0 1f c5 a1 8c c5 a1 ee 5c 5 c5 c6 91 92 d0 e0 42 c2 c1 d0 8 52 d0
  //   1f a1 8c a2 d0 3e d6 99 d0 fc d1 4 a1 d0 1f c5 a1 8c c5 d2 8 59 a1 d0 3e d6 99 d0 fc d1 4 a1 ee b ee
  //   a0 d1 10 4d e0 71 30 ee 73 d0 2 b1 8c b2 d0 fe a2 8c a1 d7 d1 4 51 d0 f8 a1 b0 d7 c1 c0 d0 38 d6 99
  //   c4 d1 fb a4 c4 d1 c 51 d0 fc a1 d0 fb b0 d7 d1 6 51 d0 fc a1 d7 c5 d0 f7 a1 ee
  //   contents of rom_5 (hex, n*v repeats v):
  //   d7 d2 fb d1 14 a9 d0 fd d1 81 a1 d0 fc d1 54 a1 d0 fd 35 a1 ba d1 10 79 e1 20 d0 f9 d1 a5 a1 d4 d3 4
  //   bf d1 fd d6 d1 1c a2 35 8c a1 8c a1 d6 9b d0 f8 d1 80 a1 d1 8 5d c1 c3 d0 1 d1 5 d6 ae c7 d0 f8 c5
  //   a1 e1 66 d0 fc d1 46 5d a1 d0 fb b0 0 e0 55 ee 2e d6 e1 d0 fb b2 d1 1f 79 e0 70 d1 14 79 e0 66 ee 2e
  //   d1 3 d6 d1 d6 d9 d6 8a ee e8 d6 c5 b0 1c d2 fc d1 3 a9 8c d1 fe b6 a2 8c 8d b6 a2 d6 d9 d0 1 d6 8a
  //   ee e8 d1 12 51 d0 fb a1 d0 fd d1 81 a1 d0 fc d1 c a1 d7 d1 10 4d e0 a3 30 ee a5 d0 2 b1 8c b2 d0 fe
  //   a2 8c a1 d7 3a c2 d3 f7 be ad cb 0 c2 d6 be ad c0 ee 0 d7 c9 0 b5 d2 4 19 d7 d0 10 4c e0 ce d0 1f ee
  //   d0 d0 2f d7 d6 c5 c0 b0 14 c5 a4 d7 d1 fe d0 0 a4 8d a4 d7 d1 80 51 d0 fc a1 d7 c5 d0 f7 a1 ee
  //   contents of rom_6 (hex, n*v repeats v):
  //   d7 d3 4 bf d0 fb d1 3 a1 d0 f8 d1 6 5d a1 b0 d1 5 41 e0 17 ee ed d3 4 bf 30 d6 e6 d0 fb b2 d1 14 79
  //   e1 27 ee 1 d0 ec 48 e0 2e ee 17 d0 3 42 9 88 78 e0 3a 88 78 e1 5c d6 be d0 ff b0 3 5 e0 54 89 8a e1
  //   4a 97 ee 4c 0 93 e3 50 ee 17 8e 5c ee 40 d2 ff a8 3a ee 7c ee 7c 6 d6 be d0 fe b0 3 5 e0 77 89 8a e2
  //   6d 97 ee 6f 0 93 e3 73 ee 17 8e 5c ee 63 d2 fe a8 d2 1 d3 4 bf d6 c6 7 d0 1 d6 e6 d0 fb b0 0 90 4*98
  //   d 71 e9 95 ee 7c d3 fe a e0 9b 8f bf 0 e0 a7 97 e3 a4 ee 17 88 ee 9c c 5 e0 b4 90 e3 b0 ee 17 53 89
  //   ee a8 d0 fe a e0 ba 8c a3 30 ee ed d6 cc d1 c 41 91 99 d7 d6 cc d1 3 41 d7 d6 d2 b0 1c b0 d7 d0 10
  //   4c e0 db d0 1f ee dd d0 2f d7 d6 d2 c0 b0 14 c5 a4 d7 d1 80 51 d0 fc a1 d7 c5 d0 f7 a1 ee
  //   contents of rom_7 (hex, n*v repeats v):
  //   d7 d3 4 bf d6 c0 b0 1c c0 3 d0 1f 73 e0 14 d0 2f 73 e1 16 ee 6e c 8c b1 d2 fe a9 8c 8e b0 a8 d0 f8
  //   d1 4 b5 d2 8 59 a1 b0 d1 2 41 e0 69 d0 8 d6 a2 bc d1 fb a4 d1 fd d0 81 a4 d0 fc d1 c a1 c c5 c1 d2 4
  //   74 e0 58 8a e0 56 c2 b2 a6 3a a2 8c 8d c6 ee 49 ee 60 8a e0 60 30 a4 8d ee 58 c3 d3 4 bf d1 3 d6 cc
  //   c7 8f 8f 8f ee a c4 d6 d4 d0 f8 d1 8 a1 d1 fd d0 81 a4 d0 40 d6 a2 d2 fb b8 0 e0 dc d0 1 d1 7 d6 a9
  //   ee 71 c1 c0 d0 38 d6 a2 c4 d1 fb a4 c4 d1 c 51 d0 fc a1 d0 fb b0 d7 d1 6 51 d0 fc a1 d7 3a c2 d3 f7
  //   be ad cb 0 c2 d6 b9 ad c0 ee 0 d7 c9 0 b5 d2 4 19 d7 d0 10 4c e0 c9 d0 1f ee cb d0 2f d7 d6 c0 c0 b0
  //   14 c5 a4 d7 d1 fe d0 0 a4 8d a4 d7 c5 d0 f7 a1 ee
  //   contents of rom_8 (hex, n*v repeats v):
  //   d7 d0 fb d1 3 a1 d3 4 bf d6 7b d0 f8 d1 5 5d a1 b0 d1 1 41 e1 b1 d2 fb 30 d6 aa b8 d1 18 47 7d e1 b1
  //   d3 f8 d1 8 ad bb d1 1f 71 e1 57 d0 1 d6 aa 8a b8 c0 8e b8 c0 d1 18 51 a1 d1 fc d0 44 a4 b8 0 ee b1
  //   d1 fd 30 a4 d0 f8 35 a1 c4 d1 8 54 c5 8a a9 35 ee 77 c0 d1 19 a9 d1 fc d0 4c a4 b8 0 e1 b1 c4 90 90
  //   90 d1 fa a4 d0 f8 35 a1 d1 fd 30 a4 d1 1 d0 9 d6 8e ee b1 d1 10 4d e0 83 30 ee 85 d0 2 b1 8c b2 d0
  //   fe a2 8c a1 d7 c1 c0 d0 38 d6 a3 c4 d1 fb a4 c4 d1 c 51 d0 fc a1 d0 fb b0 d7 d1 6 51 d0 fc a1 d7 d1
  //   80 51 d0 fc a1 d7 c5 d0 f7 a1 ee
endmodule

module IO_dmx (
  input  [7:0] Address,
  input  Selected,
  output Is_IO,
  output Cell_CSC,
  output Cell_CSR,
  output Table__CSC__CSR____Task_CS,
  output SPI_KBD_control,
  output Universal_IO_1,
  output Universal_IO_2,
  output Debug_output,
  output BC_control,
  output ROM_page_control_control
);

  wire [7:0] controlled_buffer_1_out;

  assign controlled_buffer_1_out = Selected ? Address : 8'bz;  // Controlled_Buffer controlled_buffer_1
  Pull_Resistor pull_resistor_1 (.node(controlled_buffer_1_out));
  Comparator comparator_1 (.a(controlled_buffer_1_out), .b({8{1'b1}}), .eq(Cell_CSC));  // open: gt, lt
  Comparator comparator_2 (.a(controlled_buffer_1_out), .b(8'hfe), .eq(Cell_CSR));  // open: gt, lt
  Comparator comparator_3 (.a(controlled_buffer_1_out), .b(8'hfd), .eq(Table__CSC__CSR____Task_CS));  // open: gt, lt
  Comparator comparator_4 (.a(controlled_buffer_1_out), .b(8'hfc), .eq(SPI_KBD_control));  // open: gt, lt
  Comparator comparator_5 (.a(controlled_buffer_1_out), .b(8'hfb), .eq(Universal_IO_1));  // open: gt, lt
  Comparator comparator_6 (.a(controlled_buffer_1_out), .b(8'hfa), .eq(Universal_IO_2));  // open: gt, lt
  Comparator comparator_7 (.a(controlled_buffer_1_out), .b(8'hf9), .eq(Debug_output));  // open: gt, lt
  Comparator comparator_8 (.a(controlled_buffer_1_out), .b(8'hf8), .eq(BC_control));  // open: gt, lt
  Comparator comparator_9 (.a(controlled_buffer_1_out), .b(8'hf7), .eq(ROM_page_control_control));  // open: gt, lt
  or or_1 (Is_IO, Cell_CSC, Cell_CSR, Table__CSC__CSR____Task_CS, SPI_KBD_control, Universal_IO_1, Universal_IO_2, Debug_output, BC_control, ROM_page_control_control);
endmodule

module Field_cahce (
  input  wr,
  input  [7:0] CSC,
  input  [7:0] CSR,
  input  RST,
  input  [1:0] p_sel,
  output [9:0] Task_row_1,
  output [8:0] p2_row_1,
  output [9:0] Task_row_2,
  output [8:0] p2_row_2,
  output [7:0] p1_row_1,
  output [31:0] DataO_1,
  output [31:0] DataO_2,
  output [7:0] p1_row_2,
  output [7:0] p1_row_3,
  output [8:0] p2_row_3,
  output [9:0] Task_row_3,
  output [7:0] p1_row_4,
  output [8:0] p2_row_4,
  output [9:0] Task_row_4,
  output [9:0] Task_row_5,
  output [8:0] p2_row_5,
  output [9:0] Task_row_6,
  output [7:0] p1_row_5,
  output [8:0] p2_row_6,
  output [7:0] p1_row_6,
  output [7:0] p1_row_7,
  output [7:0] p1_row_8,
  output [8:0] p2_row_7,
  output [9:0] Task_row_7,
  output [8:0] p2_row_8,
  output [9:0] Task_row_8
);

  wire decoder_1_out0, decoder_1_out1, decoder_1_out2, decoder_1_out3, or_1_out, or_4_out, or_5_out,
       or_6_out, or_7_out, or_10_out, or_11_out, or_14_out;
  wire [7:0] controlled_buffer_1_out, controlled_buffer_2_out, controlled_buffer_3_out,
       controlled_buffer_4_out, controlled_buffer_5_out, controlled_buffer_6_out, controlled_buffer_7_out,
       controlled_buffer_8_out;
  wire [31:0] and_1_out, and_2_out, and_3_out, and_4_out, and_5_out, and_6_out, multiplexer_1_out,
       multiplexer_2_out, multiplexer_3_out, multiplexer_4_out, multiplexer_5_out, multiplexer_6_out,
       or_2_out, or_3_out, or_8_out, or_9_out, or_12_out, or_13_out;

  assign controlled_buffer_1_out = CSR[0] ? CSC : 8'bz;  // Controlled_Buffer controlled_buffer_1
  assign controlled_buffer_2_out = CSR[1] ? CSC : 8'bz;  // Controlled_Buffer controlled_buffer_2
  assign controlled_buffer_3_out = CSR[2] ? CSC : 8'bz;  // Controlled_Buffer controlled_buffer_3
  assign controlled_buffer_4_out = CSR[3] ? CSC : 8'bz;  // Controlled_Buffer controlled_buffer_4
  assign controlled_buffer_5_out = CSR[4] ? CSC : 8'bz;  // Controlled_Buffer controlled_buffer_5
  assign controlled_buffer_6_out = CSR[5] ? CSC : 8'bz;  // Controlled_Buffer controlled_buffer_6
  assign controlled_buffer_7_out = CSR[6] ? CSC : 8'bz;  // Controlled_Buffer controlled_buffer_7
  assign controlled_buffer_8_out = CSR[7] ? CSC : 8'bz;  // Controlled_Buffer controlled_buffer_8
  Pull_Resistor pull_resistor_1 (.node(p_sel));
  Decoder #(.select(2), .disabled(0), .enable("false")) decoder_1 (
    .out0(decoder_1_out0), .out1(decoder_1_out1), .out2(decoder_1_out2), .out3(decoder_1_out3), .sel(p_sel));
  or or_1 (or_1_out, decoder_1_out2, decoder_1_out0);
  Multiplexer #(.width(32), .enable("false")) multiplexer_1 (
    .in0(or_2_out), .in1(and_1_out), .out(multiplexer_1_out), .sel(or_1_out));
  Pull_Resistor pull_resistor_2 (.node({controlled_buffer_4_out, controlled_buffer_3_out, controlled_buffer_2_out, controlled_buffer_1_out}));
  assign or_2_out = {controlled_buffer_4_out, controlled_buffer_3_out, controlled_buffer_2_out, controlled_buffer_1_out} | {p1_row_4[0], p1_row_4[1], p1_row_4[2], p1_row_4[3], p1_row_4[4], p1_row_4[5], p1_row_4[6], p1_row_4[7], p1_row_3[0], p1_row_3[1], p1_row_3[2], p1_row_3[3], p1_row_3[4], p1_row_3[5], p1_row_3[6], p1_row_3[7], p1_row_2[0], p1_row_2[1], p1_row_2[2], p1_row_2[3], p1_row_2[4], p1_row_2[5], p1_row_2[6], p1_row_2[7], p1_row_1[0], p1_row_1[1], p1_row_1[2], p1_row_1[3], p1_row_1[4], p1_row_1[5], p1_row_1[6], p1_row_1[7]};  // OR_Gate or_2, 32 bits wide
  Pull_Resistor pull_resistor_3 (.node({controlled_buffer_8_out, controlled_buffer_7_out, controlled_buffer_6_out, controlled_buffer_5_out}));
  assign or_3_out = {controlled_buffer_8_out, controlled_buffer_7_out, controlled_buffer_6_out, controlled_buffer_5_out} | {p1_row_8[0], p1_row_8[1], p1_row_8[2], p1_row_8[3], p1_row_8[4], p1_row_8[5], p1_row_8[6], p1_row_8[7], p1_row_7[0], p1_row_7[1], p1_row_7[2], p1_row_7[3], p1_row_7[4], p1_row_7[5], p1_row_7[6], p1_row_7[7], p1_row_6[0], p1_row_6[1], p1_row_6[2], p1_row_6[3], p1_row_6[4], p1_row_6[5], p1_row_6[6], p1_row_6[7], p1_row_5[0], p1_row_5[1], p1_row_5[2], p1_row_5[3], p1_row_5[4], p1_row_5[5], p1_row_5[6], p1_row_5[7]};  // OR_Gate or_3, 32 bits wide
  or or_4 (or_4_out, decoder_1_out1, decoder_1_out0);
  assign DataO_1 = decoder_1_out1 ? {p1_row_4[0], p1_row_4[1], p1_row_4[2], p1_row_4[3], p1_row_4[4], p1_row_4[5], p1_row_4[6], p1_row_4[7], p1_row_3[0], p1_row_3[1], p1_row_3[2], p1_row_3[3], p1_row_3[4], p1_row_3[5], p1_row_3[6], p1_row_3[7], p1_row_2[0], p1_row_2[1], p1_row_2[2], p1_row_2[3], p1_row_2[4], p1_row_2[5], p1_row_2[6], p1_row_2[7], p1_row_1[0], p1_row_1[1], p1_row_1[2], p1_row_1[3], p1_row_1[4], p1_row_1[5], p1_row_1[6], p1_row_1[7]} : 32'bz;  // Controlled_Buffer controlled_buffer_9
  Register #(.width(32)) register_1 (
    .D(multiplexer_1_out), .en(or_5_out),
    .Q({p1_row_4[0], p1_row_4[1], p1_row_4[2], p1_row_4[3], p1_row_4[4], p1_row_4[5], p1_row_4[6], p1_row_4[7], p1_row_3[0], p1_row_3[1], p1_row_3[2], p1_row_3[3], p1_row_3[4], p1_row_3[5], p1_row_3[6], p1_row_3[7], p1_row_2[0], p1_row_2[1], p1_row_2[2], p1_row_2[3], p1_row_2[4], p1_row_2[5], p1_row_2[6], p1_row_2[7], p1_row_1[0], p1_row_1[1], p1_row_1[2], p1_row_1[3], p1_row_1[4], p1_row_1[5], p1_row_1[6], p1_row_1[7]}),
    .clk(wr), .clr(RST));
  or or_5 (or_5_out, or_1_out, decoder_1_out1);
  assign and_1_out = ~{controlled_buffer_4_out, controlled_buffer_3_out, controlled_buffer_2_out, controlled_buffer_1_out} & {p1_row_4[0], p1_row_4[1], p1_row_4[2], p1_row_4[3], p1_row_4[4], p1_row_4[5], p1_row_4[6], p1_row_4[7], p1_row_3[0], p1_row_3[1], p1_row_3[2], p1_row_3[3], p1_row_3[4], p1_row_3[5], p1_row_3[6], p1_row_3[7], p1_row_2[0], p1_row_2[1], p1_row_2[2], p1_row_2[3], p1_row_2[4], p1_row_2[5], p1_row_2[6], p1_row_2[7], p1_row_1[0], p1_row_1[1], p1_row_1[2], p1_row_1[3], p1_row_1[4], p1_row_1[5], p1_row_1[6], p1_row_1[7]};  // AND_Gate and_1, 32 bits wide
  assign and_2_out = ~{controlled_buffer_8_out, controlled_buffer_7_out, controlled_buffer_6_out, controlled_buffer_5_out} & {p1_row_8[0], p1_row_8[1], p1_row_8[2], p1_row_8[3], p1_row_8[4], p1_row_8[5], p1_row_8[6], p1_row_8[7], p1_row_7[0], p1_row_7[1], p1_row_7[2], p1_row_7[3], p1_row_7[4], p1_row_7[5], p1_row_7[6], p1_row_7[7], p1_row_6[0], p1_row_6[1], p1_row_6[2], p1_row_6[3], p1_row_6[4], p1_row_6[5], p1_row_6[6], p1_row_6[7], p1_row_5[0], p1_row_5[1], p1_row_5[2], p1_row_5[3], p1_row_5[4], p1_row_5[5], p1_row_5[6], p1_row_5[7]};  // AND_Gate and_2, 32 bits wide
  Multiplexer #(.width(32), .enable("false")) multiplexer_2 (
    .in0(or_3_out), .in1(and_2_out), .out(multiplexer_2_out), .sel(or_1_out));
  Register #(.width(32)) register_2 (
    .D(multiplexer_2_out), .en(or_6_out),
    .Q({p1_row_8[0], p1_row_8[1], p1_row_8[2], p1_row_8[3], p1_row_8[4], p1_row_8[5], p1_row_8[6], p1_row_8[7], p1_row_7[0], p1_row_7[1], p1_row_7[2], p1_row_7[3], p1_row_7[4], p1_row_7[5], p1_row_7[6], p1_row_7[7], p1_row_6[0], p1_row_6[1], p1_row_6[2], p1_row_6[3], p1_row_6[4], p1_row_6[5], p1_row_6[6], p1_row_6[7], p1_row_5[0], p1_row_5[1], p1_row_5[2], p1_row_5[3], p1_row_5[4], p1_row_5[5], p1_row_5[6], p1_row_5[7]}),
    .clk(wr), .clr(RST));
  or or_6 (or_6_out, or_1_out, decoder_1_out1);
  assign DataO_2 = decoder_1_out1 ? {p1_row_8[0], p1_row_8[1], p1_row_8[2], p1_row_8[3], p1_row_8[4], p1_row_8[5], p1_row_8[6], p1_row_8[7], p1_row_7[0], p1_row_7[1], p1_row_7[2], p1_row_7[3], p1_row_7[4], p1_row_7[5], p1_row_7[6], p1_row_7[7], p1_row_6[0], p1_row_6[1], p1_row_6[2], p1_row_6[3], p1_row_6[4], p1_row_6[5], p1_row_6[6], p1_row_6[7], p1_row_5[0], p1_row_5[1], p1_row_5[2], p1_row_5[3], p1_row_5[4], p1_row_5[5], p1_row_5[6], p1_row_5[7]} : 32'bz;  // Controlled_Buffer controlled_buffer_10
  Register #(.width(32)) register_3 (
    .D(multiplexer_3_out), .en(or_7_out),
    .Q({p2_row_4[0], p2_row_4[1], p2_row_4[2], p2_row_4[3], p2_row_4[4], p2_row_4[5], p2_row_4[6], p2_row_4[7], p2_row_3[0], p2_row_3[1], p2_row_3[2], p2_row_3[3], p2_row_3[4], p2_row_3[5], p2_row_3[6], p2_row_3[7], p2_row_2[0], p2_row_2[1], p2_row_2[2], p2_row_2[3], p2_row_2[4], p2_row_2[5], p2_row_2[6], p2_row_2[7], p2_row_1[0], p2_row_1[1], p2_row_1[2], p2_row_1[3], p2_row_1[4], p2_row_1[5], p2_row_1[6], p2_row_1[7]}),
    .clk(wr), .clr(RST));
  or or_7 (or_7_out, or_4_out, decoder_1_out2);
  Multiplexer #(.width(32), .enable("false")) multiplexer_3 (
    .in0(or_8_out), .in1(and_3_out), .out(multiplexer_3_out), .sel(or_4_out));
  assign and_3_out = ~{controlled_buffer_4_out, controlled_buffer_3_out, controlled_buffer_2_out, controlled_buffer_1_out} & {p2_row_4[0], p2_row_4[1], p2_row_4[2], p2_row_4[3], p2_row_4[4], p2_row_4[5], p2_row_4[6], p2_row_4[7], p2_row_3[0], p2_row_3[1], p2_row_3[2], p2_row_3[3], p2_row_3[4], p2_row_3[5], p2_row_3[6], p2_row_3[7], p2_row_2[0], p2_row_2[1], p2_row_2[2], p2_row_2[3], p2_row_2[4], p2_row_2[5], p2_row_2[6], p2_row_2[7], p2_row_1[0], p2_row_1[1], p2_row_1[2], p2_row_1[3], p2_row_1[4], p2_row_1[5], p2_row_1[6], p2_row_1[7]};  // AND_Gate and_3, 32 bits wide
  assign or_8_out = {controlled_buffer_4_out, controlled_buffer_3_out, controlled_buffer_2_out, controlled_buffer_1_out} | {p2_row_4[0], p2_row_4[1], p2_row_4[2], p2_row_4[3], p2_row_4[4], p2_row_4[5], p2_row_4[6], p2_row_4[7], p2_row_3[0], p2_row_3[1], p2_row_3[2], p2_row_3[3], p2_row_3[4], p2_row_3[5], p2_row_3[6], p2_row_3[7], p2_row_2[0], p2_row_2[1], p2_row_2[2], p2_row_2[3], p2_row_2[4], p2_row_2[5], p2_row_2[6], p2_row_2[7], p2_row_1[0], p2_row_1[1], p2_row_1[2], p2_row_1[3], p2_row_1[4], p2_row_1[5], p2_row_1[6], p2_row_1[7]};  // OR_Gate or_8, 32 bits wide
  assign and_4_out = ~{controlled_buffer_8_out, controlled_buffer_7_out, controlled_buffer_6_out, controlled_buffer_5_out} & {p2_row_8[0], p2_row_8[1], p2_row_8[2], p2_row_8[3], p2_row_8[4], p2_row_8[5], p2_row_8[6], p2_row_8[7], p2_row_7[0], p2_row_7[1], p2_row_7[2], p2_row_7[3], p2_row_7[4], p2_row_7[5], p2_row_7[6], p2_row_7[7], p2_row_6[0], p2_row_6[1], p2_row_6[2], p2_row_6[3], p2_row_6[4], p2_row_6[5], p2_row_6[6], p2_row_6[7], p2_row_5[0], p2_row_5[1], p2_row_5[2], p2_row_5[3], p2_row_5[4], p2_row_5[5], p2_row_5[6], p2_row_5[7]};  // AND_Gate and_4, 32 bits wide
  assign or_9_out = {controlled_buffer_8_out, controlled_buffer_7_out, controlled_buffer_6_out, controlled_buffer_5_out} | {p2_row_8[0], p2_row_8[1], p2_row_8[2], p2_row_8[3], p2_row_8[4], p2_row_8[5], p2_row_8[6], p2_row_8[7], p2_row_7[0], p2_row_7[1], p2_row_7[2], p2_row_7[3], p2_row_7[4], p2_row_7[5], p2_row_7[6], p2_row_7[7], p2_row_6[0], p2_row_6[1], p2_row_6[2], p2_row_6[3], p2_row_6[4], p2_row_6[5], p2_row_6[6], p2_row_6[7], p2_row_5[0], p2_row_5[1], p2_row_5[2], p2_row_5[3], p2_row_5[4], p2_row_5[5], p2_row_5[6], p2_row_5[7]};  // OR_Gate or_9, 32 bits wide
  Multiplexer #(.width(32), .enable("false")) multiplexer_4 (
    .in0(or_9_out), .in1(and_4_out), .out(multiplexer_4_out), .sel(or_4_out));
  Register #(.width(32)) register_4 (
    .D(multiplexer_4_out), .en(or_10_out),
    .Q({p2_row_8[0], p2_row_8[1], p2_row_8[2], p2_row_8[3], p2_row_8[4], p2_row_8[5], p2_row_8[6], p2_row_8[7], p2_row_7[0], p2_row_7[1], p2_row_7[2], p2_row_7[3], p2_row_7[4], p2_row_7[5], p2_row_7[6], p2_row_7[7], p2_row_6[0], p2_row_6[1], p2_row_6[2], p2_row_6[3], p2_row_6[4], p2_row_6[5], p2_row_6[6], p2_row_6[7], p2_row_5[0], p2_row_5[1], p2_row_5[2], p2_row_5[3], p2_row_5[4], p2_row_5[5], p2_row_5[6], p2_row_5[7]}),
    .clk(wr), .clr(RST));
  or or_10 (or_10_out, or_4_out, decoder_1_out2);
  assign DataO_1 = decoder_1_out2 ? {p2_row_4[0], p2_row_4[1], p2_row_4[2], p2_row_4[3], p2_row_4[4], p2_row_4[5], p2_row_4[6], p2_row_4[7], p2_row_3[0], p2_row_3[1], p2_row_3[2], p2_row_3[3], p2_row_3[4], p2_row_3[5], p2_row_3[6], p2_row_3[7], p2_row_2[0], p2_row_2[1], p2_row_2[2], p2_row_2[3], p2_row_2[4], p2_row_2[5], p2_row_2[6], p2_row_2[7], p2_row_1[0], p2_row_1[1], p2_row_1[2], p2_row_1[3], p2_row_1[4], p2_row_1[5], p2_row_1[6], p2_row_1[7]} : 32'bz;  // Controlled_Buffer controlled_buffer_11
  or or_11 (or_11_out, decoder_1_out0, decoder_1_out3);
  Multiplexer #(.width(32), .enable("false")) multiplexer_5 (
    .in0(or_12_out), .in1(and_5_out), .out(multiplexer_5_out), .sel(decoder_1_out0));
  assign or_12_out = {controlled_buffer_4_out, controlled_buffer_3_out, controlled_buffer_2_out, controlled_buffer_1_out} | {Task_row_4[0], Task_row_4[1], Task_row_4[2], Task_row_4[3], Task_row_4[4], Task_row_4[5], Task_row_4[6], Task_row_4[7], Task_row_3[0], Task_row_3[1], Task_row_3[2], Task_row_3[3], Task_row_3[4], Task_row_3[5], Task_row_3[6], Task_row_3[7], Task_row_2[0], Task_row_2[1], Task_row_2[2], Task_row_2[3], Task_row_2[4], Task_row_2[5], Task_row_2[6], Task_row_2[7], Task_row_1[0], Task_row_1[1], Task_row_1[2], Task_row_1[3], Task_row_1[4], Task_row_1[5], Task_row_1[6], Task_row_1[7]};  // OR_Gate or_12, 32 bits wide
  assign or_13_out = {controlled_buffer_8_out, controlled_buffer_7_out, controlled_buffer_6_out, controlled_buffer_5_out} | {Task_row_8[0], Task_row_8[1], Task_row_8[2], Task_row_8[3], Task_row_8[4], Task_row_8[5], Task_row_8[6], Task_row_8[7], Task_row_7[0], Task_row_7[1], Task_row_7[2], Task_row_7[3], Task_row_7[4], Task_row_7[5], Task_row_7[6], Task_row_7[7], Task_row_6[0], Task_row_6[1], Task_row_6[2], Task_row_6[3], Task_row_6[4], Task_row_6[5], Task_row_6[6], Task_row_6[7], Task_row_5[0], Task_row_5[1], Task_row_5[2], Task_row_5[3], Task_row_5[4], Task_row_5[5], Task_row_5[6], Task_row_5[7]};  // OR_Gate or_13, 32 bits wide
  Multiplexer #(.width(32), .enable("false")) multiplexer_6 (
    .in0(or_13_out), .in1(and_6_out), .out(multiplexer_6_out), .sel(decoder_1_out0));
  or or_14 (or_14_out, decoder_1_out0, decoder_1_out3);
  assign DataO_2 = decoder_1_out2 ? {p2_row_8[0], p2_row_8[1], p2_row_8[2], p2_row_8[3], p2_row_8[4], p2_row_8[5], p2_row_8[6], p2_row_8[7], p2_row_7[0], p2_row_7[1], p2_row_7[2], p2_row_7[3], p2_row_7[4], p2_row_7[5], p2_row_7[6], p2_row_7[7], p2_row_6[0], p2_row_6[1], p2_row_6[2], p2_row_6[3], p2_row_6[4], p2_row_6[5], p2_row_6[6], p2_row_6[7], p2_row_5[0], p2_row_5[1], p2_row_5[2], p2_row_5[3], p2_row_5[4], p2_row_5[5], p2_row_5[6], p2_row_5[7]} : 32'bz;  // Controlled_Buffer controlled_buffer_12
  assign DataO_1 = decoder_1_out3 ? {Task_row_4[0], Task_row_4[1], Task_row_4[2], Task_row_4[3], Task_row_4[4], Task_row_4[5], Task_row_4[6], Task_row_4[7], Task_row_3[0], Task_row_3[1], Task_row_3[2], Task_row_3[3], Task_row_3[4], Task_row_3[5], Task_row_3[6], Task_row_3[7], Task_row_2[0], Task_row_2[1], Task_row_2[2], Task_row_2[3], Task_row_2[4], Task_row_2[5], Task_row_2[6], Task_row_2[7], Task_row_1[0], Task_row_1[1], Task_row_1[2], Task_row_1[3], Task_row_1[4], Task_row_1[5], Task_row_1[6], Task_row_1[7]} : 32'bz;  // Controlled_Buffer controlled_buffer_13
  Register #(.width(32)) register_5 (
    .D(multiplexer_5_out), .en(or_11_out),
    .Q({Task_row_4[0], Task_row_4[1], Task_row_4[2], Task_row_4[3], Task_row_4[4], Task_row_4[5], Task_row_4[6], Task_row_4[7], Task_row_3[0], Task_row_3[1], Task_row_3[2], Task_row_3[3], Task_row_3[4], Task_row_3[5], Task_row_3[6], Task_row_3[7], Task_row_2[0], Task_row_2[1], Task_row_2[2], Task_row_2[3], Task_row_2[4], Task_row_2[5], Task_row_2[6], Task_row_2[7], Task_row_1[0], Task_row_1[1], Task_row_1[2], Task_row_1[3], Task_row_1[4], Task_row_1[5], Task_row_1[6], Task_row_1[7]}),
    .clk(wr), .clr(RST));
  assign and_5_out = ~{controlled_buffer_4_out, controlled_buffer_3_out, controlled_buffer_2_out, controlled_buffer_1_out} & {Task_row_4[0], Task_row_4[1], Task_row_4[2], Task_row_4[3], Task_row_4[4], Task_row_4[5], Task_row_4[6], Task_row_4[7], Task_row_3[0], Task_row_3[1], Task_row_3[2], Task_row_3[3], Task_row_3[4], Task_row_3[5], Task_row_3[6], Task_row_3[7], Task_row_2[0], Task_row_2[1], Task_row_2[2], Task_row_2[3], Task_row_2[4], Task_row_2[5], Task_row_2[6], Task_row_2[7], Task_row_1[0], Task_row_1[1], Task_row_1[2], Task_row_1[3], Task_row_1[4], Task_row_1[5], Task_row_1[6], Task_row_1[7]};  // AND_Gate and_5, 32 bits wide
  assign and_6_out = ~{controlled_buffer_8_out, controlled_buffer_7_out, controlled_buffer_6_out, controlled_buffer_5_out} & {Task_row_8[0], Task_row_8[1], Task_row_8[2], Task_row_8[3], Task_row_8[4], Task_row_8[5], Task_row_8[6], Task_row_8[7], Task_row_7[0], Task_row_7[1], Task_row_7[2], Task_row_7[3], Task_row_7[4], Task_row_7[5], Task_row_7[6], Task_row_7[7], Task_row_6[0], Task_row_6[1], Task_row_6[2], Task_row_6[3], Task_row_6[4], Task_row_6[5], Task_row_6[6], Task_row_6[7], Task_row_5[0], Task_row_5[1], Task_row_5[2], Task_row_5[3], Task_row_5[4], Task_row_5[5], Task_row_5[6], Task_row_5[7]};  // AND_Gate and_6, 32 bits wide
  Register #(.width(32)) register_6 (
    .D(multiplexer_6_out), .en(or_14_out),
    .Q({Task_row_8[0], Task_row_8[1], Task_row_8[2], Task_row_8[3], Task_row_8[4], Task_row_8[5], Task_row_8[6], Task_row_8[7], Task_row_7[0], Task_row_7[1], Task_row_7[2], Task_row_7[3], Task_row_7[4], Task_row_7[5], Task_row_7[6], Task_row_7[7], Task_row_6[0], Task_row_6[1], Task_row_6[2], Task_row_6[3], Task_row_6[4], Task_row_6[5], Task_row_6[6], Task_row_6[7], Task_row_5[0], Task_row_5[1], Task_row_5[2], Task_row_5[3], Task_row_5[4], Task_row_5[5], Task_row_5[6], Task_row_5[7]}),
    .clk(wr), .clr(RST));
  assign DataO_2 = decoder_1_out3 ? {Task_row_8[0], Task_row_8[1], Task_row_8[2], Task_row_8[3], Task_row_8[4], Task_row_8[5], Task_row_8[6], Task_row_8[7], Task_row_7[0], Task_row_7[1], Task_row_7[2], Task_row_7[3], Task_row_7[4], Task_row_7[5], Task_row_7[6], Task_row_7[7], Task_row_6[0], Task_row_6[1], Task_row_6[2], Task_row_6[3], Task_row_6[4], Task_row_6[5], Task_row_6[6], Task_row_6[7], Task_row_5[0], Task_row_5[1], Task_row_5[2], Task_row_5[3], Task_row_5[4], Task_row_5[5], Task_row_5[6], Task_row_5[7]} : 32'bz;  // Controlled_Buffer controlled_buffer_14
  Pull_Resistor pull_resistor_4 (.node(DataO_1));
  Pull_Resistor pull_resistor_5 (.node(DataO_2));

  assign p2_row_1[8] = 1'b0;
  assign p2_row_2[8] = 1'b0;
  assign p2_row_3[8] = 1'b0;
  assign p2_row_4[8] = 1'b0;
  assign p2_row_5[8] = 1'b0;
  assign p2_row_6[8] = 1'b0;
  assign p2_row_7[8] = 1'b0;
  assign p2_row_8[8] = 1'b0;
  assign Task_row_1[9:8] = 2'b00;
  assign Task_row_2[9:8] = 2'b00;
  assign Task_row_3[9:8] = 2'b00;
  assign Task_row_4[9:8] = 2'b00;
  assign Task_row_5[9:8] = 2'b00;
  assign Task_row_6[9:8] = 2'b00;
  assign Task_row_7[9:8] = 2'b00;
  assign Task_row_8[9:8] = 2'b00;
endmodule

module pointer_mover (
  input  [4:0] KBD_command,
  input  CLK,
  input  RST,
  input  [7:0] RST_CSC,
  input  [7:0] RST_CSR,
  output [7:0] CSC,
  output [7:0] CSR
);

  wire and_1_out, and_2_out, and_3_out, and_4_out, comparator_1_eq, comparator_2_eq, comparator_3_eq,
       comparator_4_eq, not_1_out, not_2_out, or_1_out, or_2_out, or_3_out, or_4_out;
  wire [7:0] multiplexer_1_out, multiplexer_2_out, multiplexer_3_out, multiplexer_4_out;

  // Probe on KBD_command
  Comparator #(.width(5), .mode("unsigned")) comparator_1 (
    .a(KBD_command), .b(5'b10001), .eq(comparator_1_eq));  // open: gt, lt
  Comparator #(.width(5), .mode("unsigned")) comparator_2 (
    .a(KBD_command), .b(5'b10010), .eq(comparator_2_eq));  // open: gt, lt
  Comparator #(.width(5), .mode("unsigned")) comparator_3 (
    .a(KBD_command), .b(5'b10000), .eq(comparator_3_eq));  // open: gt, lt
  Comparator #(.width(5), .mode("unsigned")) comparator_4 (
    .a(KBD_command), .b(5'b10011), .eq(comparator_4_eq));  // open: gt, lt
  or or_1 (or_1_out, comparator_1_eq, comparator_2_eq);
  or or_2 (or_2_out, comparator_3_eq, comparator_4_eq);
  Multiplexer #(.width(8), .enable("false")) multiplexer_1 (
    .in0({CSC[0], CSC[7:1]}), .in1({CSC[6:0], CSC[7]}), .out(multiplexer_1_out), .sel(comparator_1_eq));
  Pull_Resistor pull_resistor_1 (.node(RST_CSC[7:1]));
  Pull_Resistor #(.pull(1)) pull_resistor_2 (.node(RST_CSC[0]));
  Multiplexer #(.width(8), .enable("false")) multiplexer_2 (
    .in0({CSR[0], CSR[7:1]}), .in1({CSR[6:0], CSR[7]}), .out(multiplexer_2_out), .sel(comparator_3_eq));
  Pull_Resistor #(.pull(1)) pull_resistor_3 (.node(RST_CSR[0]));
  Pull_Resistor pull_resistor_4 (.node(RST_CSR[7:1]));
  Multiplexer #(.width(8), .enable("false")) multiplexer_3 (
    .in0(multiplexer_1_out), .in1(RST_CSC), .out(multiplexer_3_out), .sel(RST));
  Register register_1 (.D(multiplexer_3_out), .en(1'b1), .Q(CSC), .clk(or_3_out), .clr(1'b0));
  or or_3 (or_3_out, and_3_out, and_1_out);
  and and_1 (and_1_out, CLK, or_1_out);
  Multiplexer #(.width(8), .enable("false")) multiplexer_4 (
    .in0(multiplexer_2_out), .in1(RST_CSR), .out(multiplexer_4_out), .sel(RST));
  Register register_2 (.D(multiplexer_4_out), .en(1'b1), .Q(CSR), .clk(or_4_out), .clr(1'b0));
  or or_4 (or_4_out, and_4_out, and_2_out);
  and and_2 (and_2_out, CLK, or_2_out);
  and and_3 (and_3_out, ~RST, ~not_1_out);  // AND_Gate
  not not_1 (not_1_out, RST);
  and and_4 (and_4_out, ~RST, ~not_2_out);  // AND_Gate
  not not_2 (not_2_out, RST);
endmodule

module position_checker (
  input  [7:0] CSc,
  input  [7:0] CSR,
  input  [31:0] Field_input_1,
  input  [31:0] Field_input_2,
  output Out__either,
  output Out__all
);

  wire [7:0] and_1_out, and_2_out, and_3_out, and_4_out, and_5_out, and_6_out, and_7_out, and_8_out,
       and_9_out, controlled_buffer_12_out, controlled_buffer_13_out, controlled_buffer_15_out,
       controlled_buffer_16_out, or_1_out, pull_resistor_1_node, pull_resistor_2_node, pull_resistor_3_node,
       pull_resistor_4_node, pull_resistor_5_node, pull_resistor_6_node, pull_resistor_7_node,
       pull_resistor_8_node, pull_resistor_9_node, pull_resistor_10_node, pull_resistor_11_node,
       pull_resistor_14_node;

  Pull_Resistor pull_resistor_1 (.node(pull_resistor_1_node));
  Pull_Resistor pull_resistor_2 (.node(pull_resistor_2_node));
  Pull_Resistor pull_resistor_3 (.node(pull_resistor_3_node));
  assign pull_resistor_2_node = CSR[0] ? Field_input_1[7:0] : 8'bz;  // Controlled_Buffer controlled_buffer_1
  assign pull_resistor_3_node = CSR[1] ? Field_input_1[15:8] : 8'bz;  // Controlled_Buffer controlled_buffer_2
  assign pull_resistor_1_node = CSR[2] ? Field_input_1[23:16] : 8'bz;  // Controlled_Buffer controlled_buffer_3
  Pull_Resistor pull_resistor_4 (.node(pull_resistor_4_node));
  Pull_Resistor pull_resistor_5 (.node(pull_resistor_5_node));
  Pull_Resistor pull_resistor_6 (.node(pull_resistor_6_node));
  assign pull_resistor_6_node = CSR[3] ? Field_input_1[31:24] : 8'bz;  // Controlled_Buffer controlled_buffer_4
  assign pull_resistor_5_node = CSR[4] ? Field_input_2[7:0] : 8'bz;  // Controlled_Buffer controlled_buffer_5
  assign pull_resistor_4_node = CSR[5] ? Field_input_2[15:8] : 8'bz;  // Controlled_Buffer controlled_buffer_6
  Pull_Resistor pull_resistor_7 (.node(pull_resistor_7_node));
  Pull_Resistor pull_resistor_8 (.node(pull_resistor_8_node));
  assign pull_resistor_8_node = CSR[6] ? Field_input_2[23:16] : 8'bz;  // Controlled_Buffer controlled_buffer_7
  assign pull_resistor_7_node = CSR[7] ? Field_input_2[31:24] : 8'bz;  // Controlled_Buffer controlled_buffer_8
  assign and_1_out = CSc & pull_resistor_2_node;  // AND_Gate and_1, 8 bits wide
  Pull_Resistor #(.pull(1)) pull_resistor_9 (.node(pull_resistor_9_node));
  assign pull_resistor_9_node = CSR[0] ? and_1_out : 8'bz;  // Controlled_Buffer controlled_buffer_9
  assign and_2_out = CSc & pull_resistor_3_node;  // AND_Gate and_2, 8 bits wide
  assign and_3_out = CSc & pull_resistor_1_node;  // AND_Gate and_3, 8 bits wide
  Pull_Resistor #(.pull(1)) pull_resistor_10 (.node(pull_resistor_10_node));
  assign pull_resistor_10_node = CSR[2] ? and_3_out : 8'bz;  // Controlled_Buffer controlled_buffer_10
  Pull_Resistor #(.pull(1)) pull_resistor_11 (.node(pull_resistor_11_node));
  assign pull_resistor_11_node = CSR[1] ? and_2_out : 8'bz;  // Controlled_Buffer controlled_buffer_11
  assign and_4_out = CSc & pull_resistor_6_node;  // AND_Gate and_4, 8 bits wide
  assign controlled_buffer_12_out = CSR[3] ? and_4_out : 8'bz;  // Controlled_Buffer controlled_buffer_12
  Pull_Resistor #(.pull(1)) pull_resistor_12 (.node(controlled_buffer_12_out));
  assign and_5_out = CSc & pull_resistor_5_node;  // AND_Gate and_5, 8 bits wide
  assign controlled_buffer_13_out = CSR[4] ? and_5_out : 8'bz;  // Controlled_Buffer controlled_buffer_13
  Pull_Resistor #(.pull(1)) pull_resistor_13 (.node(controlled_buffer_13_out));
  assign and_6_out = CSc & pull_resistor_4_node;  // AND_Gate and_6, 8 bits wide
  assign and_7_out = CSc & pull_resistor_8_node;  // AND_Gate and_7, 8 bits wide
  Pull_Resistor #(.pull(1)) pull_resistor_14 (.node(pull_resistor_14_node));
  assign pull_resistor_14_node = CSR[6] ? and_7_out : 8'bz;  // Controlled_Buffer controlled_buffer_14
  assign controlled_buffer_15_out = CSR[5] ? and_6_out : 8'bz;  // Controlled_Buffer controlled_buffer_15
  Pull_Resistor #(.pull(1)) pull_resistor_15 (.node(controlled_buffer_15_out));
  assign and_8_out = CSc & pull_resistor_7_node;  // AND_Gate and_8, 8 bits wide
  assign controlled_buffer_16_out = CSR[7] ? and_8_out : 8'bz;  // Controlled_Buffer controlled_buffer_16
  Pull_Resistor #(.pull(1)) pull_resistor_16 (.node(controlled_buffer_16_out));
  assign or_1_out = and_8_out | and_7_out | and_6_out | and_5_out | and_4_out | and_3_out | and_2_out | and_1_out;  // OR_Gate or_1, 8 bits wide
  or or_2 (Out__either, or_1_out[0], or_1_out[1], or_1_out[2], or_1_out[3], or_1_out[4], or_1_out[5], or_1_out[6], or_1_out[7], 1'b0);
  assign and_9_out = CSc & controlled_buffer_16_out & pull_resistor_14_node & controlled_buffer_15_out & controlled_buffer_13_out & controlled_buffer_12_out & pull_resistor_10_node & pull_resistor_11_node & pull_resistor_9_node;  // AND_Gate and_9, 8 bits wide
  Comparator comparator_1 (.a(CSc), .b(and_9_out), .eq(Out__all));  // open: gt, lt
endmodule

module pointer_controller (
  input  Active,
  input  [4:0] KBD_command,
  input  CLK,
  input  RST,
  input  [7:0] RST_CSC,
  input  [7:0] RST_CSR,
  input  Allow_nearby,
  input  [31:0] Field_state_1,
  input  [31:0] Field_state_2,
  input  Free_mode,
  output [7:0] CSC,
  output [7:0] CSR,
  output Err,
  output Ready
);

  wire and_2_out, and_3_out, clk_t, counter_1_carry, d_ff_1_q, not_1_out, not_2_out, or_1_out, or_2_out,
       or_3_out, or_4_out, position_checker_1_out__all, stop, xor_1_out;
  wire [3:0] counter_1_q;

  and and_1 (clk_t, ~stop, Active, CLK);  // AND_Gate
  pointer_mover pointer_mover_1 (
    .CLK(clk_t), .RST(RST), .CSC(CSC), .CSR(CSR), .KBD_command(KBD_command), .RST_CSC(RST_CSC),
    .RST_CSR(RST_CSR));
  position_checker position_checker_1 (
    .CSc(CSC), .CSR(CSR), .Field_input_1(Field_state_1), .Field_input_2(Field_state_2),
    .Out__all(position_checker_1_out__all));  // open: Out__either
  D_Flip_Flop d_ff_1 (
    .clk(Active), .D(position_checker_1_out__all), .Q(d_ff_1_q), .en(Allow_nearby), .reset(or_1_out));  // open: Qn, preset
  or or_1 (or_1_out, RST, and_3_out);
  and and_2 (and_2_out, Allow_nearby, d_ff_1_q);
  Counter #(.width(4), .max('h8), .trigger("falling")) counter_1 (
    .load(1'b0), .count(1'b1), .Q(counter_1_q), .carry(counter_1_carry), .clk(clk_t), .clr(or_2_out));  // open: D
  or or_2 (or_2_out, RST, xor_1_out);
  and and_3 (and_3_out, ~Active, ~not_2_out);  // AND_Gate
  or or_3 (or_3_out, 1'b0, counter_1_q[0], counter_1_q[1], counter_1_q[2], counter_1_q[3]);
  xor xor_1 (xor_1_out, ~Active, not_1_out);  // XOR_Gate
  not not_1 (not_1_out, Active);
  or or_4 (or_4_out, and_2_out, position_checker_1_out__all, Free_mode);
  not not_2 (not_2_out, Active);
  and and_4 (Err, counter_1_carry, ~Ready);  // AND_Gate
  or or_5 (stop, Err, Ready);
  and and_5 (Ready, or_3_out, or_4_out);
endmodule

module basic_controller (
  input  [4:0] KBD_command,
  input  KBD_ready,
  input  PC_ready,
  input  Is_special,
  input  Wrong_move,
  input  Active,
  input  SPI_done,
  input  [1:0] SPI_in,
  input  [1:0] Mode,
  input  CLK,
  output Req_KBD,
  output Req_KBD_num,
  output PC_active,
  output Check_speciality,
  output Error,
  output Call_CDM,
  output cmd_overwrite,
  output PC_free_mode,
  output [7:0] SPI_control,
  output PC_allow_nearby,
  output KBD_cahce_overwrite,
  output [1:0] Cache_field_sel,
  output Cache_field_wr,
  output [4:0] KBD_command_2,
  output Enter
);

  wire allow_e_manip, and_2_out, and_4_out, and_5_out, and_6_out, and_8_out, and_11_out, and_12_out,
       and_14_out, and_15_out, and_16_out, and_17_out, and_18_out, and_19_out, and_20_out, and_21_out,
       and_22_out, and_23_out, and_24_out, and_25_out, and_26_out, and_27_out, and_28_out, and_29_out,
       and_30_out, and_31_out, and_32_out, and_33_out, clk_t, col_exceeded, comparator_1_eq, comparator_2_gt,
       comparator_3_lt, comparator_4_gt, comparator_5_lt, comparator_6_eq, comparator_7_eq,
       controlled_buffer_8_out, counter_3_carry, d_ff_1_qn, d_ff_2_q, d_ff_2_qn, d_ff_4_q, d_ff_7_q,
       d_ff_8_q, decoder_1_out0, decoder_1_out1, decoder_2_out0, decoder_2_out1, decoder_2_out2,
       decoder_2_out3, decoder_2_out5, decoder_2_out6, decoder_2_out7, decoder_2_out8, decoder_2_out9,
       decoder_2_out10, decoder_2_out11, decoder_2_out12, decoder_2_out14, nor_1_out, nor_2_out, not_1_out,
       not_2_out, not_3_out, not_4_out, not_5_out, not_6_out, or_1_out, or_3_out, or_4_out, or_6_out,
       or_7_out, or_8_out, or_9_out, or_10_out, or_11_out, or_12_out, or_15_out, or_16_out, or_17_out, rst,
       SPI_wait, stop;
  wire [2:0] counter_1_q, counter_2_q;
  wire [3:0] multiplexer_3_out, multiplexer_4_out, multiplexer_5_out, multiplexer_6_out,
       pull_resistor_1_node, register_1_q;
  wire [4:0] controlled_buffer_5_out, multiplexer_1_out, multiplexer_2_out, register_2_q;

  or or_1 (or_1_out, SPI_wait, PC_active, Req_KBD, stop);
  Decoder #(.select(2), .enable("false")) decoder_1 (
    .out0(decoder_1_out0), .out1(decoder_1_out1), .out2(PC_allow_nearby), .out3(KBD_cahce_overwrite),
    .sel(Mode));
  and and_1 (clk_t, ~or_1_out, Active, CLK);  // AND_Gate
  Pull_Resistor pull_resistor_1 (.node(pull_resistor_1_node));
  not not_1 (not_1_out, Active);
  or or_2 (PC_free_mode, KBD_cahce_overwrite, decoder_1_out0);
  // Probe on pull_resistor_1_node
  Register #(.width(4), .trigger("falling")) register_1 (
    .D(pull_resistor_1_node), .en(1'b1), .Q(register_1_q), .clk(and_2_out), .clr(rst));
  and and_2 (and_2_out, or_16_out, clk_t);
  xor xor_1 (rst, ~Active, not_1_out);  // XOR_Gate
  Comparator #(.width(2)) comparator_1 (.a(2'b11), .b(SPI_in), .eq(comparator_1_eq));  // open: gt, lt
  Decoder #(.select(4), .disabled(0)) decoder_2 (
    .out0(decoder_2_out0), .out1(decoder_2_out1), .out2(decoder_2_out2), .out3(decoder_2_out3),
    .out4(Check_speciality), .out5(decoder_2_out5), .out6(decoder_2_out6), .out7(decoder_2_out7),
    .out8(decoder_2_out8), .out9(decoder_2_out9), .out10(decoder_2_out10), .out11(decoder_2_out11),
    .out12(decoder_2_out12), .out14(decoder_2_out14), .out15(Error), .sel(register_1_q), .en(Active));  // open: out13
  and and_3 (allow_e_manip, decoder_1_out1, d_ff_1_qn);
  D_Flip_Flop d_ff_1 (.clk(rst), .D(comparator_1_eq), .Qn(d_ff_1_qn));  // open: Q, preset, en, reset
  and and_4 (and_4_out, decoder_2_out6, ~or_3_out);  // AND_Gate
  and and_5 (and_5_out, decoder_2_out7, ~or_3_out);  // AND_Gate
  or or_3 (or_3_out, SPI_control[0], SPI_control[1], SPI_control[4], SPI_control[5], SPI_control[7]);
  or or_4 (or_4_out, decoder_2_out11, decoder_2_out12);
  Counter #(.width(3), .max('h7)) counter_1 (
    .load(1'b0), .count(1'b1), .Q(counter_1_q), .clk(decoder_2_out11), .clr(rst));  // open: D, carry
  Counter #(.width(3), .max('h7)) counter_2 (
    .load(1'b0), .count(1'b1), .Q(counter_2_q), .clk(decoder_2_out12), .clr(rst));  // open: D, carry
  or or_5 (Req_KBD, Req_KBD_num, and_6_out);
  and and_6 (and_6_out, Active, or_6_out, ~d_ff_7_q, ~KBD_cahce_overwrite);  // AND_Gate
  or or_6 (or_6_out, decoder_2_out0, decoder_2_out1);
  and and_7 (cmd_overwrite, CLK, KBD_cahce_overwrite, decoder_2_out7);
  or or_7 (or_7_out, decoder_2_out5, decoder_2_out6, decoder_2_out2, decoder_2_out7);
  assign SPI_control = decoder_2_out5 ? 8'h36 : 8'bz;  // Controlled_Buffer controlled_buffer_1
  Pull_Resistor pull_resistor_2 (.node(SPI_control));
  assign SPI_control = decoder_2_out2 ? 8'h3e : 8'bz;  // Controlled_Buffer controlled_buffer_2
  assign SPI_control = and_4_out ? 8'h44 : 8'bz;  // Controlled_Buffer controlled_buffer_3
  assign SPI_control = and_5_out ? 8'h4c : 8'bz;  // Controlled_Buffer controlled_buffer_4
  or or_8 (or_8_out, decoder_2_out8, or_4_out);
  Multiplexer #(.width(5), .disabled(0), .enable("false")) multiplexer_1 (
    .in0(5'b10000), .in1(5'b10001), .out(multiplexer_1_out), .sel(decoder_2_out11));
  nor nor_1 (nor_1_out, counter_1_q[0], counter_1_q[1], counter_1_q[2]);
  and and_8 (and_8_out, decoder_2_out12, nor_2_out);
  nor nor_2 (nor_2_out, counter_2_q[0], counter_2_q[1], counter_2_q[2]);
  and and_9 (Req_KBD_num, Active, decoder_2_out1, ~d_ff_7_q, ~KBD_cahce_overwrite);  // AND_Gate
  and and_10 (PC_active, decoder_2_out3, Active, ~d_ff_4_q);  // AND_Gate
  and and_11 (and_11_out, Check_speciality, Is_special);
  and and_12 (and_12_out, Check_speciality, ~Is_special);  // AND_Gate
  and and_13 (SPI_wait, Active, or_7_out, ~SPI_done);  // AND_Gate
  D_Flip_Flop #(.trigger("falling")) d_ff_2 (
    .clk(clk_t), .D(and_4_out), .Q(d_ff_2_q), .Qn(d_ff_2_qn), .preset(1'b0), .en(1'b1), .reset(rst));
  or or_9 (or_9_out, and_4_out, and_5_out);
  Multiplexer #(.width(5), .disabled(0), .enable("false")) multiplexer_2 (
    .in0(5'b00011), .in1(multiplexer_1_out), .out(multiplexer_2_out), .sel(or_4_out));
  D_Flip_Flop #(.trigger("falling")) d_ff_3 (
    .clk(clk_t), .D(nor_1_out), .Q(col_exceeded), .preset(1'b0), .en(decoder_2_out11), .reset(decoder_2_out12));  // open: Qn
  assign controlled_buffer_5_out = and_8_out ? {5{1'b1}} : 5'bz;  // Controlled_Buffer controlled_buffer_5
  not not_2 (not_2_out, KBD_cahce_overwrite);
  assign controlled_buffer_5_out = not_2_out ? KBD_command : 5'bz;  // Controlled_Buffer controlled_buffer_6
  Pull_Resistor pull_resistor_3 (.node(controlled_buffer_5_out));
  D_Flip_Flop d_ff_4 (.clk(CLK), .D(PC_ready), .Q(d_ff_4_q), .preset(1'b0), .en(1'b1), .reset(and_14_out));  // open: Qn
  D_Flip_Flop d_ff_5 (.clk(clk_t), .D(or_10_out), .Q(Call_CDM), .preset(1'b0), .en(1'b1), .reset(rst));  // open: Qn
  or or_10 (or_10_out, and_11_out, and_29_out);
  Register #(.width(5), .trigger("falling")) register_2 (
    .D(multiplexer_2_out), .en(or_8_out), .Q(register_2_q), .clk(clk_t), .clr(rst));
  assign KBD_command_2 = KBD_cahce_overwrite ? register_2_q : 5'bz;  // Controlled_Buffer controlled_buffer_7
  Comparator #(.width(5), .mode("unsigned")) comparator_2 (
    .a(controlled_buffer_5_out), .b(5'b01111), .gt(comparator_2_gt));  // open: eq, lt
  Comparator #(.width(5), .mode("unsigned")) comparator_3 (
    .a(controlled_buffer_5_out), .b(5'b10100), .lt(comparator_3_lt));  // open: gt, eq
  not not_3 (not_3_out, decoder_2_out3);
  and and_14 (and_14_out, not_3_out, decoder_2_out3);
  Comparator #(.width(5), .mode("unsigned")) comparator_4 (
    .a(controlled_buffer_5_out), .b(5'b01011), .gt(comparator_4_gt));  // open: eq, lt
  Comparator #(.width(5), .mode("unsigned")) comparator_5 (
    .a(controlled_buffer_5_out), .b(5'b10000), .lt(comparator_5_lt));  // open: gt, eq
  and and_15 (and_15_out, decoder_2_out5, SPI_done);
  or or_11 (or_11_out, SPI_in[0], SPI_in[1]);
  and and_16 (and_16_out, or_11_out, decoder_2_out9);
  or or_12 (or_12_out, SPI_in[0], SPI_in[1]);
  and and_17 (and_17_out, or_12_out, decoder_2_out10);
  Comparator #(.width(5), .mode("unsigned")) comparator_6 (
    .a(controlled_buffer_5_out), .b({5{1'b1}}), .eq(comparator_6_eq));  // open: gt, lt
  Comparator #(.width(5), .mode("unsigned")) comparator_7 (
    .a(controlled_buffer_5_out), .b(5'b10100), .eq(comparator_7_eq));  // open: gt, lt
  assign controlled_buffer_8_out = not_2_out ? KBD_ready : 1'bz;  // Controlled_Buffer controlled_buffer_8
  Pull_Resistor pull_resistor_4 (.node(controlled_buffer_8_out));
  and and_18 (and_18_out, comparator_4_gt, allow_e_manip, comparator_5_lt);
  not not_4 (not_4_out, Wrong_move);
  assign Cache_field_sel = decoder_2_out9 ? ~SPI_in : 2'bz;  // Controlled_Inverter controlled_inverter_1
  assign Cache_field_sel = decoder_2_out10 ? 2'b11 : 2'bz;  // Controlled_Buffer controlled_buffer_9
  D_Flip_Flop #(.trigger("falling")) d_ff_6 (
    .clk(clk_t), .D(comparator_6_eq), .Q(Enter), .preset(1'b0), .en(1'b1), .reset(rst));  // open: Qn
  and and_19 (and_19_out, controlled_buffer_8_out, decoder_2_out1);
  and and_20 (and_20_out, controlled_buffer_8_out, and_21_out);
  and and_21 (and_21_out, comparator_2_gt, decoder_2_out0, comparator_3_lt);
  and and_22 (and_22_out, d_ff_4_q, decoder_2_out3);
  and and_23 (and_23_out, decoder_2_out0, controlled_buffer_8_out, and_18_out, not_4_out);
  and and_24 (and_24_out, controlled_buffer_8_out, and_18_out, Wrong_move, decoder_2_out1);
  and and_25 (and_25_out, d_ff_2_q, decoder_2_out14, ~SPI_in[0], ~Error);  // AND_Gate
  and and_26 (and_26_out, or_7_out, decoder_2_out2, SPI_done);
  and and_27 (and_27_out, d_ff_2_qn, decoder_2_out14);
  and and_28 (and_28_out, SPI_done, or_9_out);
  or or_13 (Cache_field_wr, and_16_out, and_17_out);
  or or_14 (stop, Enter, Call_CDM);
  and and_29 (and_29_out, comparator_7_eq, decoder_2_out0, controlled_buffer_8_out);
  assign pull_resistor_1_node = and_19_out ? 4'b0100 : 4'bz;  // Controlled_Buffer controlled_buffer_10
  assign pull_resistor_1_node = and_20_out ? 4'b0011 : 4'bz;  // Controlled_Buffer controlled_buffer_11
  and and_30 (and_30_out, decoder_2_out0, KBD_cahce_overwrite);
  assign pull_resistor_1_node = and_30_out ? 4'b1000 : 4'bz;  // Controlled_Buffer controlled_buffer_12
  assign pull_resistor_1_node = and_22_out ? multiplexer_5_out : 4'bz;  // Controlled_Buffer controlled_buffer_13
  assign pull_resistor_1_node = and_23_out ? 4'b0001 : 4'bz;  // Controlled_Buffer controlled_buffer_14
  assign pull_resistor_1_node = and_24_out ? 4'b1111 : 4'bz;  // Controlled_Buffer controlled_buffer_15
  assign pull_resistor_1_node = and_12_out ? 4'b0010 : 4'bz;  // Controlled_Buffer controlled_buffer_16
  and and_31 (and_31_out, decoder_2_out14, d_ff_2_q, SPI_in[0], ~Error);  // AND_Gate
  assign pull_resistor_1_node = and_31_out ? 4'b1111 : 4'bz;  // Controlled_Buffer controlled_buffer_17
  assign pull_resistor_1_node = and_15_out ? 4'b0000 : 4'bz;  // Controlled_Buffer controlled_buffer_18
  Multiplexer #(.width(4), .disabled(0), .enable("false")) multiplexer_3 (
    .in0(4'b0110), .in1(4'b0111), .out(multiplexer_3_out), .sel(KBD_cahce_overwrite));
  assign pull_resistor_1_node = and_26_out ? multiplexer_3_out : 4'bz;  // Controlled_Buffer controlled_buffer_19
  assign pull_resistor_1_node = and_27_out ? 4'b1001 : 4'bz;  // Controlled_Buffer controlled_buffer_20
  assign pull_resistor_1_node = and_28_out ? 4'b1110 : 4'bz;  // Controlled_Buffer controlled_buffer_21
  assign pull_resistor_1_node = decoder_2_out8 ? 4'b0010 : 4'bz;  // Controlled_Buffer controlled_buffer_22
  assign pull_resistor_1_node = decoder_2_out9 ? 4'b1011 : 4'bz;  // Controlled_Buffer controlled_buffer_23
  assign pull_resistor_1_node = and_25_out ? 4'b0101 : 4'bz;  // Controlled_Buffer controlled_buffer_24
  assign pull_resistor_1_node = decoder_2_out10 ? 4'b1011 : 4'bz;  // Controlled_Buffer controlled_buffer_25
  assign pull_resistor_1_node = decoder_2_out11 ? 4'b0011 : 4'bz;  // Controlled_Buffer controlled_buffer_26
  assign pull_resistor_1_node = decoder_2_out12 ? 4'b0011 : 4'bz;  // Controlled_Buffer controlled_buffer_27
  Multiplexer #(.width(4), .disabled(0), .enable("false")) multiplexer_4 (
    .in0(4'b0000), .in1(4'b0101), .out(multiplexer_4_out), .sel(allow_e_manip));
  assign pull_resistor_1_node = Error ? multiplexer_4_out : 4'bz;  // Controlled_Buffer controlled_buffer_28
  and and_32 (and_32_out, decoder_2_out1, not_5_out);
  not not_5 (not_5_out, decoder_2_out1);
  not not_6 (not_6_out, decoder_2_out0);
  Multiplexer #(.width(4), .disabled(0), .enable("false")) multiplexer_5 (
    .in0(4'b0101), .in1(multiplexer_6_out), .out(multiplexer_5_out), .sel(KBD_cahce_overwrite));
  D_Flip_Flop d_ff_7 (
    .clk(CLK), .D(controlled_buffer_8_out), .Q(d_ff_7_q), .preset(1'b0), .en(1'b1), .reset(or_15_out));  // open: Qn
  or or_15 (or_15_out, and_32_out, and_33_out);
  and and_33 (and_33_out, decoder_2_out0, not_6_out);
  Multiplexer #(.width(4), .disabled(0), .enable("false")) multiplexer_6 (
    .in0(4'b1000), .in1(4'b1100), .out(multiplexer_6_out), .sel(col_exceeded));
  or or_16 (or_16_out, and_19_out, and_20_out, and_30_out, and_22_out, and_23_out, and_24_out, and_12_out, and_31_out, and_15_out, and_26_out, and_27_out, and_28_out, decoder_2_out8, decoder_2_out9, and_25_out, decoder_2_out10, decoder_2_out11, decoder_2_out12, Error, d_ff_8_q);
  Counter #(.width(2), .max('h3)) counter_3 (
    .load(1'b0), .count(1'b1), .carry(counter_3_carry), .clk(clk_t), .clr(or_17_out));  // open: D, Q
  or or_17 (or_17_out, or_16_out, rst);
  D_Flip_Flop #(.trigger("falling")) d_ff_8 (
    .clk(clk_t), .D(counter_3_carry), .Q(d_ff_8_q), .preset(1'b0), .en(1'b1), .reset(rst));  // open: Qn
  assign pull_resistor_1_node = d_ff_8_q ? 4'b1111 : 4'bz;  // Controlled_Buffer controlled_buffer_29

  // Other names for the same wires on the sheet: gathering_mode = KBD_cahce_overwrite; KBD_wait = Req_KBD;
  //   PC_wait = PC_active; raw_clk = CLK
endmodule

module move_checker (
  input  [4:0] KBD_command,
  input  [7:0] CSC,
  input  [7:0] CSR,
  output Is_wrong
);

  wire and_1_out, and_2_out, and_3_out, and_4_out, comparator_1_eq, comparator_2_eq, comparator_3_eq,
       comparator_4_eq;

  Comparator #(.width(5), .mode("unsigned")) comparator_1 (
    .a(KBD_command), .b(5'b01101), .eq(comparator_1_eq));  // open: gt, lt
  Comparator #(.width(5), .mode("unsigned")) comparator_2 (
    .a(KBD_command), .b(5'b01110), .eq(comparator_2_eq));  // open: gt, lt
  Comparator #(.width(5), .mode("unsigned")) comparator_3 (
    .a(KBD_command), .b(5'b01111), .eq(comparator_3_eq));  // open: gt, lt
  Comparator #(.width(5), .mode("unsigned")) comparator_4 (
    .a(KBD_command), .b(5'b01100), .eq(comparator_4_eq));  // open: gt, lt
  and and_1 (and_1_out, comparator_1_eq, CSC[0]);
  and and_2 (and_2_out, comparator_2_eq, CSC[7]);
  and and_3 (and_3_out, comparator_3_eq, CSR[0]);
  and and_4 (and_4_out, comparator_4_eq, CSR[7]);
  or or_1 (Is_wrong, and_1_out, and_2_out, and_3_out, and_4_out);
endmodule
