// Logisim project SPI interface.circ as structural Verilog: 10 circuits, main circuit SPI module (cell)
module local_test (
  input  [4:0] in_1,
  input  [10:0] in_2,
  input  in_3,
  input  [7:0] in_4,
  input  in_5,
  input  [1:0] in_6,
  input  [3:0] in_7,
  input  [10:0] in_8
);

  wire clock_1_out, not_1_out, not_2_out, pull_resistor_1_node, spi_module_cell_1_clk_out,
       spi_module_cell_1_input_transanction_end, spi_module_cell_1_is_selected, spi_module_cell_1_move_end_1,
       spi_module_cell_1_move_end_2, spi_module_cell_1_output_transanction_end, spi_module_cell_1_task_conf,
       spi_module_master_1_clk, spi_module_master_1_communication_end,
       spi_module_master_1_input_transanction_end, spi_module_master_1_mosi,
       spi_module_master_1_output_transanction_end;
  wire [1:0] spi_module_cell_1_is_task, spi_module_cell_1_player_select_out,
       spi_module_cell_1_type_select_out;
  wire [3:0] input_shifter_1_buffer_ptr, input_shifter_2_buffer_ptr;
  wire [4:0] spi_module_cell_1_command;
  wire [10:0] spi_module_cell_1_energy_out;
  wire [15:0] input_shifter_1_data_out, input_shifter_2_data_out, spi_module_master_1_recv_data;

  Clock clock_1 (.out(clock_1_out));
  LED led_1 (.in(spi_module_master_1_communication_end));
  LED led_2 (.in(spi_module_master_1_output_transanction_end));
  LED led_3 (.in(spi_module_master_1_input_transanction_end));
  SPI_module__master spi_module_master_1 (
    .In_clock(clock_1_out), .MISO(pull_resistor_1_node), .CLK(spi_module_master_1_clk),
    .MOSI(spi_module_master_1_mosi), .Output_transanction_end(spi_module_master_1_output_transanction_end),
    .Input_transanction_end(spi_module_master_1_input_transanction_end), .Control_command(in_4),
    .Send_command(in_1), .Send_energy(in_2), .Recv_data(spi_module_master_1_recv_data),
    .Communication_end(spi_module_master_1_communication_end));
  Pull_Resistor pull_resistor_1 (.node(pull_resistor_1_node));
  not not_1 (not_1_out, in_3);
  // Probe on spi_module_master_1_recv_data
  input_shifter input_shifter_1 (
    .MOSI(spi_module_master_1_mosi), .CLK(spi_module_master_1_clk), .Reset(not_2_out),
    .Data_out(input_shifter_1_data_out), .buffer_ptr(input_shifter_1_buffer_ptr));
  not not_2 (not_2_out, in_3);
  input_shifter input_shifter_2 (
    .MOSI(pull_resistor_1_node), .CLK(spi_module_master_1_clk), .Reset(not_1_out),
    .Data_out(input_shifter_2_data_out), .buffer_ptr(input_shifter_2_buffer_ptr));
  // Probe on input_shifter_2_data_out
  // Probe on input_shifter_2_buffer_ptr
  // Probe on input_shifter_1_buffer_ptr
  // Probe on input_shifter_1_data_out
  LED led_4 (.in(spi_module_cell_1_output_transanction_end));
  // Probe on spi_module_cell_1_player_select_out
  // Probe on spi_module_cell_1_type_select_out
  SPI_module__cell spi_module_cell_1 (
    .CS(in_3), .CLK(spi_module_master_1_clk), .MOSI(spi_module_master_1_mosi), .err(in_5), .energy_in(in_8),
    .type_select_in(in_7), .player_select_in(in_6), .clk_out(spi_module_cell_1_clk_out),
    .is_selected(spi_module_cell_1_is_selected), .move_end_1(spi_module_cell_1_move_end_1),
    .move_end_2(spi_module_cell_1_move_end_2), .is_task(spi_module_cell_1_is_task),
    .task_conf(spi_module_cell_1_task_conf), .command(spi_module_cell_1_command),
    .energy_out(spi_module_cell_1_energy_out),
    .input_transanction_end(spi_module_cell_1_input_transanction_end),
    .type_select_out(spi_module_cell_1_type_select_out),
    .player_select_out(spi_module_cell_1_player_select_out), .MISO(pull_resistor_1_node),
    .output_transanction_end(spi_module_cell_1_output_transanction_end));
  LED led_5 (.in(spi_module_cell_1_input_transanction_end));
  // Probe on spi_module_cell_1_command
  // Probe on spi_module_cell_1_energy_out
  LED led_6 (.in(spi_module_cell_1_is_selected));
  LED led_7 (.in(spi_module_cell_1_move_end_1));
  LED led_8 (.in(spi_module_cell_1_move_end_2));
  // Probe on spi_module_cell_1_is_task
  LED led_9 (.in(spi_module_cell_1_task_conf));
endmodule

module SPI_module__cell (
  input  CS,
  input  CLK,
  input  MOSI,
  input  err,
  input  [10:0] energy_in,
  input  [3:0] type_select_in,
  input  [1:0] player_select_in,
  output clk_out,
  output is_selected,
  output move_end_1,
  output [1:0] is_task,
  output task_conf,
  output move_end_2,
  output [4:0] command,
  output [10:0] energy_out,
  output input_transanction_end,
  output [1:0] type_select_out,
  output [1:0] player_select_out,
  output MISO,
  output output_transanction_end
);

  wire and_2_out, and_3_out, and_4_out, and_5_out, and_6_out, and_7_out, command_decoder_1_is_direction,
       command_decoder_1_is_energy, command_decoder_1_is_player, command_decoder_1_is_task,
       command_decoder_1_is_type, command_decoder_1_is_write, comparator_1_eq, comparator_2_eq, or_1_out,
       or_2_out, or_3_out, or_4_out, or_6_out, rst, special_sequence_decoder_1_err,
       special_sequence_decoder_1_is_transancition, special_sequence_decoder_1_move_end_1,
       special_sequence_decoder_1_move_end_2, special_sequence_decoder_1_player_2, transanction_sender_1_miso;
  wire [3:0] input_shifter_1_buffer_ptr;
  wire [10:0] transaction_parser_1_energy;
  wire [15:0] input_shifter_1_data_out;

  and and_1 (clk_out, CS, CLK);
  not not_1 (rst, CS);
  or or_1 (or_1_out, rst, special_sequence_decoder_1_is_transancition);
  or or_2 (or_2_out, rst, ~special_sequence_decoder_1_is_transancition);  // OR_Gate
  transaction_parser transaction_parser_1 (
    .CLK(clk_out), .MOSI(MOSI), .Reset(or_2_out), .Command(command), .Energy(transaction_parser_1_energy),
    .Data_ready(input_transanction_end));
  input_shifter input_shifter_1 (
    .MOSI(MOSI), .CLK(clk_out), .Reset(or_1_out), .Data_out(input_shifter_1_data_out),
    .buffer_ptr(input_shifter_1_buffer_ptr));
  special_sequence_decoder special_sequence_decoder_1 (
    .Data(input_shifter_1_data_out), .Buffer_pointer(input_shifter_1_buffer_ptr), .RST(rst),
    .move_end_1(special_sequence_decoder_1_move_end_1),
    .is_transancition(special_sequence_decoder_1_is_transancition),
    .move_end_2(special_sequence_decoder_1_move_end_2), .is_task(is_task), .is_selected(is_selected),
    .ERR(special_sequence_decoder_1_err), .CLK(clk_out), .player_2(special_sequence_decoder_1_player_2));
  or or_3 (or_3_out, is_task[0], is_task[1]);
  and and_2 (and_2_out, or_3_out, clk_out, MOSI);
  command_decoder command_decoder_1 (
    .Command_in(command), .is_direction(command_decoder_1_is_direction),
    .is_energy(command_decoder_1_is_energy), .is_type(command_decoder_1_is_type),
    .is_task(command_decoder_1_is_task), .is_player(command_decoder_1_is_player),
    .is_write(command_decoder_1_is_write));  // open: direction, is_clear, is_reset
  or or_4 (or_4_out, command_decoder_1_is_direction, command_decoder_1_is_energy);
  and and_3 (and_3_out, or_3_out, err);
  and and_4 (and_4_out, command_decoder_1_is_write, err, input_transanction_end);
  and and_5 (and_5_out, ~command_decoder_1_is_write, input_transanction_end);  // AND_Gate
  D_Flip_Flop d_ff_1 (.clk(and_2_out), .D(and_2_out), .Q(task_conf), .reset(rst));  // open: Qn, preset, en
  transanction_sender transanction_sender_1 (
    .CLK(clk_out), .Energy(energy_in), .Type_select(type_select_in[1:0]), .Task_select(type_select_in[3:2]),
    .Player_select(player_select_in), .not_Reset(and_5_out), .MISO(transanction_sender_1_miso),
    .Output_transanction_end(output_transanction_end), .Is_player(command_decoder_1_is_player),
    .Is_task(command_decoder_1_is_task), .Is_type(command_decoder_1_is_type), .Is_energy(or_4_out));
  Multiplexer #(.width(11), .enable("false")) multiplexer_1 (
    .in0({11{1'b0}}), .in1(transaction_parser_1_energy), .out(energy_out), .sel(or_4_out));
  Multiplexer #(.width(2), .enable("false")) multiplexer_2 (
    .in0(2'b00), .in1(transaction_parser_1_energy[1:0]), .out(type_select_out),
    .sel(command_decoder_1_is_type));
  Multiplexer #(.width(2), .enable("false")) multiplexer_3 (
    .in0(2'b00), .in1(transaction_parser_1_energy[1:0]), .out(player_select_out),
    .sel(command_decoder_1_is_player));
  or or_5 (MISO, special_sequence_decoder_1_err, and_3_out, and_4_out, transanction_sender_1_miso);
  Comparator #(.width(2), .mode("unsigned")) comparator_1 (
    .a(player_select_in), .b(2'b01), .eq(comparator_1_eq));  // open: gt, lt
  and and_6 (and_6_out, comparator_1_eq, ~special_sequence_decoder_1_player_2);  // AND_Gate
  and and_7 (and_7_out, special_sequence_decoder_1_player_2, comparator_2_eq);
  Comparator #(.width(2), .mode("unsigned")) comparator_2 (
    .a(player_select_in), .b(2'b10), .eq(comparator_2_eq));  // open: gt, lt
  or or_6 (or_6_out, and_6_out, and_7_out);
  and and_8 (move_end_1, special_sequence_decoder_1_move_end_1, or_6_out);
  and and_9 (move_end_2, or_6_out, special_sequence_decoder_1_move_end_2);

  // Other names for the same wires on the sheet: clk_t = clk_out; input_transaction_end = input_transanction_end

  // Notes on the sheet:
  //   player_select_in: pull=down
  //   type_select_out: pull=down
  //   type_select_in: pull=down
  //   energy_in: pull=down
  //   player_select_out: pull=down
  //   is_task: pull=down
  //   energy_out: pull=down
  //   err: pull=down
  //   command: pull=down
  //   CLK: pull=down
  //   MOSI: pull=down
  //   or_5 drives only 1 and floats otherwise
endmodule

module input_shifter (
  input  MOSI,
  input  CLK,
  input  Reset,
  output [15:0] Data_out,
  output [3:0] buffer_ptr
);

  Register #(.width(16)) register_1 (.D({Data_out[14:0], MOSI}), .en(1'b1), .Q(Data_out), .clk(CLK), .clr(Reset));
  Counter #(.width(4), .max('hf)) counter_1 (
    .load(1'b0), .count(1'b1), .Q(buffer_ptr), .clk(CLK), .clr(Reset));  // open: D, carry

  // Notes on the sheet:
  //   MOSI: pull=down
  //   Reset: pull=down
  //   Data_out: pull=down
  //   buffer_ptr: pull=down
  //   CLK: pull=down
endmodule

module special_sequence_decoder (
  input  [15:0] Data,
  input  [3:0] Buffer_pointer,
  input  CLK,
  input  RST,
  output player_2,
  output move_end_1,
  output is_transancition,
  output is_selected,
  output move_end_2,
  output [1:0] is_task,
  output ERR
);

  wire and_1_out, and_2_out, and_3_out, and_4_out, and_5_out, and_6_out, and_7_out, comparator_1_eq,
       comparator_2_eq, comparator_3_eq, comparator_4_eq, comparator_5_eq, comparator_6_eq, comparator_7_eq,
       comparator_8_eq, comparator_9_eq, comparator_9_gt, lock, or_2_out, or_3_out, or_4_out, or_5_out;

  Comparator #(.width(16)) comparator_1 (.a(Data), .b(16'h3), .eq(comparator_1_eq));  // open: gt, lt
  Comparator #(.width(16)) comparator_2 (.a(Data), .b(16'h2), .eq(comparator_2_eq));  // open: gt, lt
  Comparator #(.width(16)) comparator_3 (.a(Data), .b(16'h1), .eq(comparator_3_eq));  // open: gt, lt
  Comparator #(.width(16)) comparator_4 (.a(Data), .b(16'h6), .eq(comparator_4_eq));  // open: gt, lt
  Comparator #(.width(16)) comparator_5 (.a(Data), .b(16'h4), .eq(comparator_5_eq));  // open: gt, lt
  Comparator #(.width(4)) comparator_6 (.a(Buffer_pointer), .b(4'b0010), .eq(comparator_6_eq));  // open: gt, lt
  Comparator #(.width(4)) comparator_7 (.a(Buffer_pointer), .b(4'b0010), .eq(comparator_7_eq));  // open: gt, lt
  Comparator #(.width(4)) comparator_8 (.a(Buffer_pointer), .b(4'b0011), .eq(comparator_8_eq));  // open: gt, lt
  Comparator #(.width(4)) comparator_9 (
    .a(Buffer_pointer), .b(4'b0101), .gt(comparator_9_gt), .eq(comparator_9_eq));  // open: lt
  or or_1 (player_2, comparator_1_eq, comparator_4_eq);
  or or_2 (or_2_out, comparator_2_eq, comparator_1_eq);
  and and_1 (and_1_out, comparator_3_eq, comparator_7_eq);
  and and_2 (and_2_out, comparator_3_eq, comparator_8_eq);
  or or_3 (or_3_out, comparator_4_eq, comparator_5_eq);
  and and_3 (and_3_out, comparator_9_eq, Data[0]);
  and and_4 (and_4_out, Data[1], comparator_9_eq);
  and and_5 (and_5_out, or_2_out, comparator_6_eq);
  and and_6 (and_6_out, or_3_out, comparator_8_eq);
  or or_4 (or_4_out, comparator_9_gt, and_4_out, and_3_out, and_6_out, and_2_out, and_1_out);
  D_Flip_Flop #(.trigger("falling")) d_ff_1 (
    .clk(and_7_out), .D(or_4_out), .Q(lock), .reset(RST));  // open: Qn, preset, en
  and and_7 (and_7_out, ~lock, CLK);  // AND_Gate
  and and_8 (move_end_1, ~lock, and_5_out);  // AND_Gate
  D_Flip_Flop d_ff_2 (.clk(lock), .D(and_1_out), .Q(is_transancition), .reset(RST));  // open: Qn, preset, en
  D_Flip_Flop d_ff_3 (.clk(lock), .D(and_2_out), .Q(is_selected), .reset(RST));  // open: Qn, preset, en
  D_Flip_Flop d_ff_4 (.clk(lock), .D(and_6_out), .Q(move_end_2), .reset(RST));  // open: Qn, preset, en
  D_Flip_Flop d_ff_5 (.clk(lock), .D(and_3_out), .Q(is_task[0]), .reset(RST));  // open: Qn, preset, en
  or or_5 (or_5_out, is_task[0], is_task[1], move_end_2, is_selected, is_transancition);
  D_Flip_Flop d_ff_6 (.clk(lock), .D(and_4_out), .Q(is_task[1]), .reset(RST));  // open: Qn, preset, en
  and and_9 (ERR, ~or_5_out, lock);  // AND_Gate

  // Notes on the sheet:
  //   RST: pull=down
  //   CLK: pull=down
  //   Data: pull=down
  //   ERR: pull=down
  //   Buffer_pointer: pull=down
endmodule

module transaction_parser (
  input  CLK,
  input  MOSI,
  input  Reset,
  output [4:0] Command,
  output [10:0] Energy,
  output Data_ready
);

  wire and_1_out, and_2_out, and_3_out, and_4_out, and_5_out, and_6_out, and_7_out, and_8_out,
       command_decoder_1_is_clear, command_decoder_1_is_direction, command_decoder_1_is_energy,
       command_decoder_1_is_player, command_decoder_1_is_type, command_decoder_1_is_write, comparator_1_eq,
       comparator_2_eq, d_ff_1_q, nor_1_out, or_1_out, or_2_out, or_3_out;
  wire [3:0] input_shifter_1_buffer_ptr;
  wire [15:11] input_shifter_1_data_out;

  and and_1 (and_1_out, ~Data_ready, CLK);  // AND_Gate
  input_shifter input_shifter_1 (
    .MOSI(MOSI), .CLK(and_1_out), .Reset(Reset), .Data_out({input_shifter_1_data_out, Energy}),
    .buffer_ptr(input_shifter_1_buffer_ptr));
  Comparator #(.width(4)) comparator_1 (
    .a(input_shifter_1_buffer_ptr), .b(4'b0101), .eq(comparator_1_eq));  // open: gt, lt
  Comparator #(.width(4)) comparator_2 (
    .a(input_shifter_1_buffer_ptr), .b(4'b0111), .eq(comparator_2_eq));  // open: gt, lt
  command_decoder command_decoder_1 (
    .Command_in(Command), .is_direction(command_decoder_1_is_direction),
    .is_energy(command_decoder_1_is_energy), .is_type(command_decoder_1_is_type),
    .is_clear(command_decoder_1_is_clear), .is_player(command_decoder_1_is_player),
    .is_write(command_decoder_1_is_write));  // open: direction, is_task, is_reset
  nor nor_1 (nor_1_out, input_shifter_1_buffer_ptr[0], input_shifter_1_buffer_ptr[1], input_shifter_1_buffer_ptr[3], input_shifter_1_buffer_ptr[2]);
  or or_1 (or_1_out, command_decoder_1_is_direction, command_decoder_1_is_energy);
  or or_2 (or_2_out, command_decoder_1_is_type, command_decoder_1_is_player);
  and and_2 (and_2_out, ~d_ff_1_q, and_1_out);  // AND_Gate
  Register #(.width(5), .trigger("high")) register_1 (
    .D(Energy[4:0]), .en(1'b1), .Q(Command), .clk(and_3_out), .clr(Reset));
  and and_3 (and_3_out, comparator_1_eq, ~d_ff_1_q, CLK);  // AND_Gate
  and and_4 (and_4_out, comparator_1_eq, command_decoder_1_is_clear);
  and and_5 (and_5_out, nor_1_out, or_1_out);
  and and_6 (and_6_out, comparator_2_eq, or_2_out);
  D_Flip_Flop #(.trigger("falling")) d_ff_1 (
    .clk(and_2_out), .D(comparator_1_eq), .Q(d_ff_1_q), .reset(Reset));  // open: Qn, preset, en
  or or_3 (or_3_out, and_4_out, and_5_out, and_6_out);
  and and_7 (and_7_out, d_ff_1_q, or_3_out);
  and and_8 (and_8_out, ~command_decoder_1_is_write, d_ff_1_q);  // AND_Gate
  or or_4 (Data_ready, and_8_out, and_7_out);
endmodule

module command_decoder (
  input  [4:0] Command_in,
  output [1:0] direction,
  output is_direction,
  output is_energy,
  output is_type,
  output is_task,
  output is_clear,
  output is_player,
  output is_write,
  output is_reset
);

  wire demultiplexer_1_out2, not_1_out;
  wire [4:0] multiplexer_1_out;

  Multiplexer #(.width(5), .enable("false")) multiplexer_1 (
    .in0(Command_in), .in1({5{1'b0}}),
    .out({multiplexer_1_out[4], is_write, is_direction, multiplexer_1_out[1:0]}), .sel(Command_in[4]));
  Multiplexer #(.width(2), .enable("false")) multiplexer_2 (
    .in0(2'b00), .in1(multiplexer_1_out[1:0]), .out(direction), .sel(is_direction));
  not not_1 (not_1_out, is_direction);
  Demultiplexer #(.select(2), .enable("false")) demultiplexer_1 (
    .out0(is_energy), .out1(is_type), .out2(demultiplexer_1_out2), .out3(is_player), .in(not_1_out),
    .sel(multiplexer_1_out[1:0]));
  Demultiplexer #(.enable("false")) demultiplexer_2 (
    .out0(is_task), .out1(is_clear), .in(demultiplexer_1_out2), .sel(is_write));

  assign is_reset = Command_in[4];

  // Notes on the sheet:
  //   is_write: pull=down
  //   is_direction: pull=down
  //   is_energy: pull=down
  //   is_reset: pull=down
  //   Command_in: pull=down
  //   is_type: pull=down
  //   direction: pull=down
  //   is_task: pull=down
  //   is_clear: pull=down
  //   is_player: pull=down
endmodule

module output_shifter (
  input  [15:0] Data_in,
  input  CLK,
  input  Reset,
  output MISO,
  output [3:0] buffer_ptr
);

  wire and_1_out, and_2_out, comparator_1_eq, d_ff_1_q, or_1_out;
  wire [14:0] register_1_q;
  wire [15:0] multiplexer_1_out;

  and and_1 (and_1_out, ~CLK, d_ff_1_q);  // AND_Gate
  D_Flip_Flop d_ff_1 (.clk(CLK), .D(CLK), .Q(d_ff_1_q), .reset(and_1_out));  // open: Qn, preset, en
  Counter #(.width(4), .max('hf)) counter_1 (
    .load(1'b0), .count(1'b1), .Q(buffer_ptr), .clk(CLK), .clr(Reset));  // open: D, carry
  Comparator #(.width(4), .mode("unsigned")) comparator_1 (
    .a(4'b0000), .b(buffer_ptr), .eq(comparator_1_eq));  // open: gt, lt
  Multiplexer #(.width(16), .enable("false")) multiplexer_1 (
    .in0({1'b0, register_1_q}), .in1(Data_in), .out(multiplexer_1_out), .sel(comparator_1_eq));
  and and_2 (and_2_out, comparator_1_eq, ~CLK, ~Reset);  // AND_Gate
  Register #(.width(16), .trigger("high")) register_1 (
    .D(multiplexer_1_out), .en(1'b1), .Q({register_1_q, MISO}), .clk(or_1_out), .clr(Reset));
  or or_1 (or_1_out, and_1_out, and_2_out);
  // Probe on {register_1_q, MISO}

  // Notes on the sheet:
  //   Reset: pull=down
  //   MISO: pull=down
  //   buffer_ptr: pull=down
  //   Data_in: pull=down
  //   CLK: pull=down
endmodule

module transanction_sender (
  input  Is_player,
  input  Is_task,
  input  Is_type,
  input  Is_energy,
  input  CLK,
  input  [10:0] Energy,
  input  [1:0] Type_select,
  input  [1:0] Task_select,
  input  [1:0] Player_select,
  input  not_Reset,
  output MISO,
  output Output_transanction_end
);

  wire and_1_out, and_2_out, comparator_1_eq, comparator_2_eq, d_ff_1_q, not_1_out, or_1_out, or_3_out;
  wire [1:0] controlled_buffer_1_out;
  wire [3:0] output_shifter_1_buffer_ptr;
  wire [10:0] multiplexer_1_out;
  wire [15:0] or_2_out;

  assign controlled_buffer_1_out = Is_task ? Task_select : 2'bz;  // Controlled_Buffer controlled_buffer_1
  assign controlled_buffer_1_out = Is_player ? Player_select : 2'bz;  // Controlled_Buffer controlled_buffer_2
  assign controlled_buffer_1_out = Is_type ? Type_select : 2'bz;  // Controlled_Buffer controlled_buffer_3
  or or_1 (or_1_out, Is_player, Is_task, Is_type);
  Multiplexer #(.width(11), .enable("false")) multiplexer_1 (
    .in0({11{1'b0}}), .in1(Energy), .out(multiplexer_1_out), .sel(Is_energy));
  Pull_Resistor pull_resistor_1 (.node(controlled_buffer_1_out));
  assign or_2_out = {{5{1'b0}}, multiplexer_1_out} | {{14{1'b0}}, controlled_buffer_1_out};  // OR_Gate or_2, 16 bits wide
  or or_3 (or_3_out, not_1_out, d_ff_1_q);
  not not_1 (not_1_out, not_Reset);
  output_shifter output_shifter_1 (
    .Data_in(or_2_out), .CLK(CLK), .Reset(or_3_out), .MISO(MISO), .buffer_ptr(output_shifter_1_buffer_ptr));
  and and_1 (and_1_out, ~d_ff_1_q, CLK);  // AND_Gate
  and and_2 (and_2_out, or_1_out, comparator_1_eq);
  Comparator #(.width(4), .mode("unsigned")) comparator_1 (
    .a(output_shifter_1_buffer_ptr), .b(4'b0010), .eq(comparator_1_eq));  // open: gt, lt
  Comparator #(.width(4), .mode("unsigned")) comparator_2 (
    .a(output_shifter_1_buffer_ptr), .b(4'b1011), .eq(comparator_2_eq));  // open: gt, lt
  D_Flip_Flop #(.trigger("falling")) d_ff_1 (
    .clk(and_1_out), .D(Output_transanction_end), .Q(d_ff_1_q), .reset(not_1_out));  // open: Qn, preset, en
  or or_4 (Output_transanction_end, and_2_out, d_ff_1_q, comparator_2_eq);

  // Notes on the sheet:
  //   Output_transanction_end: pull=down
  //   MISO: pull=down
endmodule

module SPI_module__master (
  input  In_clock,
  input  [4:0] Send_command,
  input  [10:0] Send_energy,
  input  [7:0] Control_command,
  input  MISO,
  output CLK,
  output MOSI,
  output Communication_end,
  output Output_transanction_end,
  output [15:0] Recv_data,
  output Input_transanction_end
);

  wire and_1_out, and_2_out, and_4_out, and_5_out, and_6_out, and_7_out, and_8_out, and_9_out, and_10_out,
       and_11_out, and_12_out, comparator_1_eq, comparator_2_eq, Manual_transmission, multiplexer_10_out,
       nand_1_out, or_1_out, or_2_out, or_3_out, or_5_out, output_shifter_1_miso, Reset;
  wire [3:0] input_shifter_1_buffer_ptr, multiplexer_1_out, multiplexer_2_out, multiplexer_3_out,
       multiplexer_4_out, multiplexer_5_out, multiplexer_6_out, multiplexer_7_out, multiplexer_9_out,
       output_shifter_1_buffer_ptr, predefined_command_selector_1_out_3;
  wire [15:0] multiplexer_8_out, predefined_command_selector_1_out_2;

  predefined_command_selector predefined_command_selector_1 (
    .in_1(Control_command[5:3]), .out_2(predefined_command_selector_1_out_2),
    .out_3(predefined_command_selector_1_out_3));
  Multiplexer #(.width(4), .enable("false")) multiplexer_1 (
    .in0(4'b0101), .in1(4'b0111), .out(multiplexer_1_out), .sel(Control_command[0]));
  Multiplexer #(.width(4), .enable("false")) multiplexer_2 (
    .in0(4'b0010), .in1(4'b0001), .out(multiplexer_2_out), .sel(Control_command[0]));
  Multiplexer #(.width(4), .enable("false")) multiplexer_3 (
    .in0(4'b1011), .in1(4'b0000), .out(multiplexer_3_out), .sel(Control_command[0]));
  and and_1 (and_1_out, CLK, ~Input_transanction_end);  // AND_Gate
  nand nand_1 (nand_1_out, Control_command[6], Output_transanction_end);
  Multiplexer #(.select(2), .width(4), .enable("false")) multiplexer_4 (
    .in0(4'b0000), .in1(multiplexer_1_out), .in2(4'b0101), .in3(4'b0000), .out(multiplexer_4_out),
    .sel(Control_command[4:3]));
  Multiplexer #(.width(4), .enable("false")) multiplexer_5 (
    .in0(4'b0001), .in1(multiplexer_6_out), .out(multiplexer_5_out), .sel(Control_command[2]));
  Multiplexer #(.select(2), .width(4), .enable("false")) multiplexer_6 (
    .in0(4'b0001), .in1(multiplexer_2_out), .in2(multiplexer_3_out), .in3(4'b0000), .out(multiplexer_6_out),
    .sel(Control_command[4:3]));
  input_shifter input_shifter_1 (
    .MOSI(MISO), .CLK(and_1_out), .Reset(nand_1_out), .Data_out(Recv_data),
    .buffer_ptr(input_shifter_1_buffer_ptr));
  nor nor_1 (Reset, Control_command[6], Control_command[2]);
  and and_2 (and_2_out, ~Control_command[1], Control_command[2]);  // AND_Gate
  and and_3 (Manual_transmission, Control_command[1], ~Control_command[2]);  // AND_Gate
  and and_4 (and_4_out, Control_command[1], Control_command[2]);
  Multiplexer #(.width(4), .enable("false")) multiplexer_7 (
    .in0(multiplexer_5_out), .in1(4'b0001), .out(multiplexer_7_out), .sel(and_4_out));
  Comparator #(.width(4)) comparator_1 (
    .a(multiplexer_7_out), .b(input_shifter_1_buffer_ptr), .eq(comparator_1_eq));  // open: gt, lt
  and and_5 (and_5_out, CLK, ~Output_transanction_end);  // AND_Gate
  Multiplexer #(.width(16), .enable("false")) multiplexer_8 (
    .in0(predefined_command_selector_1_out_2),
    .in1({Send_energy[0], Send_energy[1], Send_energy[2], Send_energy[3], Send_energy[4], Send_energy[5], Send_energy[6], Send_energy[7], Send_energy[8], Send_energy[9], Send_energy[10], Send_command[0], Send_command[1], Send_command[2], Send_command[3], Send_command[4]}),
    .out(multiplexer_8_out), .sel(and_2_out));
  or or_1 (or_1_out, ~Control_command[2], Output_transanction_end, Reset);  // OR_Gate
  Multiplexer #(.width(4), .enable("false")) multiplexer_9 (
    .in0(predefined_command_selector_1_out_3), .in1(multiplexer_4_out), .out(multiplexer_9_out),
    .sel(and_2_out));
  and and_6 (and_6_out, comparator_1_eq, Control_command[6], ~Reset, Output_transanction_end);  // AND_Gate
  or or_2 (or_2_out, and_6_out, Input_transanction_end);
  and and_7 (and_7_out, ~Manual_transmission, Reset);  // AND_Gate
  output_shifter output_shifter_1 (
    .Data_in(multiplexer_8_out), .CLK(and_5_out), .Reset(or_1_out), .MISO(output_shifter_1_miso),
    .buffer_ptr(output_shifter_1_buffer_ptr));
  Comparator #(.width(4)) comparator_2 (
    .a(output_shifter_1_buffer_ptr), .b(multiplexer_9_out), .eq(comparator_2_eq));  // open: gt, lt
  D_Flip_Flop #(.trigger("falling")) d_ff_1 (
    .clk(CLK), .D(or_2_out), .Q(Input_transanction_end), .reset(and_7_out));  // open: Qn, preset, en
  buf buffer_1 (MOSI, multiplexer_10_out);
  Multiplexer #(.enable("false")) multiplexer_10 (
    .in0(Control_command[0]), .in1(output_shifter_1_miso), .out(multiplexer_10_out), .sel(Control_command[2]));
  Pull_Resistor pull_resistor_1 (.node(MOSI));
  and and_8 (and_8_out, comparator_2_eq, ~Reset);  // AND_Gate
  or or_3 (or_3_out, and_8_out, Manual_transmission, Output_transanction_end);
  D_Flip_Flop #(.trigger("falling")) d_ff_2 (
    .clk(CLK), .D(or_3_out), .Q(Output_transanction_end), .reset(and_9_out));  // open: Qn, preset, en
  and and_9 (and_9_out, ~Manual_transmission, Reset);  // AND_Gate
  and and_10 (and_10_out, In_clock, ~Communication_end);  // AND_Gate
  and and_11 (and_11_out, Output_transanction_end, ~Control_command[6]);  // AND_Gate
  and and_12 (and_12_out, Control_command[6], Output_transanction_end, Input_transanction_end);
  or or_4 (Communication_end, and_11_out, and_12_out);
  and and_13 (CLK, and_10_out, or_5_out);
  or or_5 (or_5_out, Manual_transmission, ~Reset);  // OR_Gate

  // Other names for the same wires on the sheet: Awaiting_receive = Control_command[6];
  //   Stop_r = Input_transanction_end; Stop_t = Output_transanction_end

  // Notes on the sheet:
  //   Control_command: pull=down
endmodule

module predefined_command_selector (
  input  [2:0] in_1,
  output [15:0] out_2,
  output [3:0] out_3
);

  Multiplexer #(.select(3), .width(16), .enable("false")) multiplexer_1 (
    .in0({16{1'b0}}), .in1(16'h8), .in2(16'h10), .in3(16'h18), .in4(16'h4), .in5(16'h2), .in6(16'h4),
    .in7(16'h6), .out(out_2), .sel(in_1));
  Multiplexer #(.select(3), .width(4), .enable("false")) multiplexer_2 (
    .in0(4'b0000), .in1(4'b0101), .in2(4'b0101), .in3(4'b0101), .in4(4'b0011), .in5(4'b0010), .in6(4'b0011),
    .in7(4'b0011), .out(out_3), .sel(in_1));

  // Notes on the sheet:
  //   in_1: pull=down
endmodule
