// Logisim project cell controller.circ as structural Verilog: 2 circuits, main circuit Cell controller
module local_test (
  input  [4:0] in_1,
  input  [10:0] in_2,
  input  in_3,
  input  in_4,
  input  [7:0] in_5,
  input  in_6
);

  wire clock_1_out, pull_resistor_1_node, spi_module_master_1_communication_end,
       spi_module_master_1_input_transanction_end, spi_module_master_1_output_transanction_end;
  wire [1:0] spi_module_master_1_clk;
  wire [4:0] cell_controller_1_out_12, cell_controller_1_out_13, cell_controller_1_out_14,
       cell_controller_1_out_15, cell_controller_1_out_16, cell_controller_1_out_17,
       cell_controller_1_out_18, cell_controller_1_out_19, cell_controller_1_out_20,
       cell_controller_1_out_21, cell_controller_1_out_22, cell_controller_2_out_12,
       cell_controller_2_out_13, cell_controller_2_out_14, cell_controller_2_out_15,
       cell_controller_2_out_16, cell_controller_2_out_17, cell_controller_2_out_18,
       cell_controller_2_out_19, cell_controller_2_out_20, cell_controller_2_out_21, cell_controller_2_out_22;
  wire [7:0] cell_controller_1_out_23, cell_controller_1_out_24, cell_controller_1_out_25,
       cell_controller_1_out_26, cell_controller_1_out_27, cell_controller_1_out_28,
       cell_controller_1_out_29, cell_controller_1_out_30, cell_controller_1_out_31,
       cell_controller_1_out_32, cell_controller_1_out_33, cell_controller_1_out_35,
       cell_controller_1_out_36, cell_controller_1_out_37, cell_controller_1_out_38,
       cell_controller_1_out_39, cell_controller_1_out_40, cell_controller_1_out_41,
       cell_controller_1_out_42, cell_controller_1_out_43, cell_controller_1_out_44,
       cell_controller_1_out_45, cell_controller_2_out_23, cell_controller_2_out_24,
       cell_controller_2_out_25, cell_controller_2_out_26, cell_controller_2_out_27,
       cell_controller_2_out_28, cell_controller_2_out_29, cell_controller_2_out_30,
       cell_controller_2_out_31, cell_controller_2_out_32, cell_controller_2_out_33,
       cell_controller_2_out_35, cell_controller_2_out_36, cell_controller_2_out_37,
       cell_controller_2_out_38, cell_controller_2_out_39, cell_controller_2_out_40,
       cell_controller_2_out_41, cell_controller_2_out_42, cell_controller_2_out_43,
       cell_controller_2_out_44, cell_controller_2_out_45;
  wire [11:0] cell_controller_1_d_datao, cell_controller_1_l_datao, cell_controller_1_r_datao,
       cell_controller_1_u_datao, cell_controller_2_l_datao;
  wire [15:0] spi_module_master_1_recv_data;

  Clock clock_1 (.out(clock_1_out));
  LED led_1 (.in(spi_module_master_1_input_transanction_end));
  LED led_2 (.in(spi_module_master_1_output_transanction_end));
  LED led_3 (.in(spi_module_master_1_communication_end));
  // Probe on spi_module_master_1_recv_data
  SPI_module__master spi_module_master_1 (
    .In_clock(clock_1_out), .MISO(pull_resistor_1_node), .CLK(spi_module_master_1_clk[0]),
    .MOSI(spi_module_master_1_clk[1]), .Output_transanction_end(spi_module_master_1_output_transanction_end),
    .Input_transanction_end(spi_module_master_1_input_transanction_end), .Control_command(in_5),
    .Send_command(in_1), .Send_energy(in_2), .Recv_data(spi_module_master_1_recv_data),
    .Communication_end(spi_module_master_1_communication_end));
  Pull_Resistor pull_resistor_1 (.node(pull_resistor_1_node));
  // Probe on spi_module_master_1_clk
  // Probe on cell_controller_1_l_datao
  // Probe on cell_controller_1_u_datao
  DotMatrix #(.matrixcols(11), .matrixrows(5)) dotmatrix_1 (
    .col0(cell_controller_1_out_12), .col1(cell_controller_1_out_13), .col2(cell_controller_1_out_14),
    .col3(cell_controller_1_out_15), .col4(cell_controller_1_out_16), .col5(cell_controller_1_out_17),
    .col6(cell_controller_1_out_18), .col7(cell_controller_1_out_19), .col8(cell_controller_1_out_20),
    .col9(cell_controller_1_out_21), .col10(cell_controller_1_out_22));
  Cell_controller cell_controller_1 (
    .out_12(cell_controller_1_out_12), .out_23(cell_controller_1_out_23), .out_13(cell_controller_1_out_13),
    .out_35(cell_controller_1_out_35), .out_24(cell_controller_1_out_24), .out_14(cell_controller_1_out_14),
    .out_36(cell_controller_1_out_36), .out_25(cell_controller_1_out_25), .out_15(cell_controller_1_out_15),
    .out_37(cell_controller_1_out_37), .out_16(cell_controller_1_out_16), .out_26(cell_controller_1_out_26),
    .out_38(cell_controller_1_out_38), .out_17(cell_controller_1_out_17), .out_27(cell_controller_1_out_27),
    .out_18(cell_controller_1_out_18), .out_39(cell_controller_1_out_39), .out_28(cell_controller_1_out_28),
    .out_19(cell_controller_1_out_19), .out_40(cell_controller_1_out_40), .out_29(cell_controller_1_out_29),
    .out_20(cell_controller_1_out_20), .out_41(cell_controller_1_out_41), .out_21(cell_controller_1_out_21),
    .out_30(cell_controller_1_out_30), .out_42(cell_controller_1_out_42), .out_22(cell_controller_1_out_22),
    .out_31(cell_controller_1_out_31), .out_43(cell_controller_1_out_43), .out_32(cell_controller_1_out_32),
    .out_44(cell_controller_1_out_44), .out_33(cell_controller_1_out_33), .out_45(cell_controller_1_out_45),
    .CSC(in_4), .CSR(in_6), .MISO(pull_resistor_1_node), .SPI(spi_module_master_1_clk),
    .L_DataO(cell_controller_1_l_datao), .U_DataO(cell_controller_1_u_datao),
    .R_DataI(cell_controller_2_l_datao), .R_DataO(cell_controller_1_r_datao),
    .D_DataO(cell_controller_1_d_datao));  // open: L_DataI, D_DataI, U_DataI
  DotMatrix #(.matrixcols(11), .matrixrows(8)) dotmatrix_2 (
    .col0(cell_controller_1_out_23), .col1(cell_controller_1_out_24), .col2(cell_controller_1_out_25),
    .col3(cell_controller_1_out_26), .col4(cell_controller_1_out_27), .col5(cell_controller_1_out_28),
    .col6(cell_controller_1_out_29), .col7(cell_controller_1_out_30), .col8(cell_controller_1_out_31),
    .col9(cell_controller_1_out_32), .col10(cell_controller_1_out_33));
  DotMatrix #(.matrixcols(11), .matrixrows(8)) dotmatrix_3 (
    .col0(cell_controller_1_out_35), .col1(cell_controller_1_out_36), .col2(cell_controller_1_out_37),
    .col3(cell_controller_1_out_38), .col4(cell_controller_1_out_39), .col5(cell_controller_1_out_40),
    .col6(cell_controller_1_out_41), .col7(cell_controller_1_out_42), .col8(cell_controller_1_out_43),
    .col9(cell_controller_1_out_44), .col10(cell_controller_1_out_45));
  // Probe on cell_controller_1_d_datao
  // Probe on cell_controller_1_r_datao
  // Probe on cell_controller_2_l_datao
  DotMatrix #(.matrixcols(11), .matrixrows(5)) dotmatrix_4 (
    .col0(cell_controller_2_out_12), .col1(cell_controller_2_out_13), .col2(cell_controller_2_out_14),
    .col3(cell_controller_2_out_15), .col4(cell_controller_2_out_16), .col5(cell_controller_2_out_17),
    .col6(cell_controller_2_out_18), .col7(cell_controller_2_out_19), .col8(cell_controller_2_out_20),
    .col9(cell_controller_2_out_21), .col10(cell_controller_2_out_22));
  Cell_controller cell_controller_2 (
    .out_12(cell_controller_2_out_12), .out_23(cell_controller_2_out_23), .out_13(cell_controller_2_out_13),
    .out_35(cell_controller_2_out_35), .out_24(cell_controller_2_out_24), .out_14(cell_controller_2_out_14),
    .out_36(cell_controller_2_out_36), .out_25(cell_controller_2_out_25), .out_15(cell_controller_2_out_15),
    .out_37(cell_controller_2_out_37), .out_16(cell_controller_2_out_16), .out_26(cell_controller_2_out_26),
    .out_38(cell_controller_2_out_38), .out_17(cell_controller_2_out_17), .out_27(cell_controller_2_out_27),
    .out_18(cell_controller_2_out_18), .out_39(cell_controller_2_out_39), .out_28(cell_controller_2_out_28),
    .out_19(cell_controller_2_out_19), .out_40(cell_controller_2_out_40), .out_29(cell_controller_2_out_29),
    .out_20(cell_controller_2_out_20), .out_41(cell_controller_2_out_41), .out_21(cell_controller_2_out_21),
    .out_30(cell_controller_2_out_30), .out_42(cell_controller_2_out_42), .out_22(cell_controller_2_out_22),
    .out_31(cell_controller_2_out_31), .out_43(cell_controller_2_out_43), .out_32(cell_controller_2_out_32),
    .out_44(cell_controller_2_out_44), .out_33(cell_controller_2_out_33), .out_45(cell_controller_2_out_45),
    .CSC(in_3), .CSR(in_6), .MISO(pull_resistor_1_node), .SPI(spi_module_master_1_clk),
    .L_DataI(cell_controller_1_r_datao), .L_DataO(cell_controller_2_l_datao));  // open: U_DataO, R_DataI, R_DataO, D_DataI, D_DataO, U_DataI
  DotMatrix #(.matrixcols(11), .matrixrows(8)) dotmatrix_5 (
    .col0(cell_controller_2_out_23), .col1(cell_controller_2_out_24), .col2(cell_controller_2_out_25),
    .col3(cell_controller_2_out_26), .col4(cell_controller_2_out_27), .col5(cell_controller_2_out_28),
    .col6(cell_controller_2_out_29), .col7(cell_controller_2_out_30), .col8(cell_controller_2_out_31),
    .col9(cell_controller_2_out_32), .col10(cell_controller_2_out_33));
  DotMatrix #(.matrixcols(11), .matrixrows(8)) dotmatrix_6 (
    .col0(cell_controller_2_out_35), .col1(cell_controller_2_out_36), .col2(cell_controller_2_out_37),
    .col3(cell_controller_2_out_38), .col4(cell_controller_2_out_39), .col5(cell_controller_2_out_40),
    .col6(cell_controller_2_out_41), .col7(cell_controller_2_out_42), .col8(cell_controller_2_out_43),
    .col9(cell_controller_2_out_44), .col10(cell_controller_2_out_45));

  // Notes on the sheet:
  //   in_4: pull=down
  //   in_6: pull=down
  //   in_3: pull=down
  //   --------------->
  //   <---------------
endmodule

module Cell_controller (
  input  CSR,
  input  CSC,
  input  [1:0] SPI,
  input  [11:0] U_DataI,
  input  [11:0] L_DataI,
  input  [11:0] R_DataI,
  input  [11:0] D_DataI,
  output [11:0] U_DataO,
  output MISO,
  output [11:0] R_DataO,
  output [11:0] L_DataO,
  output [4:0] out_12,
  output [4:0] out_13,
  output [4:0] out_14,
  output [4:0] out_15,
  output [4:0] out_16,
  output [4:0] out_17,
  output [4:0] out_18,
  output [4:0] out_19,
  output [4:0] out_20,
  output [4:0] out_21,
  output [4:0] out_22,
  output [7:0] out_23,
  output [7:0] out_24,
  output [7:0] out_25,
  output [7:0] out_26,
  output [7:0] out_27,
  output [7:0] out_28,
  output [7:0] out_29,
  output [7:0] out_30,
  output [7:0] out_31,
  output [7:0] out_32,
  output [7:0] out_33,
  output [11:0] D_DataO,
  output [7:0] out_35,
  output [7:0] out_36,
  output [7:0] out_37,
  output [7:0] out_38,
  output [7:0] out_39,
  output [7:0] out_40,
  output [7:0] out_41,
  output [7:0] out_42,
  output [7:0] out_43,
  output [7:0] out_44,
  output [7:0] out_45
);

  wire and_1_out, and_2_out, and_3_out, and_6_out, and_7_out, and_8_out, and_9_out, and_11_out, and_12_out,
       and_13_out, and_14_out, and_15_out, and_16_out, and_17_out, and_18_out, and_19_out, and_20_out,
       and_21_out, Choose, CLK, command_decoder_1_is_direction, command_decoder_1_is_energy,
       command_decoder_1_is_player, command_decoder_1_is_type, CS_RST, d_ff_2_qn, down_en, down_err, in_err,
       is_sec_player, is_write, left_en, left_err, move_end_1, move_end_2, o_math_1_err, o_math_2_err,
       o_math_3_err, o_math_4_err, or_1_out, or_2_out, or_3_out, or_4_out, or_5_out, or_6_out, or_7_out,
       or_9_out, or_10_out, or_11_out, or_12_out, or_13_out, or_14_out, or_16_out, or_17_out, or_18_out,
       or_19_out, or_20_out, planning_clr, reg_update, right_en, right_err, RST,
       spi_module_cell_1_input_transanction_end, spi_module_cell_1_task_conf, task_err, task_update, up_en,
       up_err;
  wire [1:0] command_decoder_1_direction, controlled_buffer_4_out, i_math_1_player_select_2, input_player,
       input_type, or_8_out;
  wire [3:0] actual_type, display_task_type;
  wire [3:2] spi_module_cell_1_is_task;
  wire [4:0] spi_module_cell_1_command;
  wire [9:0] actual_energy, adder_2_out, adder_3_out, adder_4_out, adder_5_out, controlled_buffer_7_out,
       down_en_out, i_math_1_energy_2, left_en_out, multiplexer_1_out, o_math_1_c_reg_2, o_math_2_c_reg_2,
       o_math_3_c_reg_2, o_math_4_c_reg_2, right_en_out, up_en_out;
  wire [10:0] adder_1_out, controlled_buffer_1_out, controlled_buffer_2_out, controlled_buffer_5_out,
       controlled_buffer_11_out, input_energy;

  assign controlled_buffer_1_out = left_en ? input_energy : 11'bz;  // Controlled_Buffer controlled_buffer_1
  and and_1 (and_1_out, CSR, CSC);
  or or_1 (or_1_out, planning_clr, left_en);
  not not_1 (CS_RST, and_1_out);
  O_math o_math_1 (
    .Energy(actual_energy), .C_reg(L_DataO[9:0]), .Cancel_transfer(planning_clr),
    .mv_energy(controlled_buffer_1_out), .Energy_2(left_en_out), .C_reg_2(o_math_1_c_reg_2),
    .err(o_math_1_err));
  and and_2 (and_2_out, or_1_out, is_write, reg_update);
  and and_3 (and_3_out, left_en, and_2_out);
  SPI_module__cell spi_module_cell_1 (
    .CS(and_1_out), .CLK(SPI[0]), .MOSI(SPI[1]), .err(or_2_out), .energy_in({1'b0, multiplexer_1_out}),
    .type_select_in(display_task_type), .player_select_in(D_DataO[11:10]), .clk_out(CLK),
    .is_selected(Choose), .move_end_1(move_end_1), .move_end_2(move_end_2),
    .is_task(spi_module_cell_1_is_task), .task_conf(spi_module_cell_1_task_conf),
    .command(spi_module_cell_1_command), .energy_out(input_energy),
    .input_transanction_end(spi_module_cell_1_input_transanction_end), .type_select_out(input_type),
    .player_select_out(input_player), .MISO(MISO), .is_player_2(is_sec_player));  // open: output_transanction_end
  D_Flip_Flop d_ff_1 (
    .clk(and_3_out), .D(o_math_1_err), .Q(left_err), .en(and_3_out), .reset(CS_RST));  // open: Qn, preset
  D_Flip_Flop #(.trigger("falling")) d_ff_2 (
    .clk(spi_module_cell_1_input_transanction_end), .D(1'b0), .Qn(d_ff_2_qn), .preset(reg_update));  // open: Q, en, reset
  and and_4 (reg_update, ~CLK, d_ff_2_qn, spi_module_cell_1_input_transanction_end);  // AND_Gate
  and and_5 (task_update, ~CLK, spi_module_cell_1_task_conf);  // AND_Gate
  or or_2 (or_2_out, down_err, left_err, in_err, task_err, right_err, up_err);
  Register #(.width(10)) Left_c_reg (
    .D(o_math_1_c_reg_2), .en(1'b1), .Q(L_DataO[9:0]), .clk(and_2_out), .clr(or_3_out));
  or or_3 (or_3_out, RST, move_end_2);
  Decoder #(.select(2), .disabled(0)) decoder_1 (
    .out0(down_en), .out1(left_en), .out2(right_en), .out3(up_en), .sel(command_decoder_1_direction),
    .en(command_decoder_1_is_direction));
  command_decoder command_decoder_1 (
    .Command_in(spi_module_cell_1_command), .direction(command_decoder_1_direction),
    .is_direction(command_decoder_1_is_direction), .is_energy(command_decoder_1_is_energy),
    .is_type(command_decoder_1_is_type), .is_clear(planning_clr), .is_player(command_decoder_1_is_player),
    .is_write(is_write), .is_reset(RST));  // open: is_task
  Multiplexer #(.select(2), .width(10)) multiplexer_1 (
    .in0(D_DataO[9:0]), .in1(L_DataO[9:0]), .in2(R_DataO[9:0]), .in3(U_DataO[9:0]), .out(multiplexer_1_out),
    .sel(command_decoder_1_direction), .en(command_decoder_1_is_direction));
  assign controlled_buffer_2_out = up_en ? input_energy : 11'bz;  // Controlled_Buffer controlled_buffer_2
  assign multiplexer_1_out = command_decoder_1_is_energy ? actual_energy : 10'bz;  // Controlled_Buffer controlled_buffer_3
  O_math o_math_2 (
    .Energy(actual_energy), .C_reg(U_DataO[9:0]), .Cancel_transfer(planning_clr),
    .mv_energy(controlled_buffer_2_out), .Energy_2(up_en_out), .C_reg_2(o_math_2_c_reg_2), .err(o_math_2_err));
  or or_4 (or_4_out, planning_clr, up_en);
  D_Flip_Flop d_ff_3 (
    .clk(and_7_out), .D(o_math_2_err), .Q(up_err), .en(and_7_out), .reset(CS_RST));  // open: Qn, preset
  and and_6 (and_6_out, or_4_out, is_write, reg_update);
  and and_7 (and_7_out, up_en, and_6_out);
  and and_8 (and_8_out, is_write, command_decoder_1_is_type);
  or or_5 (or_5_out, spi_module_cell_1_is_task[2], spi_module_cell_1_is_task[3]);
  or or_6 (or_6_out, actual_type[3], actual_type[2], D_DataO[11], D_DataO[10]);
  Register #(.width(10)) Up_c_reg (.D(o_math_2_c_reg_2), .en(1'b1), .Q(U_DataO[9:0]), .clk(and_6_out), .clr(or_7_out));
  or or_7 (or_7_out, RST, move_end_2);
  and and_9 (and_9_out, command_decoder_1_is_energy, ~RST, ~move_end_1);  // AND_Gate
  assign or_8_out = spi_module_cell_1_is_task | actual_type[3:2];  // OR_Gate or_8, 2 bits wide
  or or_9 (or_9_out, spi_module_cell_1_is_task[2], spi_module_cell_1_is_task[3], and_8_out);
  or or_10 (or_10_out, reg_update, task_update);
  and and_10 (task_err, or_5_out, or_6_out);
  assign controlled_buffer_4_out = command_decoder_1_is_player ? input_player : 2'bz;  // Controlled_Buffer controlled_buffer_4
  and and_11 (and_11_out, command_decoder_1_is_player, is_write, reg_update);
  and and_12 (and_12_out, move_end_1, ~CLK);  // AND_Gate
  assign controlled_buffer_5_out = down_en ? input_energy : 11'bz;  // Controlled_Buffer controlled_buffer_5
  or or_11 (or_11_out, command_decoder_1_is_direction, planning_clr, command_decoder_1_is_energy);
  and and_13 (and_13_out, or_9_out, or_10_out);
  assign controlled_buffer_4_out = move_end_1 ? i_math_1_player_select_2 : 2'bz;  // Controlled_Buffer controlled_buffer_6
  or or_12 (or_12_out, and_11_out, and_12_out);
  or or_13 (or_13_out, planning_clr, down_en);
  Adder #(.width(11)) adder_1 (.a({1'b0, actual_energy}), .b(input_energy), .out(adder_1_out));  // open: cin, cout
  or or_14 (or_14_out, is_write, RST);
  and and_14 (and_14_out, or_11_out, or_14_out, reg_update);
  Register #(.width(4)) type_reg (.D({or_8_out, input_type}), .en(1'b1), .Q(actual_type), .clk(and_13_out), .clr(RST));
  Register #(.width(2)) player_reg (
    .D(controlled_buffer_4_out), .en(1'b1), .Q(D_DataO[11:10]), .clk(or_12_out), .clr(RST));
  O_math o_math_3 (
    .Energy(actual_energy), .C_reg(D_DataO[9:0]), .Cancel_transfer(planning_clr),
    .mv_energy(controlled_buffer_5_out), .Energy_2(down_en_out), .C_reg_2(o_math_3_c_reg_2),
    .err(o_math_3_err));
  and and_15 (and_15_out, or_13_out, is_write, reg_update);
  and and_16 (and_16_out, down_en, and_15_out);
  assign controlled_buffer_7_out = and_9_out ? adder_1_out[9:0] : 10'bz;  // Controlled_Buffer controlled_buffer_7
  assign display_task_type = {spi_module_cell_1_is_task, 2'b00} | actual_type;  // OR_Gate or_15, 4 bits wide
  D_Flip_Flop d_ff_4 (
    .clk(and_16_out), .D(o_math_3_err), .Q(down_err), .en(and_16_out), .reset(CS_RST));  // open: Qn, preset
  assign controlled_buffer_7_out = planning_clr ? adder_5_out : 10'bz;  // Controlled_Buffer controlled_buffer_8
  assign controlled_buffer_7_out = RST ? 10'h3 : 10'bz;  // Controlled_Buffer controlled_buffer_9
  and and_17 (and_17_out, move_end_1, ~CLK);  // AND_Gate
  or or_16 (or_16_out, and_17_out, and_14_out);
  assign controlled_buffer_7_out = move_end_1 ? i_math_1_energy_2 : 10'bz;  // Controlled_Buffer controlled_buffer_10
  I_math i_math_1 (
    .Energy(actual_energy), .player_select(D_DataO[11:10]), .type_select(actual_type), .Dl_3(U_DataI),
    .Dl_4(L_DataI), .Dl_2(R_DataI), .Dl_1(D_DataI), .Energy_2(i_math_1_energy_2),
    .player_select_2(i_math_1_player_select_2), .err(in_err), .inc_en(or_17_out));
  or or_17 (or_17_out, and_18_out, and_19_out);
  and and_18 (and_18_out, i_math_1_player_select_2[1], ~i_math_1_player_select_2[0], is_sec_player);  // AND_Gate
  and and_19 (and_19_out, ~i_math_1_player_select_2[1], i_math_1_player_select_2[0], ~is_sec_player);  // AND_Gate
  Register #(.width(10)) Down_c_reg (
    .D(o_math_3_c_reg_2), .en(1'b1), .Q(D_DataO[9:0]), .clk(and_15_out), .clr(or_18_out));
  or or_18 (or_18_out, RST, move_end_2);
  Adder #(.width(10)) adder_2 (.a(U_DataO[9:0]), .b(R_DataO[9:0]), .out(adder_2_out));  // open: cin, cout
  Register #(.width(10)) Energy_reg (
    .D(controlled_buffer_7_out), .en(1'b1), .Q(actual_energy), .clk(or_16_out), .clr(1'b0));
  Multiplexer #(.select(2), .width(10)) multiplexer_2 (
    .in0(down_en_out), .in1(left_en_out), .in2(right_en_out), .in3(up_en_out), .out(controlled_buffer_7_out),
    .sel(command_decoder_1_direction), .en(command_decoder_1_is_direction));
  Adder #(.width(10)) adder_3 (.a(adder_2_out), .b(L_DataO[9:0]), .out(adder_3_out));  // open: cin, cout
  Adder #(.width(10)) adder_4 (.a(adder_3_out), .b(D_DataO[9:0]), .out(adder_4_out));  // open: cin, cout
  Adder #(.width(10)) adder_5 (.a(adder_4_out), .b(actual_energy), .out(adder_5_out));  // open: cin, cout
  assign controlled_buffer_11_out = right_en ? input_energy : 11'bz;  // Controlled_Buffer controlled_buffer_11
  or or_19 (or_19_out, planning_clr, right_en);
  O_math o_math_4 (
    .Energy(actual_energy), .C_reg(R_DataO[9:0]), .Cancel_transfer(planning_clr),
    .mv_energy(controlled_buffer_11_out), .Energy_2(right_en_out), .C_reg_2(o_math_4_c_reg_2),
    .err(o_math_4_err));
  and and_20 (and_20_out, or_19_out, is_write, reg_update);
  D_Flip_Flop d_ff_5 (
    .clk(and_21_out), .D(o_math_4_err), .Q(right_err), .en(and_21_out), .reset(CS_RST));  // open: Qn, preset
  and and_21 (and_21_out, right_en, and_20_out);
  Register #(.width(10)) Right_c_reg (
    .D(o_math_4_c_reg_2), .en(1'b1), .Q(R_DataO[9:0]), .clk(and_20_out), .clr(or_20_out));
  or or_20 (or_20_out, RST, move_end_2);
  DotMatrix #(.matrixcols(11), .matrixrows(8)) dotmatrix_1 (
    .col0(out_23), .col1(out_24), .col2(out_25), .col3(out_26), .col4(out_27), .col5(out_28), .col6(out_29),
    .col7(out_30), .col8(out_31), .col9(out_32), .col10(out_33));
  Player_Type player_type_1 (
    .in_1(D_DataO[11:10]), .in_2(display_task_type), .out_14(out_23), .out_15(out_24), .out_16(out_25),
    .out_17(out_26), .out_18(out_27), .out_19(out_28), .out_20(out_29), .out_21(out_30), .out_22(out_31),
    .out_23(out_32), .out_24(out_33), .out_3(out_35), .out_4(out_36), .out_5(out_37), .out_6(out_38),
    .out_7(out_39), .out_8(out_40), .out_9(out_41), .out_10(out_42), .out_11(out_43), .out_12(out_44),
    .out_13(out_45));
  DotMatrix #(.matrixcols(11), .matrixrows(8)) dotmatrix_2 (
    .col0(out_35), .col1(out_36), .col2(out_37), .col3(out_38), .col4(out_39), .col5(out_40), .col6(out_41),
    .col7(out_42), .col8(out_43), .col9(out_44), .col10(out_45));
  DotMatrix #(.matrixcols(11), .matrixrows(5)) dotmatrix_3 (
    .col0(out_12), .col1(out_13), .col2(out_14), .col3(out_15), .col4(out_16), .col5(out_17), .col6(out_18),
    .col7(out_19), .col8(out_20), .col9(out_21), .col10(out_22));
  // Numders numders_1: pin names not known; wires that end beside it: Choose, out_12, out_13, out_14, out_15, out_16, actual_energy, out_17, out_18, out_19, out_20, out_21, out_22

  assign L_DataO[11:10] = D_DataO[11:10];
  assign R_DataO[11:10] = D_DataO[11:10];
  assign U_DataO[11:10] = D_DataO[11:10];

  // Other names for the same wires on the sheet: display_energy[9:0] = actual_energy; down_c_out[9:0] = D_DataO[9:0];
  //   E1[4:0] = out_12; E2[4:0] = out_13; E3[4:0] = out_14; E4[4:0] = out_15; E5[4:0] = out_16; E6[4:0] = out_17;
  //   E7[4:0] = out_18; E8[4:0] = out_19; E9[4:0] = out_20; E10[4:0] = out_21; E11[4:0] = out_22;
  //   left_c_out[9:0] = L_DataO[9:0]; right_c_out[9:0] = R_DataO[9:0]; actual_player[1:0] = D_DataO[11:10];
  //   display_player[1:0] = D_DataO[11:10]; up_c_out[9:0] = U_DataO[9:0]; О1[7:0] = out_23; О2[7:0] = out_24;
  //   О3[7:0] = out_25; О4[7:0] = out_26; О5[7:0] = out_27; О6[7:0] = out_28; О7[7:0] = out_29; О8[7:0] = out_30;
  //   О9[7:0] = out_31; О10[7:0] = out_32; О11[7:0] = out_33; С1[7:0] = out_35; С2[7:0] = out_36; С3[7:0] = out_37;
  //   С4[7:0] = out_38; С5[7:0] = out_39; С6[7:0] = out_40; С7[7:0] = out_41; С8[7:0] = out_42; С9[7:0] = out_43;
  //   С10[7:0] = out_44; С11[7:0] = out_45

  // Notes on the sheet:
  //   SPI: pull=down
  //   CSR: pull=down
  //   CSC: pull=down
  //   Task+type management
  //   Number mtx output
  //   Orange mtx output
  //   Blue mtx output
endmodule
