// Logisim project display controller.circ as structural Verilog: 13 circuits, main circuit main
module main (
  input  [9:0] in_1,
  input  [9:0] in_2,
  input  [1:0] in_3,
  input  [1:0] in_4,
  input  [1:0] in_5,
  input  [3:0] in_6,
  input  [3:0] in_7,
  input  [1:0] in_8,
  input  [9:0] in_9,
  input  [9:0] in_10,
  input  [9:0] in_11,
  input  [9:0] in_12,
  input  [1:0] in_13,
  input  [1:0] in_14,
  input  [1:0] in_15,
  input  [1:0] in_16,
  input  [3:0] in_17,
  input  [3:0] in_18,
  input  [3:0] in_19,
  input  [3:0] in_20,
  input  [9:0] in_21,
  input  [9:0] in_22,
  input  [9:0] in_23,
  input  [9:0] in_24,
  input  [1:0] in_25,
  input  [1:0] in_26,
  input  [1:0] in_27,
  input  [1:0] in_28,
  input  [3:0] in_29,
  input  [3:0] in_30,
  input  [3:0] in_31,
  input  [3:0] in_32,
  input  [9:0] in_33,
  input  [9:0] in_34,
  input  [9:0] in_35,
  input  [9:0] in_36,
  input  [1:0] in_37,
  input  [1:0] in_38,
  input  [1:0] in_39,
  input  [1:0] in_40,
  input  [3:0] in_41,
  input  [3:0] in_42,
  input  [3:0] in_43,
  input  [3:0] in_44,
  input  [9:0] in_45,
  input  [9:0] in_46,
  input  [9:0] in_47,
  input  [9:0] in_48,
  input  [1:0] in_49,
  input  [1:0] in_50,
  input  [1:0] in_51,
  input  [1:0] in_52,
  input  [3:0] in_53,
  input  [3:0] in_54,
  input  [3:0] in_55,
  input  [3:0] in_56,
  input  in_57,
  input  in_58
);

  wire [4:0] \цифры_1_out_2 , \цифры_1_out_3 , \цифры_1_out_4 , \цифры_1_out_5 , \цифры_1_out_6 ,
       \цифры_1_out_7 , \цифры_1_out_8 , \цифры_1_out_9 , \цифры_1_out_10 , \цифры_1_out_11 ,
       \цифры_1_out_12 , \цифры_2_out_2 , \цифры_2_out_3 , \цифры_2_out_4 , \цифры_2_out_5 , \цифры_2_out_6 ,
       \цифры_2_out_7 , \цифры_2_out_8 , \цифры_2_out_9 , \цифры_2_out_10 , \цифры_2_out_11 ,
       \цифры_2_out_12 , \цифры_3_out_2 , \цифры_3_out_3 , \цифры_3_out_4 , \цифры_3_out_5 , \цифры_3_out_6 ,
       \цифры_3_out_7 , \цифры_3_out_8 , \цифры_3_out_9 , \цифры_3_out_10 , \цифры_3_out_11 ,
       \цифры_3_out_12 , \цифры_4_out_2 , \цифры_4_out_3 , \цифры_4_out_4 , \цифры_4_out_5 , \цифры_4_out_6 ,
       \цифры_4_out_7 , \цифры_4_out_8 , \цифры_4_out_9 , \цифры_4_out_10 , \цифры_4_out_11 ,
       \цифры_4_out_12 , \цифры_5_out_2 , \цифры_5_out_3 , \цифры_5_out_4 , \цифры_5_out_5 , \цифры_5_out_6 ,
       \цифры_5_out_7 , \цифры_5_out_8 , \цифры_5_out_9 , \цифры_5_out_10 , \цифры_5_out_11 ,
       \цифры_5_out_12 , \цифры_6_out_2 , \цифры_6_out_3 , \цифры_6_out_4 , \цифры_6_out_5 , \цифры_6_out_6 ,
       \цифры_6_out_7 , \цифры_6_out_8 , \цифры_6_out_9 , \цифры_6_out_10 , \цифры_6_out_11 ,
       \цифры_6_out_12 , \цифры_7_out_2 , \цифры_7_out_3 , \цифры_7_out_4 , \цифры_7_out_5 , \цифры_7_out_6 ,
       \цифры_7_out_7 , \цифры_7_out_8 , \цифры_7_out_9 , \цифры_7_out_10 , \цифры_7_out_11 ,
       \цифры_7_out_12 , \цифры_8_out_2 , \цифры_8_out_3 , \цифры_8_out_4 , \цифры_8_out_5 , \цифры_8_out_6 ,
       \цифры_8_out_7 , \цифры_8_out_8 , \цифры_8_out_9 , \цифры_8_out_10 , \цифры_8_out_11 ,
       \цифры_8_out_12 , \цифры_9_out_2 , \цифры_9_out_3 , \цифры_9_out_4 , \цифры_9_out_5 , \цифры_9_out_6 ,
       \цифры_9_out_7 , \цифры_9_out_8 , \цифры_9_out_9 , \цифры_9_out_10 , \цифры_9_out_11 ,
       \цифры_9_out_12 , \цифры_10_out_2 , \цифры_10_out_3 , \цифры_10_out_4 , \цифры_10_out_5 ,
       \цифры_10_out_6 , \цифры_10_out_7 , \цифры_10_out_8 , \цифры_10_out_9 , \цифры_10_out_10 ,
       \цифры_10_out_11 , \цифры_10_out_12 , \цифры_11_out_2 , \цифры_11_out_3 , \цифры_11_out_4 ,
       \цифры_11_out_5 , \цифры_11_out_6 , \цифры_11_out_7 , \цифры_11_out_8 , \цифры_11_out_9 ,
       \цифры_11_out_10 , \цифры_11_out_11 , \цифры_11_out_12 , \цифры_12_out_2 , \цифры_12_out_3 ,
       \цифры_12_out_4 , \цифры_12_out_5 , \цифры_12_out_6 , \цифры_12_out_7 , \цифры_12_out_8 ,
       \цифры_12_out_9 , \цифры_12_out_10 , \цифры_12_out_11 , \цифры_12_out_12 , \цифры_13_out_2 ,
       \цифры_13_out_3 , \цифры_13_out_4 , \цифры_13_out_5 , \цифры_13_out_6 , \цифры_13_out_7 ,
       \цифры_13_out_8 , \цифры_13_out_9 , \цифры_13_out_10 , \цифры_13_out_11 , \цифры_13_out_12 ,
       \цифры_14_out_2 , \цифры_14_out_3 , \цифры_14_out_4 , \цифры_14_out_5 , \цифры_14_out_6 ,
       \цифры_14_out_7 , \цифры_14_out_8 , \цифры_14_out_9 , \цифры_14_out_10 , \цифры_14_out_11 ,
       \цифры_14_out_12 , \цифры_15_out_2 , \цифры_15_out_3 , \цифры_15_out_4 , \цифры_15_out_5 ,
       \цифры_15_out_6 , \цифры_15_out_7 , \цифры_15_out_8 , \цифры_15_out_9 , \цифры_15_out_10 ,
       \цифры_15_out_11 , \цифры_15_out_12 , \цифры_16_out_2 , \цифры_16_out_3 , \цифры_16_out_4 ,
       \цифры_16_out_5 , \цифры_16_out_6 , \цифры_16_out_7 , \цифры_16_out_8 , \цифры_16_out_9 ,
       \цифры_16_out_10 , \цифры_16_out_11 , \цифры_16_out_12 , \цифры_17_out_2 , \цифры_17_out_3 ,
       \цифры_17_out_4 , \цифры_17_out_5 , \цифры_17_out_6 , \цифры_17_out_7 , \цифры_17_out_8 ,
       \цифры_17_out_9 , \цифры_17_out_10 , \цифры_17_out_11 , \цифры_17_out_12 , \цифры_18_out_2 ,
       \цифры_18_out_3 , \цифры_18_out_4 , \цифры_18_out_5 , \цифры_18_out_6 , \цифры_18_out_7 ,
       \цифры_18_out_8 , \цифры_18_out_9 , \цифры_18_out_10 , \цифры_18_out_11 , \цифры_18_out_12 ;
  wire [7:0] \чья_тип_1_p3 , \чья_тип_1_p4 , \чья_тип_1_p5 , \чья_тип_1_p6 , \чья_тип_1_p7 , \чья_тип_1_p8 ,
       \чья_тип_1_p9 , \чья_тип_1_p10 , \чья_тип_1_p11 , \чья_тип_1_p12 , \чья_тип_1_p13 , \чья_тип_2_p3 ,
       \чья_тип_2_p4 , \чья_тип_2_p5 , \чья_тип_2_p6 , \чья_тип_2_p7 , \чья_тип_2_p8 , \чья_тип_2_p9 ,
       \чья_тип_2_p10 , \чья_тип_2_p11 , \чья_тип_2_p12 , \чья_тип_2_p13 , \чья_тип_3_p3 , \чья_тип_3_p4 ,
       \чья_тип_3_p5 , \чья_тип_3_p6 , \чья_тип_3_p7 , \чья_тип_3_p8 , \чья_тип_3_p9 , \чья_тип_3_p10 ,
       \чья_тип_3_p11 , \чья_тип_3_p12 , \чья_тип_3_p13 , \чья_тип_4_p3 , \чья_тип_4_p4 , \чья_тип_4_p5 ,
       \чья_тип_4_p6 , \чья_тип_4_p7 , \чья_тип_4_p8 , \чья_тип_4_p9 , \чья_тип_4_p10 , \чья_тип_4_p11 ,
       \чья_тип_4_p12 , \чья_тип_4_p13 , \чья_тип_5_out_3 , \чья_тип_5_out_4 , \чья_тип_5_out_5 ,
       \чья_тип_5_out_6 , \чья_тип_5_out_7 , \чья_тип_5_out_8 , \чья_тип_5_out_9 , \чья_тип_5_out_10 ,
       \чья_тип_5_out_11 , \чья_тип_5_out_12 , \чья_тип_5_out_13 , \чья_тип_5_out_14 , \чья_тип_5_out_15 ,
       \чья_тип_5_out_16 , \чья_тип_5_out_17 , \чья_тип_5_out_18 , \чья_тип_5_out_19 , \чья_тип_5_out_20 ,
       \чья_тип_5_out_21 , \чья_тип_5_out_22 , \чья_тип_5_out_23 , \чья_тип_5_out_24 , \чья_тип_6_p3 ,
       \чья_тип_6_p4 , \чья_тип_6_p5 , \чья_тип_6_p6 , \чья_тип_6_p7 , \чья_тип_6_p8 , \чья_тип_6_p9 ,
       \чья_тип_6_p10 , \чья_тип_6_p11 , \чья_тип_6_p12 , \чья_тип_6_p13 , \чья_тип_7_p3 , \чья_тип_7_p4 ,
       \чья_тип_7_p5 , \чья_тип_7_p6 , \чья_тип_7_p7 , \чья_тип_7_p8 , \чья_тип_7_p9 , \чья_тип_7_p10 ,
       \чья_тип_7_p11 , \чья_тип_7_p12 , \чья_тип_7_p13 , \чья_тип_8_p3 , \чья_тип_8_p4 , \чья_тип_8_p5 ,
       \чья_тип_8_p6 , \чья_тип_8_p7 , \чья_тип_8_p8 , \чья_тип_8_p9 , \чья_тип_8_p10 , \чья_тип_8_p11 ,
       \чья_тип_8_p12 , \чья_тип_8_p13 , \чья_тип_9_p3 , \чья_тип_9_p4 , \чья_тип_9_p5 , \чья_тип_9_p6 ,
       \чья_тип_9_p7 , \чья_тип_9_p8 , \чья_тип_9_p9 , \чья_тип_9_p10 , \чья_тип_9_p11 , \чья_тип_9_p12 ,
       \чья_тип_9_p13 , \чья_тип_10_p3 , \чья_тип_10_p4 , \чья_тип_10_p5 , \чья_тип_10_p6 , \чья_тип_10_p7 ,
       \чья_тип_10_p8 , \чья_тип_10_p9 , \чья_тип_10_p10 , \чья_тип_10_p11 , \чья_тип_10_p12 ,
       \чья_тип_10_p13 , \чья_тип_11_p3 , \чья_тип_11_p4 , \чья_тип_11_p5 , \чья_тип_11_p6 , \чья_тип_11_p7 ,
       \чья_тип_11_p8 , \чья_тип_11_p9 , \чья_тип_11_p10 , \чья_тип_11_p11 , \чья_тип_11_p12 ,
       \чья_тип_11_p13 , \чья_тип_12_p3 , \чья_тип_12_p4 , \чья_тип_12_p5 , \чья_тип_12_p6 , \чья_тип_12_p7 ,
       \чья_тип_12_p8 , \чья_тип_12_p9 , \чья_тип_12_p10 , \чья_тип_12_p11 , \чья_тип_12_p12 ,
       \чья_тип_12_p13 , \чья_тип_13_p3 , \чья_тип_13_p4 , \чья_тип_13_p5 , \чья_тип_13_p6 , \чья_тип_13_p7 ,
       \чья_тип_13_p8 , \чья_тип_13_p9 , \чья_тип_13_p10 , \чья_тип_13_p11 , \чья_тип_13_p12 ,
       \чья_тип_13_p13 , \чья_тип_14_p3 , \чья_тип_14_p4 , \чья_тип_14_p5 , \чья_тип_14_p6 , \чья_тип_14_p7 ,
       \чья_тип_14_p8 , \чья_тип_14_p9 , \чья_тип_14_p10 , \чья_тип_14_p11 , \чья_тип_14_p12 ,
       \чья_тип_14_p13 , \чья_тип_15_p3 , \чья_тип_15_p4 , \чья_тип_15_p5 , \чья_тип_15_p6 , \чья_тип_15_p7 ,
       \чья_тип_15_p8 , \чья_тип_15_p9 , \чья_тип_15_p10 , \чья_тип_15_p11 , \чья_тип_15_p12 ,
       \чья_тип_15_p13 , \чья_тип_16_p3 , \чья_тип_16_p4 , \чья_тип_16_p5 , \чья_тип_16_p6 , \чья_тип_16_p7 ,
       \чья_тип_16_p8 , \чья_тип_16_p9 , \чья_тип_16_p10 , \чья_тип_16_p11 , \чья_тип_16_p12 ,
       \чья_тип_16_p13 , \чья_тип_17_p3 , \чья_тип_17_p4 , \чья_тип_17_p5 , \чья_тип_17_p6 , \чья_тип_17_p7 ,
       \чья_тип_17_p8 , \чья_тип_17_p9 , \чья_тип_17_p10 , \чья_тип_17_p11 , \чья_тип_17_p12 ,
       \чья_тип_17_p13 ;

  DotMatrix #(.matrixcols(11), .matrixrows(5)) dotmatrix_1 (
    .col0(\цифры_1_out_2 ), .col1(\цифры_1_out_3 ), .col2(\цифры_1_out_4 ), .col3(\цифры_1_out_5 ),
    .col4(\цифры_1_out_6 ), .col5(\цифры_1_out_7 ), .col6(\цифры_1_out_8 ), .col7(\цифры_1_out_9 ),
    .col8(\цифры_1_out_10 ), .col9(\цифры_1_out_11 ), .col10(\цифры_1_out_12 ));
  \Цифры  \u_цифры_1  (
    .out_2(\цифры_1_out_2 ), .out_3(\цифры_1_out_3 ), .out_4(\цифры_1_out_4 ), .out_5(\цифры_1_out_5 ),
    .out_6(\цифры_1_out_6 ), .out_7(\цифры_1_out_7 ), .out_8(\цифры_1_out_8 ), .out_9(\цифры_1_out_9 ),
    .out_10(\цифры_1_out_10 ), .out_11(\цифры_1_out_11 ), .out_12(\цифры_1_out_12 ));  // open: Energy
  DotMatrix #(.matrixcols(11), .matrixrows(8)) dotmatrix_2 ();  // open: col0, col1, col2, col3, col4, col5, col6, col7, col8, col9, col10
  // DotMatrix #(.matrixcols(11), .matrixrows(8)) dotmatrix_3: pin names not known; wires that end beside it: in_3, in_6
  v v_1 (.in_1(in_8));  // open: out_2, out_3, out_4, out_5, out_6
  DotMatrix dotmatrix_4 ();  // open: col0, col1, col2, col3, col4
  DotMatrix #(.matrixcols(7), .matrixrows(5)) dotmatrix_5 ();  // open: col0, col1, col2, col3, col4, col5, col6
  // circuit part_1: pin names not known; wires that end beside it: in_4, in_4, in_4
  DotMatrix #(.matrixcols(11), .matrixrows(5)) dotmatrix_6 (
    .col0(\цифры_2_out_2 ), .col1(\цифры_2_out_3 ), .col2(\цифры_2_out_4 ), .col3(\цифры_2_out_5 ),
    .col4(\цифры_2_out_6 ), .col5(\цифры_2_out_7 ), .col6(\цифры_2_out_8 ), .col7(\цифры_2_out_9 ),
    .col8(\цифры_2_out_10 ), .col9(\цифры_2_out_11 ), .col10(\цифры_2_out_12 ));
  \Цифры  \u_цифры_2  (
    .out_2(\цифры_2_out_2 ), .out_3(\цифры_2_out_3 ), .out_4(\цифры_2_out_4 ), .out_5(\цифры_2_out_5 ),
    .out_6(\цифры_2_out_6 ), .out_7(\цифры_2_out_7 ), .out_8(\цифры_2_out_8 ), .out_9(\цифры_2_out_9 ),
    .out_10(\цифры_2_out_10 ), .out_11(\цифры_2_out_11 ), .out_12(\цифры_2_out_12 ));  // open: Energy
  // Чья_Тип чья_тип_1: pin names not known; wires that end beside it: in_13, in_17, \чья_тип_1_p3 , \чья_тип_1_p4 , \чья_тип_1_p5 , \чья_тип_1_p6 , \чья_тип_1_p7 , \чья_тип_1_p8 , \чья_тип_1_p9 , \чья_тип_1_p10 , \чья_тип_1_p11 , \чья_тип_1_p12 , \чья_тип_1_p13 
  DotMatrix #(.matrixcols(11), .matrixrows(8)) dotmatrix_7 (
    .col0(\чья_тип_1_p3 ), .col1(\чья_тип_1_p4 ), .col2(\чья_тип_1_p5 ), .col3(\чья_тип_1_p6 ),
    .col4(\чья_тип_1_p7 ), .col5(\чья_тип_1_p8 ), .col6(\чья_тип_1_p9 ), .col7(\чья_тип_1_p10 ),
    .col8(\чья_тип_1_p11 ), .col9(\чья_тип_1_p12 ), .col10(\чья_тип_1_p13 ));
  // DotMatrix #(.matrixcols(11), .matrixrows(8)) dotmatrix_8: pin names not known; wires that end beside it: in_13, in_17
  \Цифры  \u_цифры_3  (
    .out_2(\цифры_3_out_2 ), .out_3(\цифры_3_out_3 ), .out_4(\цифры_3_out_4 ), .out_5(\цифры_3_out_5 ),
    .out_6(\цифры_3_out_6 ), .out_7(\цифры_3_out_7 ), .out_8(\цифры_3_out_8 ), .out_9(\цифры_3_out_9 ),
    .out_10(\цифры_3_out_10 ), .out_11(\цифры_3_out_11 ), .out_12(\цифры_3_out_12 ));  // open: Energy
  DotMatrix #(.matrixcols(11), .matrixrows(5)) dotmatrix_9 (
    .col0(\цифры_3_out_2 ), .col1(\цифры_3_out_3 ), .col2(\цифры_3_out_4 ), .col3(\цифры_3_out_5 ),
    .col4(\цифры_3_out_6 ), .col5(\цифры_3_out_7 ), .col6(\цифры_3_out_8 ), .col7(\цифры_3_out_9 ),
    .col8(\цифры_3_out_10 ), .col9(\цифры_3_out_11 ), .col10(\цифры_3_out_12 ));
  DotMatrix #(.matrixcols(11), .matrixrows(8)) dotmatrix_10 (
    .col0(\чья_тип_2_p3 ), .col1(\чья_тип_2_p4 ), .col2(\чья_тип_2_p5 ), .col3(\чья_тип_2_p6 ),
    .col4(\чья_тип_2_p7 ), .col5(\чья_тип_2_p8 ), .col6(\чья_тип_2_p9 ), .col7(\чья_тип_2_p10 ),
    .col8(\чья_тип_2_p11 ), .col9(\чья_тип_2_p12 ), .col10(\чья_тип_2_p13 ));
  // Чья_Тип чья_тип_2: pin names not known; wires that end beside it: in_27, in_31, \чья_тип_2_p3 , \чья_тип_2_p4 , \чья_тип_2_p5 , \чья_тип_2_p6 , \чья_тип_2_p7 , \чья_тип_2_p8 , \чья_тип_2_p9 , \чья_тип_2_p10 , \чья_тип_2_p11 , \чья_тип_2_p12 , \чья_тип_2_p13 
  // DotMatrix #(.matrixcols(11), .matrixrows(8)) dotmatrix_11: pin names not known; wires that end beside it: in_27, in_31
  \Цифры  \u_цифры_4  (
    .out_2(\цифры_4_out_2 ), .out_3(\цифры_4_out_3 ), .out_4(\цифры_4_out_4 ), .out_5(\цифры_4_out_5 ),
    .out_6(\цифры_4_out_6 ), .out_7(\цифры_4_out_7 ), .out_8(\цифры_4_out_8 ), .out_9(\цифры_4_out_9 ),
    .out_10(\цифры_4_out_10 ), .out_11(\цифры_4_out_11 ), .out_12(\цифры_4_out_12 ));  // open: Energy
  DotMatrix #(.matrixcols(11), .matrixrows(5)) dotmatrix_12 (
    .col0(\цифры_4_out_2 ), .col1(\цифры_4_out_3 ), .col2(\цифры_4_out_4 ), .col3(\цифры_4_out_5 ),
    .col4(\цифры_4_out_6 ), .col5(\цифры_4_out_7 ), .col6(\цифры_4_out_8 ), .col7(\цифры_4_out_9 ),
    .col8(\цифры_4_out_10 ), .col9(\цифры_4_out_11 ), .col10(\цифры_4_out_12 ));
  DotMatrix #(.matrixcols(11), .matrixrows(8)) dotmatrix_13 (
    .col0(\чья_тип_3_p3 ), .col1(\чья_тип_3_p4 ), .col2(\чья_тип_3_p5 ), .col3(\чья_тип_3_p6 ),
    .col4(\чья_тип_3_p7 ), .col5(\чья_тип_3_p8 ), .col6(\чья_тип_3_p9 ), .col7(\чья_тип_3_p10 ),
    .col8(\чья_тип_3_p11 ), .col9(\чья_тип_3_p12 ), .col10(\чья_тип_3_p13 ));
  // Чья_Тип чья_тип_3: pin names not known; wires that end beside it: in_39, in_43, \чья_тип_3_p3 , \чья_тип_3_p4 , \чья_тип_3_p5 , \чья_тип_3_p6 , \чья_тип_3_p7 , \чья_тип_3_p8 , \чья_тип_3_p9 , \чья_тип_3_p10 , \чья_тип_3_p11 , \чья_тип_3_p12 , \чья_тип_3_p13 
  // DotMatrix #(.matrixcols(11), .matrixrows(8)) dotmatrix_14: pin names not known; wires that end beside it: in_39, in_43
  \Цифры  \u_цифры_5  (
    .out_2(\цифры_5_out_2 ), .out_3(\цифры_5_out_3 ), .out_4(\цифры_5_out_4 ), .out_5(\цифры_5_out_5 ),
    .out_6(\цифры_5_out_6 ), .out_7(\цифры_5_out_7 ), .out_8(\цифры_5_out_8 ), .out_9(\цифры_5_out_9 ),
    .out_10(\цифры_5_out_10 ), .out_11(\цифры_5_out_11 ), .out_12(\цифры_5_out_12 ));  // open: Energy
  DotMatrix #(.matrixcols(11), .matrixrows(5)) dotmatrix_15 (
    .col0(\цифры_5_out_2 ), .col1(\цифры_5_out_3 ), .col2(\цифры_5_out_4 ), .col3(\цифры_5_out_5 ),
    .col4(\цифры_5_out_6 ), .col5(\цифры_5_out_7 ), .col6(\цифры_5_out_8 ), .col7(\цифры_5_out_9 ),
    .col8(\цифры_5_out_10 ), .col9(\цифры_5_out_11 ), .col10(\цифры_5_out_12 ));
  DotMatrix #(.matrixcols(11), .matrixrows(8)) dotmatrix_16 (
    .col0(\чья_тип_4_p3 ), .col1(\чья_тип_4_p4 ), .col2(\чья_тип_4_p5 ), .col3(\чья_тип_4_p6 ),
    .col4(\чья_тип_4_p7 ), .col5(\чья_тип_4_p8 ), .col6(\чья_тип_4_p9 ), .col7(\чья_тип_4_p10 ),
    .col8(\чья_тип_4_p11 ), .col9(\чья_тип_4_p12 ), .col10(\чья_тип_4_p13 ));
  // Чья_Тип чья_тип_4: pin names not known; wires that end beside it: in_49, in_53, \чья_тип_4_p3 , \чья_тип_4_p4 , \чья_тип_4_p5 , \чья_тип_4_p6 , \чья_тип_4_p7 , \чья_тип_4_p8 , \чья_тип_4_p9 , \чья_тип_4_p10 , \чья_тип_4_p11 , \чья_тип_4_p12 , \чья_тип_4_p13 
  // DotMatrix #(.matrixcols(11), .matrixrows(8)) dotmatrix_17: pin names not known; wires that end beside it: in_49, in_53
  DotMatrix #(.matrixcols(11), .matrixrows(5)) dotmatrix_18 (
    .col0(\цифры_6_out_2 ), .col1(\цифры_6_out_3 ), .col2(\цифры_6_out_4 ), .col3(\цифры_6_out_5 ),
    .col4(\цифры_6_out_6 ), .col5(\цифры_6_out_7 ), .col6(\цифры_6_out_8 ), .col7(\цифры_6_out_9 ),
    .col8(\цифры_6_out_10 ), .col9(\цифры_6_out_11 ), .col10(\цифры_6_out_12 ));
  \Цифры  \u_цифры_6  (
    .out_2(\цифры_6_out_2 ), .out_3(\цифры_6_out_3 ), .out_4(\цифры_6_out_4 ), .out_5(\цифры_6_out_5 ),
    .out_6(\цифры_6_out_6 ), .out_7(\цифры_6_out_7 ), .out_8(\цифры_6_out_8 ), .out_9(\цифры_6_out_9 ),
    .out_10(\цифры_6_out_10 ), .out_11(\цифры_6_out_11 ), .out_12(\цифры_6_out_12 ));  // open: Energy
  DotMatrix #(.matrixcols(11), .matrixrows(8)) dotmatrix_19 (
    .col0(\чья_тип_5_out_14 ), .col1(\чья_тип_5_out_15 ), .col2(\чья_тип_5_out_16 ),
    .col3(\чья_тип_5_out_17 ), .col4(\чья_тип_5_out_18 ), .col5(\чья_тип_5_out_19 ),
    .col6(\чья_тип_5_out_20 ), .col7(\чья_тип_5_out_21 ), .col8(\чья_тип_5_out_22 ),
    .col9(\чья_тип_5_out_23 ), .col10(\чья_тип_5_out_24 ));
  \Чья_Тип  \u_чья_тип_5  (
    .in_1(in_5), .in_2(in_7), .out_14(\чья_тип_5_out_14 ), .out_15(\чья_тип_5_out_15 ),
    .out_16(\чья_тип_5_out_16 ), .out_17(\чья_тип_5_out_17 ), .out_18(\чья_тип_5_out_18 ),
    .out_19(\чья_тип_5_out_19 ), .out_20(\чья_тип_5_out_20 ), .out_21(\чья_тип_5_out_21 ),
    .out_22(\чья_тип_5_out_22 ), .out_23(\чья_тип_5_out_23 ), .out_24(\чья_тип_5_out_24 ),
    .out_3(\чья_тип_5_out_3 ), .out_4(\чья_тип_5_out_4 ), .out_5(\чья_тип_5_out_5 ),
    .out_6(\чья_тип_5_out_6 ), .out_7(\чья_тип_5_out_7 ), .out_8(\чья_тип_5_out_8 ),
    .out_9(\чья_тип_5_out_9 ), .out_10(\чья_тип_5_out_10 ), .out_11(\чья_тип_5_out_11 ),
    .out_12(\чья_тип_5_out_12 ), .out_13(\чья_тип_5_out_13 ));
  DotMatrix #(.matrixcols(11), .matrixrows(8)) dotmatrix_20 (
    .col0(\чья_тип_5_out_3 ), .col1(\чья_тип_5_out_4 ), .col2(\чья_тип_5_out_5 ), .col3(\чья_тип_5_out_6 ),
    .col4(\чья_тип_5_out_7 ), .col5(\чья_тип_5_out_8 ), .col6(\чья_тип_5_out_9 ), .col7(\чья_тип_5_out_10 ),
    .col8(\чья_тип_5_out_11 ), .col9(\чья_тип_5_out_12 ), .col10(\чья_тип_5_out_13 ));
  DotMatrix #(.matrixcols(11), .matrixrows(5)) dotmatrix_21 (
    .col0(\цифры_7_out_2 ), .col1(\цифры_7_out_3 ), .col2(\цифры_7_out_4 ), .col3(\цифры_7_out_5 ),
    .col4(\цифры_7_out_6 ), .col5(\цифры_7_out_7 ), .col6(\цифры_7_out_8 ), .col7(\цифры_7_out_9 ),
    .col8(\цифры_7_out_10 ), .col9(\цифры_7_out_11 ), .col10(\цифры_7_out_12 ));
  \Цифры  \u_цифры_7  (
    .out_2(\цифры_7_out_2 ), .out_3(\цифры_7_out_3 ), .out_4(\цифры_7_out_4 ), .out_5(\цифры_7_out_5 ),
    .out_6(\цифры_7_out_6 ), .out_7(\цифры_7_out_7 ), .out_8(\цифры_7_out_8 ), .out_9(\цифры_7_out_9 ),
    .out_10(\цифры_7_out_10 ), .out_11(\цифры_7_out_11 ), .out_12(\цифры_7_out_12 ));  // open: Energy
  DotMatrix #(.matrixcols(11), .matrixrows(8)) dotmatrix_22 (
    .col0(\чья_тип_6_p3 ), .col1(\чья_тип_6_p4 ), .col2(\чья_тип_6_p5 ), .col3(\чья_тип_6_p6 ),
    .col4(\чья_тип_6_p7 ), .col5(\чья_тип_6_p8 ), .col6(\чья_тип_6_p9 ), .col7(\чья_тип_6_p10 ),
    .col8(\чья_тип_6_p11 ), .col9(\чья_тип_6_p12 ), .col10(\чья_тип_6_p13 ));
  // Чья_Тип чья_тип_6: pin names not known; wires that end beside it: in_14, in_18, \чья_тип_6_p3 , \чья_тип_6_p4 , \чья_тип_6_p5 , \чья_тип_6_p6 , \чья_тип_6_p7 , \чья_тип_6_p8 , \чья_тип_6_p9 , \чья_тип_6_p10 , \чья_тип_6_p11 , \чья_тип_6_p12 , \чья_тип_6_p13 , in_15, in_19
  // DotMatrix #(.matrixcols(11), .matrixrows(8)) dotmatrix_23: pin names not known; wires that end beside it: in_14, in_18
  DotMatrix #(.matrixcols(11), .matrixrows(5)) dotmatrix_24 (
    .col0(\цифры_8_out_2 ), .col1(\цифры_8_out_3 ), .col2(\цифры_8_out_4 ), .col3(\цифры_8_out_5 ),
    .col4(\цифры_8_out_6 ), .col5(\цифры_8_out_7 ), .col6(\цифры_8_out_8 ), .col7(\цифры_8_out_9 ),
    .col8(\цифры_8_out_10 ), .col9(\цифры_8_out_11 ), .col10(\цифры_8_out_12 ));
  \Цифры  \u_цифры_8  (
    .out_2(\цифры_8_out_2 ), .out_3(\цифры_8_out_3 ), .out_4(\цифры_8_out_4 ), .out_5(\цифры_8_out_5 ),
    .out_6(\цифры_8_out_6 ), .out_7(\цифры_8_out_7 ), .out_8(\цифры_8_out_8 ), .out_9(\цифры_8_out_9 ),
    .out_10(\цифры_8_out_10 ), .out_11(\цифры_8_out_11 ), .out_12(\цифры_8_out_12 ));  // open: Energy
  DotMatrix #(.matrixcols(11), .matrixrows(8)) dotmatrix_25 (
    .col0(\чья_тип_7_p3 ), .col1(\чья_тип_7_p4 ), .col2(\чья_тип_7_p5 ), .col3(\чья_тип_7_p6 ),
    .col4(\чья_тип_7_p7 ), .col5(\чья_тип_7_p8 ), .col6(\чья_тип_7_p9 ), .col7(\чья_тип_7_p10 ),
    .col8(\чья_тип_7_p11 ), .col9(\чья_тип_7_p12 ), .col10(\чья_тип_7_p13 ));
  // Чья_Тип чья_тип_7: pin names not known; wires that end beside it: in_28, in_32, \чья_тип_7_p3 , \чья_тип_7_p4 , \чья_тип_7_p5 , \чья_тип_7_p6 , \чья_тип_7_p7 , \чья_тип_7_p8 , \чья_тип_7_p9 , \чья_тип_7_p10 , \чья_тип_7_p11 , \чья_тип_7_p12 , \чья_тип_7_p13 , in_25, in_29
  // DotMatrix #(.matrixcols(11), .matrixrows(8)) dotmatrix_26: pin names not known; wires that end beside it: in_28, in_32
  DotMatrix #(.matrixcols(11), .matrixrows(5)) dotmatrix_27 (
    .col0(\цифры_9_out_2 ), .col1(\цифры_9_out_3 ), .col2(\цифры_9_out_4 ), .col3(\цифры_9_out_5 ),
    .col4(\цифры_9_out_6 ), .col5(\цифры_9_out_7 ), .col6(\цифры_9_out_8 ), .col7(\цифры_9_out_9 ),
    .col8(\цифры_9_out_10 ), .col9(\цифры_9_out_11 ), .col10(\цифры_9_out_12 ));
  \Цифры  \u_цифры_9  (
    .out_2(\цифры_9_out_2 ), .out_3(\цифры_9_out_3 ), .out_4(\цифры_9_out_4 ), .out_5(\цифры_9_out_5 ),
    .out_6(\цифры_9_out_6 ), .out_7(\цифры_9_out_7 ), .out_8(\цифры_9_out_8 ), .out_9(\цифры_9_out_9 ),
    .out_10(\цифры_9_out_10 ), .out_11(\цифры_9_out_11 ), .out_12(\цифры_9_out_12 ));  // open: Energy
  // Чья_Тип чья_тип_8: pin names not known; wires that end beside it: in_40, in_44, \чья_тип_8_p3 , \чья_тип_8_p4 , \чья_тип_8_p5 , \чья_тип_8_p6 , \чья_тип_8_p7 , \чья_тип_8_p8 , \чья_тип_8_p9 , \чья_тип_8_p10 , \чья_тип_8_p11 , \чья_тип_8_p12 , \чья_тип_8_p13 , in_37, in_41
  DotMatrix #(.matrixcols(11), .matrixrows(8)) dotmatrix_28 (
    .col0(\чья_тип_8_p3 ), .col1(\чья_тип_8_p4 ), .col2(\чья_тип_8_p5 ), .col3(\чья_тип_8_p6 ),
    .col4(\чья_тип_8_p7 ), .col5(\чья_тип_8_p8 ), .col6(\чья_тип_8_p9 ), .col7(\чья_тип_8_p10 ),
    .col8(\чья_тип_8_p11 ), .col9(\чья_тип_8_p12 ), .col10(\чья_тип_8_p13 ));
  // DotMatrix #(.matrixcols(11), .matrixrows(8)) dotmatrix_29: pin names not known; wires that end beside it: in_40, in_44
  \Цифры  \u_цифры_10  (
    .out_2(\цифры_10_out_2 ), .out_3(\цифры_10_out_3 ), .out_4(\цифры_10_out_4 ), .out_5(\цифры_10_out_5 ),
    .out_6(\цифры_10_out_6 ), .out_7(\цифры_10_out_7 ), .out_8(\цифры_10_out_8 ), .out_9(\цифры_10_out_9 ),
    .out_10(\цифры_10_out_10 ), .out_11(\цифры_10_out_11 ), .out_12(\цифры_10_out_12 ));  // open: Energy
  DotMatrix #(.matrixcols(11), .matrixrows(5)) dotmatrix_30 (
    .col0(\цифры_10_out_2 ), .col1(\цифры_10_out_3 ), .col2(\цифры_10_out_4 ), .col3(\цифры_10_out_5 ),
    .col4(\цифры_10_out_6 ), .col5(\цифры_10_out_7 ), .col6(\цифры_10_out_8 ), .col7(\цифры_10_out_9 ),
    .col8(\цифры_10_out_10 ), .col9(\цифры_10_out_11 ), .col10(\цифры_10_out_12 ));
  DotMatrix #(.matrixcols(11), .matrixrows(8)) dotmatrix_31 (
    .col0(\чья_тип_9_p3 ), .col1(\чья_тип_9_p4 ), .col2(\чья_тип_9_p5 ), .col3(\чья_тип_9_p6 ),
    .col4(\чья_тип_9_p7 ), .col5(\чья_тип_9_p8 ), .col6(\чья_тип_9_p9 ), .col7(\чья_тип_9_p10 ),
    .col8(\чья_тип_9_p11 ), .col9(\чья_тип_9_p12 ), .col10(\чья_тип_9_p13 ));
  // Чья_Тип чья_тип_9: pin names not known; wires that end beside it: in_50, in_54, \чья_тип_9_p3 , \чья_тип_9_p4 , \чья_тип_9_p5 , \чья_тип_9_p6 , \чья_тип_9_p7 , \чья_тип_9_p8 , \чья_тип_9_p9 , \чья_тип_9_p10 , \чья_тип_9_p11 , \чья_тип_9_p12 , \чья_тип_9_p13 , in_51, in_55
  // DotMatrix #(.matrixcols(11), .matrixrows(8)) dotmatrix_32: pin names not known; wires that end beside it: in_50, in_54
  DotMatrix #(.matrixcols(11), .matrixrows(5)) dotmatrix_33 (
    .col0(\цифры_11_out_2 ), .col1(\цифры_11_out_3 ), .col2(\цифры_11_out_4 ), .col3(\цифры_11_out_5 ),
    .col4(\цифры_11_out_6 ), .col5(\цифры_11_out_7 ), .col6(\цифры_11_out_8 ), .col7(\цифры_11_out_9 ),
    .col8(\цифры_11_out_10 ), .col9(\цифры_11_out_11 ), .col10(\цифры_11_out_12 ));
  \Цифры  \u_цифры_11  (
    .out_2(\цифры_11_out_2 ), .out_3(\цифры_11_out_3 ), .out_4(\цифры_11_out_4 ), .out_5(\цифры_11_out_5 ),
    .out_6(\цифры_11_out_6 ), .out_7(\цифры_11_out_7 ), .out_8(\цифры_11_out_8 ), .out_9(\цифры_11_out_9 ),
    .out_10(\цифры_11_out_10 ), .out_11(\цифры_11_out_11 ), .out_12(\цифры_11_out_12 ));  // open: Energy
  DotMatrix #(.matrixcols(11), .matrixrows(8)) dotmatrix_34 (
    .col0(\чья_тип_10_p3 ), .col1(\чья_тип_10_p4 ), .col2(\чья_тип_10_p5 ), .col3(\чья_тип_10_p6 ),
    .col4(\чья_тип_10_p7 ), .col5(\чья_тип_10_p8 ), .col6(\чья_тип_10_p9 ), .col7(\чья_тип_10_p10 ),
    .col8(\чья_тип_10_p11 ), .col9(\чья_тип_10_p12 ), .col10(\чья_тип_10_p13 ));
  // Чья_Тип чья_тип_10: pin names not known; wires that end beside it: in_15, in_19, \чья_тип_10_p3 , \чья_тип_10_p4 , \чья_тип_10_p5 , \чья_тип_10_p6 , \чья_тип_10_p7 , \чья_тип_10_p8 , \чья_тип_10_p9 , \чья_тип_10_p10 , \чья_тип_10_p11 , \чья_тип_10_p12 , \чья_тип_10_p13 , in_16, in_20
  // DotMatrix #(.matrixcols(11), .matrixrows(8)) dotmatrix_35: pin names not known; wires that end beside it: in_15, in_19
  DotMatrix #(.matrixcols(11), .matrixrows(5)) dotmatrix_36 (
    .col0(\цифры_12_out_2 ), .col1(\цифры_12_out_3 ), .col2(\цифры_12_out_4 ), .col3(\цифры_12_out_5 ),
    .col4(\цифры_12_out_6 ), .col5(\цифры_12_out_7 ), .col6(\цифры_12_out_8 ), .col7(\цифры_12_out_9 ),
    .col8(\цифры_12_out_10 ), .col9(\цифры_12_out_11 ), .col10(\цифры_12_out_12 ));
  \Цифры  \u_цифры_12  (
    .out_2(\цифры_12_out_2 ), .out_3(\цифры_12_out_3 ), .out_4(\цифры_12_out_4 ), .out_5(\цифры_12_out_5 ),
    .out_6(\цифры_12_out_6 ), .out_7(\цифры_12_out_7 ), .out_8(\цифры_12_out_8 ), .out_9(\цифры_12_out_9 ),
    .out_10(\цифры_12_out_10 ), .out_11(\цифры_12_out_11 ), .out_12(\цифры_12_out_12 ));  // open: Energy
  // Чья_Тип чья_тип_11: pin names not known; wires that end beside it: in_25, in_29, \чья_тип_11_p3 , \чья_тип_11_p4 , \чья_тип_11_p5 , \чья_тип_11_p6 , \чья_тип_11_p7 , \чья_тип_11_p8 , \чья_тип_11_p9 , \чья_тип_11_p10 , \чья_тип_11_p11 , \чья_тип_11_p12 , \чья_тип_11_p13 , in_26, in_30
  DotMatrix #(.matrixcols(11), .matrixrows(8)) dotmatrix_37 (
    .col0(\чья_тип_11_p3 ), .col1(\чья_тип_11_p4 ), .col2(\чья_тип_11_p5 ), .col3(\чья_тип_11_p6 ),
    .col4(\чья_тип_11_p7 ), .col5(\чья_тип_11_p8 ), .col6(\чья_тип_11_p9 ), .col7(\чья_тип_11_p10 ),
    .col8(\чья_тип_11_p11 ), .col9(\чья_тип_11_p12 ), .col10(\чья_тип_11_p13 ));
  // DotMatrix #(.matrixcols(11), .matrixrows(8)) dotmatrix_38: pin names not known; wires that end beside it: in_25, in_29
  DotMatrix #(.matrixcols(11), .matrixrows(5)) dotmatrix_39 (
    .col0(\цифры_13_out_2 ), .col1(\цифры_13_out_3 ), .col2(\цифры_13_out_4 ), .col3(\цифры_13_out_5 ),
    .col4(\цифры_13_out_6 ), .col5(\цифры_13_out_7 ), .col6(\цифры_13_out_8 ), .col7(\цифры_13_out_9 ),
    .col8(\цифры_13_out_10 ), .col9(\цифры_13_out_11 ), .col10(\цифры_13_out_12 ));
  \Цифры  \u_цифры_13  (
    .out_2(\цифры_13_out_2 ), .out_3(\цифры_13_out_3 ), .out_4(\цифры_13_out_4 ), .out_5(\цифры_13_out_5 ),
    .out_6(\цифры_13_out_6 ), .out_7(\цифры_13_out_7 ), .out_8(\цифры_13_out_8 ), .out_9(\цифры_13_out_9 ),
    .out_10(\цифры_13_out_10 ), .out_11(\цифры_13_out_11 ), .out_12(\цифры_13_out_12 ));  // open: Energy
  DotMatrix #(.matrixcols(11), .matrixrows(8)) dotmatrix_40 (
    .col0(\чья_тип_12_p3 ), .col1(\чья_тип_12_p4 ), .col2(\чья_тип_12_p5 ), .col3(\чья_тип_12_p6 ),
    .col4(\чья_тип_12_p7 ), .col5(\чья_тип_12_p8 ), .col6(\чья_тип_12_p9 ), .col7(\чья_тип_12_p10 ),
    .col8(\чья_тип_12_p11 ), .col9(\чья_тип_12_p12 ), .col10(\чья_тип_12_p13 ));
  // Чья_Тип чья_тип_12: pin names not known; wires that end beside it: in_37, in_41, \чья_тип_12_p3 , \чья_тип_12_p4 , \чья_тип_12_p5 , \чья_тип_12_p6 , \чья_тип_12_p7 , \чья_тип_12_p8 , \чья_тип_12_p9 , \чья_тип_12_p10 , \чья_тип_12_p11 , \чья_тип_12_p12 , \чья_тип_12_p13 , in_38, in_42
  // DotMatrix #(.matrixcols(11), .matrixrows(8)) dotmatrix_41: pin names not known; wires that end beside it: in_37, in_41
  \Цифры  \u_цифры_14  (
    .out_2(\цифры_14_out_2 ), .out_3(\цифры_14_out_3 ), .out_4(\цифры_14_out_4 ), .out_5(\цифры_14_out_5 ),
    .out_6(\цифры_14_out_6 ), .out_7(\цифры_14_out_7 ), .out_8(\цифры_14_out_8 ), .out_9(\цифры_14_out_9 ),
    .out_10(\цифры_14_out_10 ), .out_11(\цифры_14_out_11 ), .out_12(\цифры_14_out_12 ));  // open: Energy
  DotMatrix #(.matrixcols(11), .matrixrows(5)) dotmatrix_42 (
    .col0(\цифры_14_out_2 ), .col1(\цифры_14_out_3 ), .col2(\цифры_14_out_4 ), .col3(\цифры_14_out_5 ),
    .col4(\цифры_14_out_6 ), .col5(\цифры_14_out_7 ), .col6(\цифры_14_out_8 ), .col7(\цифры_14_out_9 ),
    .col8(\цифры_14_out_10 ), .col9(\цифры_14_out_11 ), .col10(\цифры_14_out_12 ));
  // Чья_Тип чья_тип_13: pin names not known; wires that end beside it: in_51, in_55, \чья_тип_13_p3 , \чья_тип_13_p4 , \чья_тип_13_p5 , \чья_тип_13_p6 , \чья_тип_13_p7 , \чья_тип_13_p8 , \чья_тип_13_p9 , \чья_тип_13_p10 , \чья_тип_13_p11 , \чья_тип_13_p12 , \чья_тип_13_p13 , in_52, in_56
  DotMatrix #(.matrixcols(11), .matrixrows(8)) dotmatrix_43 (
    .col0(\чья_тип_13_p3 ), .col1(\чья_тип_13_p4 ), .col2(\чья_тип_13_p5 ), .col3(\чья_тип_13_p6 ),
    .col4(\чья_тип_13_p7 ), .col5(\чья_тип_13_p8 ), .col6(\чья_тип_13_p9 ), .col7(\чья_тип_13_p10 ),
    .col8(\чья_тип_13_p11 ), .col9(\чья_тип_13_p12 ), .col10(\чья_тип_13_p13 ));
  // DotMatrix #(.matrixcols(11), .matrixrows(8)) dotmatrix_44: pin names not known; wires that end beside it: in_51, in_55
  \Цифры  \u_цифры_15  (
    .out_2(\цифры_15_out_2 ), .out_3(\цифры_15_out_3 ), .out_4(\цифры_15_out_4 ), .out_5(\цифры_15_out_5 ),
    .out_6(\цифры_15_out_6 ), .out_7(\цифры_15_out_7 ), .out_8(\цифры_15_out_8 ), .out_9(\цифры_15_out_9 ),
    .out_10(\цифры_15_out_10 ), .out_11(\цифры_15_out_11 ), .out_12(\цифры_15_out_12 ));  // open: Energy
  DotMatrix #(.matrixcols(11), .matrixrows(5)) dotmatrix_45 (
    .col0(\цифры_15_out_2 ), .col1(\цифры_15_out_3 ), .col2(\цифры_15_out_4 ), .col3(\цифры_15_out_5 ),
    .col4(\цифры_15_out_6 ), .col5(\цифры_15_out_7 ), .col6(\цифры_15_out_8 ), .col7(\цифры_15_out_9 ),
    .col8(\цифры_15_out_10 ), .col9(\цифры_15_out_11 ), .col10(\цифры_15_out_12 ));
  // Чья_Тип чья_тип_14: pin names not known; wires that end beside it: in_16, in_20, \чья_тип_14_p3 , \чья_тип_14_p4 , \чья_тип_14_p5 , \чья_тип_14_p6 , \чья_тип_14_p7 , \чья_тип_14_p8 , \чья_тип_14_p9 , \чья_тип_14_p10 , \чья_тип_14_p11 , \чья_тип_14_p12 , \чья_тип_14_p13 
  DotMatrix #(.matrixcols(11), .matrixrows(8)) dotmatrix_46 (
    .col0(\чья_тип_14_p3 ), .col1(\чья_тип_14_p4 ), .col2(\чья_тип_14_p5 ), .col3(\чья_тип_14_p6 ),
    .col4(\чья_тип_14_p7 ), .col5(\чья_тип_14_p8 ), .col6(\чья_тип_14_p9 ), .col7(\чья_тип_14_p10 ),
    .col8(\чья_тип_14_p11 ), .col9(\чья_тип_14_p12 ), .col10(\чья_тип_14_p13 ));
  // DotMatrix #(.matrixcols(11), .matrixrows(8)) dotmatrix_47: pin names not known; wires that end beside it: in_16, in_20
  \Цифры  \u_цифры_16  (
    .out_2(\цифры_16_out_2 ), .out_3(\цифры_16_out_3 ), .out_4(\цифры_16_out_4 ), .out_5(\цифры_16_out_5 ),
    .out_6(\цифры_16_out_6 ), .out_7(\цифры_16_out_7 ), .out_8(\цифры_16_out_8 ), .out_9(\цифры_16_out_9 ),
    .out_10(\цифры_16_out_10 ), .out_11(\цифры_16_out_11 ), .out_12(\цифры_16_out_12 ));  // open: Energy
  DotMatrix #(.matrixcols(11), .matrixrows(5)) dotmatrix_48 (
    .col0(\цифры_16_out_2 ), .col1(\цифры_16_out_3 ), .col2(\цифры_16_out_4 ), .col3(\цифры_16_out_5 ),
    .col4(\цифры_16_out_6 ), .col5(\цифры_16_out_7 ), .col6(\цифры_16_out_8 ), .col7(\цифры_16_out_9 ),
    .col8(\цифры_16_out_10 ), .col9(\цифры_16_out_11 ), .col10(\цифры_16_out_12 ));
  // Чья_Тип чья_тип_15: pin names not known; wires that end beside it: in_26, in_30, \чья_тип_15_p3 , \чья_тип_15_p4 , \чья_тип_15_p5 , \чья_тип_15_p6 , \чья_тип_15_p7 , \чья_тип_15_p8 , \чья_тип_15_p9 , \чья_тип_15_p10 , \чья_тип_15_p11 , \чья_тип_15_p12 , \чья_тип_15_p13 
  DotMatrix #(.matrixcols(11), .matrixrows(8)) dotmatrix_49 (
    .col0(\чья_тип_15_p3 ), .col1(\чья_тип_15_p4 ), .col2(\чья_тип_15_p5 ), .col3(\чья_тип_15_p6 ),
    .col4(\чья_тип_15_p7 ), .col5(\чья_тип_15_p8 ), .col6(\чья_тип_15_p9 ), .col7(\чья_тип_15_p10 ),
    .col8(\чья_тип_15_p11 ), .col9(\чья_тип_15_p12 ), .col10(\чья_тип_15_p13 ));
  // DotMatrix #(.matrixcols(11), .matrixrows(8)) dotmatrix_50: pin names not known; wires that end beside it: in_26, in_30
  \Цифры  \u_цифры_17  (
    .out_2(\цифры_17_out_2 ), .out_3(\цифры_17_out_3 ), .out_4(\цифры_17_out_4 ), .out_5(\цифры_17_out_5 ),
    .out_6(\цифры_17_out_6 ), .out_7(\цифры_17_out_7 ), .out_8(\цифры_17_out_8 ), .out_9(\цифры_17_out_9 ),
    .out_10(\цифры_17_out_10 ), .out_11(\цифры_17_out_11 ), .out_12(\цифры_17_out_12 ));  // open: Energy
  DotMatrix #(.matrixcols(11), .matrixrows(5)) dotmatrix_51 (
    .col0(\цифры_17_out_2 ), .col1(\цифры_17_out_3 ), .col2(\цифры_17_out_4 ), .col3(\цифры_17_out_5 ),
    .col4(\цифры_17_out_6 ), .col5(\цифры_17_out_7 ), .col6(\цифры_17_out_8 ), .col7(\цифры_17_out_9 ),
    .col8(\цифры_17_out_10 ), .col9(\цифры_17_out_11 ), .col10(\цифры_17_out_12 ));
  // Чья_Тип чья_тип_16: pin names not known; wires that end beside it: in_38, in_42, \чья_тип_16_p3 , \чья_тип_16_p4 , \чья_тип_16_p5 , \чья_тип_16_p6 , \чья_тип_16_p7 , \чья_тип_16_p8 , \чья_тип_16_p9 , \чья_тип_16_p10 , \чья_тип_16_p11 , \чья_тип_16_p12 , \чья_тип_16_p13 
  DotMatrix #(.matrixcols(11), .matrixrows(8)) dotmatrix_52 (
    .col0(\чья_тип_16_p3 ), .col1(\чья_тип_16_p4 ), .col2(\чья_тип_16_p5 ), .col3(\чья_тип_16_p6 ),
    .col4(\чья_тип_16_p7 ), .col5(\чья_тип_16_p8 ), .col6(\чья_тип_16_p9 ), .col7(\чья_тип_16_p10 ),
    .col8(\чья_тип_16_p11 ), .col9(\чья_тип_16_p12 ), .col10(\чья_тип_16_p13 ));
  // DotMatrix #(.matrixcols(11), .matrixrows(8)) dotmatrix_53: pin names not known; wires that end beside it: in_38, in_42
  DotMatrix #(.matrixcols(11), .matrixrows(5)) dotmatrix_54 (
    .col0(\цифры_18_out_2 ), .col1(\цифры_18_out_3 ), .col2(\цифры_18_out_4 ), .col3(\цифры_18_out_5 ),
    .col4(\цифры_18_out_6 ), .col5(\цифры_18_out_7 ), .col6(\цифры_18_out_8 ), .col7(\цифры_18_out_9 ),
    .col8(\цифры_18_out_10 ), .col9(\цифры_18_out_11 ), .col10(\цифры_18_out_12 ));
  \Цифры  \u_цифры_18  (
    .out_2(\цифры_18_out_2 ), .out_3(\цифры_18_out_3 ), .out_4(\цифры_18_out_4 ), .out_5(\цифры_18_out_5 ),
    .out_6(\цифры_18_out_6 ), .out_7(\цифры_18_out_7 ), .out_8(\цифры_18_out_8 ), .out_9(\цифры_18_out_9 ),
    .out_10(\цифры_18_out_10 ), .out_11(\цифры_18_out_11 ), .out_12(\цифры_18_out_12 ));  // open: Energy
  DotMatrix #(.matrixcols(11), .matrixrows(8)) dotmatrix_55 (
    .col0(\чья_тип_17_p3 ), .col1(\чья_тип_17_p4 ), .col2(\чья_тип_17_p5 ), .col3(\чья_тип_17_p6 ),
    .col4(\чья_тип_17_p7 ), .col5(\чья_тип_17_p8 ), .col6(\чья_тип_17_p9 ), .col7(\чья_тип_17_p10 ),
    .col8(\чья_тип_17_p11 ), .col9(\чья_тип_17_p12 ), .col10(\чья_тип_17_p13 ));
  // Чья_Тип чья_тип_17: pin names not known; wires that end beside it: in_52, in_56, \чья_тип_17_p3 , \чья_тип_17_p4 , \чья_тип_17_p5 , \чья_тип_17_p6 , \чья_тип_17_p7 , \чья_тип_17_p8 , \чья_тип_17_p9 , \чья_тип_17_p10 , \чья_тип_17_p11 , \чья_тип_17_p12 , \чья_тип_17_p13 
  // DotMatrix #(.matrixcols(11), .matrixrows(8)) dotmatrix_56: pin names not known; wires that end beside it: in_52, in_56
  DotMatrix #(.matrixcols(11), .matrixrows(15)) dotmatrix_57 ();  // open: col0, col1, col2, col3, col4, col5, col6, col7, col8, col9, col10
  DotMatrix #(.matrixcols(11), .matrixrows(15)) dotmatrix_58 ();  // open: col0, col1, col2, col3, col4, col5, col6, col7, col8, col9, col10
  DotMatrix #(.matrixcols(11), .matrixrows(15)) dotmatrix_59 ();  // open: col0, col1, col2, col3, col4, col5, col6, col7, col8, col9, col10
  DotMatrix #(.matrixcols(11), .matrixrows(15)) dotmatrix_60 ();  // open: col0, col1, col2, col3, col4, col5, col6, col7, col8, col9, col10
  DotMatrix #(.matrixcols(11), .matrixrows(5)) dotmatrix_61 ();  // open: col0, col1, col2, col3, col4, col5, col6, col7, col8, col9, col10
  DotMatrix #(.matrixcols(11), .matrixrows(5)) dotmatrix_62 ();  // open: col0, col1, col2, col3, col4, col5, col6, col7, col8, col9, col10
  DotMatrix #(.matrixcols(11), .matrixrows(5)) dotmatrix_63 ();  // open: col0, col1, col2, col3, col4, col5, col6, col7, col8, col9, col10
  DotMatrix #(.matrixcols(11), .matrixrows(5)) dotmatrix_64 ();  // open: col0, col1, col2, col3, col4, col5, col6, col7, col8, col9, col10
  DotMatrix #(.matrixcols(11), .matrixrows(5)) dotmatrix_65 ();  // open: col0, col1, col2, col3, col4, col5, col6, col7, col8, col9, col10
  DotMatrix #(.matrixcols(11), .matrixrows(5)) dotmatrix_66 ();  // open: col0, col1, col2, col3, col4, col5, col6, col7, col8, col9, col10
  DotMatrix #(.matrixcols(11), .matrixrows(15)) dotmatrix_67 ();  // open: col0, col1, col2, col3, col4, col5, col6, col7, col8, col9, col10
  DotMatrix #(.matrixcols(11), .matrixrows(5)) dotmatrix_68 ();  // open: col0, col1, col2, col3, col4, col5, col6, col7, col8, col9, col10
  DotMatrix #(.matrixcols(11), .matrixrows(5)) dotmatrix_69 ();  // open: col0, col1, col2, col3, col4, col5, col6, col7, col8, col9, col10
  DotMatrix #(.matrixcols(11), .matrixrows(5)) dotmatrix_70 ();  // open: col0, col1, col2, col3, col4, col5, col6, col7, col8, col9, col10
  DotMatrix #(.matrixcols(11), .matrixrows(5)) dotmatrix_71 ();  // open: col0, col1, col2, col3, col4, col5, col6, col7, col8, col9, col10
  DotMatrix #(.matrixcols(11), .matrixrows(5)) dotmatrix_72 ();  // open: col0, col1, col2, col3, col4, col5, col6, col7, col8, col9, col10
  DotMatrix #(.matrixcols(11), .matrixrows(5)) dotmatrix_73 ();  // open: col0, col1, col2, col3, col4, col5, col6, col7, col8, col9, col10
  DotMatrix #(.matrixcols(11), .matrixrows(15)) dotmatrix_74 ();  // open: col0, col1, col2, col3, col4, col5, col6, col7, col8, col9, col10
  DotMatrix #(.matrixcols(11), .matrixrows(5)) dotmatrix_75 ();  // open: col0, col1, col2, col3, col4, col5, col6, col7, col8, col9, col10
  DotMatrix #(.matrixcols(11), .matrixrows(5)) dotmatrix_76 ();  // open: col0, col1, col2, col3, col4, col5, col6, col7, col8, col9, col10
  DotMatrix #(.matrixcols(11), .matrixrows(5)) dotmatrix_77 ();  // open: col0, col1, col2, col3, col4, col5, col6, col7, col8, col9, col10
  DotMatrix #(.matrixcols(11), .matrixrows(5)) dotmatrix_78 ();  // open: col0, col1, col2, col3, col4, col5, col6, col7, col8, col9, col10
  DotMatrix #(.matrixcols(11), .matrixrows(5)) dotmatrix_79 ();  // open: col0, col1, col2, col3, col4, col5, col6, col7, col8, col9, col10
  DotMatrix #(.matrixcols(11), .matrixrows(5)) dotmatrix_80 ();  // open: col0, col1, col2, col3, col4, col5, col6, col7, col8, col9, col10

  // Notes on the sheet:
  //   Количество
  //   специальных
  //   клеток
  //   Очки прокачки
  //   Цвет
  //   Количество клеток
  //   Сумма
  //   Генерируется за ход
  //   Введите число
  //   Защитная
  //   Транспортная
  //   Энергетическая
  //   Дополнительная энергия
  //   Статистика
  //   Пусто
  //   Оранжевый
  //   Генератор задания
  //   Синий
endmodule

module \Чей_Ход  (
  input  [1:0] in_1,
  output [7:0] out_2,
  output [7:0] out_3,
  output [7:0] out_4,
  output [7:0] out_5,
  output [7:0] out_6,
  output [7:0] out_7,
  output [7:0] out_8,
  output [7:0] out_9,
  output [7:0] out_10,
  output [7:0] out_11,
  output [7:0] out_12,
  output [7:0] out_13,
  output [7:0] out_14,
  output [7:0] out_15,
  output [7:0] out_16,
  output [7:0] out_17,
  output [7:0] out_18,
  output [7:0] out_19,
  output [7:0] out_20,
  output [7:0] out_21,
  output [7:0] out_22,
  output [7:0] out_23
);

  Transistor #(.width(8)) transistor_1 (.in({8{1'b0}}), .out(out_22), .gate(in_1[1]));
  Transistor #(.width(8)) transistor_2 (.in({8{1'b0}}), .out(out_23), .gate(in_1[1]));
  Transistor #(.width(8)) transistor_3 (.in({8{1'b0}}), .out(out_21), .gate(in_1[1]));
  Transistor #(.\type ("n"), .width(8)) transistor_4 (.in({8{1'b1}}), .out(out_15), .gate(in_1[1]));
  Transistor #(.\type ("n"), .width(8)) transistor_5 (.in({8{1'b1}}), .out(out_14), .gate(in_1[1]));
  Transistor #(.\type ("n"), .width(8)) transistor_6 (.in({8{1'b1}}), .out(out_13), .gate(in_1[1]));
  Transistor #(.width(8)) transistor_7 (.in({8{1'b0}}), .out(out_12), .gate(in_1[0]));
  Transistor #(.width(8)) transistor_8 (.in({8{1'b0}}), .out(out_11), .gate(in_1[0]));
  Transistor #(.\type ("n"), .width(8)) transistor_9 (.in({8{1'b1}}), .out(out_3), .gate(in_1[0]));
  Transistor #(.\type ("n"), .width(8)) transistor_10 (.in({8{1'b1}}), .out(out_2), .gate(in_1[0]));
  Transistor #(.width(8)) transistor_11 (.in({8{1'b0}}), .out(out_17), .gate(in_1[1]));
  Transistor #(.width(8)) transistor_12 (.in({8{1'b0}}), .out(out_20), .gate(in_1[1]));
  Transistor #(.width(8)) transistor_13 (.in({8{1'b0}}), .out(out_18), .gate(in_1[1]));
  Transistor #(.width(8)) transistor_14 (.in({8{1'b0}}), .out(out_19), .gate(in_1[1]));
  Transistor #(.\type ("n"), .width(8)) transistor_15 (.in({8{1'b1}}), .out(out_16), .gate(in_1[1]));
  Transistor #(.\type ("n"), .width(8)) transistor_16 (.in({8{1'b1}}), .out(out_18), .gate(in_1[1]));
  Transistor #(.\type ("n"), .width(8)) transistor_17 (.in({8{1'b1}}), .out(out_17), .gate(in_1[1]));
  Transistor #(.\type ("n"), .width(8)) transistor_18 (.in({8{1'b1}}), .out(out_19), .gate(in_1[1]));
  Transistor #(.width(8)) transistor_19 (.in({8{1'b0}}), .out(out_7), .gate(in_1[0]));
  Transistor #(.width(8)) transistor_20 (.in({8{1'b0}}), .out(out_9), .gate(in_1[0]));
  Transistor #(.width(8)) transistor_21 (.in({8{1'b0}}), .out(out_10), .gate(in_1[0]));
  Transistor #(.width(8)) transistor_22 (.in({8{1'b0}}), .out(out_8), .gate(in_1[0]));
  Transistor #(.\type ("n"), .width(8)) transistor_23 (.in({8{1'b1}}), .out(out_6), .gate(in_1[0]));
  Transistor #(.\type ("n"), .width(8)) transistor_24 (.in({8{1'b1}}), .out(out_4), .gate(in_1[0]));
  Transistor #(.\type ("n"), .width(8)) transistor_25 (.in({8{1'b1}}), .out(out_7), .gate(in_1[0]));
  Transistor #(.\type ("n"), .width(8)) transistor_26 (.in({8{1'b1}}), .out(out_5), .gate(in_1[0]));
  Transistor #(.width(8)) transistor_27 (.in({8{1'b0}}), .out(out_15), .gate(in_1[1]));
  Transistor #(.width(8)) transistor_28 (.in({8{1'b0}}), .out(out_13), .gate(in_1[1]));
  Transistor #(.width(8)) transistor_29 (.in({8{1'b0}}), .out(out_14), .gate(in_1[1]));
  Transistor #(.width(8)) transistor_30 (.in({8{1'b0}}), .out(out_16), .gate(in_1[1]));
  Transistor #(.\type ("n"), .width(8)) transistor_31 (.in({8{1'b1}}), .out(out_23), .gate(in_1[1]));
  Transistor #(.\type ("n"), .width(8)) transistor_32 (.in({8{1'b1}}), .out(out_20), .gate(in_1[1]));
  Transistor #(.\type ("n"), .width(8)) transistor_33 (.in({8{1'b1}}), .out(out_21), .gate(in_1[1]));
  Transistor #(.\type ("n"), .width(8)) transistor_34 (.in({8{1'b1}}), .out(out_22), .gate(in_1[1]));
  Transistor #(.width(8)) transistor_35 (.in({8{1'b0}}), .out(out_4), .gate(in_1[0]));
  Transistor #(.width(8)) transistor_36 (.in({8{1'b0}}), .out(out_6), .gate(in_1[0]));
  Transistor #(.width(8)) transistor_37 (.in({8{1'b0}}), .out(out_3), .gate(in_1[0]));
  Transistor #(.width(8)) transistor_38 (.in({8{1'b0}}), .out(out_5), .gate(in_1[0]));
  Transistor #(.\type ("n"), .width(8)) transistor_39 (.in({8{1'b1}}), .out(out_10), .gate(in_1[0]));
  Transistor #(.\type ("n"), .width(8)) transistor_40 (.in({8{1'b1}}), .out(out_11), .gate(in_1[0]));
  Transistor #(.\type ("n"), .width(8)) transistor_41 (.in({8{1'b1}}), .out(out_8), .gate(in_1[0]));
  Transistor #(.\type ("n"), .width(8)) transistor_42 (.in({8{1'b1}}), .out(out_9), .gate(in_1[0]));
  Transistor #(.width(8)) transistor_43 (.in({8{1'b0}}), .out(out_2), .gate(in_1[0]));
  Transistor #(.\type ("n"), .width(8)) transistor_44 (.in({8{1'b1}}), .out(out_12), .gate(in_1[0]));
  DotMatrix #(.matrixcols(11), .matrixrows(8)) dotmatrix_1 (
    .col0(out_13), .col1(out_14), .col2(out_15), .col3(out_16), .col4(out_17), .col5(out_18), .col6(out_19),
    .col7(out_20), .col8(out_21), .col9(out_22), .col10(out_23));
  DotMatrix #(.matrixcols(11), .matrixrows(8)) dotmatrix_2 (
    .col0(out_2), .col1(out_3), .col2(out_4), .col3(out_5), .col4(out_6), .col5(out_7), .col6(out_8),
    .col7(out_9), .col8(out_10), .col9(out_11), .col10(out_12));

  // Notes on the sheet:
  //   Оранжевый
  //   Синий
endmodule

module \Тип  (
  input  in_1,
  input  [3:0] in_2,
  output [7:0] out_3,
  output [7:0] out_4,
  output [7:0] out_5,
  output [7:0] out_6,
  output [7:0] out_7,
  output [7:0] out_8,
  output [7:0] out_9,
  output [7:0] out_10,
  output [7:0] out_11,
  output [7:0] out_12,
  output [7:0] out_13
);

  wire and_1_out, and_2_out, decoder_1_out0, decoder_1_out1, decoder_1_out2, decoder_1_out3, decoder_1_out4,
       or_1_out, or_2_out;
  wire [2:2] or_3_out;

  Decoder #(.select(3)) decoder_1 (
    .out0(decoder_1_out0), .out1(decoder_1_out1), .out2(decoder_1_out2), .out3(decoder_1_out3),
    .out4(decoder_1_out4), .sel({or_3_out[2], in_2[1:0]}), .en(or_1_out));  // open: out5, out6, out7
  or or_1 (or_1_out, or_3_out[2], in_1);
  or or_2 (or_2_out, decoder_1_out0, in_2[0], in_2[1], in_2[2], in_2[3]);
  DotMatrix #(.matrixcols(11), .matrixrows(8)) dotmatrix_1 (
    .col0(out_3), .col1(out_4), .col2(out_5), .col3(out_6), .col4(out_7), .col5(out_8), .col6(out_9),
    .col7(out_10), .col8(out_11), .col9(out_12), .col10(out_13));
  Pull_Resistor pull_resistor_1 (.node(decoder_1_out4));
  or or_3 (or_3_out[2], in_2[2], in_2[3]);
  and and_1 (and_1_out, decoder_1_out4, in_2[2]);
  and and_2 (and_2_out, decoder_1_out4, in_2[3]);
  Pull_Resistor pull_resistor_2 (.node(decoder_1_out1));
  Pull_Resistor pull_resistor_3 (.node(decoder_1_out0));
  Pull_Resistor pull_resistor_4 (.node(and_2_out));
  Pull_Resistor pull_resistor_5 (.node(decoder_1_out3));
  Pull_Resistor pull_resistor_6 (.node(and_1_out));
  Pull_Resistor pull_resistor_7 (.node(decoder_1_out2));
  Transistor #(.\type ("n"), .width(8)) transistor_1 (.in({8{1'b1}}), .out(out_3), .gate(decoder_1_out0));
  Transistor #(.\type ("n"), .width(8)) transistor_2 (.in({8{1'b1}}), .out(out_6), .gate(decoder_1_out0));
  Transistor #(.\type ("n"), .width(8)) transistor_3 (.in({8{1'b1}}), .out(out_4), .gate(decoder_1_out0));
  Transistor #(.\type ("n"), .width(8)) transistor_4 (.in({8{1'b1}}), .out(out_5), .gate(decoder_1_out0));
  Transistor #(.\type ("n"), .width(8)) transistor_5 (.in({8{1'b1}}), .out(out_7), .gate(decoder_1_out0));
  Transistor #(.\type ("n"), .width(8)) transistor_6 (.in({8{1'b1}}), .out(out_8), .gate(decoder_1_out0));
  Transistor #(.\type ("n"), .width(8)) transistor_7 (.in({8{1'b1}}), .out(out_10), .gate(decoder_1_out0));
  Transistor #(.\type ("n"), .width(8)) transistor_8 (.in({8{1'b1}}), .out(out_9), .gate(decoder_1_out0));
  Transistor #(.\type ("n"), .width(8)) transistor_9 (.in({8{1'b1}}), .out(out_11), .gate(decoder_1_out0));
  Transistor #(.\type ("n"), .width(8)) transistor_10 (.in({8{1'b1}}), .out(out_13), .gate(decoder_1_out0));
  Transistor #(.\type ("n"), .width(8)) transistor_11 (.in({8{1'b1}}), .out(out_12), .gate(decoder_1_out0));
  Transistor #(.\type ("n"), .width(8)) transistor_12 (.in(8'he7), .out(out_4), .gate(decoder_1_out1));
  Transistor #(.\type ("n"), .width(8)) transistor_13 (.in(8'he7), .out(out_3), .gate(decoder_1_out1));
  Transistor #(.\type ("n"), .width(8)) transistor_14 (.in(8'he7), .out(out_5), .gate(decoder_1_out1));
  Transistor #(.\type ("n"), .width(8)) transistor_15 (.in(8'he7), .out(out_6), .gate(decoder_1_out1));
  Transistor #(.\type ("n"), .width(8)) transistor_16 (.in(8'he7), .out(out_10), .gate(decoder_1_out1));
  Transistor #(.\type ("n"), .width(8)) transistor_17 (.in({8{1'b0}}), .out(out_7), .gate(decoder_1_out1));
  Transistor #(.\type ("n"), .width(8)) transistor_18 (.in({8{1'b0}}), .out(out_9), .gate(decoder_1_out1));
  Transistor #(.\type ("n"), .width(8)) transistor_19 (.in({8{1'b0}}), .out(out_8), .gate(decoder_1_out1));
  Transistor #(.\type ("n"), .width(8)) transistor_20 (.in(8'he7), .out(out_13), .gate(decoder_1_out1));
  Transistor #(.\type ("n"), .width(8)) transistor_21 (.in(8'he7), .out(out_11), .gate(decoder_1_out1));
  Transistor #(.\type ("n"), .width(8)) transistor_22 (.in(8'he7), .out(out_12), .gate(decoder_1_out1));
  Transistor #(.\type ("n"), .width(8)) transistor_23 (.in(8'h6c), .out(out_6), .gate(decoder_1_out2));
  Transistor #(.\type ("n"), .width(8)) transistor_24 (.in({8{1'b0}}), .out(out_4), .gate(decoder_1_out2));
  Transistor #(.\type ("n"), .width(8)) transistor_25 (.in({8{1'b1}}), .out(out_3), .gate(decoder_1_out2));
  Transistor #(.\type ("n"), .width(8)) transistor_26 (.in(8'hf8), .out(out_5), .gate(decoder_1_out2));
  Transistor #(.\type ("n"), .width(8)) transistor_27 (.in(8'h6c), .out(out_10), .gate(decoder_1_out2));
  Transistor #(.\type ("n"), .width(8)) transistor_28 (.in(8'h56), .out(out_9), .gate(decoder_1_out2));
  Transistor #(.\type ("n"), .width(8)) transistor_29 (.in(8'hd3), .out(out_8), .gate(decoder_1_out2));
  Transistor #(.\type ("n"), .width(8)) transistor_30 (.in(8'h56), .out(out_7), .gate(decoder_1_out2));
  Transistor #(.\type ("n"), .width(8)) transistor_31 (.in({8{1'b1}}), .out(out_13), .gate(decoder_1_out2));
  Transistor #(.\type ("n"), .width(8)) transistor_32 (.in({8{1'b0}}), .out(out_12), .gate(decoder_1_out2));
  Transistor #(.\type ("n"), .width(8)) transistor_33 (.in(8'hf8), .out(out_11), .gate(decoder_1_out2));
  Transistor #(.\type ("n"), .width(8)) transistor_34 (.in({8{1'b0}}), .out(out_4), .gate(decoder_1_out3));
  Transistor #(.\type ("n"), .width(8)) transistor_35 (.in(8'h91), .out(out_3), .gate(decoder_1_out3));
  Transistor #(.\type ("n"), .width(8)) transistor_36 (.in(8'h18), .out(out_6), .gate(decoder_1_out3));
  Transistor #(.\type ("n"), .width(8)) transistor_37 (.in(8'h4a), .out(out_5), .gate(decoder_1_out3));
  Transistor #(.\type ("n"), .width(8)) transistor_38 (.in(8'h6b), .out(out_8), .gate(decoder_1_out3));
  Transistor #(.\type ("n"), .width(8)) transistor_39 (.in(8'h39), .out(out_7), .gate(decoder_1_out3));
  Transistor #(.\type ("n"), .width(8)) transistor_40 (.in(8'h29), .out(out_11), .gate(decoder_1_out3));
  Transistor #(.\type ("n"), .width(8)) transistor_41 (.in(8'hce), .out(out_9), .gate(decoder_1_out3));
  Transistor #(.\type ("n"), .width(8)) transistor_42 (.in(8'h80), .out(out_12), .gate(decoder_1_out3));
  Transistor #(.\type ("n"), .width(8)) transistor_43 (.in(8'hc), .out(out_10), .gate(decoder_1_out3));
  Transistor #(.\type ("n"), .width(8)) transistor_44 (.in(8'h12), .out(out_13), .gate(decoder_1_out3));
  Transistor #(.\type ("n"), .width(8)) transistor_45 (.in(8'hc0), .out(out_3), .gate(and_1_out));
  Transistor #(.\type ("n"), .width(8)) transistor_46 (.in(8'hc0), .out(out_4), .gate(and_1_out));
  Transistor #(.\type ("n"), .width(8)) transistor_47 (.in(8'hc0), .out(out_5), .gate(and_1_out));
  Transistor #(.\type ("n"), .width(8)) transistor_48 (.in(8'hc0), .out(out_7), .gate(and_1_out));
  Transistor #(.\type ("n"), .width(8)) transistor_49 (.in(8'hc0), .out(out_8), .gate(and_1_out));
  Transistor #(.\type ("n"), .width(8)) transistor_50 (.in(8'hc0), .out(out_6), .gate(and_1_out));
  Transistor #(.\type ("n"), .width(8)) transistor_51 (.in(8'hc0), .out(out_10), .gate(and_1_out));
  Transistor #(.\type ("n"), .width(8)) transistor_52 (.in(8'hc0), .out(out_11), .gate(and_1_out));
  Transistor #(.\type ("n"), .width(8)) transistor_53 (.in(8'hc0), .out(out_9), .gate(and_1_out));
  Transistor #(.\type ("n"), .width(8)) transistor_54 (.in(8'hc0), .out(out_12), .gate(and_1_out));
  Transistor #(.\type ("n"), .width(8)) transistor_55 (.in(8'hc0), .out(out_13), .gate(and_1_out));
  Transistor #(.\type ("n"), .width(8)) transistor_56 (.in(8'h3), .out(out_3), .gate(and_2_out));
  Transistor #(.\type ("n"), .width(8)) transistor_57 (.in(8'h3), .out(out_5), .gate(and_2_out));
  Transistor #(.\type ("n"), .width(8)) transistor_58 (.in(8'h3), .out(out_6), .gate(and_2_out));
  Transistor #(.\type ("n"), .width(8)) transistor_59 (.in(8'h3), .out(out_4), .gate(and_2_out));
  Transistor #(.\type ("n"), .width(8)) transistor_60 (.in(8'h3), .out(out_7), .gate(and_2_out));
  Transistor #(.\type ("n"), .width(8)) transistor_61 (.in(8'h3), .out(out_11), .gate(and_2_out));
  Transistor #(.\type ("n"), .width(8)) transistor_62 (.in(8'h3), .out(out_8), .gate(and_2_out));
  Transistor #(.\type ("n"), .width(8)) transistor_63 (.in(8'h3), .out(out_9), .gate(and_2_out));
  Transistor #(.\type ("n"), .width(8)) transistor_64 (.in(8'h3), .out(out_10), .gate(and_2_out));
  Transistor #(.\type ("n"), .width(8)) transistor_65 (.in(8'h3), .out(out_12), .gate(and_2_out));
  Transistor #(.\type ("n"), .width(8)) transistor_66 (.in(8'h3), .out(out_13), .gate(and_2_out));
  Transistor #(.width(8)) transistor_67 (.in({8{1'b0}}), .out(out_5), .gate(or_2_out));
  Transistor #(.width(8)) transistor_68 (.in({8{1'b0}}), .out(out_4), .gate(or_2_out));
  Transistor #(.width(8)) transistor_69 (.in({8{1'b0}}), .out(out_6), .gate(or_2_out));
  Transistor #(.width(8)) transistor_70 (.in({8{1'b0}}), .out(out_3), .gate(or_2_out));
  Transistor #(.width(8)) transistor_71 (.in({8{1'b0}}), .out(out_9), .gate(or_2_out));
  Transistor #(.width(8)) transistor_72 (.in({8{1'b0}}), .out(out_7), .gate(or_2_out));
  Transistor #(.width(8)) transistor_73 (.in({8{1'b0}}), .out(out_10), .gate(or_2_out));
  Transistor #(.width(8)) transistor_74 (.in({8{1'b0}}), .out(out_8), .gate(or_2_out));
  Transistor #(.width(8)) transistor_75 (.in({8{1'b0}}), .out(out_12), .gate(or_2_out));
  Transistor #(.width(8)) transistor_76 (.in({8{1'b0}}), .out(out_13), .gate(or_2_out));
  Transistor #(.width(8)) transistor_77 (.in({8{1'b0}}), .out(out_11), .gate(or_2_out));

  // Notes on the sheet:
  //   Транспорт
  //   2
  //   Щит
  //   3
  //   4
  //   Энергия
  //   Занята
  //   1
  //   Занята
  //   1
  //   Занята
  //   1
  //   Занята
  //   1
endmodule

module \Чья_Тип  (
  input  [1:0] in_1,
  input  [3:0] in_2,
  output [7:0] out_3,
  output [7:0] out_4,
  output [7:0] out_5,
  output [7:0] out_6,
  output [7:0] out_7,
  output [7:0] out_8,
  output [7:0] out_9,
  output [7:0] out_10,
  output [7:0] out_11,
  output [7:0] out_12,
  output [7:0] out_13,
  output [7:0] out_14,
  output [7:0] out_15,
  output [7:0] out_16,
  output [7:0] out_17,
  output [7:0] out_18,
  output [7:0] out_19,
  output [7:0] out_20,
  output [7:0] out_21,
  output [7:0] out_22,
  output [7:0] out_23,
  output [7:0] out_24
);

  wire and_5_out, and_6_out;
  wire [2:0] and_1_out;
  wire [3:0] and_3_out;

  and and_1 (and_1_out[0], in_1[0], in_2[0]);
  and and_2 (and_1_out[1], in_2[1], in_1[0]);
  and and_3 (and_3_out[0], in_1[1], in_2[0]);
  and and_4 (and_3_out[1], in_1[1], in_2[1]);
  xor xor_1 (and_3_out[3], in_2[3], and_6_out);
  xor xor_2 (and_1_out[2], in_2[2], and_5_out);
  and and_5 (and_5_out, in_1[0], in_2[2]);
  and and_6 (and_6_out, in_1[1], in_2[3]);
  DotMatrix #(.matrixcols(11), .matrixrows(8)) dotmatrix_1 (
    .col0(out_14), .col1(out_15), .col2(out_16), .col3(out_17), .col4(out_18), .col5(out_19), .col6(out_20),
    .col7(out_21), .col8(out_22), .col9(out_23), .col10(out_24));
  \Тип  \u_тип_1  (
    .in_1(in_1[0]), .in_2({1'b0, and_1_out}), .out_3(out_14), .out_4(out_15), .out_5(out_16), .out_6(out_17),
    .out_7(out_18), .out_8(out_19), .out_9(out_20), .out_10(out_21), .out_11(out_22), .out_12(out_23),
    .out_13(out_24));
  DotMatrix #(.matrixcols(11), .matrixrows(8)) dotmatrix_2 (
    .col0(out_3), .col1(out_4), .col2(out_5), .col3(out_6), .col4(out_7), .col5(out_8), .col6(out_9),
    .col7(out_10), .col8(out_11), .col9(out_12), .col10(out_13));
  \Тип  \u_тип_2  (
    .in_1(in_1[1]), .in_2({and_3_out[3], 1'b0, and_3_out[1:0]}), .out_3(out_3), .out_4(out_4), .out_5(out_5),
    .out_6(out_6), .out_7(out_7), .out_8(out_8), .out_9(out_9), .out_10(out_10), .out_11(out_11),
    .out_12(out_12), .out_13(out_13));

  // Notes on the sheet:
  //   Оранжевый
  //   Синий
endmodule

module \Коллона_1  (
  input  D,
  input  C,
  input  B,
  input  A,
  output e,
  output d_2,
  output c_2,
  output b_2,
  output a_2
);

  wire and_1_out, and_2_out, and_3_out, and_4_out, and_5_out, and_6_out, and_7_out, and_8_out, and_9_out,
       and_10_out, and_11_out, and_12_out, and_13_out, and_14_out, and_15_out, and_16_out, and_17_out,
       and_18_out, not_1_out, not_2_out, not_3_out, not_4_out, not_5_out, not_6_out, not_7_out, not_8_out,
       not_9_out, not_10_out, not_11_out, not_12_out, not_13_out, not_14_out, not_15_out, not_16_out,
       not_17_out, not_18_out, not_19_out, not_20_out, not_21_out, not_22_out, not_23_out, not_24_out,
       not_25_out, not_26_out, not_27_out, not_28_out, not_29_out, not_30_out, not_31_out, not_32_out,
       not_33_out, not_34_out, not_35_out, not_36_out;

  not not_1 (not_1_out, D);
  and and_1 (and_1_out, not_1_out, not_2_out);
  not not_2 (not_2_out, C);
  not not_3 (not_3_out, C);
  and and_2 (and_2_out, not_3_out, not_4_out);
  not not_4 (not_4_out, B);
  not not_5 (not_5_out, D);
  not not_6 (not_6_out, B);
  and and_3 (and_3_out, not_5_out, not_6_out, A);
  not not_7 (not_7_out, D);
  and and_4 (and_4_out, not_7_out, B, not_8_out);
  not not_8 (not_8_out, A);
  not not_9 (not_9_out, D);
  and and_5 (and_5_out, not_9_out, not_10_out, not_11_out);
  not not_10 (not_10_out, C);
  not not_11 (not_11_out, A);
  not not_12 (not_12_out, C);
  not not_13 (not_13_out, B);
  and and_6 (and_6_out, not_12_out, not_13_out, not_14_out);
  not not_14 (not_14_out, A);
  not not_15 (not_15_out, D);
  and and_7 (and_7_out, not_15_out, B, not_16_out);
  not not_16 (not_16_out, A);
  not not_17 (not_17_out, D);
  and and_8 (and_8_out, not_17_out, not_18_out);
  not not_18 (not_18_out, A);
  not not_19 (not_19_out, D);
  and and_9 (and_9_out, not_19_out, not_20_out, B);
  not not_20 (not_20_out, C);
  not not_21 (not_21_out, D);
  and and_10 (and_10_out, not_21_out, C, not_22_out);
  not not_22 (not_22_out, B);
  not not_23 (not_23_out, C);
  and and_11 (and_11_out, D, not_23_out, not_24_out);
  not not_24 (not_24_out, B);
  not not_25 (not_25_out, D);
  and and_12 (and_12_out, not_25_out, not_26_out);
  not not_26 (not_26_out, B);
  not not_27 (not_27_out, C);
  and and_13 (and_13_out, not_27_out, not_28_out);
  not not_28 (not_28_out, B);
  not not_29 (not_29_out, D);
  and and_14 (and_14_out, not_29_out, C, not_30_out);
  not not_30 (not_30_out, A);
  not not_31 (not_31_out, D);
  and and_15 (and_15_out, not_31_out, not_32_out);
  not not_32 (not_32_out, A);
  not not_33 (not_33_out, D);
  and and_16 (and_16_out, not_33_out, B);
  not not_34 (not_34_out, D);
  and and_17 (and_17_out, not_34_out, C);
  and and_18 (and_18_out, D, not_35_out, not_36_out);
  not not_35 (not_35_out, C);
  not not_36 (not_36_out, B);
  or or_1 (e, and_1_out, and_2_out, and_3_out, and_4_out);
  or or_2 (d_2, and_5_out, and_6_out, and_7_out);
  or or_3 (c_2, and_8_out, and_9_out, and_10_out, and_11_out);
  or or_4 (b_2, and_12_out, and_13_out, and_14_out);
  or or_5 (a_2, and_15_out, and_16_out, and_17_out, and_18_out);
endmodule

module \Коллона_2  (
  input  D,
  input  C,
  input  B,
  input  A,
  output e,
  output d_2,
  output c_2,
  output b_2,
  output a_2
);

  wire and_1_out, and_2_out, and_3_out, and_4_out, and_5_out, and_6_out, and_7_out, and_8_out, and_9_out,
       and_10_out, and_11_out, and_12_out, not_1_out, not_2_out, not_3_out, not_4_out, not_5_out, not_6_out,
       not_7_out, not_8_out, not_9_out, not_10_out, not_11_out, not_12_out, not_13_out, not_14_out,
       not_15_out, not_16_out, not_17_out, not_18_out, not_19_out, not_20_out, not_21_out, not_22_out,
       not_23_out, not_24_out, not_25_out, not_26_out, not_27_out, not_28_out;

  not not_1 (not_1_out, D);
  and and_1 (and_1_out, not_1_out, not_2_out);
  not not_2 (not_2_out, C);
  not not_3 (not_3_out, C);
  and and_2 (and_2_out, not_3_out, not_4_out);
  not not_4 (not_4_out, B);
  not not_5 (not_5_out, D);
  and and_3 (and_3_out, not_5_out, not_6_out, A);
  not not_6 (not_6_out, B);
  not not_7 (not_7_out, D);
  and and_4 (and_4_out, not_7_out, B, not_8_out);
  not not_8 (not_8_out, A);
  not not_9 (not_9_out, D);
  not not_10 (not_10_out, C);
  not not_11 (not_11_out, B);
  not not_12 (not_12_out, D);
  and and_5 (and_5_out, not_12_out, not_13_out, A);
  not not_13 (not_13_out, C);
  not not_14 (not_14_out, D);
  not not_15 (not_15_out, C);
  and and_6 (and_6_out, not_14_out, not_15_out, B);
  not not_16 (not_16_out, D);
  and and_7 (and_7_out, not_16_out, C, not_17_out);
  not not_17 (not_17_out, B);
  not not_18 (not_18_out, D);
  and and_8 (and_8_out, not_18_out, C, not_19_out);
  not not_19 (not_19_out, A);
  not not_20 (not_20_out, C);
  and and_9 (and_9_out, D, not_20_out, not_21_out);
  not not_21 (not_21_out, B);
  not not_22 (not_22_out, D);
  not not_23 (not_23_out, C);
  not not_24 (not_24_out, B);
  not not_25 (not_25_out, C);
  and and_10 (and_10_out, not_25_out, not_26_out);
  not not_26 (not_26_out, B);
  not not_27 (not_27_out, D);
  and and_11 (and_11_out, not_27_out, A);
  not not_28 (not_28_out, D);
  and and_12 (and_12_out, not_28_out, B);
  or or_1 (e, and_1_out, and_2_out, and_3_out, and_4_out);
  and and_13 (d_2, not_9_out, not_10_out, not_11_out, A);
  or or_2 (c_2, and_5_out, and_6_out, and_7_out, and_8_out, and_9_out);
  and and_14 (b_2, not_22_out, not_23_out, not_24_out, A);
  or or_3 (a_2, and_10_out, and_11_out, and_12_out);
endmodule

module \Коллона_3  (
  input  D,
  input  C,
  input  B,
  input  A,
  output e,
  output d_2,
  output c_2,
  output b_2,
  output a_2
);

  wire and_1_out, and_2_out, and_3_out, and_4_out, and_5_out, and_6_out, and_7_out, and_8_out, and_9_out,
       and_10_out, and_11_out, and_12_out, and_13_out, and_14_out, and_15_out, and_16_out, and_17_out,
       not_1_out, not_2_out, not_3_out, not_4_out, not_5_out, not_6_out, not_7_out, not_8_out, not_9_out,
       not_10_out, not_11_out, not_12_out, not_13_out, not_14_out, not_15_out, not_16_out, not_17_out,
       not_18_out, not_19_out, not_20_out, not_21_out, not_22_out, not_23_out, not_24_out, not_25_out,
       not_26_out, not_27_out, not_28_out, not_29_out, not_30_out, not_31_out;

  not not_1 (not_1_out, D);
  not not_2 (not_2_out, C);
  and and_1 (and_1_out, not_2_out, not_3_out);
  not not_3 (not_3_out, B);
  not not_4 (not_4_out, D);
  not not_5 (not_5_out, B);
  and and_2 (and_2_out, not_4_out, not_5_out, not_6_out);
  not not_6 (not_6_out, A);
  not not_7 (not_7_out, D);
  and and_3 (and_3_out, not_7_out, B, A);
  not not_8 (not_8_out, D);
  and and_4 (and_4_out, not_8_out, C);
  not not_9 (not_9_out, C);
  and and_5 (and_5_out, D, not_9_out, not_10_out);
  not not_10 (not_10_out, B);
  not not_11 (not_11_out, D);
  and and_6 (and_6_out, not_11_out, not_12_out);
  not not_12 (not_12_out, A);
  not not_13 (not_13_out, D);
  and and_7 (and_7_out, not_13_out, B);
  not not_14 (not_14_out, D);
  and and_8 (and_8_out, not_14_out, C);
  not not_15 (not_15_out, C);
  and and_9 (and_9_out, D, not_15_out, not_16_out);
  not not_16 (not_16_out, B);
  not not_17 (not_17_out, D);
  not not_18 (not_18_out, C);
  and and_10 (and_10_out, not_17_out, not_18_out, not_19_out);
  not not_19 (not_19_out, A);
  not not_20 (not_20_out, D);
  not not_21 (not_21_out, B);
  and and_11 (and_11_out, not_20_out, not_21_out, not_22_out);
  not not_22 (not_22_out, A);
  not not_23 (not_23_out, D);
  and and_12 (and_12_out, not_23_out, B, A);
  not not_24 (not_24_out, C);
  and and_13 (and_13_out, D, not_24_out, not_25_out);
  not not_25 (not_25_out, B);
  not not_26 (not_26_out, D);
  and and_14 (and_14_out, not_26_out, not_27_out);
  not not_27 (not_27_out, A);
  not not_28 (not_28_out, D);
  and and_15 (and_15_out, not_28_out, B);
  not not_29 (not_29_out, D);
  and and_16 (and_16_out, not_29_out, C);
  and and_17 (and_17_out, D, not_30_out, not_31_out);
  not not_30 (not_30_out, C);
  not not_31 (not_31_out, B);
  or or_1 (e, not_1_out, and_1_out);
  or or_2 (d_2, and_2_out, and_3_out, and_4_out, and_5_out);
  or or_3 (c_2, and_6_out, and_7_out, and_8_out, and_9_out);
  or or_4 (b_2, and_10_out, and_11_out, and_12_out, and_13_out);
  or or_5 (a_2, and_14_out, and_15_out, and_16_out, and_17_out);
endmodule

module \Цифра  (
  input  [9:0] in_1,
  output [4:0] out_2,
  output [4:0] out_3,
  output [4:0] out_4
);

  // Probe on in_1
  \Коллона_1  \u_коллона_1_1  (
    .D(in_1[3]), .C(in_1[2]), .B(in_1[1]), .A(in_1[0]), .e(out_2[0]), .d_2(out_2[1]), .c_2(out_2[2]),
    .b_2(out_2[3]), .a_2(out_2[4]));
  \Коллона_2  \u_коллона_2_1  (
    .D(in_1[3]), .C(in_1[2]), .B(in_1[1]), .A(in_1[0]), .e(out_3[0]), .d_2(out_3[1]), .c_2(out_3[2]),
    .b_2(out_3[3]), .a_2(out_3[4]));
  \Коллона_3  \u_коллона_3_1  (
    .D(in_1[3]), .C(in_1[2]), .B(in_1[1]), .A(in_1[0]), .e(out_4[0]), .d_2(out_4[1]), .c_2(out_4[2]),
    .b_2(out_4[3]), .a_2(out_4[4]));
  DotMatrix #(.matrixcols(3), .matrixrows(5)) dotmatrix_1 (.col0(out_2), .col1(out_3), .col2(out_4));
endmodule

module \Цифры  (
  input  [9:0] Energy,
  output [4:0] out_2,
  output [4:0] out_3,
  output [4:0] out_4,
  output [4:0] out_5,
  output [4:0] out_6,
  output [4:0] out_7,
  output [4:0] out_8,
  output [4:0] out_9,
  output [4:0] out_10,
  output [4:0] out_11,
  output [4:0] out_12
);

  wire and_1_out, or_1_out, or_2_out, or_3_out, or_4_out, or_5_out, or_6_out;
  wire [4:0] \цифра_1_out_2 , \цифра_1_out_3 , \цифра_1_out_4 , \цифра_2_out_2 , \цифра_2_out_3 ,
       \цифра_2_out_4 , \цифра_3_out_2 , \цифра_3_out_3 , \цифра_3_out_4 ;
  wire [9:0] divider_1_out, divider_1_rem, divider_2_out, divider_2_rem, divider_3_rem, transistor_4_out;

  \Цифра  \u_цифра_1  (.in_1(divider_3_rem), .out_2(\цифра_1_out_2 ), .out_3(\цифра_1_out_3 ), .out_4(\цифра_1_out_4 ));
  Transistor #(.\type ("n"), .width(5)) transistor_1 (.in(\цифра_1_out_3 ), .out(out_3), .gate(or_2_out));
  Transistor #(.\type ("n"), .width(5)) transistor_2 (.in(\цифра_1_out_4 ), .out(out_4), .gate(or_2_out));
  Transistor #(.\type ("n"), .width(5)) transistor_3 (.in(\цифра_1_out_2 ), .out(out_2), .gate(or_2_out));
  // Probe on Energy
  Transistor #(.width(10)) transistor_4 (.in(Energy), .out(transistor_4_out), .gate(and_1_out));
  Divider #(.width(10)) divider_1 (
    .a(transistor_4_out), .b(10'ha), .out(divider_1_out), .rem(divider_1_rem));  // open: upper
  Transistor #(.\type ("n"), .width(10)) transistor_5 (.in(10'h3e7), .out(transistor_4_out), .gate(and_1_out));
  \Цифра  \u_цифра_2  (.in_1(divider_2_rem), .out_2(\цифра_2_out_2 ), .out_3(\цифра_2_out_3 ), .out_4(\цифра_2_out_4 ));
  Transistor #(.\type ("n"), .width(5)) transistor_6 (.in(\цифра_2_out_2 ), .out(out_6), .gate(or_6_out));
  Transistor #(.\type ("n"), .width(5)) transistor_7 (.in(\цифра_2_out_3 ), .out(out_7), .gate(or_6_out));
  Divider #(.width(10)) divider_2 (
    .a(divider_1_out), .b(10'ha), .out(divider_2_out), .rem(divider_2_rem));  // open: upper
  Transistor #(.\type ("n"), .width(5)) transistor_8 (.in(\цифра_2_out_4 ), .out(out_8), .gate(or_6_out));
  Divider #(.width(10)) divider_3 (.a(divider_2_out), .b(10'ha), .rem(divider_3_rem));  // open: out, upper
  or or_1 (or_1_out, Energy[3], Energy[4]);
  Transistor #(.\type ("n"), .width(5)) transistor_9 (.in(\цифра_3_out_2 ), .out(out_10), .gate(or_5_out));
  and and_1 (and_1_out, or_1_out, Energy[5], Energy[6], Energy[7], Energy[8], Energy[9]);
  or or_2 (or_2_out, divider_3_rem[0], divider_3_rem[1], divider_3_rem[2], divider_3_rem[3], divider_3_rem[4], divider_3_rem[5], divider_3_rem[6], divider_3_rem[7], divider_3_rem[8], divider_3_rem[9]);
  or or_3 (or_3_out, divider_2_rem[0], divider_2_rem[1], divider_2_rem[2], divider_2_rem[3], divider_2_rem[4], divider_2_rem[5], divider_2_rem[6], divider_2_rem[7], divider_2_rem[8], divider_2_rem[9]);
  or or_4 (or_4_out, divider_1_rem[0], divider_1_rem[1], divider_1_rem[2], divider_1_rem[3], divider_1_rem[4], divider_1_rem[5], divider_1_rem[6], divider_1_rem[7], divider_1_rem[8], divider_1_rem[9]);
  or or_5 (or_5_out, or_4_out, or_3_out, or_2_out);
  \Цифра  \u_цифра_3  (.in_1(divider_1_rem), .out_2(\цифра_3_out_2 ), .out_3(\цифра_3_out_3 ), .out_4(\цифра_3_out_4 ));
  Transistor #(.\type ("n"), .width(5)) transistor_10 (.in(\цифра_3_out_4 ), .out(out_12), .gate(or_5_out));
  Transistor #(.\type ("n"), .width(5)) transistor_11 (.in(\цифра_3_out_3 ), .out(out_11), .gate(or_5_out));
  or or_6 (or_6_out, or_3_out, or_2_out);
  Transistor #(.width(5)) transistor_12 (.in({5{1'b0}}), .out(out_2), .gate(or_2_out));
  Transistor #(.width(5)) transistor_13 (.in({5{1'b0}}), .out(out_3), .gate(or_2_out));
  Transistor #(.width(5)) transistor_14 (.in({5{1'b0}}), .out(out_4), .gate(or_2_out));
  Transistor #(.width(5)) transistor_15 (.in({5{1'b0}}), .out(out_8), .gate(or_6_out));
  Transistor #(.width(5)) transistor_16 (.in({5{1'b0}}), .out(out_7), .gate(or_6_out));
  Transistor #(.width(5)) transistor_17 (.in({5{1'b0}}), .out(out_6), .gate(or_6_out));
  Transistor #(.width(5)) transistor_18 (.in({5{1'b0}}), .out(out_12), .gate(or_5_out));
  Transistor #(.width(5)) transistor_19 (.in({5{1'b0}}), .out(out_11), .gate(or_5_out));
  Transistor #(.width(5)) transistor_20 (.in({5{1'b0}}), .out(out_10), .gate(or_5_out));

  assign out_5 = {5{1'b0}};
  assign out_9 = {5{1'b0}};

  // Notes on the sheet:
  //   еденицы
  //   десятки
  //   сотни
endmodule

module \тест  (
  input  [9:0] in_1
);

  wire [4:0] \цифры_1_out_2 , \цифры_1_out_3 , \цифры_1_out_4 , \цифры_1_out_5 , \цифры_1_out_6 ,
       \цифры_1_out_7 , \цифры_1_out_8 , \цифры_1_out_9 , \цифры_1_out_10 , \цифры_1_out_11 ,
       \цифры_1_out_12 ;

  DotMatrix #(.matrixcols(11), .matrixrows(8)) dotmatrix_1 ();  // open: col0, col1, col2, col3, col4, col5, col6, col7, col8, col9, col10
  DotMatrix #(.matrixcols(11), .matrixrows(8)) dotmatrix_2 ();  // open: col0, col1, col2, col3, col4, col5, col6, col7, col8, col9, col10
  DotMatrix #(.matrixcols(11), .matrixrows(5)) dotmatrix_3 (
    .col0(\цифры_1_out_2 ), .col1(\цифры_1_out_3 ), .col2(\цифры_1_out_4 ), .col3(\цифры_1_out_5 ),
    .col4(\цифры_1_out_6 ), .col5(\цифры_1_out_7 ), .col6(\цифры_1_out_8 ), .col7(\цифры_1_out_9 ),
    .col8(\цифры_1_out_10 ), .col9(\цифры_1_out_11 ), .col10(\цифры_1_out_12 ));
  \Цифры  \u_цифры_1  (
    .out_2(\цифры_1_out_2 ), .out_3(\цифры_1_out_3 ), .out_4(\цифры_1_out_4 ), .out_5(\цифры_1_out_5 ),
    .out_6(\цифры_1_out_6 ), .out_7(\цифры_1_out_7 ), .out_8(\цифры_1_out_8 ), .out_9(\цифры_1_out_9 ),
    .out_10(\цифры_1_out_10 ), .out_11(\цифры_1_out_11 ), .out_12(\цифры_1_out_12 ));  // open: Energy
endmodule

module circuit (
  input  [1:0] in_1,
  output [4:0] out_2,
  output [4:0] out_3,
  output [4:0] out_4,
  output [4:0] out_5,
  output [4:0] out_6,
  output [4:0] out_7,
  output [4:0] out_8
);

  wire or_1_out;

  or or_1 (or_1_out, in_1[0], in_1[1]);
  Transistor #(.width(5)) transistor_1 (.in({5{1'b0}}), .out(out_2), .gate(or_1_out));
  Transistor #(.width(5)) transistor_2 (.in({5{1'b0}}), .out(out_4), .gate(or_1_out));
  Transistor #(.width(5)) transistor_3 (.in({5{1'b0}}), .out(out_3), .gate(or_1_out));
  Transistor #(.\type ("n"), .width(5)) transistor_4 (.in(5'b00100), .out(out_4), .gate(in_1[0]));
  Transistor #(.\type ("n"), .width(5)) transistor_5 (.in(5'b00100), .out(out_3), .gate(in_1[0]));
  Transistor #(.\type ("n"), .width(5)) transistor_6 (.in(5'b00100), .out(out_2), .gate(in_1[0]));
  Transistor #(.\type ("n"), .width(5)) transistor_7 (.in(5'b00100), .out(out_2), .gate(in_1[1]));
  Transistor #(.\type ("n"), .width(5)) transistor_8 (.in(5'b10101), .out(out_4), .gate(in_1[1]));
  Transistor #(.\type ("n"), .width(5)) transistor_9 (.in(5'b01110), .out(out_3), .gate(in_1[1]));
  Transistor #(.width(5)) transistor_10 (.in({5{1'b0}}), .out(out_8), .gate(or_1_out));
  Transistor #(.width(5)) transistor_11 (.in({5{1'b0}}), .out(out_5), .gate(or_1_out));
  Transistor #(.width(5)) transistor_12 (.in({5{1'b0}}), .out(out_6), .gate(or_1_out));
  Transistor #(.width(5)) transistor_13 (.in({5{1'b0}}), .out(out_7), .gate(or_1_out));
  Transistor #(.\type ("n"), .width(5)) transistor_14 (.in(5'b00100), .out(out_8), .gate(in_1[0]));
  Transistor #(.\type ("n"), .width(5)) transistor_15 (.in(5'b10101), .out(out_6), .gate(in_1[0]));
  Transistor #(.\type ("n"), .width(5)) transistor_16 (.in(5'b01110), .out(out_7), .gate(in_1[0]));
  Transistor #(.\type ("n"), .width(5)) transistor_17 (.in(5'b00100), .out(out_5), .gate(in_1[0]));
  Transistor #(.\type ("n"), .width(5)) transistor_18 (.in(5'b00100), .out(out_6), .gate(in_1[1]));
  Transistor #(.\type ("n"), .width(5)) transistor_19 (.in(5'b00100), .out(out_7), .gate(in_1[1]));
  Transistor #(.\type ("n"), .width(5)) transistor_20 (.in(5'b00100), .out(out_5), .gate(in_1[1]));
  Transistor #(.\type ("n"), .width(5)) transistor_21 (.in(5'b00100), .out(out_8), .gate(in_1[1]));
  DotMatrix #(.matrixcols(7), .matrixrows(5)) dotmatrix_1 (
    .col0(out_2), .col1(out_3), .col2(out_4), .col3(out_5), .col4(out_6), .col5(out_7), .col6(out_8));
endmodule

module v (
  input  [1:0] in_1,
  output [6:0] out_2,
  output [6:0] out_3,
  output [6:0] out_4,
  output [6:0] out_5,
  output [6:0] out_6
);

  wire or_1_out;

  or or_1 (or_1_out, in_1[0], in_1[1]);
  Transistor #(.width(7)) transistor_1 (.in({7{1'b0}}), .out(out_4), .gate(or_1_out));
  Transistor #(.width(7)) transistor_2 (.in({7{1'b0}}), .out(out_3), .gate(or_1_out));
  Transistor #(.width(7)) transistor_3 (.in({7{1'b0}}), .out(out_2), .gate(or_1_out));
  Transistor #(.\type ("n"), .width(7)) transistor_4 (.in(7'b0000100), .out(out_2), .gate(in_1[0]));
  Transistor #(.\type ("n"), .width(7)) transistor_5 (.in({7{1'b1}}), .out(out_4), .gate(in_1[0]));
  Transistor #(.\type ("n"), .width(7)) transistor_6 (.in(7'b0000010), .out(out_3), .gate(in_1[0]));
  Transistor #(.\type ("n"), .width(7)) transistor_7 (.in(7'b0010000), .out(out_2), .gate(in_1[1]));
  Transistor #(.\type ("n"), .width(7)) transistor_8 (.in({7{1'b1}}), .out(out_4), .gate(in_1[1]));
  Transistor #(.\type ("n"), .width(7)) transistor_9 (.in(7'b0100000), .out(out_3), .gate(in_1[1]));
  Transistor #(.width(7)) transistor_10 (.in({7{1'b0}}), .out(out_5), .gate(or_1_out));
  Transistor #(.width(7)) transistor_11 (.in({7{1'b0}}), .out(out_6), .gate(or_1_out));
  Transistor #(.\type ("n"), .width(7)) transistor_12 (.in(7'b0000100), .out(out_6), .gate(in_1[0]));
  Transistor #(.\type ("n"), .width(7)) transistor_13 (.in(7'b0000010), .out(out_5), .gate(in_1[0]));
  Transistor #(.\type ("n"), .width(7)) transistor_14 (.in(7'b0100000), .out(out_5), .gate(in_1[1]));
  Transistor #(.\type ("n"), .width(7)) transistor_15 (.in(7'b0010000), .out(out_6), .gate(in_1[1]));
  DotMatrix dotmatrix_1 (.col0(out_2), .col1(out_3), .col2(out_4), .col3(out_5), .col4(out_6));
endmodule

module \указатель  (
  input  in_1
);

  wire [14:0] transistor_1_out, transistor_2_out;

  DotMatrix #(.matrixcols(11), .matrixrows(15)) dotmatrix_1 (
    .col0(transistor_2_out), .col1(transistor_1_out), .col2(transistor_1_out), .col3(transistor_1_out),
    .col4(transistor_1_out), .col5(transistor_1_out), .col6(transistor_1_out), .col7(transistor_1_out),
    .col8(transistor_1_out), .col9(transistor_1_out), .col10(transistor_2_out));
  Transistor #(.width(15)) transistor_1 (.in({15{1'b0}}), .out(transistor_1_out), .gate(in_1));
  Transistor #(.\type ("n"), .width(15)) transistor_2 (.in({15{1'b1}}), .out(transistor_2_out), .gate(in_1));
  Transistor #(.\type ("n"), .width(15)) transistor_3 (.in(15'h4001), .out(transistor_1_out), .gate(in_1));
  Transistor #(.width(15)) transistor_4 (.in({15{1'b0}}), .out(transistor_2_out), .gate(in_1));
endmodule
