// Logisim project input controller.circ as structural Verilog: 5 circuits, main circuit input controller
module local_test (
  input  in_1
);

  wire and_1_out, button_1_out, clock_1_out, counter_1_carry, d_ff_1_q, demultiplexer_1_out0,
       demultiplexer_1_out1, demultiplexer_1_out2, demultiplexer_1_out3, input_controller_1_active_led,
       input_controller_1_data_ready, input_controller_1_error_led, input_controller_1_kbd_clear,
       input_controller_1_kbd_clock, input_controller_1_kbd_en, keyboard_1_avail, nor_1_out, Yea;
  wire [1:0] input_controller_1_cursor_position;
  wire [4:0] input_controller_1_command_parsed_from_user_input;
  wire [6:0] input_controller_1_input_buffer, input_controller_1_input_buffer_2,
       input_controller_1_input_buffer_3, input_controller_1_input_buffer_4, keyboard_1_data;
  wire [10:0] input_controller_1_signed_number_parsed_from_user_input;

  Button button_1 (.out(button_1_out));
  D_Flip_Flop d_ff_1 (
    .clk(button_1_out), .D(button_1_out), .Q(d_ff_1_q), .reset(input_controller_1_data_ready));  // open: Qn, preset, en
  Counter #(.width(2), .max('h3)) counter_1 (
    .carry(counter_1_carry), .clk(clock_1_out), .clr(nor_1_out));  // open: load, D, count, Q
  Clock clock_1 (.out(clock_1_out));
  input_controller input_controller_1 (
    .Signed_number_parsed_from_user_input(input_controller_1_signed_number_parsed_from_user_input),
    .Command_parsed_from_user_input(input_controller_1_command_parsed_from_user_input),
    .KBD_clock(input_controller_1_kbd_clock), .KBD_clear(input_controller_1_kbd_clear),
    .KBD_available(keyboard_1_avail), .KBD_buffer(keyboard_1_data), .KBD_en(input_controller_1_kbd_en),
    .Enabled__clears_buffer_on_rising_edge(and_1_out), .Active_LED(input_controller_1_active_led),
    .Request_number(d_ff_1_q), .User_action_LED(Yea), .Error_LED(input_controller_1_error_led),
    .Data_ready(input_controller_1_data_ready),
    .input_buffer({input_controller_1_input_buffer_4, input_controller_1_input_buffer_3, input_controller_1_input_buffer_2, input_controller_1_input_buffer}),
    .Cursor_position(input_controller_1_cursor_position), .CLK(clock_1_out));
  Keyboard #(.buflen(5)) keyboard_1 (
    .clk(input_controller_1_kbd_clock), .re(input_controller_1_kbd_en), .clr(input_controller_1_kbd_clear),
    .avail(keyboard_1_avail), .data(keyboard_1_data));
  and and_1 (and_1_out, in_1, ~counter_1_carry);  // AND_Gate
  nor nor_1 (nor_1_out, input_controller_1_error_led, input_controller_1_data_ready);
  LED led_1 (.in(demultiplexer_1_out3));
  // Probe on input_controller_1_input_buffer_4
  LED led_2 (.in(input_controller_1_error_led));
  LED led_3 (.in(input_controller_1_active_led));
  LED led_4 (.in(Yea));
  Demultiplexer #(.select(2), .enable("false")) demultiplexer_1 (
    .out0(demultiplexer_1_out0), .out1(demultiplexer_1_out1), .out2(demultiplexer_1_out2),
    .out3(demultiplexer_1_out3), .in(Yea), .sel(input_controller_1_cursor_position));
  LED led_5 (.in(demultiplexer_1_out2));
  // Probe on input_controller_1_input_buffer_3
  LED led_6 (.in(demultiplexer_1_out1));
  // Probe on input_controller_1_input_buffer_2
  // Probe on keyboard_1_data
  // Probe on input_controller_1_command_parsed_from_user_input
  LED led_7 (.in(demultiplexer_1_out0));
  // Probe on input_controller_1_input_buffer
  // Probe on input_controller_1_signed_number_parsed_from_user_input
  // Probe on input_controller_1_signed_number_parsed_from_user_input

  // Notes on the sheet:
  //   in_1: pull=down
endmodule

module input_controller (
  input  KBD_available,
  input  [6:0] KBD_buffer,
  input  Enabled__clears_buffer_on_rising_edge,
  input  Request_number,
  input  CLK,
  output [1:0] Cursor_position,
  output KBD_clock,
  output KBD_en,
  output KBD_clear,
  output [4:0] Command_parsed_from_user_input,
  output Data_ready,
  output [27:0] input_buffer,
  output [10:0] Signed_number_parsed_from_user_input,
  output Active_LED,
  output User_action_LED,
  output Error_LED
);

  wire and_1_out, and_2_out, and_3_out, and_5_out, command_decoder_1_err, d_ff_1_q, d_ff_3_q, nor_1_out,
       nor_2_out, not_1_out, not_2_out, not_3_out, number_parser_1_err, number_parser_1_ready;
  wire [6:0] demultiplexer_1_out0, demultiplexer_1_out1, register_1_q;

  and and_1 (and_1_out, CLK, Request_number);
  D_Flip_Flop d_ff_1 (
    .clk(CLK), .D(Enabled__clears_buffer_on_rising_edge), .Q(d_ff_1_q), .reset(not_1_out));  // open: Qn, preset, en
  not not_1 (not_1_out, Enabled__clears_buffer_on_rising_edge);
  D_Flip_Flop d_ff_2 (
    .clk(and_1_out), .D(Request_number), .Q(User_action_LED), .reset(and_2_out));  // open: Qn, preset, en
  and and_2 (and_2_out, Enabled__clears_buffer_on_rising_edge, ~d_ff_1_q);  // AND_Gate
  Register #(.width(7)) register_1 (
    .D(KBD_buffer), .en(Active_LED), .Q(register_1_q), .clk(and_3_out), .clr(and_2_out));
  and and_3 (and_3_out, KBD_available, CLK);
  and and_4 (Active_LED, Enabled__clears_buffer_on_rising_edge, not_2_out);
  not not_2 (not_2_out, Error_LED);
  D_Flip_Flop d_ff_3 (.clk(KBD_available), .D(1'b1), .Q(d_ff_3_q), .reset(and_5_out));  // open: Qn, preset, en
  Demultiplexer #(.width(7), .enable("false")) demultiplexer_1 (
    .out0(demultiplexer_1_out0), .out1(demultiplexer_1_out1), .in(register_1_q), .sel(User_action_LED));
  nor nor_1 (nor_1_out, register_1_q[6], register_1_q[5], register_1_q[4], register_1_q[3], register_1_q[2], register_1_q[1], register_1_q[0]);
  and and_5 (and_5_out, d_ff_3_q, ~KBD_available, ~CLK);  // AND_Gate
  command_decoder command_decoder_1 (
    .Char_input(demultiplexer_1_out0), .Command_output(Command_parsed_from_user_input),
    .err(command_decoder_1_err));
  Multiplexer #(.enable("false")) multiplexer_1 (
    .in0(command_decoder_1_err), .in1(number_parser_1_err), .out(Error_LED), .sel(User_action_LED));
  number_parser number_parser_1 (
    .\input (demultiplexer_1_out1), .clk(and_5_out), .rst(and_2_out), .output_buffer(input_buffer),
    .ready(number_parser_1_ready), .err(number_parser_1_err),
    .output_number(Signed_number_parsed_from_user_input), .Cursor_position(Cursor_position));
  nor nor_2 (nor_2_out, command_decoder_1_err, nor_1_out);
  Multiplexer #(.enable("false")) multiplexer_2 (
    .in0(number_parser_1_ready), .in1(nor_2_out), .out(Data_ready), .sel(not_3_out));
  not not_3 (not_3_out, User_action_LED);

  assign KBD_clear = 1'b0;
  assign KBD_clock = CLK;
  assign KBD_en = KBD_available;

  // Notes on the sheet:
  //   KBD_available: pull=down
  //   KBD_buffer: pull=down
  //   Request_number: pull=down
  //   CLK: pull=down
  //   Enabled__clears_buffer_on_rising_edge: pull=down
endmodule

module command_decoder (
  input  [6:0] Char_input,
  output [4:0] Command_output,
  output err
);

  wire internal_comparator_1_is_equal;

  internal_comparator internal_comparator_1 (
    .input_1(Char_input), .input_2({7{1'b0}}), .forward_value_input({5{1'b0}}),
    .is_equal(internal_comparator_1_is_equal), .forwarded_value(Command_output));
  internal_comparator internal_comparator_2 (
    .input_1(Char_input), .input_2(7'b1100001), .forward_value_input(5'b10010),
    .is_equal(internal_comparator_1_is_equal), .forwarded_value(Command_output));
  internal_comparator internal_comparator_3 (
    .input_1(Char_input), .input_2(7'b1000001), .forward_value_input(5'b01101),
    .is_equal(internal_comparator_1_is_equal), .forwarded_value(Command_output));
  internal_comparator internal_comparator_4 (
    .input_1(Char_input), .input_2(7'b1110011), .forward_value_input(5'b10000),
    .is_equal(internal_comparator_1_is_equal), .forwarded_value(Command_output));
  internal_comparator internal_comparator_5 (
    .input_1(Char_input), .input_2(7'b1010011), .forward_value_input(5'b01100),
    .is_equal(internal_comparator_1_is_equal), .forwarded_value(Command_output));
  internal_comparator internal_comparator_6 (
    .input_1(Char_input), .input_2(7'b1100100), .forward_value_input(5'b10001),
    .is_equal(internal_comparator_1_is_equal), .forwarded_value(Command_output));
  internal_comparator internal_comparator_7 (
    .input_1(Char_input), .input_2(7'b1000100), .forward_value_input(5'b01110),
    .is_equal(internal_comparator_1_is_equal), .forwarded_value(Command_output));
  internal_comparator internal_comparator_8 (
    .input_1(Char_input), .input_2(7'b1110111), .forward_value_input(5'b10011),
    .is_equal(internal_comparator_1_is_equal), .forwarded_value(Command_output));
  internal_comparator internal_comparator_9 (
    .input_1(Char_input), .input_2(7'b1010111), .forward_value_input(5'b01111),
    .is_equal(internal_comparator_1_is_equal), .forwarded_value(Command_output));
  internal_comparator internal_comparator_10 (
    .input_1(Char_input), .input_2(7'b1100101), .forward_value_input(5'b01000),
    .is_equal(internal_comparator_1_is_equal), .forwarded_value(Command_output));
  internal_comparator internal_comparator_11 (
    .input_1(Char_input), .input_2(7'b0001000), .forward_value_input(5'b10100),
    .is_equal(internal_comparator_1_is_equal), .forwarded_value(Command_output));
  internal_comparator internal_comparator_12 (
    .input_1(Char_input), .input_2(7'b1100101), .forward_value_input(5'b11011),
    .is_equal(internal_comparator_1_is_equal), .forwarded_value(Command_output));
  internal_comparator internal_comparator_13 (
    .input_1(Char_input), .input_2(7'b1110010), .forward_value_input(5'b11010),
    .is_equal(internal_comparator_1_is_equal), .forwarded_value(Command_output));
  internal_comparator internal_comparator_14 (
    .input_1(Char_input), .input_2(7'b0001010), .forward_value_input({5{1'b1}}),
    .is_equal(internal_comparator_1_is_equal), .forwarded_value(Command_output));
  Pull_Resistor pull_resistor_1 (.node(internal_comparator_1_is_equal));
  not not_1 (err, internal_comparator_1_is_equal);

  // Notes on the sheet:
  //   Char_input: pull=down
  //   Escape (BKSP)
  //   E (upgd en)
  //   R (upgd shields)
  //   -
  //   a
  //   A
  //   s
  //   S
  //   d
  //   D
  //   w
  //   W
  //   e
  //   Enter
endmodule

module internal_comparator (
  input  [6:0] input_1,
  input  [6:0] input_2,
  input  [4:0] forward_value_input,
  output is_equal,
  output [4:0] forwarded_value
);

  wire nor_1_out;
  wire [6:0] xor_1_out;

  assign xor_1_out = input_1 ^ input_2;  // XOR_Gate xor_1, 7 bits wide
  nor nor_1 (nor_1_out, xor_1_out[0], xor_1_out[1], xor_1_out[2], xor_1_out[3], xor_1_out[4], xor_1_out[5], xor_1_out[6]);
  assign is_equal = nor_1_out ? nor_1_out : 1'bz;  // Controlled_Buffer controlled_buffer_1
  assign forwarded_value = nor_1_out ? forward_value_input : 5'bz;  // Controlled_Buffer controlled_buffer_2

  // Notes on the sheet:
  //   input_2: pull=down
  //   forward_value_input: pull=down
  //   input_1: pull=down
endmodule

module number_parser (
  input  [6:0] \input ,
  input  clk,
  input  rst,
  output [27:0] output_buffer,
  output ready,
  output err,
  output [10:0] output_number,
  output [1:0] Cursor_position
);

  wire and_1_out, and_2_out, and_3_out, and_4_out, and_5_out, and_6_out, comparator_1_gt, comparator_2_lt,
       comparator_3_eq, comparator_4_eq, comparator_5_eq, comparator_6_eq, comparator_7_eq, comparator_8_eq,
       comparator_9_eq, comparator_10_eq, comparator_11_eq, demultiplexer_1_out0, demultiplexer_1_out1,
       demultiplexer_1_out2, demultiplexer_1_out3, nor_1_out, nor_2_out, not_1_out, not_3_out, or_1_out,
       or_2_out, or_3_out, or_4_out, subtractor_1_bout, subtractor_2_bout, subtractor_3_bout,
       subtractor_4_bout;
  wire [1:0] adder_1_out;
  wire [6:0] multiplexer_1_out;
  wire [10:0] adder_2_out, adder_3_out, adder_4_out, adder_5_out, multiplexer_2_out, multiplexer_3_out,
       multiplexer_4_out, multiplexer_5_out, multiplexer_6_out, multiplexer_7_out, multiplexer_8_out,
       multiplexer_9_out, multiplier_1_out, multiplier_2_out, multiplier_3_out, not_2_out, subtractor_1_out,
       subtractor_2_out, subtractor_3_out, subtractor_4_out;

  Comparator #(.width(7), .mode("unsigned")) comparator_1 (
    .a(\input ), .b(7'b0101111), .gt(comparator_1_gt));  // open: eq, lt
  Comparator #(.width(7), .mode("unsigned")) comparator_2 (
    .a(\input ), .b(7'b0111010), .lt(comparator_2_lt));  // open: gt, eq
  and and_1 (and_1_out, comparator_2_lt, comparator_1_gt);
  Comparator #(.width(7), .mode("unsigned")) comparator_3 (
    .a(\input ), .b(7'b0101101), .eq(comparator_3_eq));  // open: gt, lt
  nor nor_1 (nor_1_out, and_3_out, and_4_out);
  or or_1 (or_1_out, and_1_out, comparator_5_eq, comparator_4_eq, comparator_3_eq);
  and and_2 (and_2_out, or_1_out, clk);
  Comparator #(.width(7), .mode("unsigned")) comparator_4 (
    .a(\input ), .b(7'b0001000), .eq(comparator_4_eq));  // open: gt, lt
  Comparator #(.width(7), .mode("unsigned")) comparator_5 (
    .a(\input ), .b(7'b0001010), .eq(comparator_5_eq));  // open: gt, lt
  and and_3 (and_3_out, ~Cursor_position[0], ~Cursor_position[1], comparator_4_eq);  // AND_Gate
  and and_4 (and_4_out, ~comparator_4_eq, Cursor_position[1], Cursor_position[0]);  // AND_Gate
  and and_5 (and_5_out, ~comparator_5_eq, and_2_out);  // AND_Gate
  Multiplexer #(.width(7), .enable("false")) multiplexer_1 (
    .in0(\input ), .in1({7{1'b0}}), .out(multiplexer_1_out), .sel(comparator_4_eq));
  Demultiplexer #(.select(2), .enable("false")) demultiplexer_1 (
    .out0(demultiplexer_1_out0), .out1(demultiplexer_1_out1), .out2(demultiplexer_1_out2),
    .out3(demultiplexer_1_out3), .in(1'b1), .sel(Cursor_position));
  Counter #(.width(2), .max('h3)) counter_1 (
    .load(comparator_4_eq), .count(nor_1_out), .Q(Cursor_position), .clk(and_5_out), .clr(rst));  // open: D, carry
  Register #(.width(7)) register_1 (
    .D(multiplexer_1_out), .en(demultiplexer_1_out1), .Q(output_buffer[13:7]), .clk(and_5_out), .clr(rst));
  Register #(.width(7)) register_2 (
    .D(multiplexer_1_out), .en(demultiplexer_1_out0), .Q(output_buffer[6:0]), .clk(and_5_out), .clr(rst));
  Register #(.width(7)) register_3 (
    .D(multiplexer_1_out), .en(demultiplexer_1_out2), .Q(output_buffer[20:14]), .clk(and_5_out), .clr(rst));
  Register #(.width(7)) register_4 (
    .D(multiplexer_1_out), .en(demultiplexer_1_out3), .Q(output_buffer[27:21]), .clk(and_5_out), .clr(rst));
  Comparator #(.width(7), .mode("unsigned")) comparator_6 (
    .a(output_buffer[27:21]), .b(7'b0101101), .eq(comparator_6_eq));  // open: gt, lt
  Subtractor #(.width(11)) subtractor_1 (
    .a({4'b0000, output_buffer[27:21]}), .b(11'h30), .out(subtractor_1_out), .bout(subtractor_1_bout));  // open: bin
  Comparator #(.width(7), .mode("unsigned")) comparator_7 (
    .a(output_buffer[20:14]), .b(7'b0101101), .eq(comparator_7_eq));  // open: gt, lt
  Subtractor #(.width(11)) subtractor_2 (
    .a({4'b0000, output_buffer[20:14]}), .b(11'h30), .out(subtractor_2_out), .bout(subtractor_2_bout));  // open: bin
  Comparator #(.width(7), .mode("unsigned")) comparator_8 (
    .a(output_buffer[13:7]), .b(7'b0101101), .eq(comparator_8_eq));  // open: gt, lt
  Subtractor #(.width(11)) subtractor_3 (
    .a({4'b0000, output_buffer[13:7]}), .b(11'h30), .out(subtractor_3_out), .bout(subtractor_3_bout));  // open: bin
  Subtractor #(.width(11)) subtractor_4 (
    .a({4'b0000, output_buffer[6:0]}), .b(11'h30), .out(subtractor_4_out), .bout(subtractor_4_bout));  // open: bin
  Comparator #(.width(7), .mode("unsigned")) comparator_9 (
    .a(output_buffer[6:0]), .b(7'b0101101), .eq(comparator_9_eq));  // open: gt, lt
  nor nor_2 (nor_2_out, comparator_9_eq, subtractor_1_bout);
  Comparator #(.width(11), .mode("unsigned")) comparator_10 (
    .a({11{1'b0}}), .b(subtractor_3_out), .eq(comparator_10_eq));  // open: gt, lt
  Comparator #(.width(11), .mode("unsigned")) comparator_11 (
    .a({11{1'b0}}), .b(subtractor_4_out), .eq(comparator_11_eq));  // open: gt, lt
  or or_2 (or_2_out, subtractor_4_bout, comparator_9_eq);
  and and_6 (and_6_out, comparator_10_eq, comparator_9_eq);
  or or_3 (or_3_out, and_6_out, comparator_11_eq);
  Multiplexer #(.width(11), .enable("false")) multiplexer_2 (
    .in0(subtractor_2_out), .in1({11{1'b0}}), .out(multiplexer_2_out), .sel(subtractor_2_bout));
  not not_1 (not_1_out, subtractor_1_bout);
  Multiplexer #(.width(11), .enable("false")) multiplexer_3 (
    .in0(subtractor_3_out), .in1({11{1'b0}}), .out(multiplexer_3_out), .sel(subtractor_3_bout));
  Multiplexer #(.width(11), .enable("false")) multiplexer_4 (
    .in0(subtractor_4_out), .in1({11{1'b0}}), .out(multiplexer_4_out), .sel(or_2_out));
  Adder #(.width(2)) adder_1 (.a(Cursor_position), .b(2'b00), .out(adder_1_out), .cin(not_1_out));  // open: cout
  or or_4 (or_4_out, comparator_6_eq, comparator_7_eq, comparator_8_eq, nor_2_out, or_3_out);
  Multiplexer #(.width(11), .enable("false")) multiplexer_5 (
    .in0(subtractor_1_out), .in1({11{1'b0}}), .out(multiplexer_5_out), .sel(subtractor_1_bout));
  Multiplexer #(.select(2), .width(11), .enable("false")) multiplexer_6 (
    .in0(11'ha), .in1(11'h1), .in2(11'h1), .in3(11'h1), .out(multiplexer_6_out), .sel(adder_1_out));
  Multiplexer #(.select(2), .width(11), .enable("false")) multiplexer_7 (
    .in0(11'h64), .in1(11'h1), .in2(11'h1), .in3(11'ha), .out(multiplexer_7_out), .sel(adder_1_out));
  Multiplexer #(.select(2), .width(11), .enable("false")) multiplexer_8 (
    .in0(11'h1), .in1(11'h1), .in2(11'ha), .in3(11'h64), .out(multiplexer_8_out), .sel(Cursor_position));
  Multiplier #(.width(11)) multiplier_1 (
    .a(multiplexer_2_out), .b(multiplexer_6_out), .out(multiplier_1_out));  // open: cin, cout
  Multiplier #(.width(11)) multiplier_2 (
    .a(multiplexer_3_out), .b(multiplexer_7_out), .out(multiplier_2_out));  // open: cin, cout
  Multiplier #(.width(11)) multiplier_3 (
    .a(multiplexer_4_out), .b(multiplexer_8_out), .out(multiplier_3_out));  // open: cin, cout
  Adder #(.width(11)) adder_2 (.a(multiplexer_5_out), .b(adder_3_out), .out(adder_2_out));  // open: cin, cout
  assign not_2_out = ~adder_2_out;  // NOT_Gate not_2, 11 bits wide
  Adder #(.width(11)) adder_3 (.a(multiplier_1_out), .b(adder_4_out), .out(adder_3_out));  // open: cin, cout
  Adder #(.width(11)) adder_4 (.a(multiplier_2_out), .b(multiplier_3_out), .out(adder_4_out));  // open: cin, cout
  Multiplexer #(.width(11), .enable("false")) multiplexer_9 (
    .in0(adder_2_out), .in1(not_2_out), .out(multiplexer_9_out), .sel(comparator_9_eq));
  Adder #(.width(11)) adder_5 (
    .a(multiplexer_9_out), .b({11{1'b0}}), .out(adder_5_out), .cin(comparator_9_eq));  // open: cout
  Demultiplexer #(.enable("false")) demultiplexer_2 (.out0(ready), .out1(err), .in(comparator_5_eq), .sel(or_4_out));
  not not_3 (not_3_out, ready);
  Multiplexer #(.width(11), .enable("false")) multiplexer_10 (
    .in0(adder_5_out), .in1({11{1'b0}}), .out(output_number), .sel(not_3_out));
  // Probe on output_number

  // Notes on the sheet:
  //   input: pull=down
  //   clk: pull=down
  //   rst: pull=down
endmodule
