// Logisim project main.circ as structural Verilog: 2 circuits, main circuit main
module main (
);

  wire and_1_out, button_1_out, cell_controller_52_p31, cell_controller_53_p31, cell_controller_54_p31,
       cell_controller_55_p31, cell_controller_56_p31, clock_1_out, clock_2_out, clock_3_out,
       counter_1_carry, demultiplexer_1_out0, demultiplexer_1_out1, demultiplexer_1_out2,
       demultiplexer_1_out3, input_controller_1_active_led, input_controller_1_data_ready,
       input_controller_1_error_led, input_controller_1_kbd_clear, input_controller_1_kbd_clock,
       input_controller_1_kbd_en, input_controller_1_user_action_led, keyboard_1_avail, mcu_v2_1_p9,
       mcu_v2_1_p10, mcu_v2_1_p11, mcu_v2_1_p12, mcu_v2_1_p13, mcu_v2_1_p14, MISO, Y;
  wire [1:0] input_controller_1_cursor_position, mcu_v2_1_p16, MOSI;
  wire [4:0] cell_controller_1_p5, cell_controller_1_p8, cell_controller_1_p11, cell_controller_1_p14,
       cell_controller_1_p17, cell_controller_1_p20, cell_controller_1_p23, cell_controller_1_p26,
       cell_controller_1_p29, cell_controller_1_p32, cell_controller_1_p35, cell_controller_2_p5,
       cell_controller_2_p8, cell_controller_2_p11, cell_controller_2_p14, cell_controller_2_p17,
       cell_controller_2_p20, cell_controller_2_p23, cell_controller_2_p26, cell_controller_2_p29,
       cell_controller_2_p32, cell_controller_2_p35, cell_controller_3_p5, cell_controller_3_p8,
       cell_controller_3_p11, cell_controller_3_p14, cell_controller_3_p17, cell_controller_3_p20,
       cell_controller_3_p23, cell_controller_3_p26, cell_controller_3_p29, cell_controller_3_p32,
       cell_controller_3_p35, cell_controller_4_p5, cell_controller_4_p8, cell_controller_4_p11,
       cell_controller_4_p14, cell_controller_4_p17, cell_controller_4_p20, cell_controller_4_p23,
       cell_controller_4_p26, cell_controller_4_p29, cell_controller_4_p32, cell_controller_4_p35,
       cell_controller_5_p5, cell_controller_5_p8, cell_controller_5_p11, cell_controller_5_p14,
       cell_controller_5_p17, cell_controller_5_p20, cell_controller_5_p23, cell_controller_5_p26,
       cell_controller_5_p29, cell_controller_5_p32, cell_controller_5_p35, cell_controller_6_p5,
       cell_controller_6_p8, cell_controller_6_p11, cell_controller_6_p14, cell_controller_6_p17,
       cell_controller_6_p20, cell_controller_6_p23, cell_controller_6_p26, cell_controller_6_p29,
       cell_controller_6_p32, cell_controller_6_p35, cell_controller_7_p5, cell_controller_7_p8,
       cell_controller_7_p11, cell_controller_7_p14, cell_controller_7_p17, cell_controller_7_p20,
       cell_controller_7_p23, cell_controller_7_p26, cell_controller_7_p29, cell_controller_7_p32,
       cell_controller_7_p35, cell_controller_8_p5, cell_controller_8_p8, cell_controller_8_p11,
       cell_controller_8_p14, cell_controller_8_p17, cell_controller_8_p20, cell_controller_8_p23,
       cell_controller_8_p26, cell_controller_8_p29, cell_controller_8_p32, cell_controller_8_p35,
       cell_controller_9_p5, cell_controller_9_p8, cell_controller_9_p11, cell_controller_9_p14,
       cell_controller_9_p17, cell_controller_9_p20, cell_controller_9_p23, cell_controller_9_p26,
       cell_controller_9_p29, cell_controller_9_p32, cell_controller_9_p35, cell_controller_10_p5,
       cell_controller_10_p8, cell_controller_10_p11, cell_controller_10_p14, cell_controller_10_p17,
       cell_controller_10_p20, cell_controller_10_p23, cell_controller_10_p26, cell_controller_10_p29,
       cell_controller_10_p32, cell_controller_10_p35, cell_controller_11_p5, cell_controller_11_p8,
       cell_controller_11_p11, cell_controller_11_p14, cell_controller_11_p17, cell_controller_11_p20,
       cell_controller_11_p23, cell_controller_11_p26, cell_controller_11_p29, cell_controller_11_p32,
       cell_controller_11_p35, cell_controller_12_p5, cell_controller_12_p8, cell_controller_12_p11,
       cell_controller_12_p14, cell_controller_12_p17, cell_controller_12_p20, cell_controller_12_p23,
       cell_controller_12_p26, cell_controller_12_p29, cell_controller_12_p32, cell_controller_12_p35,
       cell_controller_13_p5, cell_controller_13_p8, cell_controller_13_p11, cell_controller_13_p14,
       cell_controller_13_p17, cell_controller_13_p20, cell_controller_13_p23, cell_controller_13_p26,
       cell_controller_13_p29, cell_controller_13_p32, cell_controller_13_p35, cell_controller_14_p5,
       cell_controller_14_p8, cell_controller_14_p11, cell_controller_14_p14, cell_controller_14_p17,
       cell_controller_14_p20, cell_controller_14_p23, cell_controller_14_p26, cell_controller_14_p29,
       cell_controller_14_p32, cell_controller_14_p35, cell_controller_15_p5, cell_controller_15_p8,
       cell_controller_15_p11, cell_controller_15_p14, cell_controller_15_p17, cell_controller_15_p20,
       cell_controller_15_p23, cell_controller_15_p26, cell_controller_15_p29, cell_controller_15_p32,
       cell_controller_15_p35, cell_controller_16_p5, cell_controller_16_p8, cell_controller_16_p11,
       cell_controller_16_p14, cell_controller_16_p17, cell_controller_16_p20, cell_controller_16_p23,
       cell_controller_16_p26, cell_controller_16_p29, cell_controller_16_p32, cell_controller_16_p35,
       cell_controller_17_p5, cell_controller_17_p8, cell_controller_17_p11, cell_controller_17_p14,
       cell_controller_17_p17, cell_controller_17_p20, cell_controller_17_p23, cell_controller_17_p26,
       cell_controller_17_p29, cell_controller_17_p32, cell_controller_17_p35, cell_controller_18_p5,
       cell_controller_18_p8, cell_controller_18_p11, cell_controller_18_p14, cell_controller_18_p17,
       cell_controller_18_p20, cell_controller_18_p23, cell_controller_18_p26, cell_controller_18_p29,
       cell_controller_18_p32, cell_controller_18_p35, cell_controller_19_p5, cell_controller_19_p8,
       cell_controller_19_p11, cell_controller_19_p14, cell_controller_19_p17, cell_controller_19_p20,
       cell_controller_19_p23, cell_controller_19_p26, cell_controller_19_p29, cell_controller_19_p32,
       cell_controller_19_p35, cell_controller_20_p5, cell_controller_20_p8, cell_controller_20_p11,
       cell_controller_20_p14, cell_controller_20_p17, cell_controller_20_p20, cell_controller_20_p23,
       cell_controller_20_p26, cell_controller_20_p29, cell_controller_20_p32, cell_controller_20_p35,
       cell_controller_21_p5, cell_controller_21_p8, cell_controller_21_p11, cell_controller_21_p14,
       cell_controller_21_p17, cell_controller_21_p20, cell_controller_21_p23, cell_controller_21_p26,
       cell_controller_21_p29, cell_controller_21_p32, cell_controller_21_p35, cell_controller_22_p5,
       cell_controller_22_p8, cell_controller_22_p11, cell_controller_22_p14, cell_controller_22_p17,
       cell_controller_22_p20, cell_controller_22_p23, cell_controller_22_p26, cell_controller_22_p29,
       cell_controller_22_p32, cell_controller_22_p35, cell_controller_23_p5, cell_controller_23_p8,
       cell_controller_23_p11, cell_controller_23_p14, cell_controller_23_p17, cell_controller_23_p20,
       cell_controller_23_p23, cell_controller_23_p26, cell_controller_23_p29, cell_controller_23_p32,
       cell_controller_23_p35, cell_controller_24_p5, cell_controller_24_p8, cell_controller_24_p11,
       cell_controller_24_p14, cell_controller_24_p17, cell_controller_24_p20, cell_controller_24_p23,
       cell_controller_24_p26, cell_controller_24_p29, cell_controller_24_p32, cell_controller_24_p35,
       cell_controller_25_p5, cell_controller_25_p8, cell_controller_25_p11, cell_controller_25_p14,
       cell_controller_25_p17, cell_controller_25_p20, cell_controller_25_p23, cell_controller_25_p26,
       cell_controller_25_p29, cell_controller_25_p32, cell_controller_25_p35, cell_controller_26_p5,
       cell_controller_26_p8, cell_controller_26_p11, cell_controller_26_p14, cell_controller_26_p17,
       cell_controller_26_p20, cell_controller_26_p23, cell_controller_26_p26, cell_controller_26_p29,
       cell_controller_26_p32, cell_controller_26_p35, cell_controller_27_p5, cell_controller_27_p8,
       cell_controller_27_p11, cell_controller_27_p14, cell_controller_27_p17, cell_controller_27_p20,
       cell_controller_27_p23, cell_controller_27_p26, cell_controller_27_p29, cell_controller_27_p32,
       cell_controller_27_p35, cell_controller_28_p5, cell_controller_28_p8, cell_controller_28_p11,
       cell_controller_28_p14, cell_controller_28_p17, cell_controller_28_p20, cell_controller_28_p23,
       cell_controller_28_p26, cell_controller_28_p29, cell_controller_28_p32, cell_controller_28_p35,
       cell_controller_29_p5, cell_controller_29_p8, cell_controller_29_p11, cell_controller_29_p14,
       cell_controller_29_p17, cell_controller_29_p20, cell_controller_29_p23, cell_controller_29_p26,
       cell_controller_29_p29, cell_controller_29_p32, cell_controller_29_p35, cell_controller_30_p5,
       cell_controller_30_p8, cell_controller_30_p11, cell_controller_30_p14, cell_controller_30_p17,
       cell_controller_30_p20, cell_controller_30_p23, cell_controller_30_p26, cell_controller_30_p29,
       cell_controller_30_p32, cell_controller_30_p35, cell_controller_31_p5, cell_controller_31_p8,
       cell_controller_31_p11, cell_controller_31_p14, cell_controller_31_p17, cell_controller_31_p20,
       cell_controller_31_p23, cell_controller_31_p26, cell_controller_31_p29, cell_controller_31_p32,
       cell_controller_31_p35, cell_controller_32_p5, cell_controller_32_p8, cell_controller_32_p11,
       cell_controller_32_p14, cell_controller_32_p17, cell_controller_32_p20, cell_controller_32_p23,
       cell_controller_32_p26, cell_controller_32_p29, cell_controller_32_p32, cell_controller_32_p35,
       cell_controller_33_p5, cell_controller_33_p8, cell_controller_33_p11, cell_controller_33_p14,
       cell_controller_33_p17, cell_controller_33_p20, cell_controller_33_p23, cell_controller_33_p26,
       cell_controller_33_p29, cell_controller_33_p32, cell_controller_33_p35, cell_controller_34_p5,
       cell_controller_34_p8, cell_controller_34_p11, cell_controller_34_p14, cell_controller_34_p17,
       cell_controller_34_p20, cell_controller_34_p23, cell_controller_34_p26, cell_controller_34_p29,
       cell_controller_34_p32, cell_controller_34_p35, cell_controller_35_p5, cell_controller_35_p8,
       cell_controller_35_p11, cell_controller_35_p14, cell_controller_35_p17, cell_controller_35_p20,
       cell_controller_35_p23, cell_controller_35_p26, cell_controller_35_p29, cell_controller_35_p32,
       cell_controller_35_p35, cell_controller_36_p5, cell_controller_36_p8, cell_controller_36_p11,
       cell_controller_36_p14, cell_controller_36_p17, cell_controller_36_p20, cell_controller_36_p23,
       cell_controller_36_p26, cell_controller_36_p29, cell_controller_36_p32, cell_controller_36_p35,
       cell_controller_37_p5, cell_controller_37_p8, cell_controller_37_p11, cell_controller_37_p14,
       cell_controller_37_p17, cell_controller_37_p20, cell_controller_37_p23, cell_controller_37_p26,
       cell_controller_37_p29, cell_controller_37_p32, cell_controller_37_p35, cell_controller_38_p5,
       cell_controller_38_p8, cell_controller_38_p11, cell_controller_38_p14, cell_controller_38_p17,
       cell_controller_38_p20, cell_controller_38_p23, cell_controller_38_p26, cell_controller_38_p29,
       cell_controller_38_p32, cell_controller_38_p35, cell_controller_39_p5, cell_controller_39_p8,
       cell_controller_39_p11, cell_controller_39_p14, cell_controller_39_p17, cell_controller_39_p20,
       cell_controller_39_p23, cell_controller_39_p26, cell_controller_39_p29, cell_controller_39_p32,
       cell_controller_39_p35, cell_controller_40_p5, cell_controller_40_p8, cell_controller_40_p11,
       cell_controller_40_p14, cell_controller_40_p17, cell_controller_40_p20, cell_controller_40_p23,
       cell_controller_40_p26, cell_controller_40_p29, cell_controller_40_p32, cell_controller_40_p35,
       cell_controller_41_p5, cell_controller_41_p8, cell_controller_41_p11, cell_controller_41_p14,
       cell_controller_41_p17, cell_controller_41_p20, cell_controller_41_p23, cell_controller_41_p26,
       cell_controller_41_p29, cell_controller_41_p32, cell_controller_41_p35, cell_controller_42_p5,
       cell_controller_42_p8, cell_controller_42_p11, cell_controller_42_p14, cell_controller_42_p17,
       cell_controller_42_p20, cell_controller_42_p23, cell_controller_42_p26, cell_controller_42_p29,
       cell_controller_42_p32, cell_controller_42_p35, cell_controller_43_p5, cell_controller_43_p8,
       cell_controller_43_p11, cell_controller_43_p14, cell_controller_43_p17, cell_controller_43_p20,
       cell_controller_43_p23, cell_controller_43_p26, cell_controller_43_p29, cell_controller_43_p32,
       cell_controller_43_p35, cell_controller_44_p5, cell_controller_44_p8, cell_controller_44_p11,
       cell_controller_44_p14, cell_controller_44_p17, cell_controller_44_p20, cell_controller_44_p23,
       cell_controller_44_p26, cell_controller_44_p29, cell_controller_44_p32, cell_controller_44_p35,
       cell_controller_45_p5, cell_controller_45_p8, cell_controller_45_p11, cell_controller_45_p14,
       cell_controller_45_p17, cell_controller_45_p20, cell_controller_45_p23, cell_controller_45_p26,
       cell_controller_45_p29, cell_controller_45_p32, cell_controller_45_p35, cell_controller_46_p5,
       cell_controller_46_p8, cell_controller_46_p11, cell_controller_46_p14, cell_controller_46_p17,
       cell_controller_46_p20, cell_controller_46_p23, cell_controller_46_p26, cell_controller_46_p29,
       cell_controller_46_p32, cell_controller_46_p35, cell_controller_47_p5, cell_controller_47_p8,
       cell_controller_47_p11, cell_controller_47_p14, cell_controller_47_p17, cell_controller_47_p20,
       cell_controller_47_p23, cell_controller_47_p26, cell_controller_47_p29, cell_controller_47_p32,
       cell_controller_47_p35, cell_controller_48_p5, cell_controller_48_p8, cell_controller_48_p11,
       cell_controller_48_p14, cell_controller_48_p17, cell_controller_48_p20, cell_controller_48_p23,
       cell_controller_48_p26, cell_controller_48_p29, cell_controller_48_p32, cell_controller_48_p35,
       cell_controller_49_p5, cell_controller_49_p8, cell_controller_49_p11, cell_controller_49_p14,
       cell_controller_49_p17, cell_controller_49_p20, cell_controller_49_p23, cell_controller_49_p26,
       cell_controller_49_p29, cell_controller_49_p32, cell_controller_49_p35, cell_controller_50_p5,
       cell_controller_50_p8, cell_controller_50_p11, cell_controller_50_p14, cell_controller_50_p17,
       cell_controller_50_p20, cell_controller_50_p23, cell_controller_50_p26, cell_controller_50_p29,
       cell_controller_50_p32, cell_controller_50_p35, cell_controller_51_p5, cell_controller_51_p8,
       cell_controller_51_p11, cell_controller_51_p14, cell_controller_51_p17, cell_controller_51_p20,
       cell_controller_51_p23, cell_controller_51_p26, cell_controller_51_p29, cell_controller_51_p32,
       cell_controller_51_p35, cell_controller_52_p5, cell_controller_52_p8, cell_controller_52_p11,
       cell_controller_52_p14, cell_controller_52_p17, cell_controller_52_p20, cell_controller_52_p23,
       cell_controller_52_p26, cell_controller_52_p29, cell_controller_52_p33, cell_controller_52_p37,
       cell_controller_53_p5, cell_controller_53_p8, cell_controller_53_p11, cell_controller_53_p14,
       cell_controller_53_p17, cell_controller_53_p20, cell_controller_53_p23, cell_controller_53_p26,
       cell_controller_53_p29, cell_controller_53_p33, cell_controller_53_p37, cell_controller_54_p5,
       cell_controller_54_p8, cell_controller_54_p11, cell_controller_54_p14, cell_controller_54_p17,
       cell_controller_54_p20, cell_controller_54_p23, cell_controller_54_p26, cell_controller_54_p29,
       cell_controller_54_p33, cell_controller_54_p37, cell_controller_55_p5, cell_controller_55_p8,
       cell_controller_55_p11, cell_controller_55_p14, cell_controller_55_p17, cell_controller_55_p20,
       cell_controller_55_p23, cell_controller_55_p26, cell_controller_55_p29, cell_controller_55_p33,
       cell_controller_55_p37, cell_controller_56_p5, cell_controller_56_p8, cell_controller_56_p11,
       cell_controller_56_p14, cell_controller_56_p17, cell_controller_56_p20, cell_controller_56_p23,
       cell_controller_56_p26, cell_controller_56_p29, cell_controller_56_p33, cell_controller_56_p37,
       cell_controller_57_p5, cell_controller_57_p8, cell_controller_57_p11, cell_controller_57_p14,
       cell_controller_57_p17, cell_controller_57_p20, cell_controller_57_p23, cell_controller_57_p26,
       cell_controller_57_p29, cell_controller_57_p32, cell_controller_57_p35, cell_controller_58_p5,
       cell_controller_58_p8, cell_controller_58_p11, cell_controller_58_p14, cell_controller_58_p17,
       cell_controller_58_p20, cell_controller_58_p23, cell_controller_58_p26, cell_controller_58_p29,
       cell_controller_58_p32, cell_controller_58_p35, cell_controller_59_p5, cell_controller_59_p8,
       cell_controller_59_p11, cell_controller_59_p14, cell_controller_59_p17, cell_controller_59_p20,
       cell_controller_59_p23, cell_controller_59_p26, cell_controller_59_p29, cell_controller_59_p32,
       cell_controller_59_p35, cell_controller_60_p5, cell_controller_60_p8, cell_controller_60_p11,
       cell_controller_60_p14, cell_controller_60_p17, cell_controller_60_p20, cell_controller_60_p23,
       cell_controller_60_p26, cell_controller_60_p29, cell_controller_60_p32, cell_controller_60_p35,
       cell_controller_61_p5, cell_controller_61_p8, cell_controller_61_p11, cell_controller_61_p14,
       cell_controller_61_p17, cell_controller_61_p20, cell_controller_61_p23, cell_controller_61_p26,
       cell_controller_61_p29, cell_controller_61_p32, cell_controller_61_p35, cell_controller_62_p5,
       cell_controller_62_p8, cell_controller_62_p11, cell_controller_62_p14, cell_controller_62_p17,
       cell_controller_62_p20, cell_controller_62_p23, cell_controller_62_p26, cell_controller_62_p29,
       cell_controller_62_p32, cell_controller_62_p35, cell_controller_63_p5, cell_controller_63_p8,
       cell_controller_63_p11, cell_controller_63_p14, cell_controller_63_p17, cell_controller_63_p20,
       cell_controller_63_p23, cell_controller_63_p26, cell_controller_63_p29, cell_controller_63_p32,
       cell_controller_63_p35, cell_controller_64_p5, cell_controller_64_p8, cell_controller_64_p11,
       cell_controller_64_p14, cell_controller_64_p17, cell_controller_64_p20, cell_controller_64_p23,
       cell_controller_64_p26, cell_controller_64_p29, cell_controller_64_p32, cell_controller_64_p35,
       input_controller_1_command_parsed_from_user_input;
  wire [6:0] input_controller_1_input_buffer_2, input_controller_1_input_buffer_3, keyboard_1_data;
  wire [7:0] cell_controller_1_p6, cell_controller_1_p7, cell_controller_1_p9, cell_controller_1_p10,
       cell_controller_1_p12, cell_controller_1_p13, cell_controller_1_p15, cell_controller_1_p16,
       cell_controller_1_p18, cell_controller_1_p19, cell_controller_1_p21, cell_controller_1_p22,
       cell_controller_1_p24, cell_controller_1_p25, cell_controller_1_p27, cell_controller_1_p28,
       cell_controller_1_p30, cell_controller_1_p31, cell_controller_1_p33, cell_controller_1_p34,
       cell_controller_1_p36, cell_controller_1_p37, cell_controller_2_p6, cell_controller_2_p7,
       cell_controller_2_p9, cell_controller_2_p10, cell_controller_2_p12, cell_controller_2_p13,
       cell_controller_2_p15, cell_controller_2_p16, cell_controller_2_p18, cell_controller_2_p19,
       cell_controller_2_p21, cell_controller_2_p22, cell_controller_2_p24, cell_controller_2_p25,
       cell_controller_2_p27, cell_controller_2_p28, cell_controller_2_p30, cell_controller_2_p31,
       cell_controller_2_p33, cell_controller_2_p34, cell_controller_2_p36, cell_controller_2_p37,
       cell_controller_3_p6, cell_controller_3_p7, cell_controller_3_p9, cell_controller_3_p10,
       cell_controller_3_p12, cell_controller_3_p13, cell_controller_3_p15, cell_controller_3_p16,
       cell_controller_3_p18, cell_controller_3_p19, cell_controller_3_p21, cell_controller_3_p22,
       cell_controller_3_p24, cell_controller_3_p25, cell_controller_3_p27, cell_controller_3_p28,
       cell_controller_3_p30, cell_controller_3_p31, cell_controller_3_p33, cell_controller_3_p34,
       cell_controller_3_p36, cell_controller_3_p37, cell_controller_4_p6, cell_controller_4_p7,
       cell_controller_4_p9, cell_controller_4_p10, cell_controller_4_p12, cell_controller_4_p13,
       cell_controller_4_p15, cell_controller_4_p16, cell_controller_4_p18, cell_controller_4_p19,
       cell_controller_4_p21, cell_controller_4_p22, cell_controller_4_p24, cell_controller_4_p25,
       cell_controller_4_p27, cell_controller_4_p28, cell_controller_4_p30, cell_controller_4_p31,
       cell_controller_4_p33, cell_controller_4_p34, cell_controller_4_p36, cell_controller_4_p37,
       cell_controller_5_p6, cell_controller_5_p7, cell_controller_5_p9, cell_controller_5_p10,
       cell_controller_5_p12, cell_controller_5_p13, cell_controller_5_p15, cell_controller_5_p16,
       cell_controller_5_p18, cell_controller_5_p19, cell_controller_5_p21, cell_controller_5_p22,
       cell_controller_5_p24, cell_controller_5_p25, cell_controller_5_p27, cell_controller_5_p28,
       cell_controller_5_p30, cell_controller_5_p31, cell_controller_5_p33, cell_controller_5_p34,
       cell_controller_5_p36, cell_controller_5_p37, cell_controller_6_p6, cell_controller_6_p7,
       cell_controller_6_p9, cell_controller_6_p10, cell_controller_6_p12, cell_controller_6_p13,
       cell_controller_6_p15, cell_controller_6_p16, cell_controller_6_p18, cell_controller_6_p19,
       cell_controller_6_p21, cell_controller_6_p22, cell_controller_6_p24, cell_controller_6_p25,
       cell_controller_6_p27, cell_controller_6_p28, cell_controller_6_p30, cell_controller_6_p31,
       cell_controller_6_p33, cell_controller_6_p34, cell_controller_6_p36, cell_controller_6_p37,
       cell_controller_7_p6, cell_controller_7_p7, cell_controller_7_p9, cell_controller_7_p10,
       cell_controller_7_p12, cell_controller_7_p13, cell_controller_7_p15, cell_controller_7_p16,
       cell_controller_7_p18, cell_controller_7_p19, cell_controller_7_p21, cell_controller_7_p22,
       cell_controller_7_p24, cell_controller_7_p25, cell_controller_7_p27, cell_controller_7_p28,
       cell_controller_7_p30, cell_controller_7_p31, cell_controller_7_p33, cell_controller_7_p34,
       cell_controller_7_p36, cell_controller_7_p37, cell_controller_8_p6, cell_controller_8_p7,
       cell_controller_8_p9, cell_controller_8_p10, cell_controller_8_p12, cell_controller_8_p13,
       cell_controller_8_p15, cell_controller_8_p16, cell_controller_8_p18, cell_controller_8_p19,
       cell_controller_8_p21, cell_controller_8_p22, cell_controller_8_p24, cell_controller_8_p25,
       cell_controller_8_p27, cell_controller_8_p28, cell_controller_8_p30, cell_controller_8_p31,
       cell_controller_8_p33, cell_controller_8_p34, cell_controller_8_p36, cell_controller_8_p37,
       cell_controller_9_p6, cell_controller_9_p7, cell_controller_9_p9, cell_controller_9_p10,
       cell_controller_9_p12, cell_controller_9_p13, cell_controller_9_p15, cell_controller_9_p16,
       cell_controller_9_p18, cell_controller_9_p19, cell_controller_9_p21, cell_controller_9_p22,
       cell_controller_9_p24, cell_controller_9_p25, cell_controller_9_p27, cell_controller_9_p28,
       cell_controller_9_p30, cell_controller_9_p31, cell_controller_9_p33, cell_controller_9_p34,
       cell_controller_9_p36, cell_controller_9_p37, cell_controller_10_p6, cell_controller_10_p7,
       cell_controller_10_p9, cell_controller_10_p10, cell_controller_10_p12, cell_controller_10_p13,
       cell_controller_10_p15, cell_controller_10_p16, cell_controller_10_p18, cell_controller_10_p19,
       cell_controller_10_p21, cell_controller_10_p22, cell_controller_10_p24, cell_controller_10_p25,
       cell_controller_10_p27, cell_controller_10_p28, cell_controller_10_p30, cell_controller_10_p31,
       cell_controller_10_p33, cell_controller_10_p34, cell_controller_10_p36, cell_controller_10_p37,
       cell_controller_11_p6, cell_controller_11_p7, cell_controller_11_p9, cell_controller_11_p10,
       cell_controller_11_p12, cell_controller_11_p13, cell_controller_11_p15, cell_controller_11_p16,
       cell_controller_11_p18, cell_controller_11_p19, cell_controller_11_p21, cell_controller_11_p22,
       cell_controller_11_p24, cell_controller_11_p25, cell_controller_11_p27, cell_controller_11_p28,
       cell_controller_11_p30, cell_controller_11_p31, cell_controller_11_p33, cell_controller_11_p34,
       cell_controller_11_p36, cell_controller_11_p37, cell_controller_12_p6, cell_controller_12_p7,
       cell_controller_12_p9, cell_controller_12_p10, cell_controller_12_p12, cell_controller_12_p13,
       cell_controller_12_p15, cell_controller_12_p16, cell_controller_12_p18, cell_controller_12_p19,
       cell_controller_12_p21, cell_controller_12_p22, cell_controller_12_p24, cell_controller_12_p25,
       cell_controller_12_p27, cell_controller_12_p28, cell_controller_12_p30, cell_controller_12_p31,
       cell_controller_12_p33, cell_controller_12_p34, cell_controller_12_p36, cell_controller_12_p37,
       cell_controller_13_p6, cell_controller_13_p7, cell_controller_13_p9, cell_controller_13_p10,
       cell_controller_13_p12, cell_controller_13_p13, cell_controller_13_p15, cell_controller_13_p16,
       cell_controller_13_p18, cell_controller_13_p19, cell_controller_13_p21, cell_controller_13_p22,
       cell_controller_13_p24, cell_controller_13_p25, cell_controller_13_p27, cell_controller_13_p28,
       cell_controller_13_p30, cell_controller_13_p31, cell_controller_13_p33, cell_controller_13_p34,
       cell_controller_13_p36, cell_controller_13_p37, cell_controller_14_p6, cell_controller_14_p7,
       cell_controller_14_p9, cell_controller_14_p10, cell_controller_14_p12, cell_controller_14_p13,
       cell_controller_14_p15, cell_controller_14_p16, cell_controller_14_p18, cell_controller_14_p19,
       cell_controller_14_p21, cell_controller_14_p22, cell_controller_14_p24, cell_controller_14_p25,
       cell_controller_14_p27, cell_controller_14_p28, cell_controller_14_p30, cell_controller_14_p31,
       cell_controller_14_p33, cell_controller_14_p34, cell_controller_14_p36, cell_controller_14_p37,
       cell_controller_15_p6, cell_controller_15_p7, cell_controller_15_p9, cell_controller_15_p10,
       cell_controller_15_p12, cell_controller_15_p13, cell_controller_15_p15, cell_controller_15_p16,
       cell_controller_15_p18, cell_controller_15_p19, cell_controller_15_p21, cell_controller_15_p22,
       cell_controller_15_p24, cell_controller_15_p25, cell_controller_15_p27, cell_controller_15_p28,
       cell_controller_15_p30, cell_controller_15_p31, cell_controller_15_p33, cell_controller_15_p34,
       cell_controller_15_p36, cell_controller_15_p37, cell_controller_16_p6, cell_controller_16_p7,
       cell_controller_16_p9, cell_controller_16_p10, cell_controller_16_p12, cell_controller_16_p13,
       cell_controller_16_p15, cell_controller_16_p16, cell_controller_16_p18, cell_controller_16_p19,
       cell_controller_16_p21, cell_controller_16_p22, cell_controller_16_p24, cell_controller_16_p25,
       cell_controller_16_p27, cell_controller_16_p28, cell_controller_16_p30, cell_controller_16_p31,
       cell_controller_16_p33, cell_controller_16_p34, cell_controller_16_p36, cell_controller_16_p37,
       cell_controller_17_p6, cell_controller_17_p7, cell_controller_17_p9, cell_controller_17_p10,
       cell_controller_17_p12, cell_controller_17_p13, cell_controller_17_p15, cell_controller_17_p16,
       cell_controller_17_p18, cell_controller_17_p19, cell_controller_17_p21, cell_controller_17_p22,
       cell_controller_17_p24, cell_controller_17_p25, cell_controller_17_p27, cell_controller_17_p28,
       cell_controller_17_p30, cell_controller_17_p31, cell_controller_17_p33, cell_controller_17_p34,
       cell_controller_17_p36, cell_controller_17_p37, cell_controller_18_p6, cell_controller_18_p7,
       cell_controller_18_p9, cell_controller_18_p10, cell_controller_18_p12, cell_controller_18_p13,
       cell_controller_18_p15, cell_controller_18_p16, cell_controller_18_p18, cell_controller_18_p19,
       cell_controller_18_p21, cell_controller_18_p22, cell_controller_18_p24, cell_controller_18_p25,
       cell_controller_18_p27, cell_controller_18_p28, cell_controller_18_p30, cell_controller_18_p31,
       cell_controller_18_p33, cell_controller_18_p34, cell_controller_18_p36, cell_controller_18_p37,
       cell_controller_19_p6, cell_controller_19_p7, cell_controller_19_p9, cell_controller_19_p10,
       cell_controller_19_p12, cell_controller_19_p13, cell_controller_19_p15, cell_controller_19_p16,
       cell_controller_19_p18, cell_controller_19_p19, cell_controller_19_p21, cell_controller_19_p22,
       cell_controller_19_p24, cell_controller_19_p25, cell_controller_19_p27, cell_controller_19_p28,
       cell_controller_19_p30, cell_controller_19_p31, cell_controller_19_p33, cell_controller_19_p34,
       cell_controller_19_p36, cell_controller_19_p37, cell_controller_20_p6, cell_controller_20_p7,
       cell_controller_20_p9, cell_controller_20_p10, cell_controller_20_p12, cell_controller_20_p13,
       cell_controller_20_p15, cell_controller_20_p16, cell_controller_20_p18, cell_controller_20_p19,
       cell_controller_20_p21, cell_controller_20_p22, cell_controller_20_p24, cell_controller_20_p25,
       cell_controller_20_p27, cell_controller_20_p28, cell_controller_20_p30, cell_controller_20_p31,
       cell_controller_20_p33, cell_controller_20_p34, cell_controller_20_p36, cell_controller_20_p37,
       cell_controller_21_p6, cell_controller_21_p7, cell_controller_21_p9, cell_controller_21_p10,
       cell_controller_21_p12, cell_controller_21_p13, cell_controller_21_p15, cell_controller_21_p16,
       cell_controller_21_p18, cell_controller_21_p19, cell_controller_21_p21, cell_controller_21_p22,
       cell_controller_21_p24, cell_controller_21_p25, cell_controller_21_p27, cell_controller_21_p28,
       cell_controller_21_p30, cell_controller_21_p31, cell_controller_21_p33, cell_controller_21_p34,
       cell_controller_21_p36, cell_controller_21_p37, cell_controller_22_p6, cell_controller_22_p7,
       cell_controller_22_p9, cell_controller_22_p10, cell_controller_22_p12, cell_controller_22_p13,
       cell_controller_22_p15, cell_controller_22_p16, cell_controller_22_p18, cell_controller_22_p19,
       cell_controller_22_p21, cell_controller_22_p22, cell_controller_22_p24, cell_controller_22_p25,
       cell_controller_22_p27, cell_controller_22_p28, cell_controller_22_p30, cell_controller_22_p31,
       cell_controller_22_p33, cell_controller_22_p34, cell_controller_22_p36, cell_controller_22_p37,
       cell_controller_23_p6, cell_controller_23_p7, cell_controller_23_p9, cell_controller_23_p10,
       cell_controller_23_p12, cell_controller_23_p13, cell_controller_23_p15, cell_controller_23_p16,
       cell_controller_23_p18, cell_controller_23_p19, cell_controller_23_p21, cell_controller_23_p22,
       cell_controller_23_p24, cell_controller_23_p25, cell_controller_23_p27, cell_controller_23_p28,
       cell_controller_23_p30, cell_controller_23_p31, cell_controller_23_p33, cell_controller_23_p34,
       cell_controller_23_p36, cell_controller_23_p37, cell_controller_24_p6, cell_controller_24_p7,
       cell_controller_24_p9, cell_controller_24_p10, cell_controller_24_p12, cell_controller_24_p13,
       cell_controller_24_p15, cell_controller_24_p16, cell_controller_24_p18, cell_controller_24_p19,
       cell_controller_24_p21, cell_controller_24_p22, cell_controller_24_p24, cell_controller_24_p25,
       cell_controller_24_p27, cell_controller_24_p28, cell_controller_24_p30, cell_controller_24_p31,
       cell_controller_24_p33, cell_controller_24_p34, cell_controller_24_p36, cell_controller_24_p37,
       cell_controller_25_p6, cell_controller_25_p7, cell_controller_25_p9, cell_controller_25_p10,
       cell_controller_25_p12, cell_controller_25_p13, cell_controller_25_p15, cell_controller_25_p16,
       cell_controller_25_p18, cell_controller_25_p19, cell_controller_25_p21, cell_controller_25_p22,
       cell_controller_25_p24, cell_controller_25_p25, cell_controller_25_p27, cell_controller_25_p28,
       cell_controller_25_p30, cell_controller_25_p31, cell_controller_25_p33, cell_controller_25_p34,
       cell_controller_25_p36, cell_controller_25_p37, cell_controller_26_p6, cell_controller_26_p7,
       cell_controller_26_p9, cell_controller_26_p10, cell_controller_26_p12, cell_controller_26_p13,
       cell_controller_26_p15, cell_controller_26_p16, cell_controller_26_p18, cell_controller_26_p19,
       cell_controller_26_p21, cell_controller_26_p22, cell_controller_26_p24, cell_controller_26_p25,
       cell_controller_26_p27, cell_controller_26_p28, cell_controller_26_p30, cell_controller_26_p31,
       cell_controller_26_p33, cell_controller_26_p34, cell_controller_26_p36, cell_controller_26_p37,
       cell_controller_27_p6, cell_controller_27_p7, cell_controller_27_p9, cell_controller_27_p10,
       cell_controller_27_p12, cell_controller_27_p13, cell_controller_27_p15, cell_controller_27_p16,
       cell_controller_27_p18, cell_controller_27_p19, cell_controller_27_p21, cell_controller_27_p22,
       cell_controller_27_p24, cell_controller_27_p25, cell_controller_27_p27, cell_controller_27_p28,
       cell_controller_27_p30, cell_controller_27_p31, cell_controller_27_p33, cell_controller_27_p34,
       cell_controller_27_p36, cell_controller_27_p37, cell_controller_28_p6, cell_controller_28_p7,
       cell_controller_28_p9, cell_controller_28_p10, cell_controller_28_p12, cell_controller_28_p13,
       cell_controller_28_p15, cell_controller_28_p16, cell_controller_28_p18, cell_controller_28_p19,
       cell_controller_28_p21, cell_controller_28_p22, cell_controller_28_p24, cell_controller_28_p25,
       cell_controller_28_p27, cell_controller_28_p28, cell_controller_28_p30, cell_controller_28_p31,
       cell_controller_28_p33, cell_controller_28_p34, cell_controller_28_p36, cell_controller_28_p37,
       cell_controller_29_p6, cell_controller_29_p7, cell_controller_29_p9, cell_controller_29_p10,
       cell_controller_29_p12, cell_controller_29_p13, cell_controller_29_p15, cell_controller_29_p16,
       cell_controller_29_p18, cell_controller_29_p19, cell_controller_29_p21, cell_controller_29_p22,
       cell_controller_29_p24, cell_controller_29_p25, cell_controller_29_p27, cell_controller_29_p28,
       cell_controller_29_p30, cell_controller_29_p31, cell_controller_29_p33, cell_controller_29_p34,
       cell_controller_29_p36, cell_controller_29_p37, cell_controller_30_p6, cell_controller_30_p7,
       cell_controller_30_p9, cell_controller_30_p10, cell_controller_30_p12, cell_controller_30_p13,
       cell_controller_30_p15, cell_controller_30_p16, cell_controller_30_p18, cell_controller_30_p19,
       cell_controller_30_p21, cell_controller_30_p22, cell_controller_30_p24, cell_controller_30_p25,
       cell_controller_30_p27, cell_controller_30_p28, cell_controller_30_p30, cell_controller_30_p31,
       cell_controller_30_p33, cell_controller_30_p34, cell_controller_30_p36, cell_controller_30_p37,
       cell_controller_31_p6, cell_controller_31_p7, cell_controller_31_p9, cell_controller_31_p10,
       cell_controller_31_p12, cell_controller_31_p13, cell_controller_31_p15, cell_controller_31_p16,
       cell_controller_31_p18, cell_controller_31_p19, cell_controller_31_p21, cell_controller_31_p22,
       cell_controller_31_p24, cell_controller_31_p25, cell_controller_31_p27, cell_controller_31_p28,
       cell_controller_31_p30, cell_controller_31_p31, cell_controller_31_p33, cell_controller_31_p34,
       cell_controller_31_p36, cell_controller_31_p37, cell_controller_32_p6, cell_controller_32_p7,
       cell_controller_32_p9, cell_controller_32_p10, cell_controller_32_p12, cell_controller_32_p13,
       cell_controller_32_p15, cell_controller_32_p16, cell_controller_32_p18, cell_controller_32_p19,
       cell_controller_32_p21, cell_controller_32_p22, cell_controller_32_p24, cell_controller_32_p25,
       cell_controller_32_p27, cell_controller_32_p28, cell_controller_32_p30, cell_controller_32_p31,
       cell_controller_32_p33, cell_controller_32_p34, cell_controller_32_p36, cell_controller_32_p37,
       cell_controller_33_p6, cell_controller_33_p7, cell_controller_33_p9, cell_controller_33_p10,
       cell_controller_33_p12, cell_controller_33_p13, cell_controller_33_p15, cell_controller_33_p16,
       cell_controller_33_p18, cell_controller_33_p19, cell_controller_33_p21, cell_controller_33_p22,
       cell_controller_33_p24, cell_controller_33_p25, cell_controller_33_p27, cell_controller_33_p28,
       cell_controller_33_p30, cell_controller_33_p31, cell_controller_33_p33, cell_controller_33_p34,
       cell_controller_33_p36, cell_controller_33_p37, cell_controller_34_p6, cell_controller_34_p7,
       cell_controller_34_p9, cell_controller_34_p10, cell_controller_34_p12, cell_controller_34_p13,
       cell_controller_34_p15, cell_controller_34_p16, cell_controller_34_p18, cell_controller_34_p19,
       cell_controller_34_p21, cell_controller_34_p22, cell_controller_34_p24, cell_controller_34_p25,
       cell_controller_34_p27, cell_controller_34_p28, cell_controller_34_p30, cell_controller_34_p31,
       cell_controller_34_p33, cell_controller_34_p34, cell_controller_34_p36, cell_controller_34_p37,
       cell_controller_35_p6, cell_controller_35_p7, cell_controller_35_p9, cell_controller_35_p10,
       cell_controller_35_p12, cell_controller_35_p13, cell_controller_35_p15, cell_controller_35_p16,
       cell_controller_35_p18, cell_controller_35_p19, cell_controller_35_p21, cell_controller_35_p22,
       cell_controller_35_p24, cell_controller_35_p25, cell_controller_35_p27, cell_controller_35_p28,
       cell_controller_35_p30, cell_controller_35_p31, cell_controller_35_p33, cell_controller_35_p34,
       cell_controller_35_p36, cell_controller_35_p37, cell_controller_36_p6, cell_controller_36_p7,
       cell_controller_36_p9, cell_controller_36_p10, cell_controller_36_p12, cell_controller_36_p13,
       cell_controller_36_p15, cell_controller_36_p16, cell_controller_36_p18, cell_controller_36_p19,
       cell_controller_36_p21, cell_controller_36_p22, cell_controller_36_p24, cell_controller_36_p25,
       cell_controller_36_p27, cell_controller_36_p28, cell_controller_36_p30, cell_controller_36_p31,
       cell_controller_36_p33, cell_controller_36_p34, cell_controller_36_p36, cell_controller_36_p37,
       cell_controller_37_p6, cell_controller_37_p7, cell_controller_37_p9, cell_controller_37_p10,
       cell_controller_37_p12, cell_controller_37_p13, cell_controller_37_p15, cell_controller_37_p16,
       cell_controller_37_p18, cell_controller_37_p19, cell_controller_37_p21, cell_controller_37_p22,
       cell_controller_37_p24, cell_controller_37_p25, cell_controller_37_p27, cell_controller_37_p28,
       cell_controller_37_p30, cell_controller_37_p31, cell_controller_37_p33, cell_controller_37_p34,
       cell_controller_37_p36, cell_controller_37_p37, cell_controller_38_p6, cell_controller_38_p7,
       cell_controller_38_p9, cell_controller_38_p10, cell_controller_38_p12, cell_controller_38_p13,
       cell_controller_38_p15, cell_controller_38_p16, cell_controller_38_p18, cell_controller_38_p19,
       cell_controller_38_p21, cell_controller_38_p22, cell_controller_38_p24, cell_controller_38_p25,
       cell_controller_38_p27, cell_controller_38_p28, cell_controller_38_p30, cell_controller_38_p31,
       cell_controller_38_p33, cell_controller_38_p34, cell_controller_38_p36, cell_controller_38_p37,
       cell_controller_39_p6, cell_controller_39_p7, cell_controller_39_p9, cell_controller_39_p10,
       cell_controller_39_p12, cell_controller_39_p13, cell_controller_39_p15, cell_controller_39_p16,
       cell_controller_39_p18, cell_controller_39_p19, cell_controller_39_p21, cell_controller_39_p22,
       cell_controller_39_p24, cell_controller_39_p25, cell_controller_39_p27, cell_controller_39_p28,
       cell_controller_39_p30, cell_controller_39_p31, cell_controller_39_p33, cell_controller_39_p34,
       cell_controller_39_p36, cell_controller_39_p37, cell_controller_40_p6, cell_controller_40_p7,
       cell_controller_40_p9, cell_controller_40_p10, cell_controller_40_p12, cell_controller_40_p13,
       cell_controller_40_p15, cell_controller_40_p16, cell_controller_40_p18, cell_controller_40_p19,
       cell_controller_40_p21, cell_controller_40_p22, cell_controller_40_p24, cell_controller_40_p25,
       cell_controller_40_p27, cell_controller_40_p28, cell_controller_40_p30, cell_controller_40_p31,
       cell_controller_40_p33, cell_controller_40_p34, cell_controller_40_p36, cell_controller_40_p37,
       cell_controller_41_p6, cell_controller_41_p7, cell_controller_41_p9, cell_controller_41_p10,
       cell_controller_41_p12, cell_controller_41_p13, cell_controller_41_p15, cell_controller_41_p16,
       cell_controller_41_p18, cell_controller_41_p19, cell_controller_41_p21, cell_controller_41_p22,
       cell_controller_41_p24, cell_controller_41_p25, cell_controller_41_p27, cell_controller_41_p28,
       cell_controller_41_p30, cell_controller_41_p31, cell_controller_41_p33, cell_controller_41_p34,
       cell_controller_41_p36, cell_controller_41_p37, cell_controller_42_p6, cell_controller_42_p7,
       cell_controller_42_p9, cell_controller_42_p10, cell_controller_42_p12, cell_controller_42_p13,
       cell_controller_42_p15, cell_controller_42_p16, cell_controller_42_p18, cell_controller_42_p19,
       cell_controller_42_p21, cell_controller_42_p22, cell_controller_42_p24, cell_controller_42_p25,
       cell_controller_42_p27, cell_controller_42_p28, cell_controller_42_p30, cell_controller_42_p31,
       cell_controller_42_p33, cell_controller_42_p34, cell_controller_42_p36, cell_controller_42_p37,
       cell_controller_43_p6, cell_controller_43_p7, cell_controller_43_p9, cell_controller_43_p10,
       cell_controller_43_p12, cell_controller_43_p13, cell_controller_43_p15, cell_controller_43_p16,
       cell_controller_43_p18, cell_controller_43_p19, cell_controller_43_p21, cell_controller_43_p22,
       cell_controller_43_p24, cell_controller_43_p25, cell_controller_43_p27, cell_controller_43_p28,
       cell_controller_43_p30, cell_controller_43_p31, cell_controller_43_p33, cell_controller_43_p34,
       cell_controller_43_p36, cell_controller_43_p37, cell_controller_44_p6, cell_controller_44_p7,
       cell_controller_44_p9, cell_controller_44_p10, cell_controller_44_p12, cell_controller_44_p13,
       cell_controller_44_p15, cell_controller_44_p16, cell_controller_44_p18, cell_controller_44_p19,
       cell_controller_44_p21, cell_controller_44_p22, cell_controller_44_p24, cell_controller_44_p25,
       cell_controller_44_p27, cell_controller_44_p28, cell_controller_44_p30, cell_controller_44_p31,
       cell_controller_44_p33, cell_controller_44_p34, cell_controller_44_p36, cell_controller_44_p37,
       cell_controller_45_p6, cell_controller_45_p7, cell_controller_45_p9, cell_controller_45_p10,
       cell_controller_45_p12, cell_controller_45_p13, cell_controller_45_p15, cell_controller_45_p16,
       cell_controller_45_p18, cell_controller_45_p19, cell_controller_45_p21, cell_controller_45_p22,
       cell_controller_45_p24, cell_controller_45_p25, cell_controller_45_p27, cell_controller_45_p28,
       cell_controller_45_p30, cell_controller_45_p31, cell_controller_45_p33, cell_controller_45_p34,
       cell_controller_45_p36, cell_controller_45_p37, cell_controller_46_p6, cell_controller_46_p7,
       cell_controller_46_p9, cell_controller_46_p10, cell_controller_46_p12, cell_controller_46_p13,
       cell_controller_46_p15, cell_controller_46_p16, cell_controller_46_p18, cell_controller_46_p19,
       cell_controller_46_p21, cell_controller_46_p22, cell_controller_46_p24, cell_controller_46_p25,
       cell_controller_46_p27, cell_controller_46_p28, cell_controller_46_p30, cell_controller_46_p31,
       cell_controller_46_p33, cell_controller_46_p34, cell_controller_46_p36, cell_controller_46_p37,
       cell_controller_47_p6, cell_controller_47_p7, cell_controller_47_p9, cell_controller_47_p10,
       cell_controller_47_p12, cell_controller_47_p13, cell_controller_47_p15, cell_controller_47_p16,
       cell_controller_47_p18, cell_controller_47_p19, cell_controller_47_p21, cell_controller_47_p22,
       cell_controller_47_p24, cell_controller_47_p25, cell_controller_47_p27, cell_controller_47_p28,
       cell_controller_47_p30, cell_controller_47_p31, cell_controller_47_p33, cell_controller_47_p34,
       cell_controller_47_p36, cell_controller_47_p37, cell_controller_48_p6, cell_controller_48_p7,
       cell_controller_48_p9, cell_controller_48_p10, cell_controller_48_p12, cell_controller_48_p13,
       cell_controller_48_p15, cell_controller_48_p16, cell_controller_48_p18, cell_controller_48_p19,
       cell_controller_48_p21, cell_controller_48_p22, cell_controller_48_p24, cell_controller_48_p25,
       cell_controller_48_p27, cell_controller_48_p28, cell_controller_48_p30, cell_controller_48_p31,
       cell_controller_48_p33, cell_controller_48_p34, cell_controller_48_p36, cell_controller_48_p37,
       cell_controller_49_p6, cell_controller_49_p7, cell_controller_49_p9, cell_controller_49_p10,
       cell_controller_49_p12, cell_controller_49_p13, cell_controller_49_p15, cell_controller_49_p16,
       cell_controller_49_p18, cell_controller_49_p19, cell_controller_49_p21, cell_controller_49_p22,
       cell_controller_49_p24, cell_controller_49_p25, cell_controller_49_p27, cell_controller_49_p28,
       cell_controller_49_p30, cell_controller_49_p31, cell_controller_49_p33, cell_controller_49_p34,
       cell_controller_49_p36, cell_controller_49_p37, cell_controller_50_p6, cell_controller_50_p7,
       cell_controller_50_p9, cell_controller_50_p10, cell_controller_50_p12, cell_controller_50_p13,
       cell_controller_50_p15, cell_controller_50_p16, cell_controller_50_p18, cell_controller_50_p19,
       cell_controller_50_p21, cell_controller_50_p22, cell_controller_50_p24, cell_controller_50_p25,
       cell_controller_50_p27, cell_controller_50_p28, cell_controller_50_p30, cell_controller_50_p31,
       cell_controller_50_p33, cell_controller_50_p34, cell_controller_50_p36, cell_controller_50_p37,
       cell_controller_51_p6, cell_controller_51_p7, cell_controller_51_p9, cell_controller_51_p10,
       cell_controller_51_p12, cell_controller_51_p13, cell_controller_51_p15, cell_controller_51_p16,
       cell_controller_51_p18, cell_controller_51_p19, cell_controller_51_p21, cell_controller_51_p22,
       cell_controller_51_p24, cell_controller_51_p25, cell_controller_51_p27, cell_controller_51_p28,
       cell_controller_51_p30, cell_controller_51_p31, cell_controller_51_p33, cell_controller_51_p34,
       cell_controller_51_p36, cell_controller_51_p37, cell_controller_52_p6, cell_controller_52_p7,
       cell_controller_52_p9, cell_controller_52_p10, cell_controller_52_p12, cell_controller_52_p13,
       cell_controller_52_p15, cell_controller_52_p16, cell_controller_52_p18, cell_controller_52_p19,
       cell_controller_52_p21, cell_controller_52_p22, cell_controller_52_p24, cell_controller_52_p25,
       cell_controller_52_p27, cell_controller_52_p28, cell_controller_52_p30, cell_controller_52_p32,
       cell_controller_52_p34, cell_controller_52_p36, cell_controller_52_p38, cell_controller_52_p39,
       cell_controller_53_p6, cell_controller_53_p7, cell_controller_53_p9, cell_controller_53_p10,
       cell_controller_53_p12, cell_controller_53_p13, cell_controller_53_p15, cell_controller_53_p16,
       cell_controller_53_p18, cell_controller_53_p19, cell_controller_53_p21, cell_controller_53_p22,
       cell_controller_53_p24, cell_controller_53_p25, cell_controller_53_p27, cell_controller_53_p28,
       cell_controller_53_p30, cell_controller_53_p32, cell_controller_53_p34, cell_controller_53_p36,
       cell_controller_53_p38, cell_controller_53_p39, cell_controller_54_p6, cell_controller_54_p7,
       cell_controller_54_p9, cell_controller_54_p10, cell_controller_54_p12, cell_controller_54_p13,
       cell_controller_54_p15, cell_controller_54_p16, cell_controller_54_p18, cell_controller_54_p19,
       cell_controller_54_p21, cell_controller_54_p22, cell_controller_54_p24, cell_controller_54_p25,
       cell_controller_54_p27, cell_controller_54_p28, cell_controller_54_p30, cell_controller_54_p32,
       cell_controller_54_p34, cell_controller_54_p36, cell_controller_54_p38, cell_controller_54_p39,
       cell_controller_55_p6, cell_controller_55_p7, cell_controller_55_p9, cell_controller_55_p10,
       cell_controller_55_p12, cell_controller_55_p13, cell_controller_55_p15, cell_controller_55_p16,
       cell_controller_55_p18, cell_controller_55_p19, cell_controller_55_p21, cell_controller_55_p22,
       cell_controller_55_p24, cell_controller_55_p25, cell_controller_55_p27, cell_controller_55_p28,
       cell_controller_55_p30, cell_controller_55_p32, cell_controller_55_p34, cell_controller_55_p36,
       cell_controller_55_p38, cell_controller_55_p39, cell_controller_56_p6, cell_controller_56_p7,
       cell_controller_56_p9, cell_controller_56_p10, cell_controller_56_p12, cell_controller_56_p13,
       cell_controller_56_p15, cell_controller_56_p16, cell_controller_56_p18, cell_controller_56_p19,
       cell_controller_56_p21, cell_controller_56_p22, cell_controller_56_p24, cell_controller_56_p25,
       cell_controller_56_p27, cell_controller_56_p28, cell_controller_56_p30, cell_controller_56_p32,
       cell_controller_56_p34, cell_controller_56_p36, cell_controller_56_p38, cell_controller_56_p39,
       cell_controller_57_p6, cell_controller_57_p7, cell_controller_57_p9, cell_controller_57_p10,
       cell_controller_57_p12, cell_controller_57_p13, cell_controller_57_p15, cell_controller_57_p16,
       cell_controller_57_p18, cell_controller_57_p19, cell_controller_57_p21, cell_controller_57_p22,
       cell_controller_57_p24, cell_controller_57_p25, cell_controller_57_p27, cell_controller_57_p28,
       cell_controller_57_p30, cell_controller_57_p31, cell_controller_57_p33, cell_controller_57_p34,
       cell_controller_57_p36, cell_controller_57_p37, cell_controller_58_p6, cell_controller_58_p7,
       cell_controller_58_p9, cell_controller_58_p10, cell_controller_58_p12, cell_controller_58_p13,
       cell_controller_58_p15, cell_controller_58_p16, cell_controller_58_p18, cell_controller_58_p19,
       cell_controller_58_p21, cell_controller_58_p22, cell_controller_58_p24, cell_controller_58_p25,
       cell_controller_58_p27, cell_controller_58_p28, cell_controller_58_p30, cell_controller_58_p31,
       cell_controller_58_p33, cell_controller_58_p34, cell_controller_58_p36, cell_controller_58_p37,
       cell_controller_59_p6, cell_controller_59_p7, cell_controller_59_p9, cell_controller_59_p10,
       cell_controller_59_p12, cell_controller_59_p13, cell_controller_59_p15, cell_controller_59_p16,
       cell_controller_59_p18, cell_controller_59_p19, cell_controller_59_p21, cell_controller_59_p22,
       cell_controller_59_p24, cell_controller_59_p25, cell_controller_59_p27, cell_controller_59_p28,
       cell_controller_59_p30, cell_controller_59_p31, cell_controller_59_p33, cell_controller_59_p34,
       cell_controller_59_p36, cell_controller_59_p37, cell_controller_60_p6, cell_controller_60_p7,
       cell_controller_60_p9, cell_controller_60_p10, cell_controller_60_p12, cell_controller_60_p13,
       cell_controller_60_p15, cell_controller_60_p16, cell_controller_60_p18, cell_controller_60_p19,
       cell_controller_60_p21, cell_controller_60_p22, cell_controller_60_p24, cell_controller_60_p25,
       cell_controller_60_p27, cell_controller_60_p28, cell_controller_60_p30, cell_controller_60_p31,
       cell_controller_60_p33, cell_controller_60_p34, cell_controller_60_p36, cell_controller_60_p37,
       cell_controller_61_p6, cell_controller_61_p7, cell_controller_61_p9, cell_controller_61_p10,
       cell_controller_61_p12, cell_controller_61_p13, cell_controller_61_p15, cell_controller_61_p16,
       cell_controller_61_p18, cell_controller_61_p19, cell_controller_61_p21, cell_controller_61_p22,
       cell_controller_61_p24, cell_controller_61_p25, cell_controller_61_p27, cell_controller_61_p28,
       cell_controller_61_p30, cell_controller_61_p31, cell_controller_61_p33, cell_controller_61_p34,
       cell_controller_61_p36, cell_controller_61_p37, cell_controller_62_p6, cell_controller_62_p7,
       cell_controller_62_p9, cell_controller_62_p10, cell_controller_62_p12, cell_controller_62_p13,
       cell_controller_62_p15, cell_controller_62_p16, cell_controller_62_p18, cell_controller_62_p19,
       cell_controller_62_p21, cell_controller_62_p22, cell_controller_62_p24, cell_controller_62_p25,
       cell_controller_62_p27, cell_controller_62_p28, cell_controller_62_p30, cell_controller_62_p31,
       cell_controller_62_p33, cell_controller_62_p34, cell_controller_62_p36, cell_controller_62_p37,
       cell_controller_63_p6, cell_controller_63_p7, cell_controller_63_p9, cell_controller_63_p10,
       cell_controller_63_p12, cell_controller_63_p13, cell_controller_63_p15, cell_controller_63_p16,
       cell_controller_63_p18, cell_controller_63_p19, cell_controller_63_p21, cell_controller_63_p22,
       cell_controller_63_p24, cell_controller_63_p25, cell_controller_63_p27, cell_controller_63_p28,
       cell_controller_63_p30, cell_controller_63_p31, cell_controller_63_p33, cell_controller_63_p34,
       cell_controller_63_p36, cell_controller_63_p37, cell_controller_64_p6, cell_controller_64_p7,
       cell_controller_64_p9, cell_controller_64_p10, cell_controller_64_p12, cell_controller_64_p13,
       cell_controller_64_p15, cell_controller_64_p16, cell_controller_64_p18, cell_controller_64_p19,
       cell_controller_64_p21, cell_controller_64_p22, cell_controller_64_p24, cell_controller_64_p25,
       cell_controller_64_p27, cell_controller_64_p28, cell_controller_64_p30, cell_controller_64_p31,
       cell_controller_64_p33, cell_controller_64_p34, cell_controller_64_p36, cell_controller_64_p37,
       Columns, field_cahce_1_p1_row_1, field_cahce_1_p1_row_2, field_cahce_1_p1_row_3,
       field_cahce_1_p1_row_4, field_cahce_1_p1_row_5, field_cahce_1_p1_row_6, field_cahce_1_p1_row_7,
       field_cahce_1_p1_row_8, mcu_v2_1_p7, Rows;
  wire [8:0] field_cahce_1_p2_row_1, field_cahce_1_p2_row_2, field_cahce_1_p2_row_3, field_cahce_1_p2_row_4,
       field_cahce_1_p2_row_5, field_cahce_1_p2_row_6, field_cahce_1_p2_row_7, field_cahce_1_p2_row_8;
  wire [9:0] field_cahce_1_task_row_1, field_cahce_1_task_row_2, field_cahce_1_task_row_3,
       field_cahce_1_task_row_4, field_cahce_1_task_row_5, field_cahce_1_task_row_6,
       field_cahce_1_task_row_7, field_cahce_1_task_row_8;
  wire [10:0] input_controller_1_signed_number_parsed_from_user_input;
  wire [14:0] output_big_numder_1_out_3, output_big_numder_1_out_4, output_big_numder_1_out_5,
       output_big_numder_1_out_6, output_big_numder_1_out_7, output_big_numder_1_out_8,
       output_big_numder_1_out_9, output_big_numder_1_out_10, output_big_numder_1_out_11,
       output_big_numder_2_out_3, output_big_numder_2_out_4, output_big_numder_2_out_5,
       output_big_numder_2_out_6, output_big_numder_2_out_7, output_big_numder_2_out_8,
       output_big_numder_2_out_9, output_big_numder_2_out_10, output_big_numder_2_out_11,
       output_big_numder_3_out_3, output_big_numder_3_out_4, output_big_numder_3_out_5,
       output_big_numder_3_out_6, output_big_numder_3_out_7, output_big_numder_3_out_8,
       output_big_numder_3_out_9, output_big_numder_3_out_10, output_big_numder_3_out_11,
       output_big_numder_4_out_3, output_big_numder_4_out_4, output_big_numder_4_out_5,
       output_big_numder_4_out_6, output_big_numder_4_out_7, output_big_numder_4_out_8,
       output_big_numder_4_out_9, output_big_numder_4_out_10, output_big_numder_4_out_11;
  wire [20:0] input_controller_1_input_buffer;
  wire [31:0] mcu_v2_1_p19, mcu_v2_1_p20;

  Button button_1 (.out(button_1_out));
  Clock clock_1 (.out(clock_1_out));
  Clock clock_2 (.out(clock_2_out));
  DotMatrix #(.inputtype("row"), .matrixcols(8), .matrixrows(1)) dotmatrix_1 (.row0(mcu_v2_1_p7));
  input_controller input_controller_1 (
    .Signed_number_parsed_from_user_input(input_controller_1_signed_number_parsed_from_user_input),
    .Command_parsed_from_user_input(input_controller_1_command_parsed_from_user_input),
    .KBD_clock(input_controller_1_kbd_clock), .KBD_clear(input_controller_1_kbd_clear),
    .KBD_available(keyboard_1_avail), .KBD_buffer(keyboard_1_data), .KBD_en(input_controller_1_kbd_en),
    .Enabled__clears_buffer_on_rising_edge(and_1_out), .Active_LED(input_controller_1_active_led),
    .Request_number(mcu_v2_1_p12), .User_action_LED(input_controller_1_user_action_led),
    .Error_LED(input_controller_1_error_led), .Data_ready(input_controller_1_data_ready),
    .input_buffer({input_controller_1_input_buffer_3, input_controller_1_input_buffer[20:14], input_controller_1_input_buffer_2, input_controller_1_input_buffer[6:0]}),
    .Cursor_position(input_controller_1_cursor_position), .CLK(clock_2_out));
  Keyboard keyboard_1 (
    .clk(input_controller_1_kbd_clock), .re(input_controller_1_kbd_en), .clr(input_controller_1_kbd_clear),
    .avail(keyboard_1_avail), .data(keyboard_1_data));
  and and_1 (and_1_out, ~counter_1_carry, mcu_v2_1_p13);  // AND_Gate
  and and_2 (Y, and_1_out, input_controller_1_user_action_led);
  LED led_1 (.in(mcu_v2_1_p10));
  LED led_2 (.in(mcu_v2_1_p11));
  LED led_3 (.in(mcu_v2_1_p9));
  DotMatrix #(.matrixcols(11), .matrixrows(5)) dotmatrix_2 (
    .col0(cell_controller_1_p5), .col1(cell_controller_1_p8), .col2(cell_controller_1_p11),
    .col3(cell_controller_1_p14), .col4(cell_controller_1_p17), .col5(cell_controller_1_p20),
    .col6(cell_controller_1_p23), .col7(cell_controller_1_p26), .col8(cell_controller_1_p29),
    .col9(cell_controller_1_p32), .col10(cell_controller_1_p35));
  // Cell_controller cell_controller_1: pin names not known; wires that end beside it: Columns[0], Rows[0], MOSI, MISO, cell_controller_1_p5, cell_controller_1_p6, cell_controller_1_p7, cell_controller_1_p8, cell_controller_1_p9, cell_controller_1_p10, cell_controller_1_p11, cell_controller_1_p12, cell_controller_1_p13, cell_controller_1_p14, cell_controller_1_p15, cell_controller_1_p16, cell_controller_1_p17, cell_controller_1_p18, cell_controller_1_p19, cell_controller_1_p20, cell_controller_1_p21, cell_controller_1_p22, cell_controller_1_p23, cell_controller_1_p24, cell_controller_1_p25, cell_controller_1_p26, cell_controller_1_p27, cell_controller_1_p28, cell_controller_1_p29, cell_controller_1_p30, cell_controller_1_p31, cell_controller_1_p32, cell_controller_1_p33, cell_controller_1_p34, cell_controller_1_p35, cell_controller_1_p36, cell_controller_1_p37
  DotMatrix #(.matrixcols(11), .matrixrows(8)) dotmatrix_3 (
    .col0(cell_controller_1_p6), .col1(cell_controller_1_p9), .col2(cell_controller_1_p12),
    .col3(cell_controller_1_p15), .col4(cell_controller_1_p18), .col5(cell_controller_1_p21),
    .col6(cell_controller_1_p24), .col7(cell_controller_1_p27), .col8(cell_controller_1_p30),
    .col9(cell_controller_1_p33), .col10(cell_controller_1_p36));
  DotMatrix #(.matrixcols(11), .matrixrows(8)) dotmatrix_4 (
    .col0(cell_controller_1_p7), .col1(cell_controller_1_p10), .col2(cell_controller_1_p13),
    .col3(cell_controller_1_p16), .col4(cell_controller_1_p19), .col5(cell_controller_1_p22),
    .col6(cell_controller_1_p25), .col7(cell_controller_1_p28), .col8(cell_controller_1_p31),
    .col9(cell_controller_1_p34), .col10(cell_controller_1_p37));
  DotMatrix #(.matrixcols(11), .matrixrows(5)) dotmatrix_5 (
    .col0(cell_controller_2_p5), .col1(cell_controller_2_p8), .col2(cell_controller_2_p11),
    .col3(cell_controller_2_p14), .col4(cell_controller_2_p17), .col5(cell_controller_2_p20),
    .col6(cell_controller_2_p23), .col7(cell_controller_2_p26), .col8(cell_controller_2_p29),
    .col9(cell_controller_2_p32), .col10(cell_controller_2_p35));
  // Cell_controller cell_controller_2: pin names not known; wires that end beside it: Columns[0], Rows[1], MOSI, MISO, cell_controller_2_p5, cell_controller_2_p6, cell_controller_2_p7, cell_controller_2_p8, cell_controller_2_p9, cell_controller_2_p10, cell_controller_2_p11, cell_controller_2_p12, cell_controller_2_p13, cell_controller_2_p14, cell_controller_2_p15, cell_controller_2_p16, cell_controller_2_p17, cell_controller_2_p18, cell_controller_2_p19, cell_controller_2_p20, cell_controller_2_p21, cell_controller_2_p22, cell_controller_2_p23, cell_controller_2_p24, cell_controller_2_p25, cell_controller_2_p26, cell_controller_2_p27, cell_controller_2_p28, cell_controller_2_p29, cell_controller_2_p30, cell_controller_2_p31, cell_controller_2_p32, cell_controller_2_p33, cell_controller_2_p34, cell_controller_2_p35, cell_controller_2_p36, cell_controller_2_p37
  DotMatrix #(.matrixcols(11), .matrixrows(8)) dotmatrix_6 (
    .col0(cell_controller_2_p6), .col1(cell_controller_2_p9), .col2(cell_controller_2_p12),
    .col3(cell_controller_2_p15), .col4(cell_controller_2_p18), .col5(cell_controller_2_p21),
    .col6(cell_controller_2_p24), .col7(cell_controller_2_p27), .col8(cell_controller_2_p30),
    .col9(cell_controller_2_p33), .col10(cell_controller_2_p36));
  DotMatrix #(.matrixcols(11), .matrixrows(8)) dotmatrix_7 (
    .col0(cell_controller_2_p7), .col1(cell_controller_2_p10), .col2(cell_controller_2_p13),
    .col3(cell_controller_2_p16), .col4(cell_controller_2_p19), .col5(cell_controller_2_p22),
    .col6(cell_controller_2_p25), .col7(cell_controller_2_p28), .col8(cell_controller_2_p31),
    .col9(cell_controller_2_p34), .col10(cell_controller_2_p37));
  // Cell_controller cell_controller_3: pin names not known; wires that end beside it: Columns[0], Rows[2], MOSI, MISO, cell_controller_3_p5, cell_controller_3_p6, cell_controller_3_p7, cell_controller_3_p8, cell_controller_3_p9, cell_controller_3_p10, cell_controller_3_p11, cell_controller_3_p12, cell_controller_3_p13, cell_controller_3_p14, cell_controller_3_p15, cell_controller_3_p16, cell_controller_3_p17, cell_controller_3_p18, cell_controller_3_p19, cell_controller_3_p20, cell_controller_3_p21, cell_controller_3_p22, cell_controller_3_p23, cell_controller_3_p24, cell_controller_3_p25, cell_controller_3_p26, cell_controller_3_p27, cell_controller_3_p28, cell_controller_3_p29, cell_controller_3_p30, cell_controller_3_p31, cell_controller_3_p32, cell_controller_3_p33, cell_controller_3_p34, cell_controller_3_p35, cell_controller_3_p36, cell_controller_3_p37
  DotMatrix #(.matrixcols(11), .matrixrows(5)) dotmatrix_8 (
    .col0(cell_controller_3_p5), .col1(cell_controller_3_p8), .col2(cell_controller_3_p11),
    .col3(cell_controller_3_p14), .col4(cell_controller_3_p17), .col5(cell_controller_3_p20),
    .col6(cell_controller_3_p23), .col7(cell_controller_3_p26), .col8(cell_controller_3_p29),
    .col9(cell_controller_3_p32), .col10(cell_controller_3_p35));
  DotMatrix #(.matrixcols(11), .matrixrows(8)) dotmatrix_9 (
    .col0(cell_controller_3_p6), .col1(cell_controller_3_p9), .col2(cell_controller_3_p12),
    .col3(cell_controller_3_p15), .col4(cell_controller_3_p18), .col5(cell_controller_3_p21),
    .col6(cell_controller_3_p24), .col7(cell_controller_3_p27), .col8(cell_controller_3_p30),
    .col9(cell_controller_3_p33), .col10(cell_controller_3_p36));
  DotMatrix #(.matrixcols(11), .matrixrows(8)) dotmatrix_10 (
    .col0(cell_controller_3_p7), .col1(cell_controller_3_p10), .col2(cell_controller_3_p13),
    .col3(cell_controller_3_p16), .col4(cell_controller_3_p19), .col5(cell_controller_3_p22),
    .col6(cell_controller_3_p25), .col7(cell_controller_3_p28), .col8(cell_controller_3_p31),
    .col9(cell_controller_3_p34), .col10(cell_controller_3_p37));
  DotMatrix #(.matrixcols(11), .matrixrows(5)) dotmatrix_11 (
    .col0(cell_controller_4_p5), .col1(cell_controller_4_p8), .col2(cell_controller_4_p11),
    .col3(cell_controller_4_p14), .col4(cell_controller_4_p17), .col5(cell_controller_4_p20),
    .col6(cell_controller_4_p23), .col7(cell_controller_4_p26), .col8(cell_controller_4_p29),
    .col9(cell_controller_4_p32), .col10(cell_controller_4_p35));
  // Cell_controller cell_controller_4: pin names not known; wires that end beside it: Columns[0], Rows[3], MOSI, MISO, cell_controller_4_p5, cell_controller_4_p6, cell_controller_4_p7, cell_controller_4_p8, cell_controller_4_p9, cell_controller_4_p10, cell_controller_4_p11, cell_controller_4_p12, cell_controller_4_p13, cell_controller_4_p14, cell_controller_4_p15, cell_controller_4_p16, cell_controller_4_p17, cell_controller_4_p18, cell_controller_4_p19, cell_controller_4_p20, cell_controller_4_p21, cell_controller_4_p22, cell_controller_4_p23, cell_controller_4_p24, cell_controller_4_p25, cell_controller_4_p26, cell_controller_4_p27, cell_controller_4_p28, cell_controller_4_p29, cell_controller_4_p30, cell_controller_4_p31, cell_controller_4_p32, cell_controller_4_p33, cell_controller_4_p34, cell_controller_4_p35, cell_controller_4_p36, cell_controller_4_p37
  DotMatrix #(.matrixcols(11), .matrixrows(8)) dotmatrix_12 (
    .col0(cell_controller_4_p6), .col1(cell_controller_4_p9), .col2(cell_controller_4_p12),
    .col3(cell_controller_4_p15), .col4(cell_controller_4_p18), .col5(cell_controller_4_p21),
    .col6(cell_controller_4_p24), .col7(cell_controller_4_p27), .col8(cell_controller_4_p30),
    .col9(cell_controller_4_p33), .col10(cell_controller_4_p36));
  DotMatrix #(.matrixcols(11), .matrixrows(8)) dotmatrix_13 (
    .col0(cell_controller_4_p7), .col1(cell_controller_4_p10), .col2(cell_controller_4_p13),
    .col3(cell_controller_4_p16), .col4(cell_controller_4_p19), .col5(cell_controller_4_p22),
    .col6(cell_controller_4_p25), .col7(cell_controller_4_p28), .col8(cell_controller_4_p31),
    .col9(cell_controller_4_p34), .col10(cell_controller_4_p37));
  DotMatrix #(.matrixcols(11), .matrixrows(5)) dotmatrix_14 (
    .col0(cell_controller_5_p5), .col1(cell_controller_5_p8), .col2(cell_controller_5_p11),
    .col3(cell_controller_5_p14), .col4(cell_controller_5_p17), .col5(cell_controller_5_p20),
    .col6(cell_controller_5_p23), .col7(cell_controller_5_p26), .col8(cell_controller_5_p29),
    .col9(cell_controller_5_p32), .col10(cell_controller_5_p35));
  // Cell_controller cell_controller_5: pin names not known; wires that end beside it: Columns[0], Rows[4], MOSI, MISO, cell_controller_5_p5, cell_controller_5_p6, cell_controller_5_p7, cell_controller_5_p8, cell_controller_5_p9, cell_controller_5_p10, cell_controller_5_p11, cell_controller_5_p12, cell_controller_5_p13, cell_controller_5_p14, cell_controller_5_p15, cell_controller_5_p16, cell_controller_5_p17, cell_controller_5_p18, cell_controller_5_p19, cell_controller_5_p20, cell_controller_5_p21, cell_controller_5_p22, cell_controller_5_p23, cell_controller_5_p24, cell_controller_5_p25, cell_controller_5_p26, cell_controller_5_p27, cell_controller_5_p28, cell_controller_5_p29, cell_controller_5_p30, cell_controller_5_p31, cell_controller_5_p32, cell_controller_5_p33, cell_controller_5_p34, cell_controller_5_p35, cell_controller_5_p36, cell_controller_5_p37
  DotMatrix #(.matrixcols(11), .matrixrows(8)) dotmatrix_15 (
    .col0(cell_controller_5_p6), .col1(cell_controller_5_p9), .col2(cell_controller_5_p12),
    .col3(cell_controller_5_p15), .col4(cell_controller_5_p18), .col5(cell_controller_5_p21),
    .col6(cell_controller_5_p24), .col7(cell_controller_5_p27), .col8(cell_controller_5_p30),
    .col9(cell_controller_5_p33), .col10(cell_controller_5_p36));
  DotMatrix #(.matrixcols(11), .matrixrows(8)) dotmatrix_16 (
    .col0(cell_controller_5_p7), .col1(cell_controller_5_p10), .col2(cell_controller_5_p13),
    .col3(cell_controller_5_p16), .col4(cell_controller_5_p19), .col5(cell_controller_5_p22),
    .col6(cell_controller_5_p25), .col7(cell_controller_5_p28), .col8(cell_controller_5_p31),
    .col9(cell_controller_5_p34), .col10(cell_controller_5_p37));
  // Cell_controller cell_controller_6: pin names not known; wires that end beside it: Columns[0], Rows[5], MOSI, MISO, cell_controller_6_p5, cell_controller_6_p6, cell_controller_6_p7, cell_controller_6_p8, cell_controller_6_p9, cell_controller_6_p10, cell_controller_6_p11, cell_controller_6_p12, cell_controller_6_p13, cell_controller_6_p14, cell_controller_6_p15, cell_controller_6_p16, cell_controller_6_p17, cell_controller_6_p18, cell_controller_6_p19, cell_controller_6_p20, cell_controller_6_p21, cell_controller_6_p22, cell_controller_6_p23, cell_controller_6_p24, cell_controller_6_p25, cell_controller_6_p26, cell_controller_6_p27, cell_controller_6_p28, cell_controller_6_p29, cell_controller_6_p30, cell_controller_6_p31, cell_controller_6_p32, cell_controller_6_p33, cell_controller_6_p34, cell_controller_6_p35, cell_controller_6_p36, cell_controller_6_p37
  DotMatrix #(.matrixcols(11), .matrixrows(5)) dotmatrix_17 (
    .col0(cell_controller_6_p5), .col1(cell_controller_6_p8), .col2(cell_controller_6_p11),
    .col3(cell_controller_6_p14), .col4(cell_controller_6_p17), .col5(cell_controller_6_p20),
    .col6(cell_controller_6_p23), .col7(cell_controller_6_p26), .col8(cell_controller_6_p29),
    .col9(cell_controller_6_p32), .col10(cell_controller_6_p35));
  DotMatrix #(.matrixcols(11), .matrixrows(8)) dotmatrix_18 (
    .col0(cell_controller_6_p6), .col1(cell_controller_6_p9), .col2(cell_controller_6_p12),
    .col3(cell_controller_6_p15), .col4(cell_controller_6_p18), .col5(cell_controller_6_p21),
    .col6(cell_controller_6_p24), .col7(cell_controller_6_p27), .col8(cell_controller_6_p30),
    .col9(cell_controller_6_p33), .col10(cell_controller_6_p36));
  DotMatrix #(.matrixcols(11), .matrixrows(8)) dotmatrix_19 (
    .col0(cell_controller_6_p7), .col1(cell_controller_6_p10), .col2(cell_controller_6_p13),
    .col3(cell_controller_6_p16), .col4(cell_controller_6_p19), .col5(cell_controller_6_p22),
    .col6(cell_controller_6_p25), .col7(cell_controller_6_p28), .col8(cell_controller_6_p31),
    .col9(cell_controller_6_p34), .col10(cell_controller_6_p37));
  DotMatrix #(.matrixcols(11), .matrixrows(5)) dotmatrix_20 (
    .col0(cell_controller_7_p5), .col1(cell_controller_7_p8), .col2(cell_controller_7_p11),
    .col3(cell_controller_7_p14), .col4(cell_controller_7_p17), .col5(cell_controller_7_p20),
    .col6(cell_controller_7_p23), .col7(cell_controller_7_p26), .col8(cell_controller_7_p29),
    .col9(cell_controller_7_p32), .col10(cell_controller_7_p35));
  // Cell_controller cell_controller_7: pin names not known; wires that end beside it: Columns[0], Rows[6], MOSI, MISO, cell_controller_7_p5, cell_controller_7_p6, cell_controller_7_p7, cell_controller_7_p8, cell_controller_7_p9, cell_controller_7_p10, cell_controller_7_p11, cell_controller_7_p12, cell_controller_7_p13, cell_controller_7_p14, cell_controller_7_p15, cell_controller_7_p16, cell_controller_7_p17, cell_controller_7_p18, cell_controller_7_p19, cell_controller_7_p20, cell_controller_7_p21, cell_controller_7_p22, cell_controller_7_p23, cell_controller_7_p24, cell_controller_7_p25, cell_controller_7_p26, cell_controller_7_p27, cell_controller_7_p28, cell_controller_7_p29, cell_controller_7_p30, cell_controller_7_p31, cell_controller_7_p32, cell_controller_7_p33, cell_controller_7_p34, cell_controller_7_p35, cell_controller_7_p36, cell_controller_7_p37
  DotMatrix #(.matrixcols(11), .matrixrows(8)) dotmatrix_21 (
    .col0(cell_controller_7_p6), .col1(cell_controller_7_p9), .col2(cell_controller_7_p12),
    .col3(cell_controller_7_p15), .col4(cell_controller_7_p18), .col5(cell_controller_7_p21),
    .col6(cell_controller_7_p24), .col7(cell_controller_7_p27), .col8(cell_controller_7_p30),
    .col9(cell_controller_7_p33), .col10(cell_controller_7_p36));
  DotMatrix #(.matrixcols(11), .matrixrows(8)) dotmatrix_22 (
    .col0(cell_controller_7_p7), .col1(cell_controller_7_p10), .col2(cell_controller_7_p13),
    .col3(cell_controller_7_p16), .col4(cell_controller_7_p19), .col5(cell_controller_7_p22),
    .col6(cell_controller_7_p25), .col7(cell_controller_7_p28), .col8(cell_controller_7_p31),
    .col9(cell_controller_7_p34), .col10(cell_controller_7_p37));
  // Cell_controller cell_controller_8: pin names not known; wires that end beside it: Columns[0], Rows[7], MOSI, MISO, cell_controller_8_p5, cell_controller_8_p6, cell_controller_8_p7, cell_controller_8_p8, cell_controller_8_p9, cell_controller_8_p10, cell_controller_8_p11, cell_controller_8_p12, cell_controller_8_p13, cell_controller_8_p14, cell_controller_8_p15, cell_controller_8_p16, cell_controller_8_p17, cell_controller_8_p18, cell_controller_8_p19, cell_controller_8_p20, cell_controller_8_p21, cell_controller_8_p22, cell_controller_8_p23, cell_controller_8_p24, cell_controller_8_p25, cell_controller_8_p26, cell_controller_8_p27, cell_controller_8_p28, cell_controller_8_p29, cell_controller_8_p30, cell_controller_8_p31, cell_controller_8_p32, cell_controller_8_p33, cell_controller_8_p34, cell_controller_8_p35, cell_controller_8_p36, cell_controller_8_p37
  DotMatrix #(.matrixcols(11), .matrixrows(5)) dotmatrix_23 (
    .col0(cell_controller_8_p5), .col1(cell_controller_8_p8), .col2(cell_controller_8_p11),
    .col3(cell_controller_8_p14), .col4(cell_controller_8_p17), .col5(cell_controller_8_p20),
    .col6(cell_controller_8_p23), .col7(cell_controller_8_p26), .col8(cell_controller_8_p29),
    .col9(cell_controller_8_p32), .col10(cell_controller_8_p35));
  DotMatrix #(.matrixcols(11), .matrixrows(8)) dotmatrix_24 (
    .col0(cell_controller_8_p6), .col1(cell_controller_8_p9), .col2(cell_controller_8_p12),
    .col3(cell_controller_8_p15), .col4(cell_controller_8_p18), .col5(cell_controller_8_p21),
    .col6(cell_controller_8_p24), .col7(cell_controller_8_p27), .col8(cell_controller_8_p30),
    .col9(cell_controller_8_p33), .col10(cell_controller_8_p36));
  DotMatrix #(.matrixcols(11), .matrixrows(8)) dotmatrix_25 (
    .col0(cell_controller_8_p7), .col1(cell_controller_8_p10), .col2(cell_controller_8_p13),
    .col3(cell_controller_8_p16), .col4(cell_controller_8_p19), .col5(cell_controller_8_p22),
    .col6(cell_controller_8_p25), .col7(cell_controller_8_p28), .col8(cell_controller_8_p31),
    .col9(cell_controller_8_p34), .col10(cell_controller_8_p37));
  LED led_4 (.in(input_controller_1_active_led));
  LED led_5 (.in(input_controller_1_error_led));
  LED led_6 (.in(input_controller_1_user_action_led));
  DotMatrix #(.inputtype("row"), .matrixcols(9), .matrixrows(8)) dotmatrix_26 (
    .row0(field_cahce_1_p2_row_1), .row1(field_cahce_1_p2_row_2), .row2(field_cahce_1_p2_row_3),
    .row3(field_cahce_1_p2_row_4), .row4(field_cahce_1_p2_row_5), .row5(field_cahce_1_p2_row_6),
    .row6(field_cahce_1_p2_row_7), .row7(field_cahce_1_p2_row_8));
  DotMatrix #(.inputtype("row"), .matrixcols(10), .matrixrows(8), .dotshape("circle")) dotmatrix_27 (
    .row0(field_cahce_1_task_row_1), .row1(field_cahce_1_task_row_2), .row2(field_cahce_1_task_row_3),
    .row3(field_cahce_1_task_row_4), .row4(field_cahce_1_task_row_5), .row5(field_cahce_1_task_row_6),
    .row6(field_cahce_1_task_row_7), .row7(field_cahce_1_task_row_8));
  DotMatrix #(.inputtype("row"), .matrixcols(8), .matrixrows(8)) dotmatrix_28 (
    .row0(field_cahce_1_p1_row_1), .row1(field_cahce_1_p1_row_2), .row2(field_cahce_1_p1_row_3),
    .row3(field_cahce_1_p1_row_4), .row4(field_cahce_1_p1_row_5), .row5(field_cahce_1_p1_row_6),
    .row6(field_cahce_1_p1_row_7), .row7(field_cahce_1_p1_row_8));
  Counter counter_1 (
    .count(input_controller_1_error_led), .carry(counter_1_carry), .clk(clock_3_out));  // open: load, D, Q, clr
  Clock clock_3 (.out(clock_3_out));
  // MCU_v2 mcu_v2_1: pin names not known; wires that end beside it: Columns, Rows, button_1_out, clock_1_out, MOSI[0], MOSI[1], mcu_v2_1_p7, MISO, mcu_v2_1_p9, mcu_v2_1_p10, mcu_v2_1_p11, mcu_v2_1_p12, mcu_v2_1_p13, mcu_v2_1_p14, input_controller_1_data_ready, mcu_v2_1_p16, input_controller_1_command_parsed_from_user_input, input_controller_1_signed_number_parsed_from_user_input, mcu_v2_1_p19, mcu_v2_1_p20
  Field_cahce field_cahce_1 (
    .Task_row_1(field_cahce_1_task_row_1), .p2_row_1(field_cahce_1_p2_row_1),
    .Task_row_2(field_cahce_1_task_row_2), .p2_row_2(field_cahce_1_p2_row_2),
    .p1_row_1(field_cahce_1_p1_row_1), .p1_row_2(field_cahce_1_p1_row_2),
    .Task_row_3(field_cahce_1_task_row_3), .p2_row_3(field_cahce_1_p2_row_3),
    .p1_row_3(field_cahce_1_p1_row_3), .Task_row_4(field_cahce_1_task_row_4),
    .p2_row_4(field_cahce_1_p2_row_4), .p1_row_4(field_cahce_1_p1_row_4),
    .Task_row_5(field_cahce_1_task_row_5), .p2_row_5(field_cahce_1_p2_row_5),
    .p1_row_5(field_cahce_1_p1_row_5), .Task_row_6(field_cahce_1_task_row_6),
    .p2_row_6(field_cahce_1_p2_row_6), .p1_row_6(field_cahce_1_p1_row_6), .p1_row_7(field_cahce_1_p1_row_7),
    .Task_row_7(field_cahce_1_task_row_7), .p2_row_7(field_cahce_1_p2_row_7),
    .p1_row_8(field_cahce_1_p1_row_8), .Task_row_8(field_cahce_1_task_row_8),
    .p2_row_8(field_cahce_1_p2_row_8), .wr(mcu_v2_1_p14), .RST(button_1_out), .p_sel(mcu_v2_1_p16),
    .DataO_1(mcu_v2_1_p19), .DataO_2(mcu_v2_1_p20), .CSC(Columns), .CSR(Rows));
  DotMatrix #(.matrixcols(11), .matrixrows(5)) dotmatrix_29 (
    .col0(cell_controller_9_p5), .col1(cell_controller_9_p8), .col2(cell_controller_9_p11),
    .col3(cell_controller_9_p14), .col4(cell_controller_9_p17), .col5(cell_controller_9_p20),
    .col6(cell_controller_9_p23), .col7(cell_controller_9_p26), .col8(cell_controller_9_p29),
    .col9(cell_controller_9_p32), .col10(cell_controller_9_p35));
  // Cell_controller cell_controller_9: pin names not known; wires that end beside it: Columns[1], Rows[0], MOSI, MISO, cell_controller_9_p5, cell_controller_9_p6, cell_controller_9_p7, cell_controller_9_p8, cell_controller_9_p9, cell_controller_9_p10, cell_controller_9_p11, cell_controller_9_p12, cell_controller_9_p13, cell_controller_9_p14, cell_controller_9_p15, cell_controller_9_p16, cell_controller_9_p17, cell_controller_9_p18, cell_controller_9_p19, cell_controller_9_p20, cell_controller_9_p21, cell_controller_9_p22, cell_controller_9_p23, cell_controller_9_p24, cell_controller_9_p25, cell_controller_9_p26, cell_controller_9_p27, cell_controller_9_p28, cell_controller_9_p29, cell_controller_9_p30, cell_controller_9_p31, cell_controller_9_p32, cell_controller_9_p33, cell_controller_9_p34, cell_controller_9_p35, cell_controller_9_p36, cell_controller_9_p37
  DotMatrix #(.matrixcols(11), .matrixrows(8)) dotmatrix_30 (
    .col0(cell_controller_9_p6), .col1(cell_controller_9_p9), .col2(cell_controller_9_p12),
    .col3(cell_controller_9_p15), .col4(cell_controller_9_p18), .col5(cell_controller_9_p21),
    .col6(cell_controller_9_p24), .col7(cell_controller_9_p27), .col8(cell_controller_9_p30),
    .col9(cell_controller_9_p33), .col10(cell_controller_9_p36));
  DotMatrix #(.matrixcols(11), .matrixrows(8)) dotmatrix_31 (
    .col0(cell_controller_9_p7), .col1(cell_controller_9_p10), .col2(cell_controller_9_p13),
    .col3(cell_controller_9_p16), .col4(cell_controller_9_p19), .col5(cell_controller_9_p22),
    .col6(cell_controller_9_p25), .col7(cell_controller_9_p28), .col8(cell_controller_9_p31),
    .col9(cell_controller_9_p34), .col10(cell_controller_9_p37));
  // Cell_controller cell_controller_10: pin names not known; wires that end beside it: Columns[1], Rows[1], MOSI, MISO, cell_controller_10_p5, cell_controller_10_p6, cell_controller_10_p7, cell_controller_10_p8, cell_controller_10_p9, cell_controller_10_p10, cell_controller_10_p11, cell_controller_10_p12, cell_controller_10_p13, cell_controller_10_p14, cell_controller_10_p15, cell_controller_10_p16, cell_controller_10_p17, cell_controller_10_p18, cell_controller_10_p19, cell_controller_10_p20, cell_controller_10_p21, cell_controller_10_p22, cell_controller_10_p23, cell_controller_10_p24, cell_controller_10_p25, cell_controller_10_p26, cell_controller_10_p27, cell_controller_10_p28, cell_controller_10_p29, cell_controller_10_p30, cell_controller_10_p31, cell_controller_10_p32, cell_controller_10_p33, cell_controller_10_p34, cell_controller_10_p35, cell_controller_10_p36, cell_controller_10_p37
  DotMatrix #(.matrixcols(11), .matrixrows(5)) dotmatrix_32 (
    .col0(cell_controller_10_p5), .col1(cell_controller_10_p8), .col2(cell_controller_10_p11),
    .col3(cell_controller_10_p14), .col4(cell_controller_10_p17), .col5(cell_controller_10_p20),
    .col6(cell_controller_10_p23), .col7(cell_controller_10_p26), .col8(cell_controller_10_p29),
    .col9(cell_controller_10_p32), .col10(cell_controller_10_p35));
  DotMatrix #(.matrixcols(11), .matrixrows(8)) dotmatrix_33 (
    .col0(cell_controller_10_p6), .col1(cell_controller_10_p9), .col2(cell_controller_10_p12),
    .col3(cell_controller_10_p15), .col4(cell_controller_10_p18), .col5(cell_controller_10_p21),
    .col6(cell_controller_10_p24), .col7(cell_controller_10_p27), .col8(cell_controller_10_p30),
    .col9(cell_controller_10_p33), .col10(cell_controller_10_p36));
  DotMatrix #(.matrixcols(11), .matrixrows(8)) dotmatrix_34 (
    .col0(cell_controller_10_p7), .col1(cell_controller_10_p10), .col2(cell_controller_10_p13),
    .col3(cell_controller_10_p16), .col4(cell_controller_10_p19), .col5(cell_controller_10_p22),
    .col6(cell_controller_10_p25), .col7(cell_controller_10_p28), .col8(cell_controller_10_p31),
    .col9(cell_controller_10_p34), .col10(cell_controller_10_p37));
  // Cell_controller cell_controller_11: pin names not known; wires that end beside it: Columns[1], Rows[2], MOSI, MISO, cell_controller_11_p5, cell_controller_11_p6, cell_controller_11_p7, cell_controller_11_p8, cell_controller_11_p9, cell_controller_11_p10, cell_controller_11_p11, cell_controller_11_p12, cell_controller_11_p13, cell_controller_11_p14, cell_controller_11_p15, cell_controller_11_p16, cell_controller_11_p17, cell_controller_11_p18, cell_controller_11_p19, cell_controller_11_p20, cell_controller_11_p21, cell_controller_11_p22, cell_controller_11_p23, cell_controller_11_p24, cell_controller_11_p25, cell_controller_11_p26, cell_controller_11_p27, cell_controller_11_p28, cell_controller_11_p29, cell_controller_11_p30, cell_controller_11_p31, cell_controller_11_p32, cell_controller_11_p33, cell_controller_11_p34, cell_controller_11_p35, cell_controller_11_p36, cell_controller_11_p37
  DotMatrix #(.matrixcols(11), .matrixrows(5)) dotmatrix_35 (
    .col0(cell_controller_11_p5), .col1(cell_controller_11_p8), .col2(cell_controller_11_p11),
    .col3(cell_controller_11_p14), .col4(cell_controller_11_p17), .col5(cell_controller_11_p20),
    .col6(cell_controller_11_p23), .col7(cell_controller_11_p26), .col8(cell_controller_11_p29),
    .col9(cell_controller_11_p32), .col10(cell_controller_11_p35));
  DotMatrix #(.matrixcols(11), .matrixrows(8)) dotmatrix_36 (
    .col0(cell_controller_11_p6), .col1(cell_controller_11_p9), .col2(cell_controller_11_p12),
    .col3(cell_controller_11_p15), .col4(cell_controller_11_p18), .col5(cell_controller_11_p21),
    .col6(cell_controller_11_p24), .col7(cell_controller_11_p27), .col8(cell_controller_11_p30),
    .col9(cell_controller_11_p33), .col10(cell_controller_11_p36));
  DotMatrix #(.matrixcols(11), .matrixrows(8)) dotmatrix_37 (
    .col0(cell_controller_11_p7), .col1(cell_controller_11_p10), .col2(cell_controller_11_p13),
    .col3(cell_controller_11_p16), .col4(cell_controller_11_p19), .col5(cell_controller_11_p22),
    .col6(cell_controller_11_p25), .col7(cell_controller_11_p28), .col8(cell_controller_11_p31),
    .col9(cell_controller_11_p34), .col10(cell_controller_11_p37));
  DotMatrix #(.matrixcols(11), .matrixrows(5)) dotmatrix_38 (
    .col0(cell_controller_12_p5), .col1(cell_controller_12_p8), .col2(cell_controller_12_p11),
    .col3(cell_controller_12_p14), .col4(cell_controller_12_p17), .col5(cell_controller_12_p20),
    .col6(cell_controller_12_p23), .col7(cell_controller_12_p26), .col8(cell_controller_12_p29),
    .col9(cell_controller_12_p32), .col10(cell_controller_12_p35));
  // Cell_controller cell_controller_12: pin names not known; wires that end beside it: Columns[1], Rows[3], MOSI, MISO, cell_controller_12_p5, cell_controller_12_p6, cell_controller_12_p7, cell_controller_12_p8, cell_controller_12_p9, cell_controller_12_p10, cell_controller_12_p11, cell_controller_12_p12, cell_controller_12_p13, cell_controller_12_p14, cell_controller_12_p15, cell_controller_12_p16, cell_controller_12_p17, cell_controller_12_p18, cell_controller_12_p19, cell_controller_12_p20, cell_controller_12_p21, cell_controller_12_p22, cell_controller_12_p23, cell_controller_12_p24, cell_controller_12_p25, cell_controller_12_p26, cell_controller_12_p27, cell_controller_12_p28, cell_controller_12_p29, cell_controller_12_p30, cell_controller_12_p31, cell_controller_12_p32, cell_controller_12_p33, cell_controller_12_p34, cell_controller_12_p35, cell_controller_12_p36, cell_controller_12_p37
  DotMatrix #(.matrixcols(11), .matrixrows(8)) dotmatrix_39 (
    .col0(cell_controller_12_p6), .col1(cell_controller_12_p9), .col2(cell_controller_12_p12),
    .col3(cell_controller_12_p15), .col4(cell_controller_12_p18), .col5(cell_controller_12_p21),
    .col6(cell_controller_12_p24), .col7(cell_controller_12_p27), .col8(cell_controller_12_p30),
    .col9(cell_controller_12_p33), .col10(cell_controller_12_p36));
  DotMatrix #(.matrixcols(11), .matrixrows(8)) dotmatrix_40 (
    .col0(cell_controller_12_p7), .col1(cell_controller_12_p10), .col2(cell_controller_12_p13),
    .col3(cell_controller_12_p16), .col4(cell_controller_12_p19), .col5(cell_controller_12_p22),
    .col6(cell_controller_12_p25), .col7(cell_controller_12_p28), .col8(cell_controller_12_p31),
    .col9(cell_controller_12_p34), .col10(cell_controller_12_p37));
  // Cell_controller cell_controller_13: pin names not known; wires that end beside it: Columns[1], Rows[4], MOSI, MISO, cell_controller_13_p5, cell_controller_13_p6, cell_controller_13_p7, cell_controller_13_p8, cell_controller_13_p9, cell_controller_13_p10, cell_controller_13_p11, cell_controller_13_p12, cell_controller_13_p13, cell_controller_13_p14, cell_controller_13_p15, cell_controller_13_p16, cell_controller_13_p17, cell_controller_13_p18, cell_controller_13_p19, cell_controller_13_p20, cell_controller_13_p21, cell_controller_13_p22, cell_controller_13_p23, cell_controller_13_p24, cell_controller_13_p25, cell_controller_13_p26, cell_controller_13_p27, cell_controller_13_p28, cell_controller_13_p29, cell_controller_13_p30, cell_controller_13_p31, cell_controller_13_p32, cell_controller_13_p33, cell_controller_13_p34, cell_controller_13_p35, cell_controller_13_p36, cell_controller_13_p37
  DotMatrix #(.matrixcols(11), .matrixrows(5)) dotmatrix_41 (
    .col0(cell_controller_13_p5), .col1(cell_controller_13_p8), .col2(cell_controller_13_p11),
    .col3(cell_controller_13_p14), .col4(cell_controller_13_p17), .col5(cell_controller_13_p20),
    .col6(cell_controller_13_p23), .col7(cell_controller_13_p26), .col8(cell_controller_13_p29),
    .col9(cell_controller_13_p32), .col10(cell_controller_13_p35));
  DotMatrix #(.matrixcols(11), .matrixrows(8)) dotmatrix_42 (
    .col0(cell_controller_13_p6), .col1(cell_controller_13_p9), .col2(cell_controller_13_p12),
    .col3(cell_controller_13_p15), .col4(cell_controller_13_p18), .col5(cell_controller_13_p21),
    .col6(cell_controller_13_p24), .col7(cell_controller_13_p27), .col8(cell_controller_13_p30),
    .col9(cell_controller_13_p33), .col10(cell_controller_13_p36));
  DotMatrix #(.matrixcols(11), .matrixrows(8)) dotmatrix_43 (
    .col0(cell_controller_13_p7), .col1(cell_controller_13_p10), .col2(cell_controller_13_p13),
    .col3(cell_controller_13_p16), .col4(cell_controller_13_p19), .col5(cell_controller_13_p22),
    .col6(cell_controller_13_p25), .col7(cell_controller_13_p28), .col8(cell_controller_13_p31),
    .col9(cell_controller_13_p34), .col10(cell_controller_13_p37));
  DotMatrix #(.matrixcols(11), .matrixrows(5)) dotmatrix_44 (
    .col0(cell_controller_14_p5), .col1(cell_controller_14_p8), .col2(cell_controller_14_p11),
    .col3(cell_controller_14_p14), .col4(cell_controller_14_p17), .col5(cell_controller_14_p20),
    .col6(cell_controller_14_p23), .col7(cell_controller_14_p26), .col8(cell_controller_14_p29),
    .col9(cell_controller_14_p32), .col10(cell_controller_14_p35));
  // Cell_controller cell_controller_14: pin names not known; wires that end beside it: Columns[1], Rows[5], MOSI, MISO, cell_controller_14_p5, cell_controller_14_p6, cell_controller_14_p7, cell_controller_14_p8, cell_controller_14_p9, cell_controller_14_p10, cell_controller_14_p11, cell_controller_14_p12, cell_controller_14_p13, cell_controller_14_p14, cell_controller_14_p15, cell_controller_14_p16, cell_controller_14_p17, cell_controller_14_p18, cell_controller_14_p19, cell_controller_14_p20, cell_controller_14_p21, cell_controller_14_p22, cell_controller_14_p23, cell_controller_14_p24, cell_controller_14_p25, cell_controller_14_p26, cell_controller_14_p27, cell_controller_14_p28, cell_controller_14_p29, cell_controller_14_p30, cell_controller_14_p31, cell_controller_14_p32, cell_controller_14_p33, cell_controller_14_p34, cell_controller_14_p35, cell_controller_14_p36, cell_controller_14_p37
  DotMatrix #(.matrixcols(11), .matrixrows(8)) dotmatrix_45 (
    .col0(cell_controller_14_p6), .col1(cell_controller_14_p9), .col2(cell_controller_14_p12),
    .col3(cell_controller_14_p15), .col4(cell_controller_14_p18), .col5(cell_controller_14_p21),
    .col6(cell_controller_14_p24), .col7(cell_controller_14_p27), .col8(cell_controller_14_p30),
    .col9(cell_controller_14_p33), .col10(cell_controller_14_p36));
  DotMatrix #(.matrixcols(11), .matrixrows(8)) dotmatrix_46 (
    .col0(cell_controller_14_p7), .col1(cell_controller_14_p10), .col2(cell_controller_14_p13),
    .col3(cell_controller_14_p16), .col4(cell_controller_14_p19), .col5(cell_controller_14_p22),
    .col6(cell_controller_14_p25), .col7(cell_controller_14_p28), .col8(cell_controller_14_p31),
    .col9(cell_controller_14_p34), .col10(cell_controller_14_p37));
  // Cell_controller cell_controller_15: pin names not known; wires that end beside it: Columns[1], Rows[6], MOSI, MISO, cell_controller_15_p5, cell_controller_15_p6, cell_controller_15_p7, cell_controller_15_p8, cell_controller_15_p9, cell_controller_15_p10, cell_controller_15_p11, cell_controller_15_p12, cell_controller_15_p13, cell_controller_15_p14, cell_controller_15_p15, cell_controller_15_p16, cell_controller_15_p17, cell_controller_15_p18, cell_controller_15_p19, cell_controller_15_p20, cell_controller_15_p21, cell_controller_15_p22, cell_controller_15_p23, cell_controller_15_p24, cell_controller_15_p25, cell_controller_15_p26, cell_controller_15_p27, cell_controller_15_p28, cell_controller_15_p29, cell_controller_15_p30, cell_controller_15_p31, cell_controller_15_p32, cell_controller_15_p33, cell_controller_15_p34, cell_controller_15_p35, cell_controller_15_p36, cell_controller_15_p37
  DotMatrix #(.matrixcols(11), .matrixrows(5)) dotmatrix_47 (
    .col0(cell_controller_15_p5), .col1(cell_controller_15_p8), .col2(cell_controller_15_p11),
    .col3(cell_controller_15_p14), .col4(cell_controller_15_p17), .col5(cell_controller_15_p20),
    .col6(cell_controller_15_p23), .col7(cell_controller_15_p26), .col8(cell_controller_15_p29),
    .col9(cell_controller_15_p32), .col10(cell_controller_15_p35));
  DotMatrix #(.matrixcols(11), .matrixrows(8)) dotmatrix_48 (
    .col0(cell_controller_15_p6), .col1(cell_controller_15_p9), .col2(cell_controller_15_p12),
    .col3(cell_controller_15_p15), .col4(cell_controller_15_p18), .col5(cell_controller_15_p21),
    .col6(cell_controller_15_p24), .col7(cell_controller_15_p27), .col8(cell_controller_15_p30),
    .col9(cell_controller_15_p33), .col10(cell_controller_15_p36));
  DotMatrix #(.matrixcols(11), .matrixrows(8)) dotmatrix_49 (
    .col0(cell_controller_15_p7), .col1(cell_controller_15_p10), .col2(cell_controller_15_p13),
    .col3(cell_controller_15_p16), .col4(cell_controller_15_p19), .col5(cell_controller_15_p22),
    .col6(cell_controller_15_p25), .col7(cell_controller_15_p28), .col8(cell_controller_15_p31),
    .col9(cell_controller_15_p34), .col10(cell_controller_15_p37));
  // Cell_controller cell_controller_16: pin names not known; wires that end beside it: Columns[1], Rows[7], MOSI, MISO, cell_controller_16_p5, cell_controller_16_p6, cell_controller_16_p7, cell_controller_16_p8, cell_controller_16_p9, cell_controller_16_p10, cell_controller_16_p11, cell_controller_16_p12, cell_controller_16_p13, cell_controller_16_p14, cell_controller_16_p15, cell_controller_16_p16, cell_controller_16_p17, cell_controller_16_p18, cell_controller_16_p19, cell_controller_16_p20, cell_controller_16_p21, cell_controller_16_p22, cell_controller_16_p23, cell_controller_16_p24, cell_controller_16_p25, cell_controller_16_p26, cell_controller_16_p27, cell_controller_16_p28, cell_controller_16_p29, cell_controller_16_p30, cell_controller_16_p31, cell_controller_16_p32, cell_controller_16_p33, cell_controller_16_p34, cell_controller_16_p35, cell_controller_16_p36, cell_controller_16_p37
  DotMatrix #(.matrixcols(11), .matrixrows(5)) dotmatrix_50 (
    .col0(cell_controller_16_p5), .col1(cell_controller_16_p8), .col2(cell_controller_16_p11),
    .col3(cell_controller_16_p14), .col4(cell_controller_16_p17), .col5(cell_controller_16_p20),
    .col6(cell_controller_16_p23), .col7(cell_controller_16_p26), .col8(cell_controller_16_p29),
    .col9(cell_controller_16_p32), .col10(cell_controller_16_p35));
  DotMatrix #(.matrixcols(11), .matrixrows(8)) dotmatrix_51 (
    .col0(cell_controller_16_p6), .col1(cell_controller_16_p9), .col2(cell_controller_16_p12),
    .col3(cell_controller_16_p15), .col4(cell_controller_16_p18), .col5(cell_controller_16_p21),
    .col6(cell_controller_16_p24), .col7(cell_controller_16_p27), .col8(cell_controller_16_p30),
    .col9(cell_controller_16_p33), .col10(cell_controller_16_p36));
  DotMatrix #(.matrixcols(11), .matrixrows(8)) dotmatrix_52 (
    .col0(cell_controller_16_p7), .col1(cell_controller_16_p10), .col2(cell_controller_16_p13),
    .col3(cell_controller_16_p16), .col4(cell_controller_16_p19), .col5(cell_controller_16_p22),
    .col6(cell_controller_16_p25), .col7(cell_controller_16_p28), .col8(cell_controller_16_p31),
    .col9(cell_controller_16_p34), .col10(cell_controller_16_p37));
  DotMatrix #(.inputtype("row"), .matrixcols(8), .matrixrows(1)) dotmatrix_53 (.row0({Columns[0], Columns[1], Columns[2], Columns[3], Columns[4], Columns[5], Columns[6], Columns[7]}));
  DotMatrix #(.matrixcols(1), .matrixrows(8)) dotmatrix_54 (.col0({Rows[0], Rows[1], Rows[2], Rows[3], Rows[4], Rows[5], Rows[6], Rows[7]}));
  DotMatrix #(.matrixcols(11), .matrixrows(5)) dotmatrix_55 (
    .col0(cell_controller_17_p5), .col1(cell_controller_17_p8), .col2(cell_controller_17_p11),
    .col3(cell_controller_17_p14), .col4(cell_controller_17_p17), .col5(cell_controller_17_p20),
    .col6(cell_controller_17_p23), .col7(cell_controller_17_p26), .col8(cell_controller_17_p29),
    .col9(cell_controller_17_p32), .col10(cell_controller_17_p35));
  // Cell_controller cell_controller_17: pin names not known; wires that end beside it: Columns[2], Rows[0], MOSI, MISO, cell_controller_17_p5, cell_controller_17_p6, cell_controller_17_p7, cell_controller_17_p8, cell_controller_17_p9, cell_controller_17_p10, cell_controller_17_p11, cell_controller_17_p12, cell_controller_17_p13, cell_controller_17_p14, cell_controller_17_p15, cell_controller_17_p16, cell_controller_17_p17, cell_controller_17_p18, cell_controller_17_p19, cell_controller_17_p20, cell_controller_17_p21, cell_controller_17_p22, cell_controller_17_p23, cell_controller_17_p24, cell_controller_17_p25, cell_controller_17_p26, cell_controller_17_p27, cell_controller_17_p28, cell_controller_17_p29, cell_controller_17_p30, cell_controller_17_p31, cell_controller_17_p32, cell_controller_17_p33, cell_controller_17_p34, cell_controller_17_p35, cell_controller_17_p36, cell_controller_17_p37
  DotMatrix #(.matrixcols(11), .matrixrows(8)) dotmatrix_56 (
    .col0(cell_controller_17_p6), .col1(cell_controller_17_p9), .col2(cell_controller_17_p12),
    .col3(cell_controller_17_p15), .col4(cell_controller_17_p18), .col5(cell_controller_17_p21),
    .col6(cell_controller_17_p24), .col7(cell_controller_17_p27), .col8(cell_controller_17_p30),
    .col9(cell_controller_17_p33), .col10(cell_controller_17_p36));
  DotMatrix #(.matrixcols(11), .matrixrows(8)) dotmatrix_57 (
    .col0(cell_controller_17_p7), .col1(cell_controller_17_p10), .col2(cell_controller_17_p13),
    .col3(cell_controller_17_p16), .col4(cell_controller_17_p19), .col5(cell_controller_17_p22),
    .col6(cell_controller_17_p25), .col7(cell_controller_17_p28), .col8(cell_controller_17_p31),
    .col9(cell_controller_17_p34), .col10(cell_controller_17_p37));
  DotMatrix #(.matrixcols(11), .matrixrows(5)) dotmatrix_58 (
    .col0(cell_controller_18_p5), .col1(cell_controller_18_p8), .col2(cell_controller_18_p11),
    .col3(cell_controller_18_p14), .col4(cell_controller_18_p17), .col5(cell_controller_18_p20),
    .col6(cell_controller_18_p23), .col7(cell_controller_18_p26), .col8(cell_controller_18_p29),
    .col9(cell_controller_18_p32), .col10(cell_controller_18_p35));
  // Cell_controller cell_controller_18: pin names not known; wires that end beside it: Columns[2], Rows[1], MOSI, MISO, cell_controller_18_p5, cell_controller_18_p6, cell_controller_18_p7, cell_controller_18_p8, cell_controller_18_p9, cell_controller_18_p10, cell_controller_18_p11, cell_controller_18_p12, cell_controller_18_p13, cell_controller_18_p14, cell_controller_18_p15, cell_controller_18_p16, cell_controller_18_p17, cell_controller_18_p18, cell_controller_18_p19, cell_controller_18_p20, cell_controller_18_p21, cell_controller_18_p22, cell_controller_18_p23, cell_controller_18_p24, cell_controller_18_p25, cell_controller_18_p26, cell_controller_18_p27, cell_controller_18_p28, cell_controller_18_p29, cell_controller_18_p30, cell_controller_18_p31, cell_controller_18_p32, cell_controller_18_p33, cell_controller_18_p34, cell_controller_18_p35, cell_controller_18_p36, cell_controller_18_p37
  DotMatrix #(.matrixcols(11), .matrixrows(8)) dotmatrix_59 (
    .col0(cell_controller_18_p6), .col1(cell_controller_18_p9), .col2(cell_controller_18_p12),
    .col3(cell_controller_18_p15), .col4(cell_controller_18_p18), .col5(cell_controller_18_p21),
    .col6(cell_controller_18_p24), .col7(cell_controller_18_p27), .col8(cell_controller_18_p30),
    .col9(cell_controller_18_p33), .col10(cell_controller_18_p36));
  DotMatrix #(.matrixcols(11), .matrixrows(8)) dotmatrix_60 (
    .col0(cell_controller_18_p7), .col1(cell_controller_18_p10), .col2(cell_controller_18_p13),
    .col3(cell_controller_18_p16), .col4(cell_controller_18_p19), .col5(cell_controller_18_p22),
    .col6(cell_controller_18_p25), .col7(cell_controller_18_p28), .col8(cell_controller_18_p31),
    .col9(cell_controller_18_p34), .col10(cell_controller_18_p37));
  DotMatrix #(.matrixcols(11), .matrixrows(5)) dotmatrix_61 (
    .col0(cell_controller_19_p5), .col1(cell_controller_19_p8), .col2(cell_controller_19_p11),
    .col3(cell_controller_19_p14), .col4(cell_controller_19_p17), .col5(cell_controller_19_p20),
    .col6(cell_controller_19_p23), .col7(cell_controller_19_p26), .col8(cell_controller_19_p29),
    .col9(cell_controller_19_p32), .col10(cell_controller_19_p35));
  // Cell_controller cell_controller_19: pin names not known; wires that end beside it: Columns[2], Rows[2], MOSI, MISO, cell_controller_19_p5, cell_controller_19_p6, cell_controller_19_p7, cell_controller_19_p8, cell_controller_19_p9, cell_controller_19_p10, cell_controller_19_p11, cell_controller_19_p12, cell_controller_19_p13, cell_controller_19_p14, cell_controller_19_p15, cell_controller_19_p16, cell_controller_19_p17, cell_controller_19_p18, cell_controller_19_p19, cell_controller_19_p20, cell_controller_19_p21, cell_controller_19_p22, cell_controller_19_p23, cell_controller_19_p24, cell_controller_19_p25, cell_controller_19_p26, cell_controller_19_p27, cell_controller_19_p28, cell_controller_19_p29, cell_controller_19_p30, cell_controller_19_p31, cell_controller_19_p32, cell_controller_19_p33, cell_controller_19_p34, cell_controller_19_p35, cell_controller_19_p36, cell_controller_19_p37
  DotMatrix #(.matrixcols(11), .matrixrows(8)) dotmatrix_62 (
    .col0(cell_controller_19_p6), .col1(cell_controller_19_p9), .col2(cell_controller_19_p12),
    .col3(cell_controller_19_p15), .col4(cell_controller_19_p18), .col5(cell_controller_19_p21),
    .col6(cell_controller_19_p24), .col7(cell_controller_19_p27), .col8(cell_controller_19_p30),
    .col9(cell_controller_19_p33), .col10(cell_controller_19_p36));
  DotMatrix #(.matrixcols(11), .matrixrows(8)) dotmatrix_63 (
    .col0(cell_controller_19_p7), .col1(cell_controller_19_p10), .col2(cell_controller_19_p13),
    .col3(cell_controller_19_p16), .col4(cell_controller_19_p19), .col5(cell_controller_19_p22),
    .col6(cell_controller_19_p25), .col7(cell_controller_19_p28), .col8(cell_controller_19_p31),
    .col9(cell_controller_19_p34), .col10(cell_controller_19_p37));
  // Cell_controller cell_controller_20: pin names not known; wires that end beside it: Columns[2], Rows[3], MOSI, MISO, cell_controller_20_p5, cell_controller_20_p6, cell_controller_20_p7, cell_controller_20_p8, cell_controller_20_p9, cell_controller_20_p10, cell_controller_20_p11, cell_controller_20_p12, cell_controller_20_p13, cell_controller_20_p14, cell_controller_20_p15, cell_controller_20_p16, cell_controller_20_p17, cell_controller_20_p18, cell_controller_20_p19, cell_controller_20_p20, cell_controller_20_p21, cell_controller_20_p22, cell_controller_20_p23, cell_controller_20_p24, cell_controller_20_p25, cell_controller_20_p26, cell_controller_20_p27, cell_controller_20_p28, cell_controller_20_p29, cell_controller_20_p30, cell_controller_20_p31, cell_controller_20_p32, cell_controller_20_p33, cell_controller_20_p34, cell_controller_20_p35, cell_controller_20_p36, cell_controller_20_p37
  DotMatrix #(.matrixcols(11), .matrixrows(5)) dotmatrix_64 (
    .col0(cell_controller_20_p5), .col1(cell_controller_20_p8), .col2(cell_controller_20_p11),
    .col3(cell_controller_20_p14), .col4(cell_controller_20_p17), .col5(cell_controller_20_p20),
    .col6(cell_controller_20_p23), .col7(cell_controller_20_p26), .col8(cell_controller_20_p29),
    .col9(cell_controller_20_p32), .col10(cell_controller_20_p35));
  DotMatrix #(.matrixcols(11), .matrixrows(8)) dotmatrix_65 (
    .col0(cell_controller_20_p6), .col1(cell_controller_20_p9), .col2(cell_controller_20_p12),
    .col3(cell_controller_20_p15), .col4(cell_controller_20_p18), .col5(cell_controller_20_p21),
    .col6(cell_controller_20_p24), .col7(cell_controller_20_p27), .col8(cell_controller_20_p30),
    .col9(cell_controller_20_p33), .col10(cell_controller_20_p36));
  DotMatrix #(.matrixcols(11), .matrixrows(8)) dotmatrix_66 (
    .col0(cell_controller_20_p7), .col1(cell_controller_20_p10), .col2(cell_controller_20_p13),
    .col3(cell_controller_20_p16), .col4(cell_controller_20_p19), .col5(cell_controller_20_p22),
    .col6(cell_controller_20_p25), .col7(cell_controller_20_p28), .col8(cell_controller_20_p31),
    .col9(cell_controller_20_p34), .col10(cell_controller_20_p37));
  DotMatrix #(.matrixcols(11), .matrixrows(5)) dotmatrix_67 (
    .col0(cell_controller_21_p5), .col1(cell_controller_21_p8), .col2(cell_controller_21_p11),
    .col3(cell_controller_21_p14), .col4(cell_controller_21_p17), .col5(cell_controller_21_p20),
    .col6(cell_controller_21_p23), .col7(cell_controller_21_p26), .col8(cell_controller_21_p29),
    .col9(cell_controller_21_p32), .col10(cell_controller_21_p35));
  // Cell_controller cell_controller_21: pin names not known; wires that end beside it: Columns[2], Rows[4], MOSI, MISO, cell_controller_21_p5, cell_controller_21_p6, cell_controller_21_p7, cell_controller_21_p8, cell_controller_21_p9, cell_controller_21_p10, cell_controller_21_p11, cell_controller_21_p12, cell_controller_21_p13, cell_controller_21_p14, cell_controller_21_p15, cell_controller_21_p16, cell_controller_21_p17, cell_controller_21_p18, cell_controller_21_p19, cell_controller_21_p20, cell_controller_21_p21, cell_controller_21_p22, cell_controller_21_p23, cell_controller_21_p24, cell_controller_21_p25, cell_controller_21_p26, cell_controller_21_p27, cell_controller_21_p28, cell_controller_21_p29, cell_controller_21_p30, cell_controller_21_p31, cell_controller_21_p32, cell_controller_21_p33, cell_controller_21_p34, cell_controller_21_p35, cell_controller_21_p36, cell_controller_21_p37
  DotMatrix #(.matrixcols(11), .matrixrows(8)) dotmatrix_68 (
    .col0(cell_controller_21_p6), .col1(cell_controller_21_p9), .col2(cell_controller_21_p12),
    .col3(cell_controller_21_p15), .col4(cell_controller_21_p18), .col5(cell_controller_21_p21),
    .col6(cell_controller_21_p24), .col7(cell_controller_21_p27), .col8(cell_controller_21_p30),
    .col9(cell_controller_21_p33), .col10(cell_controller_21_p36));
  DotMatrix #(.matrixcols(11), .matrixrows(8)) dotmatrix_69 (
    .col0(cell_controller_21_p7), .col1(cell_controller_21_p10), .col2(cell_controller_21_p13),
    .col3(cell_controller_21_p16), .col4(cell_controller_21_p19), .col5(cell_controller_21_p22),
    .col6(cell_controller_21_p25), .col7(cell_controller_21_p28), .col8(cell_controller_21_p31),
    .col9(cell_controller_21_p34), .col10(cell_controller_21_p37));
  // Cell_controller cell_controller_22: pin names not known; wires that end beside it: Columns[2], Rows[5], MOSI, MISO, cell_controller_22_p5, cell_controller_22_p6, cell_controller_22_p7, cell_controller_22_p8, cell_controller_22_p9, cell_controller_22_p10, cell_controller_22_p11, cell_controller_22_p12, cell_controller_22_p13, cell_controller_22_p14, cell_controller_22_p15, cell_controller_22_p16, cell_controller_22_p17, cell_controller_22_p18, cell_controller_22_p19, cell_controller_22_p20, cell_controller_22_p21, cell_controller_22_p22, cell_controller_22_p23, cell_controller_22_p24, cell_controller_22_p25, cell_controller_22_p26, cell_controller_22_p27, cell_controller_22_p28, cell_controller_22_p29, cell_controller_22_p30, cell_controller_22_p31, cell_controller_22_p32, cell_controller_22_p33, cell_controller_22_p34, cell_controller_22_p35, cell_controller_22_p36, cell_controller_22_p37
  DotMatrix #(.matrixcols(11), .matrixrows(5)) dotmatrix_70 (
    .col0(cell_controller_22_p5), .col1(cell_controller_22_p8), .col2(cell_controller_22_p11),
    .col3(cell_controller_22_p14), .col4(cell_controller_22_p17), .col5(cell_controller_22_p20),
    .col6(cell_controller_22_p23), .col7(cell_controller_22_p26), .col8(cell_controller_22_p29),
    .col9(cell_controller_22_p32), .col10(cell_controller_22_p35));
  DotMatrix #(.matrixcols(11), .matrixrows(8)) dotmatrix_71 (
    .col0(cell_controller_22_p6), .col1(cell_controller_22_p9), .col2(cell_controller_22_p12),
    .col3(cell_controller_22_p15), .col4(cell_controller_22_p18), .col5(cell_controller_22_p21),
    .col6(cell_controller_22_p24), .col7(cell_controller_22_p27), .col8(cell_controller_22_p30),
    .col9(cell_controller_22_p33), .col10(cell_controller_22_p36));
  DotMatrix #(.matrixcols(11), .matrixrows(8)) dotmatrix_72 (
    .col0(cell_controller_22_p7), .col1(cell_controller_22_p10), .col2(cell_controller_22_p13),
    .col3(cell_controller_22_p16), .col4(cell_controller_22_p19), .col5(cell_controller_22_p22),
    .col6(cell_controller_22_p25), .col7(cell_controller_22_p28), .col8(cell_controller_22_p31),
    .col9(cell_controller_22_p34), .col10(cell_controller_22_p37));
  DotMatrix #(.matrixcols(11), .matrixrows(5)) dotmatrix_73 (
    .col0(cell_controller_23_p5), .col1(cell_controller_23_p8), .col2(cell_controller_23_p11),
    .col3(cell_controller_23_p14), .col4(cell_controller_23_p17), .col5(cell_controller_23_p20),
    .col6(cell_controller_23_p23), .col7(cell_controller_23_p26), .col8(cell_controller_23_p29),
    .col9(cell_controller_23_p32), .col10(cell_controller_23_p35));
  // Cell_controller cell_controller_23: pin names not known; wires that end beside it: Columns[2], Rows[6], MOSI, MISO, cell_controller_23_p5, cell_controller_23_p6, cell_controller_23_p7, cell_controller_23_p8, cell_controller_23_p9, cell_controller_23_p10, cell_controller_23_p11, cell_controller_23_p12, cell_controller_23_p13, cell_controller_23_p14, cell_controller_23_p15, cell_controller_23_p16, cell_controller_23_p17, cell_controller_23_p18, cell_controller_23_p19, cell_controller_23_p20, cell_controller_23_p21, cell_controller_23_p22, cell_controller_23_p23, cell_controller_23_p24, cell_controller_23_p25, cell_controller_23_p26, cell_controller_23_p27, cell_controller_23_p28, cell_controller_23_p29, cell_controller_23_p30, cell_controller_23_p31, cell_controller_23_p32, cell_controller_23_p33, cell_controller_23_p34, cell_controller_23_p35, cell_controller_23_p36, cell_controller_23_p37
  DotMatrix #(.matrixcols(11), .matrixrows(8)) dotmatrix_74 (
    .col0(cell_controller_23_p6), .col1(cell_controller_23_p9), .col2(cell_controller_23_p12),
    .col3(cell_controller_23_p15), .col4(cell_controller_23_p18), .col5(cell_controller_23_p21),
    .col6(cell_controller_23_p24), .col7(cell_controller_23_p27), .col8(cell_controller_23_p30),
    .col9(cell_controller_23_p33), .col10(cell_controller_23_p36));
  DotMatrix #(.matrixcols(11), .matrixrows(8)) dotmatrix_75 (
    .col0(cell_controller_23_p7), .col1(cell_controller_23_p10), .col2(cell_controller_23_p13),
    .col3(cell_controller_23_p16), .col4(cell_controller_23_p19), .col5(cell_controller_23_p22),
    .col6(cell_controller_23_p25), .col7(cell_controller_23_p28), .col8(cell_controller_23_p31),
    .col9(cell_controller_23_p34), .col10(cell_controller_23_p37));
  DotMatrix #(.matrixcols(11), .matrixrows(5)) dotmatrix_76 (
    .col0(cell_controller_24_p5), .col1(cell_controller_24_p8), .col2(cell_controller_24_p11),
    .col3(cell_controller_24_p14), .col4(cell_controller_24_p17), .col5(cell_controller_24_p20),
    .col6(cell_controller_24_p23), .col7(cell_controller_24_p26), .col8(cell_controller_24_p29),
    .col9(cell_controller_24_p32), .col10(cell_controller_24_p35));
  // Cell_controller cell_controller_24: pin names not known; wires that end beside it: Columns[2], Rows[7], MOSI, MISO, cell_controller_24_p5, cell_controller_24_p6, cell_controller_24_p7, cell_controller_24_p8, cell_controller_24_p9, cell_controller_24_p10, cell_controller_24_p11, cell_controller_24_p12, cell_controller_24_p13, cell_controller_24_p14, cell_controller_24_p15, cell_controller_24_p16, cell_controller_24_p17, cell_controller_24_p18, cell_controller_24_p19, cell_controller_24_p20, cell_controller_24_p21, cell_controller_24_p22, cell_controller_24_p23, cell_controller_24_p24, cell_controller_24_p25, cell_controller_24_p26, cell_controller_24_p27, cell_controller_24_p28, cell_controller_24_p29, cell_controller_24_p30, cell_controller_24_p31, cell_controller_24_p32, cell_controller_24_p33, cell_controller_24_p34, cell_controller_24_p35, cell_controller_24_p36, cell_controller_24_p37
  DotMatrix #(.matrixcols(11), .matrixrows(8)) dotmatrix_77 (
    .col0(cell_controller_24_p6), .col1(cell_controller_24_p9), .col2(cell_controller_24_p12),
    .col3(cell_controller_24_p15), .col4(cell_controller_24_p18), .col5(cell_controller_24_p21),
    .col6(cell_controller_24_p24), .col7(cell_controller_24_p27), .col8(cell_controller_24_p30),
    .col9(cell_controller_24_p33), .col10(cell_controller_24_p36));
  DotMatrix #(.matrixcols(11), .matrixrows(8)) dotmatrix_78 (
    .col0(cell_controller_24_p7), .col1(cell_controller_24_p10), .col2(cell_controller_24_p13),
    .col3(cell_controller_24_p16), .col4(cell_controller_24_p19), .col5(cell_controller_24_p22),
    .col6(cell_controller_24_p25), .col7(cell_controller_24_p28), .col8(cell_controller_24_p31),
    .col9(cell_controller_24_p34), .col10(cell_controller_24_p37));
  Demultiplexer #(.select(2), .enable("false")) demultiplexer_1 (
    .out0(demultiplexer_1_out0), .out1(demultiplexer_1_out1), .out2(demultiplexer_1_out2),
    .out3(demultiplexer_1_out3), .in(Y), .sel(input_controller_1_cursor_position));
  DotMatrix #(.matrixcols(9), .matrixrows(15)) dotmatrix_79 (
    .col0(output_big_numder_1_out_3), .col1(output_big_numder_1_out_4), .col2(output_big_numder_1_out_5),
    .col3(output_big_numder_1_out_6), .col4(output_big_numder_1_out_7), .col5(output_big_numder_1_out_8),
    .col6(output_big_numder_1_out_9), .col7(output_big_numder_1_out_10), .col8(output_big_numder_1_out_11));
  Output_big_numder output_big_numder_1 (
    .out_3(output_big_numder_1_out_3), .out_4(output_big_numder_1_out_4), .out_5(output_big_numder_1_out_5),
    .out_6(output_big_numder_1_out_6), .out_7(output_big_numder_1_out_7), .out_8(output_big_numder_1_out_8),
    .out_9(output_big_numder_1_out_9), .out_10(output_big_numder_1_out_10),
    .out_11(output_big_numder_1_out_11), .in_1(input_controller_1_input_buffer[6:0]),
    .INV(demultiplexer_1_out0));
  // Cell_controller cell_controller_25: pin names not known; wires that end beside it: Columns[3], Rows[0], MOSI, MISO, cell_controller_25_p5, cell_controller_25_p6, cell_controller_25_p7, cell_controller_25_p8, cell_controller_25_p9, cell_controller_25_p10, cell_controller_25_p11, cell_controller_25_p12, cell_controller_25_p13, cell_controller_25_p14, cell_controller_25_p15, cell_controller_25_p16, cell_controller_25_p17, cell_controller_25_p18, cell_controller_25_p19, cell_controller_25_p20, cell_controller_25_p21, cell_controller_25_p22, cell_controller_25_p23, cell_controller_25_p24, cell_controller_25_p25, cell_controller_25_p26, cell_controller_25_p27, cell_controller_25_p28, cell_controller_25_p29, cell_controller_25_p30, cell_controller_25_p31, cell_controller_25_p32, cell_controller_25_p33, cell_controller_25_p34, cell_controller_25_p35, cell_controller_25_p36, cell_controller_25_p37
  DotMatrix #(.matrixcols(11), .matrixrows(5)) dotmatrix_80 (
    .col0(cell_controller_25_p5), .col1(cell_controller_25_p8), .col2(cell_controller_25_p11),
    .col3(cell_controller_25_p14), .col4(cell_controller_25_p17), .col5(cell_controller_25_p20),
    .col6(cell_controller_25_p23), .col7(cell_controller_25_p26), .col8(cell_controller_25_p29),
    .col9(cell_controller_25_p32), .col10(cell_controller_25_p35));
  DotMatrix #(.matrixcols(11), .matrixrows(8)) dotmatrix_81 (
    .col0(cell_controller_25_p6), .col1(cell_controller_25_p9), .col2(cell_controller_25_p12),
    .col3(cell_controller_25_p15), .col4(cell_controller_25_p18), .col5(cell_controller_25_p21),
    .col6(cell_controller_25_p24), .col7(cell_controller_25_p27), .col8(cell_controller_25_p30),
    .col9(cell_controller_25_p33), .col10(cell_controller_25_p36));
  DotMatrix #(.matrixcols(11), .matrixrows(8)) dotmatrix_82 (
    .col0(cell_controller_25_p7), .col1(cell_controller_25_p10), .col2(cell_controller_25_p13),
    .col3(cell_controller_25_p16), .col4(cell_controller_25_p19), .col5(cell_controller_25_p22),
    .col6(cell_controller_25_p25), .col7(cell_controller_25_p28), .col8(cell_controller_25_p31),
    .col9(cell_controller_25_p34), .col10(cell_controller_25_p37));
  DotMatrix #(.matrixcols(11), .matrixrows(5)) dotmatrix_83 (
    .col0(cell_controller_26_p5), .col1(cell_controller_26_p8), .col2(cell_controller_26_p11),
    .col3(cell_controller_26_p14), .col4(cell_controller_26_p17), .col5(cell_controller_26_p20),
    .col6(cell_controller_26_p23), .col7(cell_controller_26_p26), .col8(cell_controller_26_p29),
    .col9(cell_controller_26_p32), .col10(cell_controller_26_p35));
  // Cell_controller cell_controller_26: pin names not known; wires that end beside it: Columns[3], Rows[1], MOSI, MISO, cell_controller_26_p5, cell_controller_26_p6, cell_controller_26_p7, cell_controller_26_p8, cell_controller_26_p9, cell_controller_26_p10, cell_controller_26_p11, cell_controller_26_p12, cell_controller_26_p13, cell_controller_26_p14, cell_controller_26_p15, cell_controller_26_p16, cell_controller_26_p17, cell_controller_26_p18, cell_controller_26_p19, cell_controller_26_p20, cell_controller_26_p21, cell_controller_26_p22, cell_controller_26_p23, cell_controller_26_p24, cell_controller_26_p25, cell_controller_26_p26, cell_controller_26_p27, cell_controller_26_p28, cell_controller_26_p29, cell_controller_26_p30, cell_controller_26_p31, cell_controller_26_p32, cell_controller_26_p33, cell_controller_26_p34, cell_controller_26_p35, cell_controller_26_p36, cell_controller_26_p37
  DotMatrix #(.matrixcols(11), .matrixrows(8)) dotmatrix_84 (
    .col0(cell_controller_26_p6), .col1(cell_controller_26_p9), .col2(cell_controller_26_p12),
    .col3(cell_controller_26_p15), .col4(cell_controller_26_p18), .col5(cell_controller_26_p21),
    .col6(cell_controller_26_p24), .col7(cell_controller_26_p27), .col8(cell_controller_26_p30),
    .col9(cell_controller_26_p33), .col10(cell_controller_26_p36));
  DotMatrix #(.matrixcols(11), .matrixrows(8)) dotmatrix_85 (
    .col0(cell_controller_26_p7), .col1(cell_controller_26_p10), .col2(cell_controller_26_p13),
    .col3(cell_controller_26_p16), .col4(cell_controller_26_p19), .col5(cell_controller_26_p22),
    .col6(cell_controller_26_p25), .col7(cell_controller_26_p28), .col8(cell_controller_26_p31),
    .col9(cell_controller_26_p34), .col10(cell_controller_26_p37));
  DotMatrix #(.matrixcols(11), .matrixrows(5)) dotmatrix_86 (
    .col0(cell_controller_27_p5), .col1(cell_controller_27_p8), .col2(cell_controller_27_p11),
    .col3(cell_controller_27_p14), .col4(cell_controller_27_p17), .col5(cell_controller_27_p20),
    .col6(cell_controller_27_p23), .col7(cell_controller_27_p26), .col8(cell_controller_27_p29),
    .col9(cell_controller_27_p32), .col10(cell_controller_27_p35));
  // Cell_controller cell_controller_27: pin names not known; wires that end beside it: Columns[3], Rows[2], MOSI, MISO, cell_controller_27_p5, cell_controller_27_p6, cell_controller_27_p7, cell_controller_27_p8, cell_controller_27_p9, cell_controller_27_p10, cell_controller_27_p11, cell_controller_27_p12, cell_controller_27_p13, cell_controller_27_p14, cell_controller_27_p15, cell_controller_27_p16, cell_controller_27_p17, cell_controller_27_p18, cell_controller_27_p19, cell_controller_27_p20, cell_controller_27_p21, cell_controller_27_p22, cell_controller_27_p23, cell_controller_27_p24, cell_controller_27_p25, cell_controller_27_p26, cell_controller_27_p27, cell_controller_27_p28, cell_controller_27_p29, cell_controller_27_p30, cell_controller_27_p31, cell_controller_27_p32, cell_controller_27_p33, cell_controller_27_p34, cell_controller_27_p35, cell_controller_27_p36, cell_controller_27_p37
  DotMatrix #(.matrixcols(11), .matrixrows(8)) dotmatrix_87 (
    .col0(cell_controller_27_p6), .col1(cell_controller_27_p9), .col2(cell_controller_27_p12),
    .col3(cell_controller_27_p15), .col4(cell_controller_27_p18), .col5(cell_controller_27_p21),
    .col6(cell_controller_27_p24), .col7(cell_controller_27_p27), .col8(cell_controller_27_p30),
    .col9(cell_controller_27_p33), .col10(cell_controller_27_p36));
  DotMatrix #(.matrixcols(11), .matrixrows(8)) dotmatrix_88 (
    .col0(cell_controller_27_p7), .col1(cell_controller_27_p10), .col2(cell_controller_27_p13),
    .col3(cell_controller_27_p16), .col4(cell_controller_27_p19), .col5(cell_controller_27_p22),
    .col6(cell_controller_27_p25), .col7(cell_controller_27_p28), .col8(cell_controller_27_p31),
    .col9(cell_controller_27_p34), .col10(cell_controller_27_p37));
  // Cell_controller cell_controller_28: pin names not known; wires that end beside it: Columns[3], Rows[3], MOSI, MISO, cell_controller_28_p5, cell_controller_28_p6, cell_controller_28_p7, cell_controller_28_p8, cell_controller_28_p9, cell_controller_28_p10, cell_controller_28_p11, cell_controller_28_p12, cell_controller_28_p13, cell_controller_28_p14, cell_controller_28_p15, cell_controller_28_p16, cell_controller_28_p17, cell_controller_28_p18, cell_controller_28_p19, cell_controller_28_p20, cell_controller_28_p21, cell_controller_28_p22, cell_controller_28_p23, cell_controller_28_p24, cell_controller_28_p25, cell_controller_28_p26, cell_controller_28_p27, cell_controller_28_p28, cell_controller_28_p29, cell_controller_28_p30, cell_controller_28_p31, cell_controller_28_p32, cell_controller_28_p33, cell_controller_28_p34, cell_controller_28_p35, cell_controller_28_p36, cell_controller_28_p37
  DotMatrix #(.matrixcols(11), .matrixrows(5)) dotmatrix_89 (
    .col0(cell_controller_28_p5), .col1(cell_controller_28_p8), .col2(cell_controller_28_p11),
    .col3(cell_controller_28_p14), .col4(cell_controller_28_p17), .col5(cell_controller_28_p20),
    .col6(cell_controller_28_p23), .col7(cell_controller_28_p26), .col8(cell_controller_28_p29),
    .col9(cell_controller_28_p32), .col10(cell_controller_28_p35));
  DotMatrix #(.matrixcols(11), .matrixrows(8)) dotmatrix_90 (
    .col0(cell_controller_28_p6), .col1(cell_controller_28_p9), .col2(cell_controller_28_p12),
    .col3(cell_controller_28_p15), .col4(cell_controller_28_p18), .col5(cell_controller_28_p21),
    .col6(cell_controller_28_p24), .col7(cell_controller_28_p27), .col8(cell_controller_28_p30),
    .col9(cell_controller_28_p33), .col10(cell_controller_28_p36));
  DotMatrix #(.matrixcols(11), .matrixrows(8)) dotmatrix_91 (
    .col0(cell_controller_28_p7), .col1(cell_controller_28_p10), .col2(cell_controller_28_p13),
    .col3(cell_controller_28_p16), .col4(cell_controller_28_p19), .col5(cell_controller_28_p22),
    .col6(cell_controller_28_p25), .col7(cell_controller_28_p28), .col8(cell_controller_28_p31),
    .col9(cell_controller_28_p34), .col10(cell_controller_28_p37));
  // Cell_controller cell_controller_29: pin names not known; wires that end beside it: Columns[3], Rows[4], MOSI, MISO, cell_controller_29_p5, cell_controller_29_p6, cell_controller_29_p7, cell_controller_29_p8, cell_controller_29_p9, cell_controller_29_p10, cell_controller_29_p11, cell_controller_29_p12, cell_controller_29_p13, cell_controller_29_p14, cell_controller_29_p15, cell_controller_29_p16, cell_controller_29_p17, cell_controller_29_p18, cell_controller_29_p19, cell_controller_29_p20, cell_controller_29_p21, cell_controller_29_p22, cell_controller_29_p23, cell_controller_29_p24, cell_controller_29_p25, cell_controller_29_p26, cell_controller_29_p27, cell_controller_29_p28, cell_controller_29_p29, cell_controller_29_p30, cell_controller_29_p31, cell_controller_29_p32, cell_controller_29_p33, cell_controller_29_p34, cell_controller_29_p35, cell_controller_29_p36, cell_controller_29_p37
  DotMatrix #(.matrixcols(11), .matrixrows(5)) dotmatrix_92 (
    .col0(cell_controller_29_p5), .col1(cell_controller_29_p8), .col2(cell_controller_29_p11),
    .col3(cell_controller_29_p14), .col4(cell_controller_29_p17), .col5(cell_controller_29_p20),
    .col6(cell_controller_29_p23), .col7(cell_controller_29_p26), .col8(cell_controller_29_p29),
    .col9(cell_controller_29_p32), .col10(cell_controller_29_p35));
  DotMatrix #(.matrixcols(11), .matrixrows(8)) dotmatrix_93 (
    .col0(cell_controller_29_p6), .col1(cell_controller_29_p9), .col2(cell_controller_29_p12),
    .col3(cell_controller_29_p15), .col4(cell_controller_29_p18), .col5(cell_controller_29_p21),
    .col6(cell_controller_29_p24), .col7(cell_controller_29_p27), .col8(cell_controller_29_p30),
    .col9(cell_controller_29_p33), .col10(cell_controller_29_p36));
  DotMatrix #(.matrixcols(11), .matrixrows(8)) dotmatrix_94 (
    .col0(cell_controller_29_p7), .col1(cell_controller_29_p10), .col2(cell_controller_29_p13),
    .col3(cell_controller_29_p16), .col4(cell_controller_29_p19), .col5(cell_controller_29_p22),
    .col6(cell_controller_29_p25), .col7(cell_controller_29_p28), .col8(cell_controller_29_p31),
    .col9(cell_controller_29_p34), .col10(cell_controller_29_p37));
  // Cell_controller cell_controller_30: pin names not known; wires that end beside it: Columns[3], Rows[5], MOSI, MISO, cell_controller_30_p5, cell_controller_30_p6, cell_controller_30_p7, cell_controller_30_p8, cell_controller_30_p9, cell_controller_30_p10, cell_controller_30_p11, cell_controller_30_p12, cell_controller_30_p13, cell_controller_30_p14, cell_controller_30_p15, cell_controller_30_p16, cell_controller_30_p17, cell_controller_30_p18, cell_controller_30_p19, cell_controller_30_p20, cell_controller_30_p21, cell_controller_30_p22, cell_controller_30_p23, cell_controller_30_p24, cell_controller_30_p25, cell_controller_30_p26, cell_controller_30_p27, cell_controller_30_p28, cell_controller_30_p29, cell_controller_30_p30, cell_controller_30_p31, cell_controller_30_p32, cell_controller_30_p33, cell_controller_30_p34, cell_controller_30_p35, cell_controller_30_p36, cell_controller_30_p37
  DotMatrix #(.matrixcols(11), .matrixrows(5)) dotmatrix_95 (
    .col0(cell_controller_30_p5), .col1(cell_controller_30_p8), .col2(cell_controller_30_p11),
    .col3(cell_controller_30_p14), .col4(cell_controller_30_p17), .col5(cell_controller_30_p20),
    .col6(cell_controller_30_p23), .col7(cell_controller_30_p26), .col8(cell_controller_30_p29),
    .col9(cell_controller_30_p32), .col10(cell_controller_30_p35));
  DotMatrix #(.matrixcols(11), .matrixrows(8)) dotmatrix_96 (
    .col0(cell_controller_30_p6), .col1(cell_controller_30_p9), .col2(cell_controller_30_p12),
    .col3(cell_controller_30_p15), .col4(cell_controller_30_p18), .col5(cell_controller_30_p21),
    .col6(cell_controller_30_p24), .col7(cell_controller_30_p27), .col8(cell_controller_30_p30),
    .col9(cell_controller_30_p33), .col10(cell_controller_30_p36));
  DotMatrix #(.matrixcols(11), .matrixrows(8)) dotmatrix_97 (
    .col0(cell_controller_30_p7), .col1(cell_controller_30_p10), .col2(cell_controller_30_p13),
    .col3(cell_controller_30_p16), .col4(cell_controller_30_p19), .col5(cell_controller_30_p22),
    .col6(cell_controller_30_p25), .col7(cell_controller_30_p28), .col8(cell_controller_30_p31),
    .col9(cell_controller_30_p34), .col10(cell_controller_30_p37));
  // Cell_controller cell_controller_31: pin names not known; wires that end beside it: Columns[3], Rows[6], MOSI, MISO, cell_controller_31_p5, cell_controller_31_p6, cell_controller_31_p7, cell_controller_31_p8, cell_controller_31_p9, cell_controller_31_p10, cell_controller_31_p11, cell_controller_31_p12, cell_controller_31_p13, cell_controller_31_p14, cell_controller_31_p15, cell_controller_31_p16, cell_controller_31_p17, cell_controller_31_p18, cell_controller_31_p19, cell_controller_31_p20, cell_controller_31_p21, cell_controller_31_p22, cell_controller_31_p23, cell_controller_31_p24, cell_controller_31_p25, cell_controller_31_p26, cell_controller_31_p27, cell_controller_31_p28, cell_controller_31_p29, cell_controller_31_p30, cell_controller_31_p31, cell_controller_31_p32, cell_controller_31_p33, cell_controller_31_p34, cell_controller_31_p35, cell_controller_31_p36, cell_controller_31_p37
  DotMatrix #(.matrixcols(11), .matrixrows(5)) dotmatrix_98 (
    .col0(cell_controller_31_p5), .col1(cell_controller_31_p8), .col2(cell_controller_31_p11),
    .col3(cell_controller_31_p14), .col4(cell_controller_31_p17), .col5(cell_controller_31_p20),
    .col6(cell_controller_31_p23), .col7(cell_controller_31_p26), .col8(cell_controller_31_p29),
    .col9(cell_controller_31_p32), .col10(cell_controller_31_p35));
  DotMatrix #(.matrixcols(11), .matrixrows(8)) dotmatrix_99 (
    .col0(cell_controller_31_p6), .col1(cell_controller_31_p9), .col2(cell_controller_31_p12),
    .col3(cell_controller_31_p15), .col4(cell_controller_31_p18), .col5(cell_controller_31_p21),
    .col6(cell_controller_31_p24), .col7(cell_controller_31_p27), .col8(cell_controller_31_p30),
    .col9(cell_controller_31_p33), .col10(cell_controller_31_p36));
  DotMatrix #(.matrixcols(11), .matrixrows(8)) dotmatrix_100 (
    .col0(cell_controller_31_p7), .col1(cell_controller_31_p10), .col2(cell_controller_31_p13),
    .col3(cell_controller_31_p16), .col4(cell_controller_31_p19), .col5(cell_controller_31_p22),
    .col6(cell_controller_31_p25), .col7(cell_controller_31_p28), .col8(cell_controller_31_p31),
    .col9(cell_controller_31_p34), .col10(cell_controller_31_p37));
  DotMatrix #(.matrixcols(11), .matrixrows(5)) dotmatrix_101 (
    .col0(cell_controller_32_p5), .col1(cell_controller_32_p8), .col2(cell_controller_32_p11),
    .col3(cell_controller_32_p14), .col4(cell_controller_32_p17), .col5(cell_controller_32_p20),
    .col6(cell_controller_32_p23), .col7(cell_controller_32_p26), .col8(cell_controller_32_p29),
    .col9(cell_controller_32_p32), .col10(cell_controller_32_p35));
  // Cell_controller cell_controller_32: pin names not known; wires that end beside it: Columns[3], Rows[7], MOSI, MISO, cell_controller_32_p5, cell_controller_32_p6, cell_controller_32_p7, cell_controller_32_p8, cell_controller_32_p9, cell_controller_32_p10, cell_controller_32_p11, cell_controller_32_p12, cell_controller_32_p13, cell_controller_32_p14, cell_controller_32_p15, cell_controller_32_p16, cell_controller_32_p17, cell_controller_32_p18, cell_controller_32_p19, cell_controller_32_p20, cell_controller_32_p21, cell_controller_32_p22, cell_controller_32_p23, cell_controller_32_p24, cell_controller_32_p25, cell_controller_32_p26, cell_controller_32_p27, cell_controller_32_p28, cell_controller_32_p29, cell_controller_32_p30, cell_controller_32_p31, cell_controller_32_p32, cell_controller_32_p33, cell_controller_32_p34, cell_controller_32_p35, cell_controller_32_p36, cell_controller_32_p37
  DotMatrix #(.matrixcols(11), .matrixrows(8)) dotmatrix_102 (
    .col0(cell_controller_32_p6), .col1(cell_controller_32_p9), .col2(cell_controller_32_p12),
    .col3(cell_controller_32_p15), .col4(cell_controller_32_p18), .col5(cell_controller_32_p21),
    .col6(cell_controller_32_p24), .col7(cell_controller_32_p27), .col8(cell_controller_32_p30),
    .col9(cell_controller_32_p33), .col10(cell_controller_32_p36));
  DotMatrix #(.matrixcols(11), .matrixrows(8)) dotmatrix_103 (
    .col0(cell_controller_32_p7), .col1(cell_controller_32_p10), .col2(cell_controller_32_p13),
    .col3(cell_controller_32_p16), .col4(cell_controller_32_p19), .col5(cell_controller_32_p22),
    .col6(cell_controller_32_p25), .col7(cell_controller_32_p28), .col8(cell_controller_32_p31),
    .col9(cell_controller_32_p34), .col10(cell_controller_32_p37));
  DotMatrix #(.matrixcols(9), .matrixrows(15)) dotmatrix_104 (
    .col0(output_big_numder_2_out_3), .col1(output_big_numder_2_out_4), .col2(output_big_numder_2_out_5),
    .col3(output_big_numder_2_out_6), .col4(output_big_numder_2_out_7), .col5(output_big_numder_2_out_8),
    .col6(output_big_numder_2_out_9), .col7(output_big_numder_2_out_10), .col8(output_big_numder_2_out_11));
  Output_big_numder output_big_numder_2 (
    .out_3(output_big_numder_2_out_3), .out_4(output_big_numder_2_out_4), .out_5(output_big_numder_2_out_5),
    .out_6(output_big_numder_2_out_6), .out_7(output_big_numder_2_out_7), .out_8(output_big_numder_2_out_8),
    .out_9(output_big_numder_2_out_9), .out_10(output_big_numder_2_out_10),
    .out_11(output_big_numder_2_out_11), .in_1(input_controller_1_input_buffer_2), .INV(demultiplexer_1_out1));
  DotMatrix #(.matrixcols(9), .matrixrows(15)) dotmatrix_105 (
    .col0(output_big_numder_3_out_3), .col1(output_big_numder_3_out_4), .col2(output_big_numder_3_out_5),
    .col3(output_big_numder_3_out_6), .col4(output_big_numder_3_out_7), .col5(output_big_numder_3_out_8),
    .col6(output_big_numder_3_out_9), .col7(output_big_numder_3_out_10), .col8(output_big_numder_3_out_11));
  Output_big_numder output_big_numder_3 (
    .out_3(output_big_numder_3_out_3), .out_4(output_big_numder_3_out_4), .out_5(output_big_numder_3_out_5),
    .out_6(output_big_numder_3_out_6), .out_7(output_big_numder_3_out_7), .out_8(output_big_numder_3_out_8),
    .out_9(output_big_numder_3_out_9), .out_10(output_big_numder_3_out_10),
    .out_11(output_big_numder_3_out_11), .in_1(input_controller_1_input_buffer[20:14]),
    .INV(demultiplexer_1_out2));
  DotMatrix #(.matrixcols(11), .matrixrows(5)) dotmatrix_106 (
    .col0(cell_controller_33_p5), .col1(cell_controller_33_p8), .col2(cell_controller_33_p11),
    .col3(cell_controller_33_p14), .col4(cell_controller_33_p17), .col5(cell_controller_33_p20),
    .col6(cell_controller_33_p23), .col7(cell_controller_33_p26), .col8(cell_controller_33_p29),
    .col9(cell_controller_33_p32), .col10(cell_controller_33_p35));
  // Cell_controller cell_controller_33: pin names not known; wires that end beside it: Columns[4], Rows[0], MOSI, MISO, cell_controller_33_p5, cell_controller_33_p6, cell_controller_33_p7, cell_controller_33_p8, cell_controller_33_p9, cell_controller_33_p10, cell_controller_33_p11, cell_controller_33_p12, cell_controller_33_p13, cell_controller_33_p14, cell_controller_33_p15, cell_controller_33_p16, cell_controller_33_p17, cell_controller_33_p18, cell_controller_33_p19, cell_controller_33_p20, cell_controller_33_p21, cell_controller_33_p22, cell_controller_33_p23, cell_controller_33_p24, cell_controller_33_p25, cell_controller_33_p26, cell_controller_33_p27, cell_controller_33_p28, cell_controller_33_p29, cell_controller_33_p30, cell_controller_33_p31, cell_controller_33_p32, cell_controller_33_p33, cell_controller_33_p34, cell_controller_33_p35, cell_controller_33_p36, cell_controller_33_p37
  DotMatrix #(.matrixcols(11), .matrixrows(8)) dotmatrix_107 (
    .col0(cell_controller_33_p6), .col1(cell_controller_33_p9), .col2(cell_controller_33_p12),
    .col3(cell_controller_33_p15), .col4(cell_controller_33_p18), .col5(cell_controller_33_p21),
    .col6(cell_controller_33_p24), .col7(cell_controller_33_p27), .col8(cell_controller_33_p30),
    .col9(cell_controller_33_p33), .col10(cell_controller_33_p36));
  DotMatrix #(.matrixcols(11), .matrixrows(8)) dotmatrix_108 (
    .col0(cell_controller_33_p7), .col1(cell_controller_33_p10), .col2(cell_controller_33_p13),
    .col3(cell_controller_33_p16), .col4(cell_controller_33_p19), .col5(cell_controller_33_p22),
    .col6(cell_controller_33_p25), .col7(cell_controller_33_p28), .col8(cell_controller_33_p31),
    .col9(cell_controller_33_p34), .col10(cell_controller_33_p37));
  // Cell_controller cell_controller_34: pin names not known; wires that end beside it: Columns[4], Rows[1], MOSI, MISO, cell_controller_34_p5, cell_controller_34_p6, cell_controller_34_p7, cell_controller_34_p8, cell_controller_34_p9, cell_controller_34_p10, cell_controller_34_p11, cell_controller_34_p12, cell_controller_34_p13, cell_controller_34_p14, cell_controller_34_p15, cell_controller_34_p16, cell_controller_34_p17, cell_controller_34_p18, cell_controller_34_p19, cell_controller_34_p20, cell_controller_34_p21, cell_controller_34_p22, cell_controller_34_p23, cell_controller_34_p24, cell_controller_34_p25, cell_controller_34_p26, cell_controller_34_p27, cell_controller_34_p28, cell_controller_34_p29, cell_controller_34_p30, cell_controller_34_p31, cell_controller_34_p32, cell_controller_34_p33, cell_controller_34_p34, cell_controller_34_p35, cell_controller_34_p36, cell_controller_34_p37
  DotMatrix #(.matrixcols(11), .matrixrows(5)) dotmatrix_109 (
    .col0(cell_controller_34_p5), .col1(cell_controller_34_p8), .col2(cell_controller_34_p11),
    .col3(cell_controller_34_p14), .col4(cell_controller_34_p17), .col5(cell_controller_34_p20),
    .col6(cell_controller_34_p23), .col7(cell_controller_34_p26), .col8(cell_controller_34_p29),
    .col9(cell_controller_34_p32), .col10(cell_controller_34_p35));
  DotMatrix #(.matrixcols(11), .matrixrows(8)) dotmatrix_110 (
    .col0(cell_controller_34_p6), .col1(cell_controller_34_p9), .col2(cell_controller_34_p12),
    .col3(cell_controller_34_p15), .col4(cell_controller_34_p18), .col5(cell_controller_34_p21),
    .col6(cell_controller_34_p24), .col7(cell_controller_34_p27), .col8(cell_controller_34_p30),
    .col9(cell_controller_34_p33), .col10(cell_controller_34_p36));
  DotMatrix #(.matrixcols(11), .matrixrows(8)) dotmatrix_111 (
    .col0(cell_controller_34_p7), .col1(cell_controller_34_p10), .col2(cell_controller_34_p13),
    .col3(cell_controller_34_p16), .col4(cell_controller_34_p19), .col5(cell_controller_34_p22),
    .col6(cell_controller_34_p25), .col7(cell_controller_34_p28), .col8(cell_controller_34_p31),
    .col9(cell_controller_34_p34), .col10(cell_controller_34_p37));
  DotMatrix #(.matrixcols(11), .matrixrows(5)) dotmatrix_112 (
    .col0(cell_controller_35_p5), .col1(cell_controller_35_p8), .col2(cell_controller_35_p11),
    .col3(cell_controller_35_p14), .col4(cell_controller_35_p17), .col5(cell_controller_35_p20),
    .col6(cell_controller_35_p23), .col7(cell_controller_35_p26), .col8(cell_controller_35_p29),
    .col9(cell_controller_35_p32), .col10(cell_controller_35_p35));
  // Cell_controller cell_controller_35: pin names not known; wires that end beside it: Columns[4], Rows[2], MOSI, MISO, cell_controller_35_p5, cell_controller_35_p6, cell_controller_35_p7, cell_controller_35_p8, cell_controller_35_p9, cell_controller_35_p10, cell_controller_35_p11, cell_controller_35_p12, cell_controller_35_p13, cell_controller_35_p14, cell_controller_35_p15, cell_controller_35_p16, cell_controller_35_p17, cell_controller_35_p18, cell_controller_35_p19, cell_controller_35_p20, cell_controller_35_p21, cell_controller_35_p22, cell_controller_35_p23, cell_controller_35_p24, cell_controller_35_p25, cell_controller_35_p26, cell_controller_35_p27, cell_controller_35_p28, cell_controller_35_p29, cell_controller_35_p30, cell_controller_35_p31, cell_controller_35_p32, cell_controller_35_p33, cell_controller_35_p34, cell_controller_35_p35, cell_controller_35_p36, cell_controller_35_p37
  DotMatrix #(.matrixcols(11), .matrixrows(8)) dotmatrix_113 (
    .col0(cell_controller_35_p6), .col1(cell_controller_35_p9), .col2(cell_controller_35_p12),
    .col3(cell_controller_35_p15), .col4(cell_controller_35_p18), .col5(cell_controller_35_p21),
    .col6(cell_controller_35_p24), .col7(cell_controller_35_p27), .col8(cell_controller_35_p30),
    .col9(cell_controller_35_p33), .col10(cell_controller_35_p36));
  DotMatrix #(.matrixcols(11), .matrixrows(8)) dotmatrix_114 (
    .col0(cell_controller_35_p7), .col1(cell_controller_35_p10), .col2(cell_controller_35_p13),
    .col3(cell_controller_35_p16), .col4(cell_controller_35_p19), .col5(cell_controller_35_p22),
    .col6(cell_controller_35_p25), .col7(cell_controller_35_p28), .col8(cell_controller_35_p31),
    .col9(cell_controller_35_p34), .col10(cell_controller_35_p37));
  // Cell_controller cell_controller_36: pin names not known; wires that end beside it: Columns[4], Rows[3], MOSI, MISO, cell_controller_36_p5, cell_controller_36_p6, cell_controller_36_p7, cell_controller_36_p8, cell_controller_36_p9, cell_controller_36_p10, cell_controller_36_p11, cell_controller_36_p12, cell_controller_36_p13, cell_controller_36_p14, cell_controller_36_p15, cell_controller_36_p16, cell_controller_36_p17, cell_controller_36_p18, cell_controller_36_p19, cell_controller_36_p20, cell_controller_36_p21, cell_controller_36_p22, cell_controller_36_p23, cell_controller_36_p24, cell_controller_36_p25, cell_controller_36_p26, cell_controller_36_p27, cell_controller_36_p28, cell_controller_36_p29, cell_controller_36_p30, cell_controller_36_p31, cell_controller_36_p32, cell_controller_36_p33, cell_controller_36_p34, cell_controller_36_p35, cell_controller_36_p36, cell_controller_36_p37
  DotMatrix #(.matrixcols(11), .matrixrows(5)) dotmatrix_115 (
    .col0(cell_controller_36_p5), .col1(cell_controller_36_p8), .col2(cell_controller_36_p11),
    .col3(cell_controller_36_p14), .col4(cell_controller_36_p17), .col5(cell_controller_36_p20),
    .col6(cell_controller_36_p23), .col7(cell_controller_36_p26), .col8(cell_controller_36_p29),
    .col9(cell_controller_36_p32), .col10(cell_controller_36_p35));
  DotMatrix #(.matrixcols(11), .matrixrows(8)) dotmatrix_116 (
    .col0(cell_controller_36_p6), .col1(cell_controller_36_p9), .col2(cell_controller_36_p12),
    .col3(cell_controller_36_p15), .col4(cell_controller_36_p18), .col5(cell_controller_36_p21),
    .col6(cell_controller_36_p24), .col7(cell_controller_36_p27), .col8(cell_controller_36_p30),
    .col9(cell_controller_36_p33), .col10(cell_controller_36_p36));
  DotMatrix #(.matrixcols(11), .matrixrows(8)) dotmatrix_117 (
    .col0(cell_controller_36_p7), .col1(cell_controller_36_p10), .col2(cell_controller_36_p13),
    .col3(cell_controller_36_p16), .col4(cell_controller_36_p19), .col5(cell_controller_36_p22),
    .col6(cell_controller_36_p25), .col7(cell_controller_36_p28), .col8(cell_controller_36_p31),
    .col9(cell_controller_36_p34), .col10(cell_controller_36_p37));
  // Cell_controller cell_controller_37: pin names not known; wires that end beside it: Columns[4], Rows[4], MOSI, MISO, cell_controller_37_p5, cell_controller_37_p6, cell_controller_37_p7, cell_controller_37_p8, cell_controller_37_p9, cell_controller_37_p10, cell_controller_37_p11, cell_controller_37_p12, cell_controller_37_p13, cell_controller_37_p14, cell_controller_37_p15, cell_controller_37_p16, cell_controller_37_p17, cell_controller_37_p18, cell_controller_37_p19, cell_controller_37_p20, cell_controller_37_p21, cell_controller_37_p22, cell_controller_37_p23, cell_controller_37_p24, cell_controller_37_p25, cell_controller_37_p26, cell_controller_37_p27, cell_controller_37_p28, cell_controller_37_p29, cell_controller_37_p30, cell_controller_37_p31, cell_controller_37_p32, cell_controller_37_p33, cell_controller_37_p34, cell_controller_37_p35, cell_controller_37_p36, cell_controller_37_p37
  DotMatrix #(.matrixcols(11), .matrixrows(5)) dotmatrix_118 (
    .col0(cell_controller_37_p5), .col1(cell_controller_37_p8), .col2(cell_controller_37_p11),
    .col3(cell_controller_37_p14), .col4(cell_controller_37_p17), .col5(cell_controller_37_p20),
    .col6(cell_controller_37_p23), .col7(cell_controller_37_p26), .col8(cell_controller_37_p29),
    .col9(cell_controller_37_p32), .col10(cell_controller_37_p35));
  DotMatrix #(.matrixcols(11), .matrixrows(8)) dotmatrix_119 (
    .col0(cell_controller_37_p6), .col1(cell_controller_37_p9), .col2(cell_controller_37_p12),
    .col3(cell_controller_37_p15), .col4(cell_controller_37_p18), .col5(cell_controller_37_p21),
    .col6(cell_controller_37_p24), .col7(cell_controller_37_p27), .col8(cell_controller_37_p30),
    .col9(cell_controller_37_p33), .col10(cell_controller_37_p36));
  DotMatrix #(.matrixcols(11), .matrixrows(8)) dotmatrix_120 (
    .col0(cell_controller_37_p7), .col1(cell_controller_37_p10), .col2(cell_controller_37_p13),
    .col3(cell_controller_37_p16), .col4(cell_controller_37_p19), .col5(cell_controller_37_p22),
    .col6(cell_controller_37_p25), .col7(cell_controller_37_p28), .col8(cell_controller_37_p31),
    .col9(cell_controller_37_p34), .col10(cell_controller_37_p37));
  // Cell_controller cell_controller_38: pin names not known; wires that end beside it: Columns[4], Rows[5], MOSI, MISO, cell_controller_38_p5, cell_controller_38_p6, cell_controller_38_p7, cell_controller_38_p8, cell_controller_38_p9, cell_controller_38_p10, cell_controller_38_p11, cell_controller_38_p12, cell_controller_38_p13, cell_controller_38_p14, cell_controller_38_p15, cell_controller_38_p16, cell_controller_38_p17, cell_controller_38_p18, cell_controller_38_p19, cell_controller_38_p20, cell_controller_38_p21, cell_controller_38_p22, cell_controller_38_p23, cell_controller_38_p24, cell_controller_38_p25, cell_controller_38_p26, cell_controller_38_p27, cell_controller_38_p28, cell_controller_38_p29, cell_controller_38_p30, cell_controller_38_p31, cell_controller_38_p32, cell_controller_38_p33, cell_controller_38_p34, cell_controller_38_p35, cell_controller_38_p36, cell_controller_38_p37
  DotMatrix #(.matrixcols(11), .matrixrows(5)) dotmatrix_121 (
    .col0(cell_controller_38_p5), .col1(cell_controller_38_p8), .col2(cell_controller_38_p11),
    .col3(cell_controller_38_p14), .col4(cell_controller_38_p17), .col5(cell_controller_38_p20),
    .col6(cell_controller_38_p23), .col7(cell_controller_38_p26), .col8(cell_controller_38_p29),
    .col9(cell_controller_38_p32), .col10(cell_controller_38_p35));
  DotMatrix #(.matrixcols(11), .matrixrows(8)) dotmatrix_122 (
    .col0(cell_controller_38_p6), .col1(cell_controller_38_p9), .col2(cell_controller_38_p12),
    .col3(cell_controller_38_p15), .col4(cell_controller_38_p18), .col5(cell_controller_38_p21),
    .col6(cell_controller_38_p24), .col7(cell_controller_38_p27), .col8(cell_controller_38_p30),
    .col9(cell_controller_38_p33), .col10(cell_controller_38_p36));
  DotMatrix #(.matrixcols(11), .matrixrows(8)) dotmatrix_123 (
    .col0(cell_controller_38_p7), .col1(cell_controller_38_p10), .col2(cell_controller_38_p13),
    .col3(cell_controller_38_p16), .col4(cell_controller_38_p19), .col5(cell_controller_38_p22),
    .col6(cell_controller_38_p25), .col7(cell_controller_38_p28), .col8(cell_controller_38_p31),
    .col9(cell_controller_38_p34), .col10(cell_controller_38_p37));
  // Cell_controller cell_controller_39: pin names not known; wires that end beside it: Columns[4], Rows[6], MOSI, MISO, cell_controller_39_p5, cell_controller_39_p6, cell_controller_39_p7, cell_controller_39_p8, cell_controller_39_p9, cell_controller_39_p10, cell_controller_39_p11, cell_controller_39_p12, cell_controller_39_p13, cell_controller_39_p14, cell_controller_39_p15, cell_controller_39_p16, cell_controller_39_p17, cell_controller_39_p18, cell_controller_39_p19, cell_controller_39_p20, cell_controller_39_p21, cell_controller_39_p22, cell_controller_39_p23, cell_controller_39_p24, cell_controller_39_p25, cell_controller_39_p26, cell_controller_39_p27, cell_controller_39_p28, cell_controller_39_p29, cell_controller_39_p30, cell_controller_39_p31, cell_controller_39_p32, cell_controller_39_p33, cell_controller_39_p34, cell_controller_39_p35, cell_controller_39_p36, cell_controller_39_p37
  DotMatrix #(.matrixcols(11), .matrixrows(5)) dotmatrix_124 (
    .col0(cell_controller_39_p5), .col1(cell_controller_39_p8), .col2(cell_controller_39_p11),
    .col3(cell_controller_39_p14), .col4(cell_controller_39_p17), .col5(cell_controller_39_p20),
    .col6(cell_controller_39_p23), .col7(cell_controller_39_p26), .col8(cell_controller_39_p29),
    .col9(cell_controller_39_p32), .col10(cell_controller_39_p35));
  DotMatrix #(.matrixcols(11), .matrixrows(8)) dotmatrix_125 (
    .col0(cell_controller_39_p6), .col1(cell_controller_39_p9), .col2(cell_controller_39_p12),
    .col3(cell_controller_39_p15), .col4(cell_controller_39_p18), .col5(cell_controller_39_p21),
    .col6(cell_controller_39_p24), .col7(cell_controller_39_p27), .col8(cell_controller_39_p30),
    .col9(cell_controller_39_p33), .col10(cell_controller_39_p36));
  DotMatrix #(.matrixcols(11), .matrixrows(8)) dotmatrix_126 (
    .col0(cell_controller_39_p7), .col1(cell_controller_39_p10), .col2(cell_controller_39_p13),
    .col3(cell_controller_39_p16), .col4(cell_controller_39_p19), .col5(cell_controller_39_p22),
    .col6(cell_controller_39_p25), .col7(cell_controller_39_p28), .col8(cell_controller_39_p31),
    .col9(cell_controller_39_p34), .col10(cell_controller_39_p37));
  // Cell_controller cell_controller_40: pin names not known; wires that end beside it: Columns[4], Rows[7], MOSI, MISO, cell_controller_40_p5, cell_controller_40_p6, cell_controller_40_p7, cell_controller_40_p8, cell_controller_40_p9, cell_controller_40_p10, cell_controller_40_p11, cell_controller_40_p12, cell_controller_40_p13, cell_controller_40_p14, cell_controller_40_p15, cell_controller_40_p16, cell_controller_40_p17, cell_controller_40_p18, cell_controller_40_p19, cell_controller_40_p20, cell_controller_40_p21, cell_controller_40_p22, cell_controller_40_p23, cell_controller_40_p24, cell_controller_40_p25, cell_controller_40_p26, cell_controller_40_p27, cell_controller_40_p28, cell_controller_40_p29, cell_controller_40_p30, cell_controller_40_p31, cell_controller_40_p32, cell_controller_40_p33, cell_controller_40_p34, cell_controller_40_p35, cell_controller_40_p36, cell_controller_40_p37
  DotMatrix #(.matrixcols(11), .matrixrows(5)) dotmatrix_127 (
    .col0(cell_controller_40_p5), .col1(cell_controller_40_p8), .col2(cell_controller_40_p11),
    .col3(cell_controller_40_p14), .col4(cell_controller_40_p17), .col5(cell_controller_40_p20),
    .col6(cell_controller_40_p23), .col7(cell_controller_40_p26), .col8(cell_controller_40_p29),
    .col9(cell_controller_40_p32), .col10(cell_controller_40_p35));
  DotMatrix #(.matrixcols(11), .matrixrows(8)) dotmatrix_128 (
    .col0(cell_controller_40_p6), .col1(cell_controller_40_p9), .col2(cell_controller_40_p12),
    .col3(cell_controller_40_p15), .col4(cell_controller_40_p18), .col5(cell_controller_40_p21),
    .col6(cell_controller_40_p24), .col7(cell_controller_40_p27), .col8(cell_controller_40_p30),
    .col9(cell_controller_40_p33), .col10(cell_controller_40_p36));
  DotMatrix #(.matrixcols(11), .matrixrows(8)) dotmatrix_129 (
    .col0(cell_controller_40_p7), .col1(cell_controller_40_p10), .col2(cell_controller_40_p13),
    .col3(cell_controller_40_p16), .col4(cell_controller_40_p19), .col5(cell_controller_40_p22),
    .col6(cell_controller_40_p25), .col7(cell_controller_40_p28), .col8(cell_controller_40_p31),
    .col9(cell_controller_40_p34), .col10(cell_controller_40_p37));
  DotMatrix #(.matrixcols(9), .matrixrows(15)) dotmatrix_130 (
    .col0(output_big_numder_4_out_3), .col1(output_big_numder_4_out_4), .col2(output_big_numder_4_out_5),
    .col3(output_big_numder_4_out_6), .col4(output_big_numder_4_out_7), .col5(output_big_numder_4_out_8),
    .col6(output_big_numder_4_out_9), .col7(output_big_numder_4_out_10), .col8(output_big_numder_4_out_11));
  Output_big_numder output_big_numder_4 (
    .out_3(output_big_numder_4_out_3), .out_4(output_big_numder_4_out_4), .out_5(output_big_numder_4_out_5),
    .out_6(output_big_numder_4_out_6), .out_7(output_big_numder_4_out_7), .out_8(output_big_numder_4_out_8),
    .out_9(output_big_numder_4_out_9), .out_10(output_big_numder_4_out_10),
    .out_11(output_big_numder_4_out_11), .in_1(input_controller_1_input_buffer_3), .INV(demultiplexer_1_out3));
  // Cell_controller cell_controller_41: pin names not known; wires that end beside it: Columns[5], Rows[0], MOSI, MISO, cell_controller_41_p5, cell_controller_41_p6, cell_controller_41_p7, cell_controller_41_p8, cell_controller_41_p9, cell_controller_41_p10, cell_controller_41_p11, cell_controller_41_p12, cell_controller_41_p13, cell_controller_41_p14, cell_controller_41_p15, cell_controller_41_p16, cell_controller_41_p17, cell_controller_41_p18, cell_controller_41_p19, cell_controller_41_p20, cell_controller_41_p21, cell_controller_41_p22, cell_controller_41_p23, cell_controller_41_p24, cell_controller_41_p25, cell_controller_41_p26, cell_controller_41_p27, cell_controller_41_p28, cell_controller_41_p29, cell_controller_41_p30, cell_controller_41_p31, cell_controller_41_p32, cell_controller_41_p33, cell_controller_41_p34, cell_controller_41_p35, cell_controller_41_p36, cell_controller_41_p37
  DotMatrix #(.matrixcols(11), .matrixrows(5)) dotmatrix_131 (
    .col0(cell_controller_41_p5), .col1(cell_controller_41_p8), .col2(cell_controller_41_p11),
    .col3(cell_controller_41_p14), .col4(cell_controller_41_p17), .col5(cell_controller_41_p20),
    .col6(cell_controller_41_p23), .col7(cell_controller_41_p26), .col8(cell_controller_41_p29),
    .col9(cell_controller_41_p32), .col10(cell_controller_41_p35));
  DotMatrix #(.matrixcols(11), .matrixrows(8)) dotmatrix_132 (
    .col0(cell_controller_41_p6), .col1(cell_controller_41_p9), .col2(cell_controller_41_p12),
    .col3(cell_controller_41_p15), .col4(cell_controller_41_p18), .col5(cell_controller_41_p21),
    .col6(cell_controller_41_p24), .col7(cell_controller_41_p27), .col8(cell_controller_41_p30),
    .col9(cell_controller_41_p33), .col10(cell_controller_41_p36));
  DotMatrix #(.matrixcols(11), .matrixrows(8)) dotmatrix_133 (
    .col0(cell_controller_41_p7), .col1(cell_controller_41_p10), .col2(cell_controller_41_p13),
    .col3(cell_controller_41_p16), .col4(cell_controller_41_p19), .col5(cell_controller_41_p22),
    .col6(cell_controller_41_p25), .col7(cell_controller_41_p28), .col8(cell_controller_41_p31),
    .col9(cell_controller_41_p34), .col10(cell_controller_41_p37));
  DotMatrix #(.matrixcols(11), .matrixrows(5)) dotmatrix_134 (
    .col0(cell_controller_42_p5), .col1(cell_controller_42_p8), .col2(cell_controller_42_p11),
    .col3(cell_controller_42_p14), .col4(cell_controller_42_p17), .col5(cell_controller_42_p20),
    .col6(cell_controller_42_p23), .col7(cell_controller_42_p26), .col8(cell_controller_42_p29),
    .col9(cell_controller_42_p32), .col10(cell_controller_42_p35));
  // Cell_controller cell_controller_42: pin names not known; wires that end beside it: Columns[5], Rows[1], MOSI, MISO, cell_controller_42_p5, cell_controller_42_p6, cell_controller_42_p7, cell_controller_42_p8, cell_controller_42_p9, cell_controller_42_p10, cell_controller_42_p11, cell_controller_42_p12, cell_controller_42_p13, cell_controller_42_p14, cell_controller_42_p15, cell_controller_42_p16, cell_controller_42_p17, cell_controller_42_p18, cell_controller_42_p19, cell_controller_42_p20, cell_controller_42_p21, cell_controller_42_p22, cell_controller_42_p23, cell_controller_42_p24, cell_controller_42_p25, cell_controller_42_p26, cell_controller_42_p27, cell_controller_42_p28, cell_controller_42_p29, cell_controller_42_p30, cell_controller_42_p31, cell_controller_42_p32, cell_controller_42_p33, cell_controller_42_p34, cell_controller_42_p35, cell_controller_42_p36, cell_controller_42_p37
  DotMatrix #(.matrixcols(11), .matrixrows(8)) dotmatrix_135 (
    .col0(cell_controller_42_p6), .col1(cell_controller_42_p9), .col2(cell_controller_42_p12),
    .col3(cell_controller_42_p15), .col4(cell_controller_42_p18), .col5(cell_controller_42_p21),
    .col6(cell_controller_42_p24), .col7(cell_controller_42_p27), .col8(cell_controller_42_p30),
    .col9(cell_controller_42_p33), .col10(cell_controller_42_p36));
  DotMatrix #(.matrixcols(11), .matrixrows(8)) dotmatrix_136 (
    .col0(cell_controller_42_p7), .col1(cell_controller_42_p10), .col2(cell_controller_42_p13),
    .col3(cell_controller_42_p16), .col4(cell_controller_42_p19), .col5(cell_controller_42_p22),
    .col6(cell_controller_42_p25), .col7(cell_controller_42_p28), .col8(cell_controller_42_p31),
    .col9(cell_controller_42_p34), .col10(cell_controller_42_p37));
  DotMatrix #(.matrixcols(11), .matrixrows(5)) dotmatrix_137 (
    .col0(cell_controller_43_p5), .col1(cell_controller_43_p8), .col2(cell_controller_43_p11),
    .col3(cell_controller_43_p14), .col4(cell_controller_43_p17), .col5(cell_controller_43_p20),
    .col6(cell_controller_43_p23), .col7(cell_controller_43_p26), .col8(cell_controller_43_p29),
    .col9(cell_controller_43_p32), .col10(cell_controller_43_p35));
  // Cell_controller cell_controller_43: pin names not known; wires that end beside it: Columns[5], Rows[2], MOSI, MISO, cell_controller_43_p5, cell_controller_43_p6, cell_controller_43_p7, cell_controller_43_p8, cell_controller_43_p9, cell_controller_43_p10, cell_controller_43_p11, cell_controller_43_p12, cell_controller_43_p13, cell_controller_43_p14, cell_controller_43_p15, cell_controller_43_p16, cell_controller_43_p17, cell_controller_43_p18, cell_controller_43_p19, cell_controller_43_p20, cell_controller_43_p21, cell_controller_43_p22, cell_controller_43_p23, cell_controller_43_p24, cell_controller_43_p25, cell_controller_43_p26, cell_controller_43_p27, cell_controller_43_p28, cell_controller_43_p29, cell_controller_43_p30, cell_controller_43_p31, cell_controller_43_p32, cell_controller_43_p33, cell_controller_43_p34, cell_controller_43_p35, cell_controller_43_p36, cell_controller_43_p37
  DotMatrix #(.matrixcols(11), .matrixrows(8)) dotmatrix_138 (
    .col0(cell_controller_43_p6), .col1(cell_controller_43_p9), .col2(cell_controller_43_p12),
    .col3(cell_controller_43_p15), .col4(cell_controller_43_p18), .col5(cell_controller_43_p21),
    .col6(cell_controller_43_p24), .col7(cell_controller_43_p27), .col8(cell_controller_43_p30),
    .col9(cell_controller_43_p33), .col10(cell_controller_43_p36));
  DotMatrix #(.matrixcols(11), .matrixrows(8)) dotmatrix_139 (
    .col0(cell_controller_43_p7), .col1(cell_controller_43_p10), .col2(cell_controller_43_p13),
    .col3(cell_controller_43_p16), .col4(cell_controller_43_p19), .col5(cell_controller_43_p22),
    .col6(cell_controller_43_p25), .col7(cell_controller_43_p28), .col8(cell_controller_43_p31),
    .col9(cell_controller_43_p34), .col10(cell_controller_43_p37));
  DotMatrix #(.matrixcols(11), .matrixrows(5)) dotmatrix_140 (
    .col0(cell_controller_44_p5), .col1(cell_controller_44_p8), .col2(cell_controller_44_p11),
    .col3(cell_controller_44_p14), .col4(cell_controller_44_p17), .col5(cell_controller_44_p20),
    .col6(cell_controller_44_p23), .col7(cell_controller_44_p26), .col8(cell_controller_44_p29),
    .col9(cell_controller_44_p32), .col10(cell_controller_44_p35));
  // Cell_controller cell_controller_44: pin names not known; wires that end beside it: Columns[5], Rows[3], MOSI, MISO, cell_controller_44_p5, cell_controller_44_p6, cell_controller_44_p7, cell_controller_44_p8, cell_controller_44_p9, cell_controller_44_p10, cell_controller_44_p11, cell_controller_44_p12, cell_controller_44_p13, cell_controller_44_p14, cell_controller_44_p15, cell_controller_44_p16, cell_controller_44_p17, cell_controller_44_p18, cell_controller_44_p19, cell_controller_44_p20, cell_controller_44_p21, cell_controller_44_p22, cell_controller_44_p23, cell_controller_44_p24, cell_controller_44_p25, cell_controller_44_p26, cell_controller_44_p27, cell_controller_44_p28, cell_controller_44_p29, cell_controller_44_p30, cell_controller_44_p31, cell_controller_44_p32, cell_controller_44_p33, cell_controller_44_p34, cell_controller_44_p35, cell_controller_44_p36, cell_controller_44_p37
  DotMatrix #(.matrixcols(11), .matrixrows(8)) dotmatrix_141 (
    .col0(cell_controller_44_p6), .col1(cell_controller_44_p9), .col2(cell_controller_44_p12),
    .col3(cell_controller_44_p15), .col4(cell_controller_44_p18), .col5(cell_controller_44_p21),
    .col6(cell_controller_44_p24), .col7(cell_controller_44_p27), .col8(cell_controller_44_p30),
    .col9(cell_controller_44_p33), .col10(cell_controller_44_p36));
  DotMatrix #(.matrixcols(11), .matrixrows(8)) dotmatrix_142 (
    .col0(cell_controller_44_p7), .col1(cell_controller_44_p10), .col2(cell_controller_44_p13),
    .col3(cell_controller_44_p16), .col4(cell_controller_44_p19), .col5(cell_controller_44_p22),
    .col6(cell_controller_44_p25), .col7(cell_controller_44_p28), .col8(cell_controller_44_p31),
    .col9(cell_controller_44_p34), .col10(cell_controller_44_p37));
  DotMatrix #(.matrixcols(11), .matrixrows(5)) dotmatrix_143 (
    .col0(cell_controller_45_p5), .col1(cell_controller_45_p8), .col2(cell_controller_45_p11),
    .col3(cell_controller_45_p14), .col4(cell_controller_45_p17), .col5(cell_controller_45_p20),
    .col6(cell_controller_45_p23), .col7(cell_controller_45_p26), .col8(cell_controller_45_p29),
    .col9(cell_controller_45_p32), .col10(cell_controller_45_p35));
  // Cell_controller cell_controller_45: pin names not known; wires that end beside it: Columns[5], Rows[4], MOSI, MISO, cell_controller_45_p5, cell_controller_45_p6, cell_controller_45_p7, cell_controller_45_p8, cell_controller_45_p9, cell_controller_45_p10, cell_controller_45_p11, cell_controller_45_p12, cell_controller_45_p13, cell_controller_45_p14, cell_controller_45_p15, cell_controller_45_p16, cell_controller_45_p17, cell_controller_45_p18, cell_controller_45_p19, cell_controller_45_p20, cell_controller_45_p21, cell_controller_45_p22, cell_controller_45_p23, cell_controller_45_p24, cell_controller_45_p25, cell_controller_45_p26, cell_controller_45_p27, cell_controller_45_p28, cell_controller_45_p29, cell_controller_45_p30, cell_controller_45_p31, cell_controller_45_p32, cell_controller_45_p33, cell_controller_45_p34, cell_controller_45_p35, cell_controller_45_p36, cell_controller_45_p37
  DotMatrix #(.matrixcols(11), .matrixrows(8)) dotmatrix_144 (
    .col0(cell_controller_45_p6), .col1(cell_controller_45_p9), .col2(cell_controller_45_p12),
    .col3(cell_controller_45_p15), .col4(cell_controller_45_p18), .col5(cell_controller_45_p21),
    .col6(cell_controller_45_p24), .col7(cell_controller_45_p27), .col8(cell_controller_45_p30),
    .col9(cell_controller_45_p33), .col10(cell_controller_45_p36));
  DotMatrix #(.matrixcols(11), .matrixrows(8)) dotmatrix_145 (
    .col0(cell_controller_45_p7), .col1(cell_controller_45_p10), .col2(cell_controller_45_p13),
    .col3(cell_controller_45_p16), .col4(cell_controller_45_p19), .col5(cell_controller_45_p22),
    .col6(cell_controller_45_p25), .col7(cell_controller_45_p28), .col8(cell_controller_45_p31),
    .col9(cell_controller_45_p34), .col10(cell_controller_45_p37));
  // Cell_controller cell_controller_46: pin names not known; wires that end beside it: Columns[5], Rows[5], MOSI, MISO, cell_controller_46_p5, cell_controller_46_p6, cell_controller_46_p7, cell_controller_46_p8, cell_controller_46_p9, cell_controller_46_p10, cell_controller_46_p11, cell_controller_46_p12, cell_controller_46_p13, cell_controller_46_p14, cell_controller_46_p15, cell_controller_46_p16, cell_controller_46_p17, cell_controller_46_p18, cell_controller_46_p19, cell_controller_46_p20, cell_controller_46_p21, cell_controller_46_p22, cell_controller_46_p23, cell_controller_46_p24, cell_controller_46_p25, cell_controller_46_p26, cell_controller_46_p27, cell_controller_46_p28, cell_controller_46_p29, cell_controller_46_p30, cell_controller_46_p31, cell_controller_46_p32, cell_controller_46_p33, cell_controller_46_p34, cell_controller_46_p35, cell_controller_46_p36, cell_controller_46_p37
  DotMatrix #(.matrixcols(11), .matrixrows(5)) dotmatrix_146 (
    .col0(cell_controller_46_p5), .col1(cell_controller_46_p8), .col2(cell_controller_46_p11),
    .col3(cell_controller_46_p14), .col4(cell_controller_46_p17), .col5(cell_controller_46_p20),
    .col6(cell_controller_46_p23), .col7(cell_controller_46_p26), .col8(cell_controller_46_p29),
    .col9(cell_controller_46_p32), .col10(cell_controller_46_p35));
  DotMatrix #(.matrixcols(11), .matrixrows(8)) dotmatrix_147 (
    .col0(cell_controller_46_p6), .col1(cell_controller_46_p9), .col2(cell_controller_46_p12),
    .col3(cell_controller_46_p15), .col4(cell_controller_46_p18), .col5(cell_controller_46_p21),
    .col6(cell_controller_46_p24), .col7(cell_controller_46_p27), .col8(cell_controller_46_p30),
    .col9(cell_controller_46_p33), .col10(cell_controller_46_p36));
  DotMatrix #(.matrixcols(11), .matrixrows(8)) dotmatrix_148 (
    .col0(cell_controller_46_p7), .col1(cell_controller_46_p10), .col2(cell_controller_46_p13),
    .col3(cell_controller_46_p16), .col4(cell_controller_46_p19), .col5(cell_controller_46_p22),
    .col6(cell_controller_46_p25), .col7(cell_controller_46_p28), .col8(cell_controller_46_p31),
    .col9(cell_controller_46_p34), .col10(cell_controller_46_p37));
  // Cell_controller cell_controller_47: pin names not known; wires that end beside it: Columns[5], Rows[6], MOSI, MISO, cell_controller_47_p5, cell_controller_47_p6, cell_controller_47_p7, cell_controller_47_p8, cell_controller_47_p9, cell_controller_47_p10, cell_controller_47_p11, cell_controller_47_p12, cell_controller_47_p13, cell_controller_47_p14, cell_controller_47_p15, cell_controller_47_p16, cell_controller_47_p17, cell_controller_47_p18, cell_controller_47_p19, cell_controller_47_p20, cell_controller_47_p21, cell_controller_47_p22, cell_controller_47_p23, cell_controller_47_p24, cell_controller_47_p25, cell_controller_47_p26, cell_controller_47_p27, cell_controller_47_p28, cell_controller_47_p29, cell_controller_47_p30, cell_controller_47_p31, cell_controller_47_p32, cell_controller_47_p33, cell_controller_47_p34, cell_controller_47_p35, cell_controller_47_p36, cell_controller_47_p37
  DotMatrix #(.matrixcols(11), .matrixrows(5)) dotmatrix_149 (
    .col0(cell_controller_47_p5), .col1(cell_controller_47_p8), .col2(cell_controller_47_p11),
    .col3(cell_controller_47_p14), .col4(cell_controller_47_p17), .col5(cell_controller_47_p20),
    .col6(cell_controller_47_p23), .col7(cell_controller_47_p26), .col8(cell_controller_47_p29),
    .col9(cell_controller_47_p32), .col10(cell_controller_47_p35));
  DotMatrix #(.matrixcols(11), .matrixrows(8)) dotmatrix_150 (
    .col0(cell_controller_47_p6), .col1(cell_controller_47_p9), .col2(cell_controller_47_p12),
    .col3(cell_controller_47_p15), .col4(cell_controller_47_p18), .col5(cell_controller_47_p21),
    .col6(cell_controller_47_p24), .col7(cell_controller_47_p27), .col8(cell_controller_47_p30),
    .col9(cell_controller_47_p33), .col10(cell_controller_47_p36));
  DotMatrix #(.matrixcols(11), .matrixrows(8)) dotmatrix_151 (
    .col0(cell_controller_47_p7), .col1(cell_controller_47_p10), .col2(cell_controller_47_p13),
    .col3(cell_controller_47_p16), .col4(cell_controller_47_p19), .col5(cell_controller_47_p22),
    .col6(cell_controller_47_p25), .col7(cell_controller_47_p28), .col8(cell_controller_47_p31),
    .col9(cell_controller_47_p34), .col10(cell_controller_47_p37));
  // Cell_controller cell_controller_48: pin names not known; wires that end beside it: Columns[5], Rows[7], MOSI, MISO, cell_controller_48_p5, cell_controller_48_p6, cell_controller_48_p7, cell_controller_48_p8, cell_controller_48_p9, cell_controller_48_p10, cell_controller_48_p11, cell_controller_48_p12, cell_controller_48_p13, cell_controller_48_p14, cell_controller_48_p15, cell_controller_48_p16, cell_controller_48_p17, cell_controller_48_p18, cell_controller_48_p19, cell_controller_48_p20, cell_controller_48_p21, cell_controller_48_p22, cell_controller_48_p23, cell_controller_48_p24, cell_controller_48_p25, cell_controller_48_p26, cell_controller_48_p27, cell_controller_48_p28, cell_controller_48_p29, cell_controller_48_p30, cell_controller_48_p31, cell_controller_48_p32, cell_controller_48_p33, cell_controller_48_p34, cell_controller_48_p35, cell_controller_48_p36, cell_controller_48_p37
  DotMatrix #(.matrixcols(11), .matrixrows(5)) dotmatrix_152 (
    .col0(cell_controller_48_p5), .col1(cell_controller_48_p8), .col2(cell_controller_48_p11),
    .col3(cell_controller_48_p14), .col4(cell_controller_48_p17), .col5(cell_controller_48_p20),
    .col6(cell_controller_48_p23), .col7(cell_controller_48_p26), .col8(cell_controller_48_p29),
    .col9(cell_controller_48_p32), .col10(cell_controller_48_p35));
  DotMatrix #(.matrixcols(11), .matrixrows(8)) dotmatrix_153 (
    .col0(cell_controller_48_p6), .col1(cell_controller_48_p9), .col2(cell_controller_48_p12),
    .col3(cell_controller_48_p15), .col4(cell_controller_48_p18), .col5(cell_controller_48_p21),
    .col6(cell_controller_48_p24), .col7(cell_controller_48_p27), .col8(cell_controller_48_p30),
    .col9(cell_controller_48_p33), .col10(cell_controller_48_p36));
  DotMatrix #(.matrixcols(11), .matrixrows(8)) dotmatrix_154 (
    .col0(cell_controller_48_p7), .col1(cell_controller_48_p10), .col2(cell_controller_48_p13),
    .col3(cell_controller_48_p16), .col4(cell_controller_48_p19), .col5(cell_controller_48_p22),
    .col6(cell_controller_48_p25), .col7(cell_controller_48_p28), .col8(cell_controller_48_p31),
    .col9(cell_controller_48_p34), .col10(cell_controller_48_p37));
  // Cell_controller cell_controller_49: pin names not known; wires that end beside it: Columns[6], Rows[0], MOSI, MISO, cell_controller_49_p5, cell_controller_49_p6, cell_controller_49_p7, cell_controller_49_p8, cell_controller_49_p9, cell_controller_49_p10, cell_controller_49_p11, cell_controller_49_p12, cell_controller_49_p13, cell_controller_49_p14, cell_controller_49_p15, cell_controller_49_p16, cell_controller_49_p17, cell_controller_49_p18, cell_controller_49_p19, cell_controller_49_p20, cell_controller_49_p21, cell_controller_49_p22, cell_controller_49_p23, cell_controller_49_p24, cell_controller_49_p25, cell_controller_49_p26, cell_controller_49_p27, cell_controller_49_p28, cell_controller_49_p29, cell_controller_49_p30, cell_controller_49_p31, cell_controller_49_p32, cell_controller_49_p33, cell_controller_49_p34, cell_controller_49_p35, cell_controller_49_p36, cell_controller_49_p37
  DotMatrix #(.matrixcols(11), .matrixrows(5)) dotmatrix_155 (
    .col0(cell_controller_49_p5), .col1(cell_controller_49_p8), .col2(cell_controller_49_p11),
    .col3(cell_controller_49_p14), .col4(cell_controller_49_p17), .col5(cell_controller_49_p20),
    .col6(cell_controller_49_p23), .col7(cell_controller_49_p26), .col8(cell_controller_49_p29),
    .col9(cell_controller_49_p32), .col10(cell_controller_49_p35));
  DotMatrix #(.matrixcols(11), .matrixrows(8)) dotmatrix_156 (
    .col0(cell_controller_49_p6), .col1(cell_controller_49_p9), .col2(cell_controller_49_p12),
    .col3(cell_controller_49_p15), .col4(cell_controller_49_p18), .col5(cell_controller_49_p21),
    .col6(cell_controller_49_p24), .col7(cell_controller_49_p27), .col8(cell_controller_49_p30),
    .col9(cell_controller_49_p33), .col10(cell_controller_49_p36));
  DotMatrix #(.matrixcols(11), .matrixrows(8)) dotmatrix_157 (
    .col0(cell_controller_49_p7), .col1(cell_controller_49_p10), .col2(cell_controller_49_p13),
    .col3(cell_controller_49_p16), .col4(cell_controller_49_p19), .col5(cell_controller_49_p22),
    .col6(cell_controller_49_p25), .col7(cell_controller_49_p28), .col8(cell_controller_49_p31),
    .col9(cell_controller_49_p34), .col10(cell_controller_49_p37));
  DotMatrix #(.matrixcols(11), .matrixrows(5)) dotmatrix_158 (
    .col0(cell_controller_50_p5), .col1(cell_controller_50_p8), .col2(cell_controller_50_p11),
    .col3(cell_controller_50_p14), .col4(cell_controller_50_p17), .col5(cell_controller_50_p20),
    .col6(cell_controller_50_p23), .col7(cell_controller_50_p26), .col8(cell_controller_50_p29),
    .col9(cell_controller_50_p32), .col10(cell_controller_50_p35));
  // Cell_controller cell_controller_50: pin names not known; wires that end beside it: Columns[6], Rows[1], MOSI, MISO, cell_controller_50_p5, cell_controller_50_p6, cell_controller_50_p7, cell_controller_50_p8, cell_controller_50_p9, cell_controller_50_p10, cell_controller_50_p11, cell_controller_50_p12, cell_controller_50_p13, cell_controller_50_p14, cell_controller_50_p15, cell_controller_50_p16, cell_controller_50_p17, cell_controller_50_p18, cell_controller_50_p19, cell_controller_50_p20, cell_controller_50_p21, cell_controller_50_p22, cell_controller_50_p23, cell_controller_50_p24, cell_controller_50_p25, cell_controller_50_p26, cell_controller_50_p27, cell_controller_50_p28, cell_controller_50_p29, cell_controller_50_p30, cell_controller_50_p31, cell_controller_50_p32, cell_controller_50_p33, cell_controller_50_p34, cell_controller_50_p35, cell_controller_50_p36, cell_controller_50_p37
  DotMatrix #(.matrixcols(11), .matrixrows(8)) dotmatrix_159 (
    .col0(cell_controller_50_p6), .col1(cell_controller_50_p9), .col2(cell_controller_50_p12),
    .col3(cell_controller_50_p15), .col4(cell_controller_50_p18), .col5(cell_controller_50_p21),
    .col6(cell_controller_50_p24), .col7(cell_controller_50_p27), .col8(cell_controller_50_p30),
    .col9(cell_controller_50_p33), .col10(cell_controller_50_p36));
  DotMatrix #(.matrixcols(11), .matrixrows(8)) dotmatrix_160 (
    .col0(cell_controller_50_p7), .col1(cell_controller_50_p10), .col2(cell_controller_50_p13),
    .col3(cell_controller_50_p16), .col4(cell_controller_50_p19), .col5(cell_controller_50_p22),
    .col6(cell_controller_50_p25), .col7(cell_controller_50_p28), .col8(cell_controller_50_p31),
    .col9(cell_controller_50_p34), .col10(cell_controller_50_p37));
  // Cell_controller cell_controller_51: pin names not known; wires that end beside it: Columns[6], Rows[2], MOSI, MISO, cell_controller_51_p5, cell_controller_51_p6, cell_controller_51_p7, cell_controller_51_p8, cell_controller_51_p9, cell_controller_51_p10, cell_controller_51_p11, cell_controller_51_p12, cell_controller_51_p13, cell_controller_51_p14, cell_controller_51_p15, cell_controller_51_p16, cell_controller_51_p17, cell_controller_51_p18, cell_controller_51_p19, cell_controller_51_p20, cell_controller_51_p21, cell_controller_51_p22, cell_controller_51_p23, cell_controller_51_p24, cell_controller_51_p25, cell_controller_51_p26, cell_controller_51_p27, cell_controller_51_p28, cell_controller_51_p29, cell_controller_51_p30, cell_controller_51_p31, cell_controller_51_p32, cell_controller_51_p33, cell_controller_51_p34, cell_controller_51_p35, cell_controller_51_p36, cell_controller_51_p37
  DotMatrix #(.matrixcols(11), .matrixrows(5)) dotmatrix_161 (
    .col0(cell_controller_51_p5), .col1(cell_controller_51_p8), .col2(cell_controller_51_p11),
    .col3(cell_controller_51_p14), .col4(cell_controller_51_p17), .col5(cell_controller_51_p20),
    .col6(cell_controller_51_p23), .col7(cell_controller_51_p26), .col8(cell_controller_51_p29),
    .col9(cell_controller_51_p32), .col10(cell_controller_51_p35));
  DotMatrix #(.matrixcols(11), .matrixrows(8)) dotmatrix_162 (
    .col0(cell_controller_51_p6), .col1(cell_controller_51_p9), .col2(cell_controller_51_p12),
    .col3(cell_controller_51_p15), .col4(cell_controller_51_p18), .col5(cell_controller_51_p21),
    .col6(cell_controller_51_p24), .col7(cell_controller_51_p27), .col8(cell_controller_51_p30),
    .col9(cell_controller_51_p33), .col10(cell_controller_51_p36));
  DotMatrix #(.matrixcols(11), .matrixrows(8)) dotmatrix_163 (
    .col0(cell_controller_51_p7), .col1(cell_controller_51_p10), .col2(cell_controller_51_p13),
    .col3(cell_controller_51_p16), .col4(cell_controller_51_p19), .col5(cell_controller_51_p22),
    .col6(cell_controller_51_p25), .col7(cell_controller_51_p28), .col8(cell_controller_51_p31),
    .col9(cell_controller_51_p34), .col10(cell_controller_51_p37));
  // Cell_controller cell_controller_52: pin names not known; wires that end beside it: Columns[6], Rows[3], MOSI, MISO, cell_controller_52_p5, cell_controller_52_p6, cell_controller_52_p7, cell_controller_52_p8, cell_controller_52_p9, cell_controller_52_p10, cell_controller_52_p11, cell_controller_52_p12, cell_controller_52_p13, cell_controller_52_p14, cell_controller_52_p15, cell_controller_52_p16, cell_controller_52_p17, cell_controller_52_p18, cell_controller_52_p19, cell_controller_52_p20, cell_controller_52_p21, cell_controller_52_p22, cell_controller_52_p23, cell_controller_52_p24, cell_controller_52_p25, cell_controller_52_p26, cell_controller_52_p27, cell_controller_52_p28, cell_controller_52_p29, cell_controller_52_p30, cell_controller_52_p31, cell_controller_52_p32, cell_controller_52_p33, cell_controller_52_p34, cell_controller_52_p31, cell_controller_52_p36, cell_controller_52_p37, cell_controller_52_p38, cell_controller_52_p39
  DotMatrix #(.matrixcols(11), .matrixrows(5)) dotmatrix_164 (
    .col0(cell_controller_52_p5), .col1(cell_controller_52_p8), .col2(cell_controller_52_p11),
    .col3(cell_controller_52_p14), .col4(cell_controller_52_p17), .col5(cell_controller_52_p20),
    .col6(cell_controller_52_p23), .col7(cell_controller_52_p26), .col8(cell_controller_52_p29),
    .col9(cell_controller_52_p33), .col10(cell_controller_52_p37));
  DotMatrix #(.matrixcols(11), .matrixrows(8)) dotmatrix_165 (
    .col0(cell_controller_52_p6), .col1(cell_controller_52_p9), .col2(cell_controller_52_p12),
    .col3(cell_controller_52_p15), .col4(cell_controller_52_p18), .col5(cell_controller_52_p21),
    .col6(cell_controller_52_p24), .col7(cell_controller_52_p27), .col8(cell_controller_52_p30),
    .col9(cell_controller_52_p34), .col10(cell_controller_52_p38));
  DotMatrix #(.matrixcols(11), .matrixrows(8)) dotmatrix_166 (
    .col0(cell_controller_52_p7), .col1(cell_controller_52_p10), .col2(cell_controller_52_p13),
    .col3(cell_controller_52_p16), .col4(cell_controller_52_p19), .col5(cell_controller_52_p22),
    .col6(cell_controller_52_p25), .col7(cell_controller_52_p28), .col8(cell_controller_52_p32),
    .col9(cell_controller_52_p36), .col10(cell_controller_52_p39));
  DotMatrix #(.matrixcols(11), .matrixrows(5)) dotmatrix_167 (
    .col0(cell_controller_53_p5), .col1(cell_controller_53_p8), .col2(cell_controller_53_p11),
    .col3(cell_controller_53_p14), .col4(cell_controller_53_p17), .col5(cell_controller_53_p20),
    .col6(cell_controller_53_p23), .col7(cell_controller_53_p26), .col8(cell_controller_53_p29),
    .col9(cell_controller_53_p33), .col10(cell_controller_53_p37));
  // Cell_controller cell_controller_53: pin names not known; wires that end beside it: Columns[6], Rows[4], MOSI, MISO, cell_controller_53_p5, cell_controller_53_p6, cell_controller_53_p7, cell_controller_53_p8, cell_controller_53_p9, cell_controller_53_p10, cell_controller_53_p11, cell_controller_53_p12, cell_controller_53_p13, cell_controller_53_p14, cell_controller_53_p15, cell_controller_53_p16, cell_controller_53_p17, cell_controller_53_p18, cell_controller_53_p19, cell_controller_53_p20, cell_controller_53_p21, cell_controller_53_p22, cell_controller_53_p23, cell_controller_53_p24, cell_controller_53_p25, cell_controller_53_p26, cell_controller_53_p27, cell_controller_53_p28, cell_controller_53_p29, cell_controller_53_p30, cell_controller_53_p31, cell_controller_53_p32, cell_controller_53_p33, cell_controller_53_p34, cell_controller_53_p31, cell_controller_53_p36, cell_controller_53_p37, cell_controller_53_p38, cell_controller_53_p39
  DotMatrix #(.matrixcols(11), .matrixrows(8)) dotmatrix_168 (
    .col0(cell_controller_53_p6), .col1(cell_controller_53_p9), .col2(cell_controller_53_p12),
    .col3(cell_controller_53_p15), .col4(cell_controller_53_p18), .col5(cell_controller_53_p21),
    .col6(cell_controller_53_p24), .col7(cell_controller_53_p27), .col8(cell_controller_53_p30),
    .col9(cell_controller_53_p34), .col10(cell_controller_53_p38));
  DotMatrix #(.matrixcols(11), .matrixrows(8)) dotmatrix_169 (
    .col0(cell_controller_53_p7), .col1(cell_controller_53_p10), .col2(cell_controller_53_p13),
    .col3(cell_controller_53_p16), .col4(cell_controller_53_p19), .col5(cell_controller_53_p22),
    .col6(cell_controller_53_p25), .col7(cell_controller_53_p28), .col8(cell_controller_53_p32),
    .col9(cell_controller_53_p36), .col10(cell_controller_53_p39));
  // Cell_controller cell_controller_54: pin names not known; wires that end beside it: Columns[6], Rows[5], MOSI, MISO, cell_controller_54_p5, cell_controller_54_p6, cell_controller_54_p7, cell_controller_54_p8, cell_controller_54_p9, cell_controller_54_p10, cell_controller_54_p11, cell_controller_54_p12, cell_controller_54_p13, cell_controller_54_p14, cell_controller_54_p15, cell_controller_54_p16, cell_controller_54_p17, cell_controller_54_p18, cell_controller_54_p19, cell_controller_54_p20, cell_controller_54_p21, cell_controller_54_p22, cell_controller_54_p23, cell_controller_54_p24, cell_controller_54_p25, cell_controller_54_p26, cell_controller_54_p27, cell_controller_54_p28, cell_controller_54_p29, cell_controller_54_p30, cell_controller_54_p31, cell_controller_54_p32, cell_controller_54_p33, cell_controller_54_p34, cell_controller_54_p31, cell_controller_54_p36, cell_controller_54_p37, cell_controller_54_p38, cell_controller_54_p39
  DotMatrix #(.matrixcols(11), .matrixrows(5)) dotmatrix_170 (
    .col0(cell_controller_54_p5), .col1(cell_controller_54_p8), .col2(cell_controller_54_p11),
    .col3(cell_controller_54_p14), .col4(cell_controller_54_p17), .col5(cell_controller_54_p20),
    .col6(cell_controller_54_p23), .col7(cell_controller_54_p26), .col8(cell_controller_54_p29),
    .col9(cell_controller_54_p33), .col10(cell_controller_54_p37));
  DotMatrix #(.matrixcols(11), .matrixrows(8)) dotmatrix_171 (
    .col0(cell_controller_54_p6), .col1(cell_controller_54_p9), .col2(cell_controller_54_p12),
    .col3(cell_controller_54_p15), .col4(cell_controller_54_p18), .col5(cell_controller_54_p21),
    .col6(cell_controller_54_p24), .col7(cell_controller_54_p27), .col8(cell_controller_54_p30),
    .col9(cell_controller_54_p34), .col10(cell_controller_54_p38));
  DotMatrix #(.matrixcols(11), .matrixrows(8)) dotmatrix_172 (
    .col0(cell_controller_54_p7), .col1(cell_controller_54_p10), .col2(cell_controller_54_p13),
    .col3(cell_controller_54_p16), .col4(cell_controller_54_p19), .col5(cell_controller_54_p22),
    .col6(cell_controller_54_p25), .col7(cell_controller_54_p28), .col8(cell_controller_54_p32),
    .col9(cell_controller_54_p36), .col10(cell_controller_54_p39));
  DotMatrix #(.matrixcols(11), .matrixrows(5)) dotmatrix_173 (
    .col0(cell_controller_55_p5), .col1(cell_controller_55_p8), .col2(cell_controller_55_p11),
    .col3(cell_controller_55_p14), .col4(cell_controller_55_p17), .col5(cell_controller_55_p20),
    .col6(cell_controller_55_p23), .col7(cell_controller_55_p26), .col8(cell_controller_55_p29),
    .col9(cell_controller_55_p33), .col10(cell_controller_55_p37));
  // Cell_controller cell_controller_55: pin names not known; wires that end beside it: Columns[6], Rows[6], MOSI, MISO, cell_controller_55_p5, cell_controller_55_p6, cell_controller_55_p7, cell_controller_55_p8, cell_controller_55_p9, cell_controller_55_p10, cell_controller_55_p11, cell_controller_55_p12, cell_controller_55_p13, cell_controller_55_p14, cell_controller_55_p15, cell_controller_55_p16, cell_controller_55_p17, cell_controller_55_p18, cell_controller_55_p19, cell_controller_55_p20, cell_controller_55_p21, cell_controller_55_p22, cell_controller_55_p23, cell_controller_55_p24, cell_controller_55_p25, cell_controller_55_p26, cell_controller_55_p27, cell_controller_55_p28, cell_controller_55_p29, cell_controller_55_p30, cell_controller_55_p31, cell_controller_55_p32, cell_controller_55_p33, cell_controller_55_p34, cell_controller_55_p31, cell_controller_55_p36, cell_controller_55_p37, cell_controller_55_p38, cell_controller_55_p39
  DotMatrix #(.matrixcols(11), .matrixrows(8)) dotmatrix_174 (
    .col0(cell_controller_55_p6), .col1(cell_controller_55_p9), .col2(cell_controller_55_p12),
    .col3(cell_controller_55_p15), .col4(cell_controller_55_p18), .col5(cell_controller_55_p21),
    .col6(cell_controller_55_p24), .col7(cell_controller_55_p27), .col8(cell_controller_55_p30),
    .col9(cell_controller_55_p34), .col10(cell_controller_55_p38));
  DotMatrix #(.matrixcols(11), .matrixrows(8)) dotmatrix_175 (
    .col0(cell_controller_55_p7), .col1(cell_controller_55_p10), .col2(cell_controller_55_p13),
    .col3(cell_controller_55_p16), .col4(cell_controller_55_p19), .col5(cell_controller_55_p22),
    .col6(cell_controller_55_p25), .col7(cell_controller_55_p28), .col8(cell_controller_55_p32),
    .col9(cell_controller_55_p36), .col10(cell_controller_55_p39));
  // Cell_controller cell_controller_56: pin names not known; wires that end beside it: Columns[6], Rows[7], MOSI, MISO, cell_controller_56_p5, cell_controller_56_p6, cell_controller_56_p7, cell_controller_56_p8, cell_controller_56_p9, cell_controller_56_p10, cell_controller_56_p11, cell_controller_56_p12, cell_controller_56_p13, cell_controller_56_p14, cell_controller_56_p15, cell_controller_56_p16, cell_controller_56_p17, cell_controller_56_p18, cell_controller_56_p19, cell_controller_56_p20, cell_controller_56_p21, cell_controller_56_p22, cell_controller_56_p23, cell_controller_56_p24, cell_controller_56_p25, cell_controller_56_p26, cell_controller_56_p27, cell_controller_56_p28, cell_controller_56_p29, cell_controller_56_p30, cell_controller_56_p31, cell_controller_56_p32, cell_controller_56_p33, cell_controller_56_p34, cell_controller_56_p31, cell_controller_56_p36, cell_controller_56_p37, cell_controller_56_p38, cell_controller_56_p39
  DotMatrix #(.matrixcols(11), .matrixrows(5)) dotmatrix_176 (
    .col0(cell_controller_56_p5), .col1(cell_controller_56_p8), .col2(cell_controller_56_p11),
    .col3(cell_controller_56_p14), .col4(cell_controller_56_p17), .col5(cell_controller_56_p20),
    .col6(cell_controller_56_p23), .col7(cell_controller_56_p26), .col8(cell_controller_56_p29),
    .col9(cell_controller_56_p33), .col10(cell_controller_56_p37));
  DotMatrix #(.matrixcols(11), .matrixrows(8)) dotmatrix_177 (
    .col0(cell_controller_56_p6), .col1(cell_controller_56_p9), .col2(cell_controller_56_p12),
    .col3(cell_controller_56_p15), .col4(cell_controller_56_p18), .col5(cell_controller_56_p21),
    .col6(cell_controller_56_p24), .col7(cell_controller_56_p27), .col8(cell_controller_56_p30),
    .col9(cell_controller_56_p34), .col10(cell_controller_56_p38));
  DotMatrix #(.matrixcols(11), .matrixrows(8)) dotmatrix_178 (
    .col0(cell_controller_56_p7), .col1(cell_controller_56_p10), .col2(cell_controller_56_p13),
    .col3(cell_controller_56_p16), .col4(cell_controller_56_p19), .col5(cell_controller_56_p22),
    .col6(cell_controller_56_p25), .col7(cell_controller_56_p28), .col8(cell_controller_56_p32),
    .col9(cell_controller_56_p36), .col10(cell_controller_56_p39));
  DotMatrix #(.matrixcols(11), .matrixrows(5)) dotmatrix_179 (
    .col0(cell_controller_57_p5), .col1(cell_controller_57_p8), .col2(cell_controller_57_p11),
    .col3(cell_controller_57_p14), .col4(cell_controller_57_p17), .col5(cell_controller_57_p20),
    .col6(cell_controller_57_p23), .col7(cell_controller_57_p26), .col8(cell_controller_57_p29),
    .col9(cell_controller_57_p32), .col10(cell_controller_57_p35));
  // Cell_controller cell_controller_57: pin names not known; wires that end beside it: Columns[7], Rows[0], MOSI, MISO, cell_controller_57_p5, cell_controller_57_p6, cell_controller_57_p7, cell_controller_57_p8, cell_controller_57_p9, cell_controller_57_p10, cell_controller_57_p11, cell_controller_57_p12, cell_controller_57_p13, cell_controller_57_p14, cell_controller_57_p15, cell_controller_57_p16, cell_controller_57_p17, cell_controller_57_p18, cell_controller_57_p19, cell_controller_57_p20, cell_controller_57_p21, cell_controller_57_p22, cell_controller_57_p23, cell_controller_57_p24, cell_controller_57_p25, cell_controller_57_p26, cell_controller_57_p27, cell_controller_57_p28, cell_controller_57_p29, cell_controller_57_p30, cell_controller_57_p31, cell_controller_57_p32, cell_controller_57_p33, cell_controller_57_p34, cell_controller_57_p35, cell_controller_57_p36, cell_controller_57_p37
  DotMatrix #(.matrixcols(11), .matrixrows(8)) dotmatrix_180 (
    .col0(cell_controller_57_p6), .col1(cell_controller_57_p9), .col2(cell_controller_57_p12),
    .col3(cell_controller_57_p15), .col4(cell_controller_57_p18), .col5(cell_controller_57_p21),
    .col6(cell_controller_57_p24), .col7(cell_controller_57_p27), .col8(cell_controller_57_p30),
    .col9(cell_controller_57_p33), .col10(cell_controller_57_p36));
  DotMatrix #(.matrixcols(11), .matrixrows(8)) dotmatrix_181 (
    .col0(cell_controller_57_p7), .col1(cell_controller_57_p10), .col2(cell_controller_57_p13),
    .col3(cell_controller_57_p16), .col4(cell_controller_57_p19), .col5(cell_controller_57_p22),
    .col6(cell_controller_57_p25), .col7(cell_controller_57_p28), .col8(cell_controller_57_p31),
    .col9(cell_controller_57_p34), .col10(cell_controller_57_p37));
  DotMatrix #(.matrixcols(11), .matrixrows(5)) dotmatrix_182 (
    .col0(cell_controller_58_p5), .col1(cell_controller_58_p8), .col2(cell_controller_58_p11),
    .col3(cell_controller_58_p14), .col4(cell_controller_58_p17), .col5(cell_controller_58_p20),
    .col6(cell_controller_58_p23), .col7(cell_controller_58_p26), .col8(cell_controller_58_p29),
    .col9(cell_controller_58_p32), .col10(cell_controller_58_p35));
  // Cell_controller cell_controller_58: pin names not known; wires that end beside it: Columns[7], Rows[1], MOSI, MISO, cell_controller_58_p5, cell_controller_58_p6, cell_controller_58_p7, cell_controller_58_p8, cell_controller_58_p9, cell_controller_58_p10, cell_controller_58_p11, cell_controller_58_p12, cell_controller_58_p13, cell_controller_58_p14, cell_controller_58_p15, cell_controller_58_p16, cell_controller_58_p17, cell_controller_58_p18, cell_controller_58_p19, cell_controller_58_p20, cell_controller_58_p21, cell_controller_58_p22, cell_controller_58_p23, cell_controller_58_p24, cell_controller_58_p25, cell_controller_58_p26, cell_controller_58_p27, cell_controller_58_p28, cell_controller_58_p29, cell_controller_58_p30, cell_controller_58_p31, cell_controller_58_p32, cell_controller_58_p33, cell_controller_58_p34, cell_controller_58_p35, cell_controller_58_p36, cell_controller_58_p37
  DotMatrix #(.matrixcols(11), .matrixrows(8)) dotmatrix_183 (
    .col0(cell_controller_58_p6), .col1(cell_controller_58_p9), .col2(cell_controller_58_p12),
    .col3(cell_controller_58_p15), .col4(cell_controller_58_p18), .col5(cell_controller_58_p21),
    .col6(cell_controller_58_p24), .col7(cell_controller_58_p27), .col8(cell_controller_58_p30),
    .col9(cell_controller_58_p33), .col10(cell_controller_58_p36));
  DotMatrix #(.matrixcols(11), .matrixrows(8)) dotmatrix_184 (
    .col0(cell_controller_58_p7), .col1(cell_controller_58_p10), .col2(cell_controller_58_p13),
    .col3(cell_controller_58_p16), .col4(cell_controller_58_p19), .col5(cell_controller_58_p22),
    .col6(cell_controller_58_p25), .col7(cell_controller_58_p28), .col8(cell_controller_58_p31),
    .col9(cell_controller_58_p34), .col10(cell_controller_58_p37));
  DotMatrix #(.matrixcols(11), .matrixrows(5)) dotmatrix_185 (
    .col0(cell_controller_59_p5), .col1(cell_controller_59_p8), .col2(cell_controller_59_p11),
    .col3(cell_controller_59_p14), .col4(cell_controller_59_p17), .col5(cell_controller_59_p20),
    .col6(cell_controller_59_p23), .col7(cell_controller_59_p26), .col8(cell_controller_59_p29),
    .col9(cell_controller_59_p32), .col10(cell_controller_59_p35));
  // Cell_controller cell_controller_59: pin names not known; wires that end beside it: Columns[7], Rows[2], MOSI, MISO, cell_controller_59_p5, cell_controller_59_p6, cell_controller_59_p7, cell_controller_59_p8, cell_controller_59_p9, cell_controller_59_p10, cell_controller_59_p11, cell_controller_59_p12, cell_controller_59_p13, cell_controller_59_p14, cell_controller_59_p15, cell_controller_59_p16, cell_controller_59_p17, cell_controller_59_p18, cell_controller_59_p19, cell_controller_59_p20, cell_controller_59_p21, cell_controller_59_p22, cell_controller_59_p23, cell_controller_59_p24, cell_controller_59_p25, cell_controller_59_p26, cell_controller_59_p27, cell_controller_59_p28, cell_controller_59_p29, cell_controller_59_p30, cell_controller_59_p31, cell_controller_59_p32, cell_controller_59_p33, cell_controller_59_p34, cell_controller_59_p35, cell_controller_59_p36, cell_controller_59_p37
  DotMatrix #(.matrixcols(11), .matrixrows(8)) dotmatrix_186 (
    .col0(cell_controller_59_p6), .col1(cell_controller_59_p9), .col2(cell_controller_59_p12),
    .col3(cell_controller_59_p15), .col4(cell_controller_59_p18), .col5(cell_controller_59_p21),
    .col6(cell_controller_59_p24), .col7(cell_controller_59_p27), .col8(cell_controller_59_p30),
    .col9(cell_controller_59_p33), .col10(cell_controller_59_p36));
  DotMatrix #(.matrixcols(11), .matrixrows(8)) dotmatrix_187 (
    .col0(cell_controller_59_p7), .col1(cell_controller_59_p10), .col2(cell_controller_59_p13),
    .col3(cell_controller_59_p16), .col4(cell_controller_59_p19), .col5(cell_controller_59_p22),
    .col6(cell_controller_59_p25), .col7(cell_controller_59_p28), .col8(cell_controller_59_p31),
    .col9(cell_controller_59_p34), .col10(cell_controller_59_p37));
  DotMatrix #(.matrixcols(11), .matrixrows(5)) dotmatrix_188 (
    .col0(cell_controller_60_p5), .col1(cell_controller_60_p8), .col2(cell_controller_60_p11),
    .col3(cell_controller_60_p14), .col4(cell_controller_60_p17), .col5(cell_controller_60_p20),
    .col6(cell_controller_60_p23), .col7(cell_controller_60_p26), .col8(cell_controller_60_p29),
    .col9(cell_controller_60_p32), .col10(cell_controller_60_p35));
  // Cell_controller cell_controller_60: pin names not known; wires that end beside it: Columns[7], Rows[3], MOSI, MISO, cell_controller_60_p5, cell_controller_60_p6, cell_controller_60_p7, cell_controller_60_p8, cell_controller_60_p9, cell_controller_60_p10, cell_controller_60_p11, cell_controller_60_p12, cell_controller_60_p13, cell_controller_60_p14, cell_controller_60_p15, cell_controller_60_p16, cell_controller_60_p17, cell_controller_60_p18, cell_controller_60_p19, cell_controller_60_p20, cell_controller_60_p21, cell_controller_60_p22, cell_controller_60_p23, cell_controller_60_p24, cell_controller_60_p25, cell_controller_60_p26, cell_controller_60_p27, cell_controller_60_p28, cell_controller_60_p29, cell_controller_60_p30, cell_controller_60_p31, cell_controller_60_p32, cell_controller_60_p33, cell_controller_60_p34, cell_controller_60_p35, cell_controller_60_p36, cell_controller_60_p37
  DotMatrix #(.matrixcols(11), .matrixrows(8)) dotmatrix_189 (
    .col0(cell_controller_60_p6), .col1(cell_controller_60_p9), .col2(cell_controller_60_p12),
    .col3(cell_controller_60_p15), .col4(cell_controller_60_p18), .col5(cell_controller_60_p21),
    .col6(cell_controller_60_p24), .col7(cell_controller_60_p27), .col8(cell_controller_60_p30),
    .col9(cell_controller_60_p33), .col10(cell_controller_60_p36));
  DotMatrix #(.matrixcols(11), .matrixrows(8)) dotmatrix_190 (
    .col0(cell_controller_60_p7), .col1(cell_controller_60_p10), .col2(cell_controller_60_p13),
    .col3(cell_controller_60_p16), .col4(cell_controller_60_p19), .col5(cell_controller_60_p22),
    .col6(cell_controller_60_p25), .col7(cell_controller_60_p28), .col8(cell_controller_60_p31),
    .col9(cell_controller_60_p34), .col10(cell_controller_60_p37));
  // Cell_controller cell_controller_61: pin names not known; wires that end beside it: Columns[7], Rows[4], MOSI, MISO, cell_controller_61_p5, cell_controller_61_p6, cell_controller_61_p7, cell_controller_61_p8, cell_controller_61_p9, cell_controller_61_p10, cell_controller_61_p11, cell_controller_61_p12, cell_controller_61_p13, cell_controller_61_p14, cell_controller_61_p15, cell_controller_61_p16, cell_controller_61_p17, cell_controller_61_p18, cell_controller_61_p19, cell_controller_61_p20, cell_controller_61_p21, cell_controller_61_p22, cell_controller_61_p23, cell_controller_61_p24, cell_controller_61_p25, cell_controller_61_p26, cell_controller_61_p27, cell_controller_61_p28, cell_controller_61_p29, cell_controller_61_p30, cell_controller_61_p31, cell_controller_61_p32, cell_controller_61_p33, cell_controller_61_p34, cell_controller_61_p35, cell_controller_61_p36, cell_controller_61_p37
  DotMatrix #(.matrixcols(11), .matrixrows(5)) dotmatrix_191 (
    .col0(cell_controller_61_p5), .col1(cell_controller_61_p8), .col2(cell_controller_61_p11),
    .col3(cell_controller_61_p14), .col4(cell_controller_61_p17), .col5(cell_controller_61_p20),
    .col6(cell_controller_61_p23), .col7(cell_controller_61_p26), .col8(cell_controller_61_p29),
    .col9(cell_controller_61_p32), .col10(cell_controller_61_p35));
  DotMatrix #(.matrixcols(11), .matrixrows(8)) dotmatrix_192 (
    .col0(cell_controller_61_p6), .col1(cell_controller_61_p9), .col2(cell_controller_61_p12),
    .col3(cell_controller_61_p15), .col4(cell_controller_61_p18), .col5(cell_controller_61_p21),
    .col6(cell_controller_61_p24), .col7(cell_controller_61_p27), .col8(cell_controller_61_p30),
    .col9(cell_controller_61_p33), .col10(cell_controller_61_p36));
  DotMatrix #(.matrixcols(11), .matrixrows(8)) dotmatrix_193 (
    .col0(cell_controller_61_p7), .col1(cell_controller_61_p10), .col2(cell_controller_61_p13),
    .col3(cell_controller_61_p16), .col4(cell_controller_61_p19), .col5(cell_controller_61_p22),
    .col6(cell_controller_61_p25), .col7(cell_controller_61_p28), .col8(cell_controller_61_p31),
    .col9(cell_controller_61_p34), .col10(cell_controller_61_p37));
  // Cell_controller cell_controller_62: pin names not known; wires that end beside it: Columns[7], Rows[5], MOSI, MISO, cell_controller_62_p5, cell_controller_62_p6, cell_controller_62_p7, cell_controller_62_p8, cell_controller_62_p9, cell_controller_62_p10, cell_controller_62_p11, cell_controller_62_p12, cell_controller_62_p13, cell_controller_62_p14, cell_controller_62_p15, cell_controller_62_p16, cell_controller_62_p17, cell_controller_62_p18, cell_controller_62_p19, cell_controller_62_p20, cell_controller_62_p21, cell_controller_62_p22, cell_controller_62_p23, cell_controller_62_p24, cell_controller_62_p25, cell_controller_62_p26, cell_controller_62_p27, cell_controller_62_p28, cell_controller_62_p29, cell_controller_62_p30, cell_controller_62_p31, cell_controller_62_p32, cell_controller_62_p33, cell_controller_62_p34, cell_controller_62_p35, cell_controller_62_p36, cell_controller_62_p37
  DotMatrix #(.matrixcols(11), .matrixrows(5)) dotmatrix_194 (
    .col0(cell_controller_62_p5), .col1(cell_controller_62_p8), .col2(cell_controller_62_p11),
    .col3(cell_controller_62_p14), .col4(cell_controller_62_p17), .col5(cell_controller_62_p20),
    .col6(cell_controller_62_p23), .col7(cell_controller_62_p26), .col8(cell_controller_62_p29),
    .col9(cell_controller_62_p32), .col10(cell_controller_62_p35));
  DotMatrix #(.matrixcols(11), .matrixrows(8)) dotmatrix_195 (
    .col0(cell_controller_62_p6), .col1(cell_controller_62_p9), .col2(cell_controller_62_p12),
    .col3(cell_controller_62_p15), .col4(cell_controller_62_p18), .col5(cell_controller_62_p21),
    .col6(cell_controller_62_p24), .col7(cell_controller_62_p27), .col8(cell_controller_62_p30),
    .col9(cell_controller_62_p33), .col10(cell_controller_62_p36));
  DotMatrix #(.matrixcols(11), .matrixrows(8)) dotmatrix_196 (
    .col0(cell_controller_62_p7), .col1(cell_controller_62_p10), .col2(cell_controller_62_p13),
    .col3(cell_controller_62_p16), .col4(cell_controller_62_p19), .col5(cell_controller_62_p22),
    .col6(cell_controller_62_p25), .col7(cell_controller_62_p28), .col8(cell_controller_62_p31),
    .col9(cell_controller_62_p34), .col10(cell_controller_62_p37));
  DotMatrix #(.matrixcols(11), .matrixrows(5)) dotmatrix_197 (
    .col0(cell_controller_63_p5), .col1(cell_controller_63_p8), .col2(cell_controller_63_p11),
    .col3(cell_controller_63_p14), .col4(cell_controller_63_p17), .col5(cell_controller_63_p20),
    .col6(cell_controller_63_p23), .col7(cell_controller_63_p26), .col8(cell_controller_63_p29),
    .col9(cell_controller_63_p32), .col10(cell_controller_63_p35));
  // Cell_controller cell_controller_63: pin names not known; wires that end beside it: Columns[7], Rows[6], MOSI, MISO, cell_controller_63_p5, cell_controller_63_p6, cell_controller_63_p7, cell_controller_63_p8, cell_controller_63_p9, cell_controller_63_p10, cell_controller_63_p11, cell_controller_63_p12, cell_controller_63_p13, cell_controller_63_p14, cell_controller_63_p15, cell_controller_63_p16, cell_controller_63_p17, cell_controller_63_p18, cell_controller_63_p19, cell_controller_63_p20, cell_controller_63_p21, cell_controller_63_p22, cell_controller_63_p23, cell_controller_63_p24, cell_controller_63_p25, cell_controller_63_p26, cell_controller_63_p27, cell_controller_63_p28, cell_controller_63_p29, cell_controller_63_p30, cell_controller_63_p31, cell_controller_63_p32, cell_controller_63_p33, cell_controller_63_p34, cell_controller_63_p35, cell_controller_63_p36, cell_controller_63_p37
  DotMatrix #(.matrixcols(11), .matrixrows(8)) dotmatrix_198 (
    .col0(cell_controller_63_p6), .col1(cell_controller_63_p9), .col2(cell_controller_63_p12),
    .col3(cell_controller_63_p15), .col4(cell_controller_63_p18), .col5(cell_controller_63_p21),
    .col6(cell_controller_63_p24), .col7(cell_controller_63_p27), .col8(cell_controller_63_p30),
    .col9(cell_controller_63_p33), .col10(cell_controller_63_p36));
  DotMatrix #(.matrixcols(11), .matrixrows(8)) dotmatrix_199 (
    .col0(cell_controller_63_p7), .col1(cell_controller_63_p10), .col2(cell_controller_63_p13),
    .col3(cell_controller_63_p16), .col4(cell_controller_63_p19), .col5(cell_controller_63_p22),
    .col6(cell_controller_63_p25), .col7(cell_controller_63_p28), .col8(cell_controller_63_p31),
    .col9(cell_controller_63_p34), .col10(cell_controller_63_p37));
  // Cell_controller cell_controller_64: pin names not known; wires that end beside it: Columns[7], Rows[7], MOSI, MISO, cell_controller_64_p5, cell_controller_64_p6, cell_controller_64_p7, cell_controller_64_p8, cell_controller_64_p9, cell_controller_64_p10, cell_controller_64_p11, cell_controller_64_p12, cell_controller_64_p13, cell_controller_64_p14, cell_controller_64_p15, cell_controller_64_p16, cell_controller_64_p17, cell_controller_64_p18, cell_controller_64_p19, cell_controller_64_p20, cell_controller_64_p21, cell_controller_64_p22, cell_controller_64_p23, cell_controller_64_p24, cell_controller_64_p25, cell_controller_64_p26, cell_controller_64_p27, cell_controller_64_p28, cell_controller_64_p29, cell_controller_64_p30, cell_controller_64_p31, cell_controller_64_p32, cell_controller_64_p33, cell_controller_64_p34, cell_controller_64_p35, cell_controller_64_p36, cell_controller_64_p37
  DotMatrix #(.matrixcols(11), .matrixrows(5)) dotmatrix_200 (
    .col0(cell_controller_64_p5), .col1(cell_controller_64_p8), .col2(cell_controller_64_p11),
    .col3(cell_controller_64_p14), .col4(cell_controller_64_p17), .col5(cell_controller_64_p20),
    .col6(cell_controller_64_p23), .col7(cell_controller_64_p26), .col8(cell_controller_64_p29),
    .col9(cell_controller_64_p32), .col10(cell_controller_64_p35));
  DotMatrix #(.matrixcols(11), .matrixrows(8)) dotmatrix_201 (
    .col0(cell_controller_64_p6), .col1(cell_controller_64_p9), .col2(cell_controller_64_p12),
    .col3(cell_controller_64_p15), .col4(cell_controller_64_p18), .col5(cell_controller_64_p21),
    .col6(cell_controller_64_p24), .col7(cell_controller_64_p27), .col8(cell_controller_64_p30),
    .col9(cell_controller_64_p33), .col10(cell_controller_64_p36));
  DotMatrix #(.matrixcols(11), .matrixrows(8)) dotmatrix_202 (
    .col0(cell_controller_64_p7), .col1(cell_controller_64_p10), .col2(cell_controller_64_p13),
    .col3(cell_controller_64_p16), .col4(cell_controller_64_p19), .col5(cell_controller_64_p22),
    .col6(cell_controller_64_p25), .col7(cell_controller_64_p28), .col8(cell_controller_64_p31),
    .col9(cell_controller_64_p34), .col10(cell_controller_64_p37));
endmodule

module main_sonia (
);

  wire and_1_out, button_1_out, clock_1_out, clock_2_out, clock_3_out, counter_1_carry,
       input_controller_1_active_led, input_controller_1_data_ready, input_controller_1_error_led,
       input_controller_1_kbd_clear, input_controller_1_kbd_clock, input_controller_1_kbd_en,
       input_controller_1_user_action_led, keyboard_1_avail, MISO, undriven_2, undriven_3, undriven_4,
       undriven_5;
  wire [1:0] MOSI;
  wire [4:0] cell_controller_1_p5, cell_controller_1_p8, cell_controller_1_p11, cell_controller_1_p14,
       cell_controller_1_p17, cell_controller_1_p20, cell_controller_1_p23, cell_controller_1_p26,
       cell_controller_1_p29, cell_controller_1_p32, cell_controller_1_p35, cell_controller_2_p5,
       cell_controller_2_p8, cell_controller_2_p11, cell_controller_2_p14, cell_controller_2_p17,
       cell_controller_2_p20, cell_controller_2_p23, cell_controller_2_p26, cell_controller_2_p29,
       cell_controller_2_p32, cell_controller_2_p35, cell_controller_3_p5, cell_controller_3_p8,
       cell_controller_3_p11, cell_controller_3_p14, cell_controller_3_p17, cell_controller_3_p20,
       cell_controller_3_p23, cell_controller_3_p26, cell_controller_3_p29, cell_controller_3_p32,
       cell_controller_3_p35, cell_controller_4_p5, cell_controller_4_p8, cell_controller_4_p11,
       cell_controller_4_p14, cell_controller_4_p17, cell_controller_4_p20, cell_controller_4_p23,
       cell_controller_4_p26, cell_controller_4_p29, cell_controller_4_p32, cell_controller_4_p35,
       cell_controller_5_p5, cell_controller_5_p8, cell_controller_5_p11, cell_controller_5_p14,
       cell_controller_5_p17, cell_controller_5_p20, cell_controller_5_p23, cell_controller_5_p26,
       cell_controller_5_p29, cell_controller_5_p32, cell_controller_5_p35, cell_controller_6_p5,
       cell_controller_6_p8, cell_controller_6_p11, cell_controller_6_p14, cell_controller_6_p17,
       cell_controller_6_p20, cell_controller_6_p23, cell_controller_6_p26, cell_controller_6_p29,
       cell_controller_6_p32, cell_controller_6_p35, cell_controller_7_p5, cell_controller_7_p8,
       cell_controller_7_p11, cell_controller_7_p14, cell_controller_7_p17, cell_controller_7_p20,
       cell_controller_7_p23, cell_controller_7_p26, cell_controller_7_p29, cell_controller_7_p32,
       cell_controller_7_p35, cell_controller_8_p5, cell_controller_8_p8, cell_controller_8_p11,
       cell_controller_8_p14, cell_controller_8_p17, cell_controller_8_p20, cell_controller_8_p23,
       cell_controller_8_p26, cell_controller_8_p29, cell_controller_8_p32, cell_controller_8_p35,
       input_controller_1_command_parsed_from_user_input;
  wire [6:0] keyboard_1_data;
  wire [7:0] cell_controller_1_p6, cell_controller_1_p7, cell_controller_1_p9, cell_controller_1_p10,
       cell_controller_1_p12, cell_controller_1_p13, cell_controller_1_p15, cell_controller_1_p16,
       cell_controller_1_p18, cell_controller_1_p19, cell_controller_1_p21, cell_controller_1_p22,
       cell_controller_1_p24, cell_controller_1_p25, cell_controller_1_p27, cell_controller_1_p28,
       cell_controller_1_p30, cell_controller_1_p31, cell_controller_1_p33, cell_controller_1_p34,
       cell_controller_1_p36, cell_controller_1_p37, cell_controller_2_p6, cell_controller_2_p7,
       cell_controller_2_p9, cell_controller_2_p10, cell_controller_2_p12, cell_controller_2_p13,
       cell_controller_2_p15, cell_controller_2_p16, cell_controller_2_p18, cell_controller_2_p19,
       cell_controller_2_p21, cell_controller_2_p22, cell_controller_2_p24, cell_controller_2_p25,
       cell_controller_2_p27, cell_controller_2_p28, cell_controller_2_p30, cell_controller_2_p31,
       cell_controller_2_p33, cell_controller_2_p34, cell_controller_2_p36, cell_controller_2_p37,
       cell_controller_3_p6, cell_controller_3_p7, cell_controller_3_p9, cell_controller_3_p10,
       cell_controller_3_p12, cell_controller_3_p13, cell_controller_3_p15, cell_controller_3_p16,
       cell_controller_3_p18, cell_controller_3_p19, cell_controller_3_p21, cell_controller_3_p22,
       cell_controller_3_p24, cell_controller_3_p25, cell_controller_3_p27, cell_controller_3_p28,
       cell_controller_3_p30, cell_controller_3_p31, cell_controller_3_p33, cell_controller_3_p34,
       cell_controller_3_p36, cell_controller_3_p37, cell_controller_4_p6, cell_controller_4_p7,
       cell_controller_4_p9, cell_controller_4_p10, cell_controller_4_p12, cell_controller_4_p13,
       cell_controller_4_p15, cell_controller_4_p16, cell_controller_4_p18, cell_controller_4_p19,
       cell_controller_4_p21, cell_controller_4_p22, cell_controller_4_p24, cell_controller_4_p25,
       cell_controller_4_p27, cell_controller_4_p28, cell_controller_4_p30, cell_controller_4_p31,
       cell_controller_4_p33, cell_controller_4_p34, cell_controller_4_p36, cell_controller_4_p37,
       cell_controller_5_p6, cell_controller_5_p7, cell_controller_5_p9, cell_controller_5_p10,
       cell_controller_5_p12, cell_controller_5_p13, cell_controller_5_p15, cell_controller_5_p16,
       cell_controller_5_p18, cell_controller_5_p19, cell_controller_5_p21, cell_controller_5_p22,
       cell_controller_5_p24, cell_controller_5_p25, cell_controller_5_p27, cell_controller_5_p28,
       cell_controller_5_p30, cell_controller_5_p31, cell_controller_5_p33, cell_controller_5_p34,
       cell_controller_5_p36, cell_controller_5_p37, cell_controller_6_p6, cell_controller_6_p7,
       cell_controller_6_p9, cell_controller_6_p10, cell_controller_6_p12, cell_controller_6_p13,
       cell_controller_6_p15, cell_controller_6_p16, cell_controller_6_p18, cell_controller_6_p19,
       cell_controller_6_p21, cell_controller_6_p22, cell_controller_6_p24, cell_controller_6_p25,
       cell_controller_6_p27, cell_controller_6_p28, cell_controller_6_p30, cell_controller_6_p31,
       cell_controller_6_p33, cell_controller_6_p34, cell_controller_6_p36, cell_controller_6_p37,
       cell_controller_7_p6, cell_controller_7_p7, cell_controller_7_p9, cell_controller_7_p10,
       cell_controller_7_p12, cell_controller_7_p13, cell_controller_7_p15, cell_controller_7_p16,
       cell_controller_7_p18, cell_controller_7_p19, cell_controller_7_p21, cell_controller_7_p22,
       cell_controller_7_p24, cell_controller_7_p25, cell_controller_7_p27, cell_controller_7_p28,
       cell_controller_7_p30, cell_controller_7_p31, cell_controller_7_p33, cell_controller_7_p34,
       cell_controller_7_p36, cell_controller_7_p37, cell_controller_8_p6, cell_controller_8_p7,
       cell_controller_8_p9, cell_controller_8_p10, cell_controller_8_p12, cell_controller_8_p13,
       cell_controller_8_p15, cell_controller_8_p16, cell_controller_8_p18, cell_controller_8_p19,
       cell_controller_8_p21, cell_controller_8_p22, cell_controller_8_p24, cell_controller_8_p25,
       cell_controller_8_p27, cell_controller_8_p28, cell_controller_8_p30, cell_controller_8_p31,
       cell_controller_8_p33, cell_controller_8_p34, cell_controller_8_p36, cell_controller_8_p37, Columns,
       Rows, undriven;
  wire [10:0] input_controller_1_signed_number_parsed_from_user_input;

  Button button_1 (.out(button_1_out));
  Clock clock_1 (.out(clock_1_out));
  Clock clock_2 (.out(clock_2_out));
  LED led_1 (.in(undriven_2));
  LED led_2 (.in(undriven_3));
  DotMatrix #(.inputtype("row"), .matrixcols(8), .matrixrows(1)) dotmatrix_1 (.row0(undriven));
  input_controller input_controller_1 (
    .Signed_number_parsed_from_user_input(input_controller_1_signed_number_parsed_from_user_input),
    .Command_parsed_from_user_input(input_controller_1_command_parsed_from_user_input),
    .KBD_clock(input_controller_1_kbd_clock), .KBD_clear(input_controller_1_kbd_clear),
    .KBD_available(keyboard_1_avail), .KBD_buffer(keyboard_1_data), .KBD_en(input_controller_1_kbd_en),
    .Enabled__clears_buffer_on_rising_edge(and_1_out), .Active_LED(input_controller_1_active_led),
    .Request_number(undriven_4), .User_action_LED(input_controller_1_user_action_led),
    .Error_LED(input_controller_1_error_led), .Data_ready(input_controller_1_data_ready), .CLK(clock_2_out));  // open: input_buffer, Cursor_position
  Keyboard keyboard_1 (
    .clk(input_controller_1_kbd_clock), .re(input_controller_1_kbd_en), .clr(input_controller_1_kbd_clear),
    .avail(keyboard_1_avail), .data(keyboard_1_data));
  and and_1 (and_1_out, ~counter_1_carry, undriven_5);  // AND_Gate
  LED led_3 (.in(input_controller_1_active_led));
  LED led_4 (.in(input_controller_1_user_action_led));
  Counter counter_1 (
    .count(input_controller_1_error_led), .carry(counter_1_carry), .clk(clock_3_out));  // open: load, D, Q, clr
  LED led_5 (.in(input_controller_1_error_led));
  Clock clock_3 (.out(clock_3_out));
  DotMatrix #(.inputtype("row"), .matrixcols(8), .matrixrows(1)) dotmatrix_2 (.row0({Columns[0], Columns[1], Columns[2], Columns[3], Columns[4], Columns[5], Columns[6], Columns[7]}));
  DotMatrix #(.matrixcols(1), .matrixrows(8)) dotmatrix_3 (.col0({Rows[0], Rows[1], Rows[2], Rows[3], Rows[4], Rows[5], Rows[6], Rows[7]}));
  DotMatrix #(.matrixcols(11), .matrixrows(5)) dotmatrix_4 (
    .col0(cell_controller_1_p5), .col1(cell_controller_1_p8), .col2(cell_controller_1_p11),
    .col3(cell_controller_1_p14), .col4(cell_controller_1_p17), .col5(cell_controller_1_p20),
    .col6(cell_controller_1_p23), .col7(cell_controller_1_p26), .col8(cell_controller_1_p29),
    .col9(cell_controller_1_p32), .col10(cell_controller_1_p35));
  // Cell_controller cell_controller_1: pin names not known; wires that end beside it: Columns[0], Rows[0], MOSI, MISO, cell_controller_1_p5, cell_controller_1_p6, cell_controller_1_p7, cell_controller_1_p8, cell_controller_1_p9, cell_controller_1_p10, cell_controller_1_p11, cell_controller_1_p12, cell_controller_1_p13, cell_controller_1_p14, cell_controller_1_p15, cell_controller_1_p16, cell_controller_1_p17, cell_controller_1_p18, cell_controller_1_p19, cell_controller_1_p20, cell_controller_1_p21, cell_controller_1_p22, cell_controller_1_p23, cell_controller_1_p24, cell_controller_1_p25, cell_controller_1_p26, cell_controller_1_p27, cell_controller_1_p28, cell_controller_1_p29, cell_controller_1_p30, cell_controller_1_p31, cell_controller_1_p32, cell_controller_1_p33, cell_controller_1_p34, cell_controller_1_p35, cell_controller_1_p36, cell_controller_1_p37
  DotMatrix #(.matrixcols(11), .matrixrows(8)) dotmatrix_5 (
    .col0(cell_controller_1_p6), .col1(cell_controller_1_p9), .col2(cell_controller_1_p12),
    .col3(cell_controller_1_p15), .col4(cell_controller_1_p18), .col5(cell_controller_1_p21),
    .col6(cell_controller_1_p24), .col7(cell_controller_1_p27), .col8(cell_controller_1_p30),
    .col9(cell_controller_1_p33), .col10(cell_controller_1_p36));
  DotMatrix #(.matrixcols(11), .matrixrows(8)) dotmatrix_6 (
    .col0(cell_controller_1_p7), .col1(cell_controller_1_p10), .col2(cell_controller_1_p13),
    .col3(cell_controller_1_p16), .col4(cell_controller_1_p19), .col5(cell_controller_1_p22),
    .col6(cell_controller_1_p25), .col7(cell_controller_1_p28), .col8(cell_controller_1_p31),
    .col9(cell_controller_1_p34), .col10(cell_controller_1_p37));
  // Cell_controller cell_controller_2: pin names not known; wires that end beside it: Columns[1], Rows[0], MOSI, MISO, cell_controller_2_p5, cell_controller_2_p6, cell_controller_2_p7, cell_controller_2_p8, cell_controller_2_p9, cell_controller_2_p10, cell_controller_2_p11, cell_controller_2_p12, cell_controller_2_p13, cell_controller_2_p14, cell_controller_2_p15, cell_controller_2_p16, cell_controller_2_p17, cell_controller_2_p18, cell_controller_2_p19, cell_controller_2_p20, cell_controller_2_p21, cell_controller_2_p22, cell_controller_2_p23, cell_controller_2_p24, cell_controller_2_p25, cell_controller_2_p26, cell_controller_2_p27, cell_controller_2_p28, cell_controller_2_p29, cell_controller_2_p30, cell_controller_2_p31, cell_controller_2_p32, cell_controller_2_p33, cell_controller_2_p34, cell_controller_2_p35, cell_controller_2_p36, cell_controller_2_p37
  DotMatrix #(.matrixcols(11), .matrixrows(5)) dotmatrix_7 (
    .col0(cell_controller_2_p5), .col1(cell_controller_2_p8), .col2(cell_controller_2_p11),
    .col3(cell_controller_2_p14), .col4(cell_controller_2_p17), .col5(cell_controller_2_p20),
    .col6(cell_controller_2_p23), .col7(cell_controller_2_p26), .col8(cell_controller_2_p29),
    .col9(cell_controller_2_p32), .col10(cell_controller_2_p35));
  DotMatrix #(.matrixcols(11), .matrixrows(8)) dotmatrix_8 (
    .col0(cell_controller_2_p6), .col1(cell_controller_2_p9), .col2(cell_controller_2_p12),
    .col3(cell_controller_2_p15), .col4(cell_controller_2_p18), .col5(cell_controller_2_p21),
    .col6(cell_controller_2_p24), .col7(cell_controller_2_p27), .col8(cell_controller_2_p30),
    .col9(cell_controller_2_p33), .col10(cell_controller_2_p36));
  DotMatrix #(.matrixcols(11), .matrixrows(8)) dotmatrix_9 (
    .col0(cell_controller_2_p7), .col1(cell_controller_2_p10), .col2(cell_controller_2_p13),
    .col3(cell_controller_2_p16), .col4(cell_controller_2_p19), .col5(cell_controller_2_p22),
    .col6(cell_controller_2_p25), .col7(cell_controller_2_p28), .col8(cell_controller_2_p31),
    .col9(cell_controller_2_p34), .col10(cell_controller_2_p37));
  DotMatrix #(.matrixcols(11), .matrixrows(5)) dotmatrix_10 (
    .col0(cell_controller_3_p5), .col1(cell_controller_3_p8), .col2(cell_controller_3_p11),
    .col3(cell_controller_3_p14), .col4(cell_controller_3_p17), .col5(cell_controller_3_p20),
    .col6(cell_controller_3_p23), .col7(cell_controller_3_p26), .col8(cell_controller_3_p29),
    .col9(cell_controller_3_p32), .col10(cell_controller_3_p35));
  // Cell_controller cell_controller_3: pin names not known; wires that end beside it: Columns[2], Rows[0], MOSI, MISO, cell_controller_3_p5, cell_controller_3_p6, cell_controller_3_p7, cell_controller_3_p8, cell_controller_3_p9, cell_controller_3_p10, cell_controller_3_p11, cell_controller_3_p12, cell_controller_3_p13, cell_controller_3_p14, cell_controller_3_p15, cell_controller_3_p16, cell_controller_3_p17, cell_controller_3_p18, cell_controller_3_p19, cell_controller_3_p20, cell_controller_3_p21, cell_controller_3_p22, cell_controller_3_p23, cell_controller_3_p24, cell_controller_3_p25, cell_controller_3_p26, cell_controller_3_p27, cell_controller_3_p28, cell_controller_3_p29, cell_controller_3_p30, cell_controller_3_p31, cell_controller_3_p32, cell_controller_3_p33, cell_controller_3_p34, cell_controller_3_p35, cell_controller_3_p36, cell_controller_3_p37
  DotMatrix #(.matrixcols(11), .matrixrows(8)) dotmatrix_11 (
    .col0(cell_controller_3_p6), .col1(cell_controller_3_p9), .col2(cell_controller_3_p12),
    .col3(cell_controller_3_p15), .col4(cell_controller_3_p18), .col5(cell_controller_3_p21),
    .col6(cell_controller_3_p24), .col7(cell_controller_3_p27), .col8(cell_controller_3_p30),
    .col9(cell_controller_3_p33), .col10(cell_controller_3_p36));
  DotMatrix #(.matrixcols(11), .matrixrows(8)) dotmatrix_12 (
    .col0(cell_controller_3_p7), .col1(cell_controller_3_p10), .col2(cell_controller_3_p13),
    .col3(cell_controller_3_p16), .col4(cell_controller_3_p19), .col5(cell_controller_3_p22),
    .col6(cell_controller_3_p25), .col7(cell_controller_3_p28), .col8(cell_controller_3_p31),
    .col9(cell_controller_3_p34), .col10(cell_controller_3_p37));
  // Cell_controller cell_controller_4: pin names not known; wires that end beside it: Columns[3], Rows[0], MOSI, MISO, cell_controller_4_p5, cell_controller_4_p6, cell_controller_4_p7, cell_controller_4_p8, cell_controller_4_p9, cell_controller_4_p10, cell_controller_4_p11, cell_controller_4_p12, cell_controller_4_p13, cell_controller_4_p14, cell_controller_4_p15, cell_controller_4_p16, cell_controller_4_p17, cell_controller_4_p18, cell_controller_4_p19, cell_controller_4_p20, cell_controller_4_p21, cell_controller_4_p22, cell_controller_4_p23, cell_controller_4_p24, cell_controller_4_p25, cell_controller_4_p26, cell_controller_4_p27, cell_controller_4_p28, cell_controller_4_p29, cell_controller_4_p30, cell_controller_4_p31, cell_controller_4_p32, cell_controller_4_p33, cell_controller_4_p34, cell_controller_4_p35, cell_controller_4_p36, cell_controller_4_p37
  DotMatrix #(.matrixcols(11), .matrixrows(5)) dotmatrix_13 (
    .col0(cell_controller_4_p5), .col1(cell_controller_4_p8), .col2(cell_controller_4_p11),
    .col3(cell_controller_4_p14), .col4(cell_controller_4_p17), .col5(cell_controller_4_p20),
    .col6(cell_controller_4_p23), .col7(cell_controller_4_p26), .col8(cell_controller_4_p29),
    .col9(cell_controller_4_p32), .col10(cell_controller_4_p35));
  DotMatrix #(.matrixcols(11), .matrixrows(8)) dotmatrix_14 (
    .col0(cell_controller_4_p6), .col1(cell_controller_4_p9), .col2(cell_controller_4_p12),
    .col3(cell_controller_4_p15), .col4(cell_controller_4_p18), .col5(cell_controller_4_p21),
    .col6(cell_controller_4_p24), .col7(cell_controller_4_p27), .col8(cell_controller_4_p30),
    .col9(cell_controller_4_p33), .col10(cell_controller_4_p36));
  DotMatrix #(.matrixcols(11), .matrixrows(8)) dotmatrix_15 (
    .col0(cell_controller_4_p7), .col1(cell_controller_4_p10), .col2(cell_controller_4_p13),
    .col3(cell_controller_4_p16), .col4(cell_controller_4_p19), .col5(cell_controller_4_p22),
    .col6(cell_controller_4_p25), .col7(cell_controller_4_p28), .col8(cell_controller_4_p31),
    .col9(cell_controller_4_p34), .col10(cell_controller_4_p37));
  // Cell_controller cell_controller_5: pin names not known; wires that end beside it: Columns[4], Rows[0], MOSI, MISO, cell_controller_5_p5, cell_controller_5_p6, cell_controller_5_p7, cell_controller_5_p8, cell_controller_5_p9, cell_controller_5_p10, cell_controller_5_p11, cell_controller_5_p12, cell_controller_5_p13, cell_controller_5_p14, cell_controller_5_p15, cell_controller_5_p16, cell_controller_5_p17, cell_controller_5_p18, cell_controller_5_p19, cell_controller_5_p20, cell_controller_5_p21, cell_controller_5_p22, cell_controller_5_p23, cell_controller_5_p24, cell_controller_5_p25, cell_controller_5_p26, cell_controller_5_p27, cell_controller_5_p28, cell_controller_5_p29, cell_controller_5_p30, cell_controller_5_p31, cell_controller_5_p32, cell_controller_5_p33, cell_controller_5_p34, cell_controller_5_p35, cell_controller_5_p36, cell_controller_5_p37
  DotMatrix #(.matrixcols(11), .matrixrows(5)) dotmatrix_16 (
    .col0(cell_controller_5_p5), .col1(cell_controller_5_p8), .col2(cell_controller_5_p11),
    .col3(cell_controller_5_p14), .col4(cell_controller_5_p17), .col5(cell_controller_5_p20),
    .col6(cell_controller_5_p23), .col7(cell_controller_5_p26), .col8(cell_controller_5_p29),
    .col9(cell_controller_5_p32), .col10(cell_controller_5_p35));
  DotMatrix #(.matrixcols(11), .matrixrows(8)) dotmatrix_17 (
    .col0(cell_controller_5_p6), .col1(cell_controller_5_p9), .col2(cell_controller_5_p12),
    .col3(cell_controller_5_p15), .col4(cell_controller_5_p18), .col5(cell_controller_5_p21),
    .col6(cell_controller_5_p24), .col7(cell_controller_5_p27), .col8(cell_controller_5_p30),
    .col9(cell_controller_5_p33), .col10(cell_controller_5_p36));
  DotMatrix #(.matrixcols(11), .matrixrows(8)) dotmatrix_18 (
    .col0(cell_controller_5_p7), .col1(cell_controller_5_p10), .col2(cell_controller_5_p13),
    .col3(cell_controller_5_p16), .col4(cell_controller_5_p19), .col5(cell_controller_5_p22),
    .col6(cell_controller_5_p25), .col7(cell_controller_5_p28), .col8(cell_controller_5_p31),
    .col9(cell_controller_5_p34), .col10(cell_controller_5_p37));
  DotMatrix #(.matrixcols(11), .matrixrows(5)) dotmatrix_19 (
    .col0(cell_controller_6_p5), .col1(cell_controller_6_p8), .col2(cell_controller_6_p11),
    .col3(cell_controller_6_p14), .col4(cell_controller_6_p17), .col5(cell_controller_6_p20),
    .col6(cell_controller_6_p23), .col7(cell_controller_6_p26), .col8(cell_controller_6_p29),
    .col9(cell_controller_6_p32), .col10(cell_controller_6_p35));
  // Cell_controller cell_controller_6: pin names not known; wires that end beside it: Columns[5], Rows[0], MOSI, MISO, cell_controller_6_p5, cell_controller_6_p6, cell_controller_6_p7, cell_controller_6_p8, cell_controller_6_p9, cell_controller_6_p10, cell_controller_6_p11, cell_controller_6_p12, cell_controller_6_p13, cell_controller_6_p14, cell_controller_6_p15, cell_controller_6_p16, cell_controller_6_p17, cell_controller_6_p18, cell_controller_6_p19, cell_controller_6_p20, cell_controller_6_p21, cell_controller_6_p22, cell_controller_6_p23, cell_controller_6_p24, cell_controller_6_p25, cell_controller_6_p26, cell_controller_6_p27, cell_controller_6_p28, cell_controller_6_p29, cell_controller_6_p30, cell_controller_6_p31, cell_controller_6_p32, cell_controller_6_p33, cell_controller_6_p34, cell_controller_6_p35, cell_controller_6_p36, cell_controller_6_p37
  DotMatrix #(.matrixcols(11), .matrixrows(8)) dotmatrix_20 (
    .col0(cell_controller_6_p6), .col1(cell_controller_6_p9), .col2(cell_controller_6_p12),
    .col3(cell_controller_6_p15), .col4(cell_controller_6_p18), .col5(cell_controller_6_p21),
    .col6(cell_controller_6_p24), .col7(cell_controller_6_p27), .col8(cell_controller_6_p30),
    .col9(cell_controller_6_p33), .col10(cell_controller_6_p36));
  DotMatrix #(.matrixcols(11), .matrixrows(8)) dotmatrix_21 (
    .col0(cell_controller_6_p7), .col1(cell_controller_6_p10), .col2(cell_controller_6_p13),
    .col3(cell_controller_6_p16), .col4(cell_controller_6_p19), .col5(cell_controller_6_p22),
    .col6(cell_controller_6_p25), .col7(cell_controller_6_p28), .col8(cell_controller_6_p31),
    .col9(cell_controller_6_p34), .col10(cell_controller_6_p37));
  // Cell_controller cell_controller_7: pin names not known; wires that end beside it: Columns[6], Rows[0], MOSI, MISO, cell_controller_7_p5, cell_controller_7_p6, cell_controller_7_p7, cell_controller_7_p8, cell_controller_7_p9, cell_controller_7_p10, cell_controller_7_p11, cell_controller_7_p12, cell_controller_7_p13, cell_controller_7_p14, cell_controller_7_p15, cell_controller_7_p16, cell_controller_7_p17, cell_controller_7_p18, cell_controller_7_p19, cell_controller_7_p20, cell_controller_7_p21, cell_controller_7_p22, cell_controller_7_p23, cell_controller_7_p24, cell_controller_7_p25, cell_controller_7_p26, cell_controller_7_p27, cell_controller_7_p28, cell_controller_7_p29, cell_controller_7_p30, cell_controller_7_p31, cell_controller_7_p32, cell_controller_7_p33, cell_controller_7_p34, cell_controller_7_p35, cell_controller_7_p36, cell_controller_7_p37
  DotMatrix #(.matrixcols(11), .matrixrows(5)) dotmatrix_22 (
    .col0(cell_controller_7_p5), .col1(cell_controller_7_p8), .col2(cell_controller_7_p11),
    .col3(cell_controller_7_p14), .col4(cell_controller_7_p17), .col5(cell_controller_7_p20),
    .col6(cell_controller_7_p23), .col7(cell_controller_7_p26), .col8(cell_controller_7_p29),
    .col9(cell_controller_7_p32), .col10(cell_controller_7_p35));
  DotMatrix #(.matrixcols(11), .matrixrows(8)) dotmatrix_23 (
    .col0(cell_controller_7_p6), .col1(cell_controller_7_p9), .col2(cell_controller_7_p12),
    .col3(cell_controller_7_p15), .col4(cell_controller_7_p18), .col5(cell_controller_7_p21),
    .col6(cell_controller_7_p24), .col7(cell_controller_7_p27), .col8(cell_controller_7_p30),
    .col9(cell_controller_7_p33), .col10(cell_controller_7_p36));
  DotMatrix #(.matrixcols(11), .matrixrows(8)) dotmatrix_24 (
    .col0(cell_controller_7_p7), .col1(cell_controller_7_p10), .col2(cell_controller_7_p13),
    .col3(cell_controller_7_p16), .col4(cell_controller_7_p19), .col5(cell_controller_7_p22),
    .col6(cell_controller_7_p25), .col7(cell_controller_7_p28), .col8(cell_controller_7_p31),
    .col9(cell_controller_7_p34), .col10(cell_controller_7_p37));
  // Cell_controller cell_controller_8: pin names not known; wires that end beside it: Columns[7], Rows[0], MOSI, MISO, cell_controller_8_p5, cell_controller_8_p6, cell_controller_8_p7, cell_controller_8_p8, cell_controller_8_p9, cell_controller_8_p10, cell_controller_8_p11, cell_controller_8_p12, cell_controller_8_p13, cell_controller_8_p14, cell_controller_8_p15, cell_controller_8_p16, cell_controller_8_p17, cell_controller_8_p18, cell_controller_8_p19, cell_controller_8_p20, cell_controller_8_p21, cell_controller_8_p22, cell_controller_8_p23, cell_controller_8_p24, cell_controller_8_p25, cell_controller_8_p26, cell_controller_8_p27, cell_controller_8_p28, cell_controller_8_p29, cell_controller_8_p30, cell_controller_8_p31, cell_controller_8_p32, cell_controller_8_p33, cell_controller_8_p34, cell_controller_8_p35, cell_controller_8_p36, cell_controller_8_p37
  DotMatrix #(.matrixcols(11), .matrixrows(5)) dotmatrix_25 (
    .col0(cell_controller_8_p5), .col1(cell_controller_8_p8), .col2(cell_controller_8_p11),
    .col3(cell_controller_8_p14), .col4(cell_controller_8_p17), .col5(cell_controller_8_p20),
    .col6(cell_controller_8_p23), .col7(cell_controller_8_p26), .col8(cell_controller_8_p29),
    .col9(cell_controller_8_p32), .col10(cell_controller_8_p35));
  DotMatrix #(.matrixcols(11), .matrixrows(8)) dotmatrix_26 (
    .col0(cell_controller_8_p6), .col1(cell_controller_8_p9), .col2(cell_controller_8_p12),
    .col3(cell_controller_8_p15), .col4(cell_controller_8_p18), .col5(cell_controller_8_p21),
    .col6(cell_controller_8_p24), .col7(cell_controller_8_p27), .col8(cell_controller_8_p30),
    .col9(cell_controller_8_p33), .col10(cell_controller_8_p36));
  DotMatrix #(.matrixcols(11), .matrixrows(8)) dotmatrix_27 (
    .col0(cell_controller_8_p7), .col1(cell_controller_8_p10), .col2(cell_controller_8_p13),
    .col3(cell_controller_8_p16), .col4(cell_controller_8_p19), .col5(cell_controller_8_p22),
    .col6(cell_controller_8_p25), .col7(cell_controller_8_p28), .col8(cell_controller_8_p31),
    .col9(cell_controller_8_p34), .col10(cell_controller_8_p37));
endmodule
