// Logisim project o_math_i_math.circ as structural Verilog: 7 circuits, main circuit O_math
module local_test (
);

  O_math o_math_1 ();  // open: Energy, C_reg, Cancel_transfer, mv_energy, Energy_2, C_reg_2, err
  I_math i_math_1 ();  // open: Energy, player_select, type_select, Dl_3, Dl_4, Dl_2, Dl_1, Energy_2, player_select_2, err, inc_en
endmodule

module O_math (
  input  [9:0] Energy,
  input  [9:0] C_reg,
  input  Cancel_transfer,
  input  [10:0] mv_energy,
  output [9:0] Energy_2,
  output [9:0] C_reg_2,
  output err
);

  wire comparator_1_eq, comparator_1_gt, comparator_2_lt, comparator_3_gt, comparator_4_lt, comparator_5_lt,
       not_1_out, not_2_out, or_1_out, pull_resistor_5_node;
  wire [9:0] adder_3_out, adder_4_out, multiplexer_2_out, multiplexer_3_out, multiplexer_4_out,
       multiplexer_5_out, multiplexer_6_out, multiplexer_7_out, multiplexer_8_out, subtractor_5_out,
       subtractor_6_out;
  wire [10:0] adder_1_out, adder_2_out, multiplexer_1_out, subtractor_1_out, subtractor_2_out,
       subtractor_3_out, subtractor_4_out;
  wire [10:10] adder_3_out_2, adder_4_out_2, subtractor_5_out_2, subtractor_6_out_2;

  Pull_Resistor pull_resistor_1 (.node(Energy));
  Pull_Resistor pull_resistor_2 (.node(C_reg));
  Pull_Resistor pull_resistor_3 (.node(Cancel_transfer));
  // Probe on adder_1_out
  Pull_Resistor pull_resistor_4 (.node(mv_energy));
  // Probe on mv_energy
  // Probe on {1'b0, C_reg}
  // Probe on {1'b0, C_reg}
  // Probe on {1'b0, Energy}
  Subtractor #(.width(11)) subtractor_1 (.a({1'b0, C_reg}), .b(mv_energy), .out(subtractor_1_out));  // open: bin, bout
  Adder #(.width(11)) adder_1 (.a({1'b0, Energy}), .b({1'b0, C_reg}), .out(adder_1_out));  // open: cin, cout
  Subtractor #(.width(11)) subtractor_2 (.a({1'b0, Energy}), .b(mv_energy), .out(subtractor_2_out));  // open: bin, bout
  // Probe on subtractor_2_out
  Comparator #(.width(11)) comparator_1 (
    .a({1'b0, Energy}), .b(mv_energy), .gt(comparator_1_gt), .eq(comparator_1_eq));  // open: lt
  Comparator #(.width(11)) comparator_2 (.a(mv_energy), .b(11'h3e7), .lt(comparator_2_lt));  // open: gt, eq
  // Probe on subtractor_1_out
  Comparator #(.width(11), .mode("unsigned")) comparator_3 (
    .a(adder_1_out), .b(11'h3e7), .gt(comparator_3_gt));  // open: eq, lt
  or or_1 (or_1_out, comparator_1_gt, comparator_1_eq);
  Comparator #(.width(11)) comparator_4 (.a(mv_energy), .b(11'h419), .lt(comparator_4_lt));  // open: gt, eq
  Adder #(.width(11)) adder_2 (.a(mv_energy), .b({1'b0, C_reg}), .out(adder_2_out));  // open: cin, cout
  // Probe on {1'b0, Energy}
  Multiplexer #(.width(11), .enable("false")) multiplexer_1 (
    .in0(adder_1_out), .in1(11'h3e7), .out(multiplexer_1_out), .sel(comparator_3_gt));
  Subtractor #(.width(11)) subtractor_3 (
    .a({1'b0, Energy}), .b(subtractor_2_out), .out(subtractor_3_out));  // open: bin, bout
  // Probe on adder_2_out
  Subtractor #(.width(11)) subtractor_4 (
    .a({1'b0, C_reg}), .b(subtractor_1_out), .out(subtractor_4_out));  // open: bin, bout
  // Probe on subtractor_4_out
  // Probe on subtractor_3_out
  Subtractor #(.width(11)) subtractor_5 (
    .a({1'b0, Energy}), .b(subtractor_3_out), .out({subtractor_5_out_2[10], subtractor_5_out}));  // open: bin, bout
  Adder #(.width(11)) adder_3 (
    .a({1'b0, C_reg}), .b(subtractor_3_out), .out({adder_3_out_2[10], adder_3_out}));  // open: cin, cout
  // Probe on {adder_3_out_2[10], adder_3_out}
  not not_1 (not_1_out, or_1_out);
  Pull_Resistor pull_resistor_5 (.node(pull_resistor_5_node));
  Transistor #(.\type ("n")) transistor_1 (.in(adder_2_out[10]), .out(pull_resistor_5_node), .gate(mv_energy[10]));
  Adder #(.width(11)) adder_4 (
    .a({1'b0, C_reg}), .b(subtractor_4_out), .out({adder_4_out_2[10], adder_4_out}));  // open: cin, cout
  Subtractor #(.width(11)) subtractor_6 (
    .a({1'b0, Energy}), .b(subtractor_4_out), .out({subtractor_6_out_2[10], subtractor_6_out}));  // open: bin, bout
  // Probe on {subtractor_6_out_2[10], subtractor_6_out}
  not not_2 (not_2_out, comparator_2_lt);
  // Probe on adder_4_out
  or or_2 (err, not_1_out, comparator_4_lt, pull_resistor_5_node, not_2_out);
  Multiplexer #(.width(10), .enable("false")) multiplexer_2 (
    .in0(adder_3_out), .in1(10'h3e7), .out(multiplexer_2_out), .sel(adder_3_out_2[10]));
  Multiplexer #(.width(10), .enable("false")) multiplexer_3 (
    .in0(adder_4_out), .in1(10'h3e7), .out(multiplexer_3_out), .sel(adder_4_out_2[10]));
  Comparator #(.width(11), .mode("unsigned")) comparator_5 (
    .a({subtractor_6_out_2[10], subtractor_6_out}), .b(11'h3e7), .lt(comparator_5_lt));  // open: gt, eq
  // Probe on multiplexer_4_out
  Multiplexer #(.width(10), .enable("false")) multiplexer_4 (
    .in0(10'h3e7), .in1(subtractor_6_out), .out(multiplexer_4_out), .sel(comparator_5_lt));
  // Probe on multiplexer_2_out
  Multiplexer #(.width(10), .enable("false")) multiplexer_5 (
    .in0(subtractor_5_out), .in1(multiplexer_4_out), .out(multiplexer_5_out), .sel(mv_energy[10]));
  Multiplexer #(.width(10), .enable("false")) multiplexer_6 (
    .in0(multiplexer_2_out), .in1(multiplexer_3_out), .out(multiplexer_6_out), .sel(mv_energy[10]));
  Multiplexer #(.width(10), .enable("false")) multiplexer_7 (
    .in0(multiplexer_5_out), .in1(Energy), .out(multiplexer_7_out), .sel(err));
  // Probe on multiplexer_6_out
  Multiplexer #(.width(10), .enable("false")) multiplexer_8 (
    .in0(multiplexer_6_out), .in1(C_reg), .out(multiplexer_8_out), .sel(err));
  Multiplexer #(.width(10), .enable("false")) multiplexer_9 (
    .in0(multiplexer_8_out), .in1({10{1'b0}}), .out(C_reg_2), .sel(Cancel_transfer));
  Multiplexer #(.width(10), .enable("false")) multiplexer_10 (
    .in0(multiplexer_7_out), .in1(multiplexer_1_out[9:0]), .out(Energy_2), .sel(Cancel_transfer));
  // Probe on C_reg_2
  // Probe on Energy_2
endmodule

module I_math (
  input  [9:0] Energy,
  input  [1:0] player_select,
  input  [3:0] type_select,
  input  inc_en,
  input  [11:0] Dl_3,
  input  [11:0] Dl_4,
  input  [11:0] Dl_2,
  input  [11:0] Dl_1,
  output [9:0] Energy_2,
  output [1:0] player_select_2,
  output err
);

  wire comparator_1_lt, comparator_2_lt, comparator_3_eq, not_1_out, subtractor_2_bout;
  wire [1:0] sum_1_player_select, sum_2_player_select, sum_3_player_select;
  wire [9:0] adder_1_out, adder_2_out, adder_3_out, increment_1_out_2, multiplexer_1_out, multiplexer_2_out,
       multiplexer_3_out, multiplexer_4_out, subtractor_1_out, sum2_1_energy_2, sum_1_energy, sum_2_energy,
       sum_3_energy, type_math_1_defence, type_math_1_energy_2;

  Adder #(.width(10)) adder_1 (.a(Energy), .b(type_math_1_defence), .out(adder_1_out));  // open: cin, cout
  increment increment_1 (.in_1(type_select), .out_2(increment_1_out_2));
  // Probe on increment_1_out_2
  // Probe on sum_1_energy
  Pull_Resistor pull_resistor_1 (.node(Dl_4));
  sum sum_1 (.Energy_1(Dl_4), .Energy_2(Dl_2), .Energy(sum_1_energy), .player_select(sum_1_player_select));
  Pull_Resistor pull_resistor_2 (.node(Dl_2));
  type_math type_math_1 (
    .Energy(Energy), .in_2(type_select), .Energy_2(type_math_1_energy_2), .Defence(type_math_1_defence));
  Adder #(.width(10)) adder_2 (
    .a(type_math_1_energy_2), .b(type_math_1_defence), .out(adder_2_out));  // open: cin, cout
  // Probe on type_math_1_defence
  Subtractor #(.width(10)) subtractor_1 (
    .a(sum2_1_energy_2), .b(type_math_1_defence), .out(subtractor_1_out));  // open: bin, bout
  // Probe on adder_2_out
  Comparator #(.width(10), .mode("unsigned")) comparator_1 (
    .a(sum2_1_energy_2), .b(adder_1_out), .lt(comparator_1_lt));  // open: gt, eq
  Comparator #(.width(10), .mode("unsigned")) comparator_2 (
    .a(sum2_1_energy_2), .b(type_math_1_defence), .lt(comparator_2_lt));  // open: gt, eq
  sum sum_2 (
    .Energy_1({sum_1_player_select, sum_1_energy}), .Energy_2(Dl_1), .Energy(sum_2_energy),
    .player_select(sum_2_player_select));
  Pull_Resistor pull_resistor_3 (.node(Dl_1));
  Multiplexer #(.width(10), .enable("false")) multiplexer_1 (
    .in0(subtractor_1_out), .in1(sum2_1_energy_2), .out(multiplexer_1_out), .sel(comparator_2_lt));
  // Probe on sum_2_energy
  // Probe on multiplexer_1_out
  // Probe on sum2_1_energy_2
  Subtractor #(.width(10)) subtractor_2 (.a(sum2_1_energy_2), .b(Energy), .bout(subtractor_2_bout));  // open: out, bin
  sum2 sum2_1 (
    .Energy_cell(adder_2_out), .Player_select(player_select), .Energy(sum_3_energy),
    .player_select2(sum_3_player_select), .Energy_2(sum2_1_energy_2), .player_select_2(player_select_2));
  Multiplexer #(.width(10), .enable("false")) multiplexer_2 (
    .in0(Energy), .in1(sum2_1_energy_2), .out(multiplexer_2_out), .sel(subtractor_2_bout));
  Comparator #(.width(2), .mode("unsigned")) comparator_3 (
    .a(player_select_2), .b(2'b00), .eq(comparator_3_eq));  // open: gt, lt
  Pull_Resistor pull_resistor_4 (.node(Dl_3));
  Multiplexer #(.width(10), .enable("false")) multiplexer_3 (
    .in0(multiplexer_1_out), .in1(multiplexer_2_out), .out(multiplexer_3_out), .sel(comparator_1_lt));
  sum sum_3 (
    .Energy_1({sum_2_player_select, sum_2_energy}), .Energy_2(Dl_3), .Energy(sum_3_energy),
    .player_select(sum_3_player_select));
  // Probe on Dl_3
  // Probe on multiplexer_2_out
  not not_1 (not_1_out, inc_en);
  // Probe on sum_3_energy
  Adder #(.width(10)) adder_3 (.a(multiplexer_3_out), .b(increment_1_out_2), .out(adder_3_out));  // open: cin, cout
  Multiplexer #(.width(10), .enable("false")) multiplexer_4 (
    .in0(adder_3_out), .in1(multiplexer_3_out), .out(multiplexer_4_out), .sel(not_1_out));
  // Probe on multiplexer_4_out
  Multiplexer #(.width(10), .enable("false")) multiplexer_5 (
    .in0(multiplexer_4_out), .in1(multiplexer_3_out), .out(Energy_2), .sel(comparator_3_eq));
  // Probe on Energy_2

  assign err = 1'b0;
endmodule

module sum (
  input  [11:0] Energy_1,
  input  [11:0] Energy_2,
  output [9:0] Energy,
  output [1:0] player_select
);

  wire and_1_out, comparator_1_eq, comparator_1_lt, comparator_2_eq;
  wire [1:0] multiplexer_3_out;
  wire [9:0] adder_1_out, adder_2_out, multiplexer_1_out, not_1_out, subtractor_1_out;

  // Probe on Energy_2[9:0]
  // Probe on Energy_1[9:0]
  // Probe on Energy_2[11:10]
  // Probe on Energy_1[11:10]
  Adder #(.width(10)) adder_1 (.a(Energy_1[9:0]), .b(Energy_2[9:0]), .out(adder_1_out));  // open: cin, cout
  Comparator #(.width(10), .mode("unsigned")) comparator_1 (
    .a(Energy_1[9:0]), .b(Energy_2[9:0]), .eq(comparator_1_eq), .lt(comparator_1_lt));  // open: gt
  Subtractor #(.width(10)) subtractor_1 (
    .a(Energy_1[9:0]), .b(Energy_2[9:0]), .out(subtractor_1_out));  // open: bin, bout
  Comparator #(.width(2), .mode("unsigned")) comparator_2 (
    .a(Energy_1[11:10]), .b(Energy_2[11:10]), .eq(comparator_2_eq));  // open: gt, lt
  Multiplexer #(.width(10), .enable("false")) multiplexer_1 (
    .in0(subtractor_1_out), .in1(adder_1_out), .out(multiplexer_1_out), .sel(comparator_2_eq));
  assign not_1_out = ~multiplexer_1_out;  // NOT_Gate not_1, 10 bits wide
  Adder #(.width(10)) adder_2 (.a(not_1_out), .b(10'h1), .out(adder_2_out));  // open: cin, cout
  and and_1 (and_1_out, comparator_2_eq, comparator_1_eq);
  Multiplexer #(.width(10), .enable("false")) multiplexer_2 (
    .in0(multiplexer_1_out), .in1(adder_2_out), .out(Energy), .sel(multiplexer_1_out[9]));
  // Probe on Energy
  Multiplexer #(.width(2), .enable("false")) multiplexer_3 (
    .in0(Energy_1[11:10]), .in1(Energy_2[11:10]), .out(multiplexer_3_out), .sel(comparator_1_lt));
  Multiplexer #(.width(2), .enable("false")) multiplexer_4 (
    .in0(multiplexer_3_out), .in1(2'b00), .out(player_select), .sel(and_1_out));
endmodule

module type_math (
  input  [9:0] Energy,
  input  [3:0] in_2,
  output [9:0] Energy_2,
  output [9:0] Defence
);

  wire comparator_1_eq, comparator_2_eq, comparator_3_eq, comparator_4_eq;
  wire [9:0] multiplexer_1_out, multiplexer_2_out, multiplexer_3_out;

  Comparator #(.width(2), .mode("unsigned")) comparator_1 (
    .a(2'b00), .b(in_2[1:0]), .eq(comparator_1_eq));  // open: gt, lt
  Comparator #(.width(2), .mode("unsigned")) comparator_2 (
    .a(in_2[1:0]), .b(2'b01), .eq(comparator_2_eq));  // open: gt, lt
  Comparator #(.width(2), .mode("unsigned")) comparator_3 (
    .a(in_2[1:0]), .b(2'b10), .eq(comparator_3_eq));  // open: gt, lt
  Comparator #(.width(2), .mode("unsigned")) comparator_4 (
    .a(in_2[1:0]), .b(2'b11), .eq(comparator_4_eq));  // open: gt, lt
  Multiplexer #(.width(10), .enable("false")) multiplexer_1 (
    .in0({10{1'b0}}), .in1(10'h7), .out(multiplexer_1_out), .sel(comparator_1_eq));
  Multiplexer #(.width(10), .enable("false")) multiplexer_2 (
    .in0(multiplexer_1_out), .in1({10{1'b0}}), .out(multiplexer_2_out), .sel(comparator_2_eq));
  Multiplexer #(.width(10), .enable("false")) multiplexer_3 (
    .in0(multiplexer_2_out), .in1(10'he), .out(multiplexer_3_out), .sel(comparator_3_eq));
  Multiplexer #(.width(10), .enable("false")) multiplexer_4 (
    .in0(multiplexer_3_out), .in1({10{1'b0}}), .out(Defence), .sel(comparator_4_eq));
  // Probe on Energy
  // Probe on Defence

  assign Energy_2 = Energy;
endmodule

module sum2 (
  input  [9:0] Energy_cell,
  input  [1:0] Player_select,
  input  [9:0] Energy,
  input  [1:0] player_select2,
  output [9:0] Energy_2,
  output [1:0] player_select_2
);

  wire and_1_out, comparator_1_eq, comparator_2_eq;
  wire [1:0] sum_1_player_select;

  sum sum_1 (
    .Energy_1({Player_select, Energy_cell}), .Energy_2({player_select2, Energy}), .Energy(Energy_2),
    .player_select(sum_1_player_select));
  Comparator #(.width(2), .mode("unsigned")) comparator_1 (
    .a(Player_select), .b(2'b00), .eq(comparator_1_eq));  // open: gt, lt
  // Probe on sum_1_player_select
  Comparator #(.width(10), .mode("unsigned")) comparator_2 (
    .a(Energy_2), .b({10{1'b0}}), .eq(comparator_2_eq));  // open: gt, lt
  and and_1 (and_1_out, comparator_1_eq, comparator_2_eq);
  Multiplexer #(.width(2), .enable("false")) multiplexer_1 (
    .in0(sum_1_player_select), .in1(player_select2), .out(player_select_2), .sel(and_1_out));
endmodule

module increment (
  input  [3:0] in_1,
  output [9:0] out_2
);

  wire comparator_1_eq, comparator_2_eq, comparator_3_eq, comparator_4_eq;
  wire [9:0] multiplexer_1_out, multiplexer_2_out, multiplexer_3_out;

  Multiplexer #(.width(10), .enable("false")) multiplexer_1 (
    .in0({10{1'b0}}), .in1(10'h2), .out(multiplexer_1_out), .sel(comparator_1_eq));
  Comparator #(.width(2), .mode("unsigned")) comparator_1 (
    .a(in_1[1:0]), .b(2'b00), .eq(comparator_1_eq));  // open: gt, lt
  Comparator #(.width(2), .mode("unsigned")) comparator_2 (
    .a(in_1[1:0]), .b(2'b01), .eq(comparator_2_eq));  // open: gt, lt
  Comparator #(.width(2), .mode("unsigned")) comparator_3 (
    .a(in_1[1:0]), .b(2'b10), .eq(comparator_3_eq));  // open: gt, lt
  Comparator #(.width(2), .mode("unsigned")) comparator_4 (
    .a(in_1[1:0]), .b(2'b11), .eq(comparator_4_eq));  // open: gt, lt
  Multiplexer #(.width(10), .enable("false")) multiplexer_2 (
    .in0(multiplexer_1_out), .in1({10{1'b0}}), .out(multiplexer_2_out), .sel(comparator_2_eq));
  Multiplexer #(.width(10), .enable("false")) multiplexer_3 (
    .in0(multiplexer_2_out), .in1(10'h1), .out(multiplexer_3_out), .sel(comparator_3_eq));
  Multiplexer #(.width(10), .enable("false")) multiplexer_4 (
    .in0(multiplexer_3_out), .in1(10'h4), .out(out_2), .sel(comparator_4_eq));
  // Probe on out_2
endmodule
