// Logisim project people_controller.circ as structural Verilog
module local_test (
  input  [4:0] in_1,
  input  [10:0] in_2,
  input  [7:0] in_3,
  input  in_4,
  input  in_5,
  input  in_6,
  input  in_7,
  output out_8
);

  wire clock_1_out, spi_module_master_1_clk, spi_module_master_1_communication_end,
       spi_module_master_1_input_transanction_end, spi_module_master_1_mosi,
       spi_module_master_1_output_transanction_end;
  wire [1:0] fasa_1_people;
  wire [4:0] generator_1_out_5, generator_1_out_6, generator_1_out_7, generator_1_out_8, generator_1_out_9,
       generator_1_out_10, generator_1_out_11, generator_1_out_12, generator_1_out_13, generator_1_out_14,
       generator_1_out_15, generator_1_out_16, generator_1_out_17, generator_1_out_18, generator_1_out_19,
       generator_1_out_20, generator_1_out_21, generator_1_out_22, generator_1_out_23, generator_1_out_24,
       generator_1_out_25, generator_1_out_26, generator_1_out_27, generator_1_out_28, generator_1_out_29,
       generator_1_out_30, generator_1_out_31, generator_1_out_32, generator_1_out_33, generator_1_out_34,
       generator_1_out_35, generator_1_out_36, generator_1_out_37, generator_1_out_38, generator_1_out_39,
       generator_1_out_58, generator_1_out_59, generator_1_out_60, generator_1_out_61, generator_1_out_62,
       generator_1_out_63, generator_1_out_64, generator_1_out_65, generator_1_out_66, generator_1_out_67,
       generator_1_out_68, generator_1_out_69, generator_1_out_70, generator_1_out_71, generator_1_out_72,
       generator_1_out_73, generator_1_out_74, generator_1_out_75, generator_1_out_76, generator_1_out_77,
       generator_1_out_78, generator_1_out_79, generator_1_out_80, generator_1_out_81, generator_1_out_82,
       generator_1_out_83, generator_1_out_84, generator_1_out_85, generator_1_out_86, generator_1_out_87,
       generator_1_out_88, generator_1_out_89, generator_1_out_90, generator_1_out_91, generator_1_out_92,
       generator_1_out_94, generator_1_out_95, generator_1_out_96, generator_1_out_97, generator_1_out_98,
       generator_1_out_99, generator_1_out_100, generator_1_out_101, generator_1_out_102,
       generator_1_out_103, generator_1_out_104, generator_1_out_105, generator_1_out_106,
       generator_1_out_107, generator_1_out_108, generator_1_out_109, generator_1_out_110,
       generator_1_out_111, generator_1_out_112, generator_1_out_113, generator_1_out_114,
       generator_1_out_115, generator_1_out_116, generator_1_out_117, generator_1_out_118,
       generator_1_out_119, generator_1_out_120, generator_1_out_121, generator_1_out_122,
       generator_1_out_123, generator_1_out_124, generator_1_out_125, generator_1_out_126,
       generator_1_out_127, generator_1_out_128, generator_1_out_129, generator_1_out_130,
       generator_1_out_131, generator_1_out_132, generator_1_out_133, generator_1_out_134,
       generator_1_out_135, generator_1_out_136, generator_1_out_137;
  wire [14:0] fasa_1_out_4, fasa_1_out_5, fasa_1_out_6, fasa_1_out_7, fasa_1_out_8, fasa_1_out_9,
       fasa_1_out_10, fasa_1_out_11, fasa_1_out_12, fasa_1_out_13, fasa_1_out_14, fasa_1_out_15,
       fasa_1_out_16, fasa_1_out_17, fasa_1_out_18, fasa_1_out_19, fasa_1_out_20, fasa_1_out_21,
       fasa_1_out_22, fasa_1_out_23, fasa_1_out_24, fasa_1_out_25, fasa_1_out_26, fasa_1_out_27,
       fasa_1_out_28, fasa_1_out_29, fasa_1_out_30, fasa_1_out_31, fasa_1_out_32, fasa_1_out_33,
       generator_1_out_40, generator_1_out_41, generator_1_out_42, generator_1_out_43, generator_1_out_44,
       generator_1_out_45, generator_1_out_46, generator_1_out_47, generator_1_out_48, generator_1_out_49,
       generator_1_out_50, generator_1_out_51, generator_1_out_52, generator_1_out_53, generator_1_out_54,
       generator_1_out_55, generator_1_out_56, generator_1_out_57;

  generator generator_1 (
    .out_40(generator_1_out_40), .out_42(generator_1_out_42), .out_44(generator_1_out_44),
    .out_46(generator_1_out_46), .out_48(generator_1_out_48), .out_50(generator_1_out_50),
    .out_52(generator_1_out_52), .out_54(generator_1_out_54), .out_56(generator_1_out_56), .in_3(in_6),
    .in_4(in_7), .Who(fasa_1_people), .out_41(generator_1_out_41), .out_43(generator_1_out_43),
    .out_45(generator_1_out_45), .out_47(generator_1_out_47), .out_49(generator_1_out_49),
    .out_51(generator_1_out_51), .out_53(generator_1_out_53), .out_55(generator_1_out_55),
    .out_57(generator_1_out_57), .out_35(generator_1_out_35), .out_30(generator_1_out_30),
    .out_25(generator_1_out_25), .out_10(generator_1_out_10), .out_15(generator_1_out_15),
    .out_20(generator_1_out_20), .out_5(generator_1_out_5), .out_6(generator_1_out_6),
    .out_11(generator_1_out_11), .out_16(generator_1_out_16), .out_21(generator_1_out_21),
    .out_26(generator_1_out_26), .out_31(generator_1_out_31), .out_36(generator_1_out_36),
    .out_7(generator_1_out_7), .out_12(generator_1_out_12), .out_17(generator_1_out_17),
    .out_22(generator_1_out_22), .out_27(generator_1_out_27), .out_32(generator_1_out_32),
    .out_37(generator_1_out_37), .out_8(generator_1_out_8), .out_13(generator_1_out_13),
    .out_18(generator_1_out_18), .out_23(generator_1_out_23), .out_28(generator_1_out_28),
    .out_33(generator_1_out_33), .out_38(generator_1_out_38), .out_9(generator_1_out_9),
    .out_14(generator_1_out_14), .out_19(generator_1_out_19), .out_24(generator_1_out_24),
    .out_29(generator_1_out_29), .out_34(generator_1_out_34), .out_39(generator_1_out_39),
    .out_58(generator_1_out_58), .out_63(generator_1_out_63), .out_68(generator_1_out_68),
    .out_73(generator_1_out_73), .out_78(generator_1_out_78), .out_83(generator_1_out_83),
    .out_88(generator_1_out_88), .out_59(generator_1_out_59), .out_64(generator_1_out_64),
    .out_69(generator_1_out_69), .out_74(generator_1_out_74), .out_79(generator_1_out_79),
    .out_84(generator_1_out_84), .out_89(generator_1_out_89), .out_60(generator_1_out_60),
    .out_65(generator_1_out_65), .out_70(generator_1_out_70), .out_75(generator_1_out_75),
    .out_80(generator_1_out_80), .out_85(generator_1_out_85), .out_90(generator_1_out_90),
    .out_61(generator_1_out_61), .out_66(generator_1_out_66), .out_71(generator_1_out_71),
    .out_76(generator_1_out_76), .out_81(generator_1_out_81), .out_86(generator_1_out_86),
    .out_91(generator_1_out_91), .out_62(generator_1_out_62), .out_67(generator_1_out_67),
    .out_72(generator_1_out_72), .out_77(generator_1_out_77), .out_82(generator_1_out_82),
    .out_87(generator_1_out_87), .out_92(generator_1_out_92), .out_94(generator_1_out_94),
    .out_95(generator_1_out_95), .out_97(generator_1_out_97), .out_99(generator_1_out_99),
    .out_101(generator_1_out_101), .out_103(generator_1_out_103), .out_105(generator_1_out_105),
    .out_107(generator_1_out_107), .out_109(generator_1_out_109), .out_111(generator_1_out_111),
    .out_113(generator_1_out_113), .out_116(generator_1_out_116), .out_118(generator_1_out_118),
    .out_120(generator_1_out_120), .out_122(generator_1_out_122), .out_124(generator_1_out_124),
    .out_126(generator_1_out_126), .out_128(generator_1_out_128), .out_130(generator_1_out_130),
    .out_132(generator_1_out_132), .out_134(generator_1_out_134), .out_136(generator_1_out_136),
    .out_96(generator_1_out_96), .out_98(generator_1_out_98), .out_100(generator_1_out_100),
    .out_102(generator_1_out_102), .out_104(generator_1_out_104), .out_106(generator_1_out_106),
    .out_108(generator_1_out_108), .out_110(generator_1_out_110), .out_112(generator_1_out_112),
    .out_114(generator_1_out_114), .out_115(generator_1_out_115), .out_117(generator_1_out_117),
    .out_119(generator_1_out_119), .out_121(generator_1_out_121), .out_123(generator_1_out_123),
    .out_125(generator_1_out_125), .out_127(generator_1_out_127), .out_129(generator_1_out_129),
    .out_131(generator_1_out_131), .out_133(generator_1_out_133), .out_135(generator_1_out_135),
    .out_137(generator_1_out_137), .CS(in_5), .out_93(out_8));
  Clock clock_1 (.out(clock_1_out));
  LED led_1 (.in(spi_module_master_1_input_transanction_end));
  DotMatrix #(.matrixcols(9), .matrixrows(15)) dotmatrix_1 (
    .col0(generator_1_out_56), .col1(generator_1_out_54), .col2(generator_1_out_52),
    .col3(generator_1_out_50), .col4(generator_1_out_48), .col5(generator_1_out_46),
    .col6(generator_1_out_44), .col7(generator_1_out_42), .col8(generator_1_out_40));
  SPI_module__master spi_module_master_1 (
    .In_clock(clock_1_out), .CLK(spi_module_master_1_clk), .MOSI(spi_module_master_1_mosi),
    .Output_transanction_end(spi_module_master_1_output_transanction_end),
    .Input_transanction_end(spi_module_master_1_input_transanction_end), .Control_command(in_3),
    .Send_command(in_1), .Send_energy(in_2), .Communication_end(spi_module_master_1_communication_end));  // open: MISO, Recv_data
  LED led_2 (.in(spi_module_master_1_output_transanction_end));
  LED led_3 (.in(spi_module_master_1_communication_end));
  DotMatrix #(.matrixcols(9), .matrixrows(15)) dotmatrix_2 (
    .col0(generator_1_out_57), .col1(generator_1_out_55), .col2(generator_1_out_53),
    .col3(generator_1_out_51), .col4(generator_1_out_49), .col5(generator_1_out_47),
    .col6(generator_1_out_45), .col7(generator_1_out_43), .col8(generator_1_out_41));
  DotMatrix #(.matrixcols(11), .matrixrows(5)) dotmatrix_3 (
    .col0(generator_1_out_113), .col1(generator_1_out_111), .col2(generator_1_out_109),
    .col3(generator_1_out_107), .col4(generator_1_out_105), .col5(generator_1_out_103),
    .col6(generator_1_out_101), .col7(generator_1_out_99), .col8(generator_1_out_97),
    .col9(generator_1_out_95), .col10(generator_1_out_94));
  DotMatrix #(.matrixcols(11), .matrixrows(5)) dotmatrix_4 (
    .col0(generator_1_out_115), .col1(generator_1_out_114), .col2(generator_1_out_112),
    .col3(generator_1_out_110), .col4(generator_1_out_108), .col5(generator_1_out_106),
    .col6(generator_1_out_104), .col7(generator_1_out_102), .col8(generator_1_out_100),
    .col9(generator_1_out_98), .col10(generator_1_out_96));
  DotMatrix #(.matrixcols(11), .matrixrows(5)) dotmatrix_5 (
    .col0(generator_1_out_136), .col1(generator_1_out_134), .col2(generator_1_out_132),
    .col3(generator_1_out_130), .col4(generator_1_out_128), .col5(generator_1_out_126),
    .col6(generator_1_out_124), .col7(generator_1_out_122), .col8(generator_1_out_120),
    .col9(generator_1_out_118), .col10(generator_1_out_116));
  DotMatrix #(.matrixcols(11), .matrixrows(5)) dotmatrix_6 (
    .col0(generator_1_out_137), .col1(generator_1_out_135), .col2(generator_1_out_133),
    .col3(generator_1_out_131), .col4(generator_1_out_129), .col5(generator_1_out_127),
    .col6(generator_1_out_125), .col7(generator_1_out_123), .col8(generator_1_out_121),
    .col9(generator_1_out_119), .col10(generator_1_out_117));
  DotMatrix #(.matrixcols(7), .matrixrows(5)) dotmatrix_7 (
    .col0(generator_1_out_35), .col1(generator_1_out_30), .col2(generator_1_out_25),
    .col3(generator_1_out_20), .col4(generator_1_out_15), .col5(generator_1_out_10), .col6(generator_1_out_5));
  DotMatrix #(.matrixcols(7), .matrixrows(5)) dotmatrix_8 (
    .col0(generator_1_out_88), .col1(generator_1_out_83), .col2(generator_1_out_78),
    .col3(generator_1_out_73), .col4(generator_1_out_68), .col5(generator_1_out_63), .col6(generator_1_out_58));
  DotMatrix #(.matrixcols(15), .matrixrows(15)) dotmatrix_9 (
    .col0(fasa_1_out_33), .col1(fasa_1_out_31), .col2(fasa_1_out_29), .col3(fasa_1_out_27),
    .col4(fasa_1_out_25), .col5(fasa_1_out_23), .col6(fasa_1_out_21), .col7(fasa_1_out_19),
    .col8(fasa_1_out_17), .col9(fasa_1_out_15), .col10(fasa_1_out_13), .col11(fasa_1_out_11),
    .col12(fasa_1_out_9), .col13(fasa_1_out_7), .col14(fasa_1_out_5));
  DotMatrix #(.matrixcols(15), .matrixrows(15)) dotmatrix_10 (
    .col0(fasa_1_out_32), .col1(fasa_1_out_30), .col2(fasa_1_out_28), .col3(fasa_1_out_26),
    .col4(fasa_1_out_24), .col5(fasa_1_out_22), .col6(fasa_1_out_20), .col7(fasa_1_out_18),
    .col8(fasa_1_out_16), .col9(fasa_1_out_14), .col10(fasa_1_out_12), .col11(fasa_1_out_10),
    .col12(fasa_1_out_8), .col13(fasa_1_out_6), .col14(fasa_1_out_4));
  DotMatrix #(.matrixcols(7), .matrixrows(5)) dotmatrix_11 (
    .col0(generator_1_out_36), .col1(generator_1_out_31), .col2(generator_1_out_26),
    .col3(generator_1_out_21), .col4(generator_1_out_16), .col5(generator_1_out_11), .col6(generator_1_out_6));
  DotMatrix #(.matrixcols(7), .matrixrows(5)) dotmatrix_12 (
    .col0(generator_1_out_89), .col1(generator_1_out_84), .col2(generator_1_out_79),
    .col3(generator_1_out_74), .col4(generator_1_out_69), .col5(generator_1_out_64), .col6(generator_1_out_59));
  Fasa fasa_1 (
    .out_4(fasa_1_out_4), .out_6(fasa_1_out_6), .out_8(fasa_1_out_8), .out_10(fasa_1_out_10),
    .out_12(fasa_1_out_12), .out_14(fasa_1_out_14), .out_16(fasa_1_out_16), .out_18(fasa_1_out_18),
    .out_20(fasa_1_out_20), .out_22(fasa_1_out_22), .out_24(fasa_1_out_24), .out_26(fasa_1_out_26),
    .CLK(spi_module_master_1_clk), .out_28(fasa_1_out_28), .out_30(fasa_1_out_30),
    .MOSI(spi_module_master_1_mosi), .out_32(fasa_1_out_32), .out_5(fasa_1_out_5), .out_7(fasa_1_out_7),
    .out_9(fasa_1_out_9), .out_11(fasa_1_out_11), .out_13(fasa_1_out_13), .out_15(fasa_1_out_15),
    .out_17(fasa_1_out_17), .out_19(fasa_1_out_19), .out_21(fasa_1_out_21), .out_23(fasa_1_out_23),
    .out_25(fasa_1_out_25), .out_27(fasa_1_out_27), .out_29(fasa_1_out_29), .out_31(fasa_1_out_31),
    .out_33(fasa_1_out_33), .People(fasa_1_people), .CS(in_4));
  DotMatrix #(.matrixcols(7), .matrixrows(5)) dotmatrix_13 (
    .col0(generator_1_out_37), .col1(generator_1_out_32), .col2(generator_1_out_27),
    .col3(generator_1_out_22), .col4(generator_1_out_17), .col5(generator_1_out_12), .col6(generator_1_out_7));
  DotMatrix #(.matrixcols(7), .matrixrows(5)) dotmatrix_14 (
    .col0(generator_1_out_90), .col1(generator_1_out_85), .col2(generator_1_out_80),
    .col3(generator_1_out_75), .col4(generator_1_out_70), .col5(generator_1_out_65), .col6(generator_1_out_60));
  DotMatrix #(.matrixcols(7), .matrixrows(5)) dotmatrix_15 (
    .col0(generator_1_out_38), .col1(generator_1_out_33), .col2(generator_1_out_28),
    .col3(generator_1_out_23), .col4(generator_1_out_18), .col5(generator_1_out_13), .col6(generator_1_out_8));
  DotMatrix #(.matrixcols(7), .matrixrows(5)) dotmatrix_16 (
    .col0(generator_1_out_91), .col1(generator_1_out_86), .col2(generator_1_out_81),
    .col3(generator_1_out_76), .col4(generator_1_out_71), .col5(generator_1_out_66), .col6(generator_1_out_61));
  DotMatrix #(.matrixcols(7), .matrixrows(5)) dotmatrix_17 (
    .col0(generator_1_out_39), .col1(generator_1_out_34), .col2(generator_1_out_29),
    .col3(generator_1_out_24), .col4(generator_1_out_19), .col5(generator_1_out_14), .col6(generator_1_out_9));
  DotMatrix #(.matrixcols(7), .matrixrows(5)) dotmatrix_18 (
    .col0(generator_1_out_92), .col1(generator_1_out_87), .col2(generator_1_out_82),
    .col3(generator_1_out_77), .col4(generator_1_out_72), .col5(generator_1_out_67), .col6(generator_1_out_62));
endmodule

module Fasa (
  input  CS,
  input  CLK,
  input  MOSI,
  output [14:0] out_4,
  output [14:0] out_5,
  output [14:0] out_6,
  output [14:0] out_7,
  output [14:0] out_8,
  output [14:0] out_9,
  output [14:0] out_10,
  output [14:0] out_11,
  output [14:0] out_12,
  output [14:0] out_13,
  output [14:0] out_14,
  output [14:0] out_15,
  output [14:0] out_16,
  output [14:0] out_17,
  output [14:0] out_18,
  output [14:0] out_19,
  output [14:0] out_20,
  output [14:0] out_21,
  output [14:0] out_22,
  output [14:0] out_23,
  output [14:0] out_24,
  output [14:0] out_25,
  output [14:0] out_26,
  output [14:0] out_27,
  output [14:0] out_28,
  output [14:0] out_29,
  output [14:0] out_30,
  output [14:0] out_31,
  output [14:0] out_32,
  output [14:0] out_33,
  output [1:0] People
);

  wire comparator_1_eq, not_1_out;
  wire [3:0] input_shifter_1_buffer_ptr;
  wire [15:0] input_shifter_1_data_out, register_1_q;

  not not_1 (not_1_out, CS);
  input_shifter input_shifter_1 (
    .MOSI(MOSI), .CLK(CLK), .Reset(not_1_out), .Data_out(input_shifter_1_data_out),
    .buffer_ptr(input_shifter_1_buffer_ptr));
  Comparator #(.width(4)) comparator_1 (
    .a(input_shifter_1_buffer_ptr), .b(4'b0101), .eq(comparator_1_eq));  // open: gt, lt
  Register #(.width(16)) register_1 (
    .D(input_shifter_1_data_out), .en(1'b1), .Q({register_1_q[15:4], People, register_1_q[1:0]}),
    .clk(comparator_1_eq), .clr(register_1_q[4]));
  DotMatrix #(.matrixcols(15), .matrixrows(15)) dotmatrix_1 (
    .col0(out_32), .col1(out_30), .col2(out_28), .col3(out_26), .col4(out_24), .col5(out_22), .col6(out_20),
    .col7(out_18), .col8(out_16), .col9(out_14), .col10(out_12), .col11(out_10), .col12(out_8),
    .col13(out_6), .col14(out_4));
  orange orange_1 (
    .in_1(People), .in_2(register_1_q[1:0]), .out_14(out_32), .out_9(out_30), .out_3(out_28),
    .out_15(out_26), .out_10(out_24), .out_4(out_22), .out_13(out_20), .out_8(out_18), .out_5(out_16),
    .out_16(out_14), .out_11(out_12), .out_6(out_10), .out_17(out_8), .out_12(out_6), .out_7(out_4));
  DotMatrix #(.matrixcols(15), .matrixrows(15)) dotmatrix_2 (
    .col0(out_33), .col1(out_31), .col2(out_29), .col3(out_27), .col4(out_25), .col5(out_23), .col6(out_21),
    .col7(out_19), .col8(out_17), .col9(out_15), .col10(out_13), .col11(out_11), .col12(out_9),
    .col13(out_7), .col14(out_5));
  blue blue_1 (
    .in_2(register_1_q[1:0]), .out_14(out_33), .out_9(out_31), .out_3(out_29), .out_15(out_27),
    .out_10(out_25), .out_4(out_23), .out_13(out_21), .out_8(out_19), .out_5(out_17), .out_16(out_15),
    .out_11(out_13), .out_6(out_11), .out_17(out_9), .out_12(out_7), .out_7(out_5), .in_1(People));
endmodule

module blue (
  input  [1:0] in_1,
  input  [1:0] in_2,
  output [14:0] out_3,
  output [14:0] out_4,
  output [14:0] out_5,
  output [14:0] out_6,
  output [14:0] out_7,
  output [14:0] out_8,
  output [14:0] out_9,
  output [14:0] out_10,
  output [14:0] out_11,
  output [14:0] out_12,
  output [14:0] out_13,
  output [14:0] out_14,
  output [14:0] out_15,
  output [14:0] out_16,
  output [14:0] out_17
);

  wire and_1_out, controlled_buffer_2_out, decoder_1_out0, decoder_1_out1, decoder_1_out2, decoder_1_out3,
       not_1_out;
  wire [1:0] pull_resistor_1_node;

  Decoder #(.select(2), .enable("false")) decoder_1 (
    .out0(decoder_1_out0), .out1(decoder_1_out1), .out2(decoder_1_out2), .out3(decoder_1_out3),
    .sel(pull_resistor_1_node));
  Pull_Resistor pull_resistor_1 (.node(pull_resistor_1_node));
  assign pull_resistor_1_node = in_1[0] ? in_2 : 2'bz;  // Controlled_Buffer controlled_buffer_1
  DotMatrix #(.matrixcols(15), .matrixrows(15)) dotmatrix_1 (
    .col0(out_14), .col1(out_9), .col2(out_3), .col3(out_15), .col4(out_10), .col5(out_4), .col6(out_13),
    .col7(out_8), .col8(out_5), .col9(out_16), .col10(out_11), .col11(out_6), .col12(out_17), .col13(out_12),
    .col14(out_7));
  assign controlled_buffer_2_out = not_1_out ? decoder_1_out0 : 1'bz;  // Controlled_Buffer controlled_buffer_2
  not not_1 (not_1_out, and_1_out);
  and and_1 (and_1_out, in_1[0], in_1[1]);
  Pull_Resistor pull_resistor_2 (.node(controlled_buffer_2_out));
  Transistor #(.\type ("n"), .width(15)) transistor_1 (.in({15{1'b0}}), .out(out_3), .gate(controlled_buffer_2_out));
  Transistor #(.\type ("n"), .width(15)) transistor_2 (.in({15{1'b0}}), .out(out_15), .gate(controlled_buffer_2_out));
  Transistor #(.\type ("n"), .width(15)) transistor_3 (.in({15{1'b0}}), .out(out_9), .gate(controlled_buffer_2_out));
  Transistor #(.\type ("n"), .width(15)) transistor_4 (.in({15{1'b0}}), .out(out_14), .gate(controlled_buffer_2_out));
  Transistor #(.\type ("n"), .width(15)) transistor_5 (.in({15{1'b0}}), .out(out_8), .gate(controlled_buffer_2_out));
  Transistor #(.\type ("n"), .width(15)) transistor_6 (.in({15{1'b0}}), .out(out_10), .gate(controlled_buffer_2_out));
  Transistor #(.\type ("n"), .width(15)) transistor_7 (.in({15{1'b0}}), .out(out_13), .gate(controlled_buffer_2_out));
  Transistor #(.\type ("n"), .width(15)) transistor_8 (.in({15{1'b0}}), .out(out_4), .gate(controlled_buffer_2_out));
  Transistor #(.\type ("n"), .width(15)) transistor_9 (.in({15{1'b0}}), .out(out_11), .gate(controlled_buffer_2_out));
  Transistor #(.\type ("n"), .width(15)) transistor_10 (.in({15{1'b0}}), .out(out_5), .gate(controlled_buffer_2_out));
  Transistor #(.\type ("n"), .width(15)) transistor_11 (.in({15{1'b0}}), .out(out_16), .gate(controlled_buffer_2_out));
  Transistor #(.\type ("n"), .width(15)) transistor_12 (.in({15{1'b0}}), .out(out_6), .gate(controlled_buffer_2_out));
  Transistor #(.\type ("n"), .width(15)) transistor_13 (.in({15{1'b0}}), .out(out_7), .gate(controlled_buffer_2_out));
  Transistor #(.\type ("n"), .width(15)) transistor_14 (.in({15{1'b0}}), .out(out_17), .gate(controlled_buffer_2_out));
  Transistor #(.\type ("n"), .width(15)) transistor_15 (.in({15{1'b0}}), .out(out_12), .gate(controlled_buffer_2_out));
  Transistor #(.\type ("n"), .width(15)) transistor_16 (.in(15'h180c), .out(out_9), .gate(decoder_1_out1));
  Transistor #(.\type ("n"), .width(15)) transistor_17 (.in(15'h2412), .out(out_3), .gate(decoder_1_out1));
  Transistor #(.\type ("n"), .width(15)) transistor_18 (.in(15'h23d6), .out(out_15), .gate(decoder_1_out1));
  Transistor #(.\type ("n"), .width(15)) transistor_19 (.in({15{1'b0}}), .out(out_14), .gate(decoder_1_out1));
  Transistor #(.\type ("n"), .width(15)) transistor_20 (.in(15'h2aa2), .out(out_8), .gate(decoder_1_out1));
  Transistor #(.\type ("n"), .width(15)) transistor_21 (.in(15'h2aa2), .out(out_13), .gate(decoder_1_out1));
  Transistor #(.\type ("n"), .width(15)) transistor_22 (.in(15'h2a82), .out(out_4), .gate(decoder_1_out1));
  Transistor #(.\type ("n"), .width(15)) transistor_23 (.in(15'h383a), .out(out_10), .gate(decoder_1_out1));
  Transistor #(.\type ("n"), .width(15)) transistor_24 (.in(15'h2c02), .out(out_6), .gate(decoder_1_out1));
  Transistor #(.\type ("n"), .width(15)) transistor_25 (.in(15'h2882), .out(out_11), .gate(decoder_1_out1));
  Transistor #(.\type ("n"), .width(15)) transistor_26 (.in(15'h2aa2), .out(out_16), .gate(decoder_1_out1));
  Transistor #(.\type ("n"), .width(15)) transistor_27 (.in(15'h2a22), .out(out_5), .gate(decoder_1_out1));
  Transistor #(.\type ("n"), .width(15)) transistor_28 (.in({15{1'b0}}), .out(out_7), .gate(decoder_1_out1));
  Transistor #(.\type ("n"), .width(15)) transistor_29 (.in(15'h2bc4), .out(out_17), .gate(decoder_1_out1));
  Transistor #(.\type ("n"), .width(15)) transistor_30 (.in(15'h1838), .out(out_12), .gate(decoder_1_out1));
  Transistor #(.\type ("n"), .width(15)) transistor_31 (.in(15'h140), .out(out_9), .gate(decoder_1_out2));
  Transistor #(.\type ("n"), .width(15)) transistor_32 (.in(15'h220), .out(out_3), .gate(decoder_1_out2));
  Transistor #(.\type ("n"), .width(15)) transistor_33 (.in(15'h80), .out(out_14), .gate(decoder_1_out2));
  Transistor #(.\type ("n"), .width(15)) transistor_34 (.in({15{1'b0}}), .out(out_15), .gate(decoder_1_out2));
  Transistor #(.\type ("n"), .width(15)) transistor_35 (.in(15'h1084), .out(out_4), .gate(decoder_1_out2));
  Transistor #(.\type ("n"), .width(15)) transistor_36 (.in(15'h21b2), .out(out_13), .gate(decoder_1_out2));
  Transistor #(.\type ("n"), .width(15)) transistor_37 (.in({15{1'b0}}), .out(out_10), .gate(decoder_1_out2));
  Transistor #(.\type ("n"), .width(15)) transistor_38 (.in(15'h43e1), .out(out_8), .gate(decoder_1_out2));
  Transistor #(.\type ("n"), .width(15)) transistor_39 (.in({15{1'b0}}), .out(out_11), .gate(decoder_1_out2));
  Transistor #(.\type ("n"), .width(15)) transistor_40 (.in({15{1'b0}}), .out(out_6), .gate(decoder_1_out2));
  Transistor #(.\type ("n"), .width(15)) transistor_41 (.in(15'h1084), .out(out_16), .gate(decoder_1_out2));
  Transistor #(.\type ("n"), .width(15)) transistor_42 (.in(15'h26c2), .out(out_5), .gate(decoder_1_out2));
  Transistor #(.\type ("n"), .width(15)) transistor_43 (.in(15'h220), .out(out_17), .gate(decoder_1_out2));
  Transistor #(.\type ("n"), .width(15)) transistor_44 (.in(15'h140), .out(out_12), .gate(decoder_1_out2));
  Transistor #(.\type ("n"), .width(15)) transistor_45 (.in(15'h80), .out(out_7), .gate(decoder_1_out2));
  Transistor #(.\type ("n"), .width(15)) transistor_46 (.in({15{1'b0}}), .out(out_14), .gate(decoder_1_out3));
  Transistor #(.\type ("n"), .width(15)) transistor_47 (.in({15{1'b0}}), .out(out_9), .gate(decoder_1_out3));
  Transistor #(.\type ("n"), .width(15)) transistor_48 (.in(15'h100), .out(out_3), .gate(decoder_1_out3));
  Transistor #(.\type ("n"), .width(15)) transistor_49 (.in(15'h700), .out(out_10), .gate(decoder_1_out3));
  Transistor #(.\type ("n"), .width(15)) transistor_50 (.in(15'he00), .out(out_4), .gate(decoder_1_out3));
  Transistor #(.\type ("n"), .width(15)) transistor_51 (.in(15'h1ffe), .out(out_13), .gate(decoder_1_out3));
  Transistor #(.\type ("n"), .width(15)) transistor_52 (.in(15'h300), .out(out_15), .gate(decoder_1_out3));
  Transistor #(.\type ("n"), .width(15)) transistor_53 (.in(15'h3ffe), .out(out_8), .gate(decoder_1_out3));
  Transistor #(.\type ("n"), .width(15)) transistor_54 (.in(15'he00), .out(out_16), .gate(decoder_1_out3));
  Transistor #(.\type ("n"), .width(15)) transistor_55 (.in(15'h700), .out(out_11), .gate(decoder_1_out3));
  Transistor #(.\type ("n"), .width(15)) transistor_56 (.in(15'h1ffe), .out(out_5), .gate(decoder_1_out3));
  Transistor #(.\type ("n"), .width(15)) transistor_57 (.in({15{1'b0}}), .out(out_12), .gate(decoder_1_out3));
  Transistor #(.\type ("n"), .width(15)) transistor_58 (.in({15{1'b0}}), .out(out_7), .gate(decoder_1_out3));
  Transistor #(.\type ("n"), .width(15)) transistor_59 (.in(15'h100), .out(out_17), .gate(decoder_1_out3));
  Transistor #(.\type ("n"), .width(15)) transistor_60 (.in(15'h300), .out(out_6), .gate(decoder_1_out3));
  Transistor #(.\type ("n"), .width(15)) transistor_61 (.in(15'h1c0), .out(out_14), .gate(and_1_out));
  Transistor #(.\type ("n"), .width(15)) transistor_62 (.in(15'h630), .out(out_9), .gate(and_1_out));
  Transistor #(.\type ("n"), .width(15)) transistor_63 (.in(15'h2002), .out(out_4), .gate(and_1_out));
  Transistor #(.\type ("n"), .width(15)) transistor_64 (.in(15'h2002), .out(out_10), .gate(and_1_out));
  Transistor #(.\type ("n"), .width(15)) transistor_65 (.in(15'h808), .out(out_3), .gate(and_1_out));
  Transistor #(.\type ("n"), .width(15)) transistor_66 (.in(15'h1004), .out(out_15), .gate(and_1_out));
  Transistor #(.\type ("n"), .width(15)) transistor_67 (.in(15'h5f81), .out(out_8), .gate(and_1_out));
  Transistor #(.\type ("n"), .width(15)) transistor_68 (.in(15'h4001), .out(out_13), .gate(and_1_out));
  Transistor #(.\type ("n"), .width(15)) transistor_69 (.in(15'h2082), .out(out_16), .gate(and_1_out));
  Transistor #(.\type ("n"), .width(15)) transistor_70 (.in(15'h4081), .out(out_5), .gate(and_1_out));
  Transistor #(.\type ("n"), .width(15)) transistor_71 (.in(15'h630), .out(out_12), .gate(and_1_out));
  Transistor #(.\type ("n"), .width(15)) transistor_72 (.in(15'h1004), .out(out_6), .gate(and_1_out));
  Transistor #(.\type ("n"), .width(15)) transistor_73 (.in(15'h808), .out(out_17), .gate(and_1_out));
  Transistor #(.\type ("n"), .width(15)) transistor_74 (.in(15'h2082), .out(out_11), .gate(and_1_out));
  Transistor #(.\type ("n"), .width(15)) transistor_75 (.in(15'h1c0), .out(out_7), .gate(and_1_out));
endmodule

module orange (
  input  [1:0] in_1,
  input  [1:0] in_2,
  output [14:0] out_3,
  output [14:0] out_4,
  output [14:0] out_5,
  output [14:0] out_6,
  output [14:0] out_7,
  output [14:0] out_8,
  output [14:0] out_9,
  output [14:0] out_10,
  output [14:0] out_11,
  output [14:0] out_12,
  output [14:0] out_13,
  output [14:0] out_14,
  output [14:0] out_15,
  output [14:0] out_16,
  output [14:0] out_17
);

  wire and_1_out, controlled_buffer_2_out, decoder_1_out0, decoder_1_out1, decoder_1_out2, decoder_1_out3,
       not_1_out;
  wire [1:0] pull_resistor_1_node;

  DotMatrix #(.matrixcols(15), .matrixrows(15)) dotmatrix_1 (
    .col0(out_14), .col1(out_9), .col2(out_3), .col3(out_15), .col4(out_10), .col5(out_4), .col6(out_13),
    .col7(out_8), .col8(out_5), .col9(out_16), .col10(out_11), .col11(out_6), .col12(out_17), .col13(out_12),
    .col14(out_7));
  Decoder #(.select(2), .enable("false")) decoder_1 (
    .out0(decoder_1_out0), .out1(decoder_1_out1), .out2(decoder_1_out2), .out3(decoder_1_out3),
    .sel(pull_resistor_1_node));
  Pull_Resistor pull_resistor_1 (.node(pull_resistor_1_node));
  assign pull_resistor_1_node = in_1[1] ? in_2 : 2'bz;  // Controlled_Buffer controlled_buffer_1
  and and_1 (and_1_out, in_1[1], in_1[0]);
  assign controlled_buffer_2_out = not_1_out ? decoder_1_out0 : 1'bz;  // Controlled_Buffer controlled_buffer_2
  not not_1 (not_1_out, and_1_out);
  Pull_Resistor pull_resistor_2 (.node(controlled_buffer_2_out));
  Transistor #(.\type ("n"), .width(15)) transistor_1 (.in({15{1'b0}}), .out(out_9), .gate(controlled_buffer_2_out));
  Transistor #(.\type ("n"), .width(15)) transistor_2 (.in({15{1'b0}}), .out(out_14), .gate(controlled_buffer_2_out));
  Transistor #(.\type ("n"), .width(15)) transistor_3 (.in({15{1'b0}}), .out(out_4), .gate(controlled_buffer_2_out));
  Transistor #(.\type ("n"), .width(15)) transistor_4 (.in({15{1'b0}}), .out(out_10), .gate(controlled_buffer_2_out));
  Transistor #(.\type ("n"), .width(15)) transistor_5 (.in({15{1'b0}}), .out(out_15), .gate(controlled_buffer_2_out));
  Transistor #(.\type ("n"), .width(15)) transistor_6 (.in({15{1'b0}}), .out(out_3), .gate(controlled_buffer_2_out));
  Transistor #(.\type ("n"), .width(15)) transistor_7 (.in({15{1'b0}}), .out(out_13), .gate(controlled_buffer_2_out));
  Transistor #(.\type ("n"), .width(15)) transistor_8 (.in({15{1'b0}}), .out(out_16), .gate(controlled_buffer_2_out));
  Transistor #(.\type ("n"), .width(15)) transistor_9 (.in({15{1'b0}}), .out(out_8), .gate(controlled_buffer_2_out));
  Transistor #(.\type ("n"), .width(15)) transistor_10 (.in({15{1'b0}}), .out(out_5), .gate(controlled_buffer_2_out));
  Transistor #(.\type ("n"), .width(15)) transistor_11 (.in({15{1'b0}}), .out(out_12), .gate(controlled_buffer_2_out));
  Transistor #(.\type ("n"), .width(15)) transistor_12 (.in({15{1'b0}}), .out(out_11), .gate(controlled_buffer_2_out));
  Transistor #(.\type ("n"), .width(15)) transistor_13 (.in({15{1'b0}}), .out(out_6), .gate(controlled_buffer_2_out));
  Transistor #(.\type ("n"), .width(15)) transistor_14 (.in({15{1'b0}}), .out(out_17), .gate(controlled_buffer_2_out));
  Transistor #(.\type ("n"), .width(15)) transistor_15 (.in({15{1'b0}}), .out(out_7), .gate(controlled_buffer_2_out));
  Transistor #(.\type ("n"), .width(15)) transistor_16 (.in(15'h180c), .out(out_9), .gate(decoder_1_out1));
  Transistor #(.\type ("n"), .width(15)) transistor_17 (.in(15'h2412), .out(out_3), .gate(decoder_1_out1));
  Transistor #(.\type ("n"), .width(15)) transistor_18 (.in({15{1'b0}}), .out(out_14), .gate(decoder_1_out1));
  Transistor #(.\type ("n"), .width(15)) transistor_19 (.in(15'h2aa2), .out(out_13), .gate(decoder_1_out1));
  Transistor #(.\type ("n"), .width(15)) transistor_20 (.in(15'h23d6), .out(out_15), .gate(decoder_1_out1));
  Transistor #(.\type ("n"), .width(15)) transistor_21 (.in(15'h383a), .out(out_10), .gate(decoder_1_out1));
  Transistor #(.\type ("n"), .width(15)) transistor_22 (.in(15'h2a82), .out(out_4), .gate(decoder_1_out1));
  Transistor #(.\type ("n"), .width(15)) transistor_23 (.in(15'h2882), .out(out_11), .gate(decoder_1_out1));
  Transistor #(.\type ("n"), .width(15)) transistor_24 (.in(15'h2a22), .out(out_5), .gate(decoder_1_out1));
  Transistor #(.\type ("n"), .width(15)) transistor_25 (.in(15'h2aa2), .out(out_8), .gate(decoder_1_out1));
  Transistor #(.\type ("n"), .width(15)) transistor_26 (.in(15'h2aa2), .out(out_16), .gate(decoder_1_out1));
  Transistor #(.\type ("n"), .width(15)) transistor_27 (.in(15'h1838), .out(out_12), .gate(decoder_1_out1));
  Transistor #(.\type ("n"), .width(15)) transistor_28 (.in(15'h2bc4), .out(out_17), .gate(decoder_1_out1));
  Transistor #(.\type ("n"), .width(15)) transistor_29 (.in(15'h2c02), .out(out_6), .gate(decoder_1_out1));
  Transistor #(.\type ("n"), .width(15)) transistor_30 (.in({15{1'b0}}), .out(out_7), .gate(decoder_1_out1));
  Transistor #(.\type ("n"), .width(15)) transistor_31 (.in(15'h140), .out(out_9), .gate(decoder_1_out2));
  Transistor #(.\type ("n"), .width(15)) transistor_32 (.in(15'h80), .out(out_14), .gate(decoder_1_out2));
  Transistor #(.\type ("n"), .width(15)) transistor_33 (.in(15'h220), .out(out_3), .gate(decoder_1_out2));
  Transistor #(.\type ("n"), .width(15)) transistor_34 (.in({15{1'b0}}), .out(out_10), .gate(decoder_1_out2));
  Transistor #(.\type ("n"), .width(15)) transistor_35 (.in(15'h1084), .out(out_4), .gate(decoder_1_out2));
  Transistor #(.\type ("n"), .width(15)) transistor_36 (.in({15{1'b0}}), .out(out_15), .gate(decoder_1_out2));
  Transistor #(.\type ("n"), .width(15)) transistor_37 (.in(15'h21b2), .out(out_13), .gate(decoder_1_out2));
  Transistor #(.\type ("n"), .width(15)) transistor_38 (.in(15'h1084), .out(out_16), .gate(decoder_1_out2));
  Transistor #(.\type ("n"), .width(15)) transistor_39 (.in(15'h43e1), .out(out_8), .gate(decoder_1_out2));
  Transistor #(.\type ("n"), .width(15)) transistor_40 (.in(15'h26c2), .out(out_5), .gate(decoder_1_out2));
  Transistor #(.\type ("n"), .width(15)) transistor_41 (.in(15'h220), .out(out_17), .gate(decoder_1_out2));
  Transistor #(.\type ("n"), .width(15)) transistor_42 (.in(15'h140), .out(out_12), .gate(decoder_1_out2));
  Transistor #(.\type ("n"), .width(15)) transistor_43 (.in({15{1'b0}}), .out(out_11), .gate(decoder_1_out2));
  Transistor #(.\type ("n"), .width(15)) transistor_44 (.in({15{1'b0}}), .out(out_6), .gate(decoder_1_out2));
  Transistor #(.\type ("n"), .width(15)) transistor_45 (.in(15'h80), .out(out_7), .gate(decoder_1_out2));
  Transistor #(.\type ("n"), .width(15)) transistor_46 (.in({15{1'b0}}), .out(out_14), .gate(decoder_1_out3));
  Transistor #(.\type ("n"), .width(15)) transistor_47 (.in(15'h700), .out(out_10), .gate(decoder_1_out3));
  Transistor #(.\type ("n"), .width(15)) transistor_48 (.in({15{1'b0}}), .out(out_9), .gate(decoder_1_out3));
  Transistor #(.\type ("n"), .width(15)) transistor_49 (.in(15'h300), .out(out_15), .gate(decoder_1_out3));
  Transistor #(.\type ("n"), .width(15)) transistor_50 (.in(15'h100), .out(out_3), .gate(decoder_1_out3));
  Transistor #(.\type ("n"), .width(15)) transistor_51 (.in(15'he00), .out(out_4), .gate(decoder_1_out3));
  Transistor #(.\type ("n"), .width(15)) transistor_52 (.in(15'h1ffe), .out(out_5), .gate(decoder_1_out3));
  Transistor #(.\type ("n"), .width(15)) transistor_53 (.in(15'h1ffe), .out(out_13), .gate(decoder_1_out3));
  Transistor #(.\type ("n"), .width(15)) transistor_54 (.in(15'h3ffe), .out(out_8), .gate(decoder_1_out3));
  Transistor #(.\type ("n"), .width(15)) transistor_55 (.in(15'h100), .out(out_17), .gate(decoder_1_out3));
  Transistor #(.\type ("n"), .width(15)) transistor_56 (.in(15'h700), .out(out_11), .gate(decoder_1_out3));
  Transistor #(.\type ("n"), .width(15)) transistor_57 (.in(15'h300), .out(out_6), .gate(decoder_1_out3));
  Transistor #(.\type ("n"), .width(15)) transistor_58 (.in(15'he00), .out(out_16), .gate(decoder_1_out3));
  Transistor #(.\type ("n"), .width(15)) transistor_59 (.in({15{1'b0}}), .out(out_12), .gate(decoder_1_out3));
  Transistor #(.\type ("n"), .width(15)) transistor_60 (.in({15{1'b0}}), .out(out_7), .gate(decoder_1_out3));
  Transistor #(.\type ("n"), .width(15)) transistor_61 (.in(15'h630), .out(out_9), .gate(and_1_out));
  Transistor #(.\type ("n"), .width(15)) transistor_62 (.in(15'h808), .out(out_3), .gate(and_1_out));
  Transistor #(.\type ("n"), .width(15)) transistor_63 (.in(15'h1c0), .out(out_14), .gate(and_1_out));
  Transistor #(.\type ("n"), .width(15)) transistor_64 (.in(15'h1004), .out(out_15), .gate(and_1_out));
  Transistor #(.\type ("n"), .width(15)) transistor_65 (.in(15'h4001), .out(out_13), .gate(and_1_out));
  Transistor #(.\type ("n"), .width(15)) transistor_66 (.in(15'h2002), .out(out_10), .gate(and_1_out));
  Transistor #(.\type ("n"), .width(15)) transistor_67 (.in(15'h5f81), .out(out_8), .gate(and_1_out));
  Transistor #(.\type ("n"), .width(15)) transistor_68 (.in(15'h2002), .out(out_4), .gate(and_1_out));
  Transistor #(.\type ("n"), .width(15)) transistor_69 (.in(15'h2082), .out(out_11), .gate(and_1_out));
  Transistor #(.\type ("n"), .width(15)) transistor_70 (.in(15'h2082), .out(out_16), .gate(and_1_out));
  Transistor #(.\type ("n"), .width(15)) transistor_71 (.in(15'h4081), .out(out_5), .gate(and_1_out));
  Transistor #(.\type ("n"), .width(15)) transistor_72 (.in(15'h1004), .out(out_6), .gate(and_1_out));
  Transistor #(.\type ("n"), .width(15)) transistor_73 (.in(15'h808), .out(out_17), .gate(and_1_out));
  Transistor #(.\type ("n"), .width(15)) transistor_74 (.in(15'h630), .out(out_12), .gate(and_1_out));
  Transistor #(.\type ("n"), .width(15)) transistor_75 (.in(15'h1c0), .out(out_7), .gate(and_1_out));
endmodule

module generator (
  input  [1:0] Who,
  input  CS,
  input  in_3,
  input  in_4,
  output [4:0] out_5,
  output [4:0] out_6,
  output [4:0] out_7,
  output [4:0] out_8,
  output [4:0] out_9,
  output [4:0] out_10,
  output [4:0] out_11,
  output [4:0] out_12,
  output [4:0] out_13,
  output [4:0] out_14,
  output [4:0] out_15,
  output [4:0] out_16,
  output [4:0] out_17,
  output [4:0] out_18,
  output [4:0] out_19,
  output [4:0] out_20,
  output [4:0] out_21,
  output [4:0] out_22,
  output [4:0] out_23,
  output [4:0] out_24,
  output [4:0] out_25,
  output [4:0] out_26,
  output [4:0] out_27,
  output [4:0] out_28,
  output [4:0] out_29,
  output [4:0] out_30,
  output [4:0] out_31,
  output [4:0] out_32,
  output [4:0] out_33,
  output [4:0] out_34,
  output [4:0] out_35,
  output [4:0] out_36,
  output [4:0] out_37,
  output [4:0] out_38,
  output [4:0] out_39,
  output [14:0] out_40,
  output [14:0] out_41,
  output [14:0] out_42,
  output [14:0] out_43,
  output [14:0] out_44,
  output [14:0] out_45,
  output [14:0] out_46,
  output [14:0] out_47,
  output [14:0] out_48,
  output [14:0] out_49,
  output [14:0] out_50,
  output [14:0] out_51,
  output [14:0] out_52,
  output [14:0] out_53,
  output [14:0] out_54,
  output [14:0] out_55,
  output [14:0] out_56,
  output [14:0] out_57,
  output [4:0] out_58,
  output [4:0] out_59,
  output [4:0] out_60,
  output [4:0] out_61,
  output [4:0] out_62,
  output [4:0] out_63,
  output [4:0] out_64,
  output [4:0] out_65,
  output [4:0] out_66,
  output [4:0] out_67,
  output [4:0] out_68,
  output [4:0] out_69,
  output [4:0] out_70,
  output [4:0] out_71,
  output [4:0] out_72,
  output [4:0] out_73,
  output [4:0] out_74,
  output [4:0] out_75,
  output [4:0] out_76,
  output [4:0] out_77,
  output [4:0] out_78,
  output [4:0] out_79,
  output [4:0] out_80,
  output [4:0] out_81,
  output [4:0] out_82,
  output [4:0] out_83,
  output [4:0] out_84,
  output [4:0] out_85,
  output [4:0] out_86,
  output [4:0] out_87,
  output [4:0] out_88,
  output [4:0] out_89,
  output [4:0] out_90,
  output [4:0] out_91,
  output [4:0] out_92,
  output out_93,
  output [4:0] out_94,
  output [4:0] out_95,
  output [4:0] out_96,
  output [4:0] out_97,
  output [4:0] out_98,
  output [4:0] out_99,
  output [4:0] out_100,
  output [4:0] out_101,
  output [4:0] out_102,
  output [4:0] out_103,
  output [4:0] out_104,
  output [4:0] out_105,
  output [4:0] out_106,
  output [4:0] out_107,
  output [4:0] out_108,
  output [4:0] out_109,
  output [4:0] out_110,
  output [4:0] out_111,
  output [4:0] out_112,
  output [4:0] out_113,
  output [4:0] out_114,
  output [4:0] out_115,
  output [4:0] out_116,
  output [4:0] out_117,
  output [4:0] out_118,
  output [4:0] out_119,
  output [4:0] out_120,
  output [4:0] out_121,
  output [4:0] out_122,
  output [4:0] out_123,
  output [4:0] out_124,
  output [4:0] out_125,
  output [4:0] out_126,
  output [4:0] out_127,
  output [4:0] out_128,
  output [4:0] out_129,
  output [4:0] out_130,
  output [4:0] out_131,
  output [4:0] out_132,
  output [4:0] out_133,
  output [4:0] out_134,
  output [4:0] out_135,
  output [4:0] out_136,
  output [4:0] out_137
);

  wire _1_b, _1_o, _2_b, _2_o, _3_b, _3_o, _4_b, _4_o, _5_b, _5_o, and_1_out, and_2_out, and_3_out,
       and_4_out, and_5_out, and_6_out, and_8_out, and_9_out, and_10_out, and_11_out, and_25_out, and_26_out,
       and_27_out, and_28_out, and_29_out, and_30_out, and_31_out, and_32_out, and_33_out, and_34_out,
       and_35_out, and_36_out, and_37_out, and_38_out, and_39_out, comparator_2_eq, comparator_4_eq,
       comparator_7_eq, comparator_8_eq, controlled_buffer_3_out, controlled_buffer_4_out, CS_t, d_ff_1_q,
       d_ff_2_q, dec_DE, dec_OP, demultiplexer_8_out1, demultiplexer_8_out2, dog_b, dog_o, err_00, err_01,
       err_10, err_11, err_b, err_o, exit_OP, gen_task, god_b, god_o, jk, kj, ne_Soh_prime, not_2_out,
       not_3_out, not_4_out, not_5_out, not_6_out, or_3_out, or_4_out, or_5_out, or_6_out, or_7_out,
       or_9_out, or_10_out, or_11_out, or_12_out, or_13_out, or_14_out, or_15_out, or_16_out, or_17_out,
       or_18_out, or_19_out, or_20_out, output_shifter_1_miso, prov, pull_resistor_1_node,
       pull_resistor_15_node, pull_resistor_19_node, rst, rst_1, rst_2, rst_3, rst_4, rst_5, rst_6, rst_7,
       rst_8, rst_9, rst_10, Soh_prime, transistor_5_out, transistor_6_out, transistor_7_out,
       transistor_8_out;
  wire [0:0] or_2_out;
  wire [1:0] xx, xx_exit, yy, yy_exit;
  wire [1:1] or_1_out;
  wire [2:0] controlled_buffer_1_out, controlled_buffer_2_out, h_1b, h_1o, inc_1_out_2, inc_2_out_2,
       inc_3_out_2, inc_4_out_2, multiplier_1_cout, multiplier_1_out, w_1b, w_1o;
  wire [3:0] input_shifter_1_buffer_ptr, output_shifter_1_buffer_ptr, transistor_3_out;
  wire [4:0] pull_resistor_10_node, pull_resistor_20_node, undriven, undriven_2;
  wire [5:0] b_exzit_1, b_exzit_2, b_exzit_3, b_exzit_4, b_exzit_5, multiplexer_4_out, multiplexer_5_out,
       multiplexer_6_out, multiplexer_7_out, multiplexer_8_out, o_exzit_1, o_exzit_2, o_exzit_3, o_exzit_4,
       o_exzit_5;
  wire [9:0] adder_1_out, adder_2_out, adder_3_out, adder_4_out, adder_5_out, de_b, de_o, dec,
       demultiplexer_6_out1, demultiplexer_6_out2, demultiplexer_7_out1, demultiplexer_7_out2, divider_1_out,
       divider_1_rem, multiplexer_1_out, multiplexer_2_out, op_b, op_o, subtractor_1_out, subtractor_2_out,
       subtractor_3_out, subtractor_4_out, transistor_9_out, transistor_10_out, transistor_11_out,
       transistor_13_out, transistor_14_out, transistor_16_out, transistor_18_out, transistor_19_out;
  wire [15:0] input_shifter_1_data_out, multiplexer_3_out, transistor_1_out;
  wire [15:4] register_1_q;
  wire [15:10] pull_resistor_2_node;

  and and_1 (and_1_out, err_01, Who[0]);
  or or_1 (or_1_out[1], and_1_out, and_2_out);
  and and_2 (and_2_out, Who[1], err_00);
  Multiplexer #(.select(2), .width(10), .enable("false")) multiplexer_1 (
    .in1(de_o), .in2(de_b), .out(multiplexer_1_out), .sel(Who));  // open: in0, in3
  Multiplexer #(.select(2), .width(10), .enable("false")) multiplexer_2 (
    .in1(op_o), .in2(op_b), .out(multiplexer_2_out), .sel(Who));  // open: in0, in3
  or or_2 (or_2_out[0], err_o, err_b);
  Multiplexer #(.select(2), .width(16), .enable("false")) multiplexer_3 (
    .in0({undriven, yy_exit[0], yy_exit[1], xx_exit[0], xx_exit[1], {7{1'b0}}}), .in1(16'h40),
    .in2({undriven_2, multiplexer_2_out[3:0], multiplexer_1_out[6:0]}), .out(multiplexer_3_out),
    .sel({exit_OP, or_2_out[0]}));  // open: in3
  Transistor #(.width(16)) transistor_1 (.in(multiplexer_3_out), .out(transistor_1_out), .gate(dec_OP));
  Transistor #(.\type ("n"), .width(16)) transistor_2 (
    .in({{14{1'b0}}, {2{or_1_out[1]}}}), .out(transistor_1_out), .gate(dec_OP));
  Transistor #(.\type ("n"), .width(4)) transistor_3 (
    .in(input_shifter_1_buffer_ptr), .out(transistor_3_out), .gate(d_ff_1_q));
  // Probe on {pull_resistor_2_node, dec}
  Pull_Resistor pull_resistor_1 (.node(pull_resistor_1_node));
  Comparator #(.width(4), .mode("unsigned")) comparator_1 (
    .a(4'b0000), .b(transistor_3_out), .eq(pull_resistor_1_node));  // open: gt, lt
  Pull_Resistor pull_resistor_2 (.node({pull_resistor_2_node, dec}));
  Transistor #(.\type ("n"), .width(16)) transistor_4 (
    .in(input_shifter_1_data_out), .out({pull_resistor_2_node, dec}), .gate(pull_resistor_1_node));
  not not_1 (CS_t, CS);
  or or_3 (or_3_out, exit_OP, dec_OP, gen_task);
  input_shifter input_shifter_1 (
    .MOSI(in_4), .CLK(in_3), .Reset(CS_t), .Data_out(input_shifter_1_data_out),
    .buffer_ptr(input_shifter_1_buffer_ptr));
  and and_3 (and_3_out, in_3, ~d_ff_1_q);  // AND_Gate
  Transistor #(.\type ("n")) transistor_5 (.in(in_3), .out(transistor_5_out), .gate(d_ff_1_q));
  Pull_Resistor pull_resistor_3 (.node(transistor_5_out));
  and and_4 (and_4_out, transistor_5_out, or_3_out);
  not not_2 (not_2_out, or_3_out);
  and and_5 (and_5_out, err_11, Who[0]);
  and and_6 (and_6_out, Who[1], err_10);
  and and_7 (dec_DE, register_1_q[4], xx[1], ~xx[0], ~yy[1], ~yy[0]);  // AND_Gate
  // Probe on input_shifter_1_data_out
  D_Flip_Flop #(.trigger("falling")) d_ff_1 (
    .clk(and_3_out), .D(comparator_2_eq), .Q(d_ff_1_q), .reset(CS_t));  // open: Qn, preset, en
  or or_4 (or_4_out, and_5_out, and_6_out);
  and and_8 (and_8_out, Who[1], dog_b);
  or or_5 (or_5_out, and_8_out, and_9_out);
  and and_9 (and_9_out, Who[1], god_b);
  and and_10 (and_10_out, Who[0], dog_o);
  or or_6 (or_6_out, and_10_out, and_11_out);
  and and_11 (and_11_out, Who[0], god_o);
  and and_12 (dec_OP, register_1_q[4], xx[1], ~xx[0], ~yy[1], yy[0]);  // AND_Gate
  // Probe on {register_1_q, xx, yy}
  Register #(.width(16)) register_1 (
    .D(input_shifter_1_data_out), .en(1'b1), .Q({register_1_q, xx, yy}), .clk(comparator_2_eq), .clr(CS_t));
  Transistor #(.\type ("n")) transistor_6 (.in(or_4_out), .out(transistor_6_out), .gate(dec_DE));
  Pull_Resistor pull_resistor_4 (.node(transistor_6_out));
  Transistor #(.\type ("n")) transistor_7 (.in(or_5_out), .out(transistor_7_out), .gate(prov));
  Pull_Resistor pull_resistor_5 (.node(transistor_7_out));
  Transistor #(.\type ("n")) transistor_8 (.in(or_6_out), .out(transistor_8_out), .gate(prov));
  Pull_Resistor pull_resistor_6 (.node(transistor_8_out));
  and and_13 (prov, register_1_q[4], xx[1], ~xx[0], yy[1], ~yy[0]);  // AND_Gate
  Pull_Resistor pull_resistor_7 (.node({register_1_q, xx, yy}));
  Comparator #(.width(4), .mode("unsigned")) comparator_2 (
    .a(input_shifter_1_buffer_ptr), .b(4'b0101), .eq(comparator_2_eq));  // open: gt, lt
  and and_14 (exit_OP, comparator_2_eq, ~register_1_q[4]);  // AND_Gate
  output_shifter output_shifter_1 (
    .Data_in(transistor_1_out), .CLK(and_4_out), .Reset(not_2_out), .MISO(output_shifter_1_miso),
    .buffer_ptr(output_shifter_1_buffer_ptr));
  // Probe on output_shifter_1_buffer_ptr
  inc inc_1 (.in_1(yy), .out_2(inc_1_out_2));
  inc inc_2 (.in_1(xx), .out_2(inc_2_out_2));
  and and_15 (ne_Soh_prime, register_1_q[4], ~xx[1], ~xx[0], yy[1], ~yy[0]);  // AND_Gate
  or or_7 (or_7_out, ne_Soh_prime, Soh_prime, rst);
  Demultiplexer #(.select(2), .enable("false")) demultiplexer_1 (
    .out1(rst_1), .out2(rst_6), .in(pull_resistor_20_node[0]), .sel(Who));  // open: out0, out3
  or or_8 (out_93, output_shifter_1_miso, transistor_6_out, transistor_7_out, transistor_8_out);
  // Probe on controlled_buffer_1_out
  assign controlled_buffer_1_out = exit_OP ? inc_1_out_2 : 3'bz;  // Controlled_Buffer controlled_buffer_1
  Pull_Resistor pull_resistor_8 (.node(controlled_buffer_1_out));
  assign controlled_buffer_2_out = exit_OP ? inc_2_out_2 : 3'bz;  // Controlled_Buffer controlled_buffer_2
  Pull_Resistor pull_resistor_9 (.node(controlled_buffer_2_out));
  // Probe on controlled_buffer_2_out
  and and_16 (Soh_prime, register_1_q[4], ~xx[1], ~xx[0], yy[1], yy[0]);  // AND_Gate
  and and_17 (gen_task, ~yy[0], ~yy[1], xx[0], ~xx[1], register_1_q[4]);  // AND_Gate
  Multiplexer #(.select(2), .width(6), .enable("false")) multiplexer_4 (
    .in1(o_exzit_1), .in2(b_exzit_1), .out(multiplexer_4_out), .sel(Who));  // open: in0, in3
  and and_18 (rst, ~yy[0], ~yy[1], ~xx[0], ~xx[1], register_1_q[4]);  // AND_Gate
  Weight weight_1 (
    .new_task(gen_task), .out_4(out_56), .out_5(out_54), .out_6(out_52), .out_7(out_50), .out_8(out_48),
    .out_9(out_46), .out_10(out_44), .out_11(out_42), .out_12(out_40), .out_3(xx_exit), .in_1(d_ff_2_q));
  D_Flip_Flop d_ff_2 (.Q(d_ff_2_q), .preset(gen_task), .reset(or_7_out));  // open: clk, D, Qn, en
  Demultiplexer #(.select(2), .enable("false")) demultiplexer_2 (
    .out1(rst_2), .out2(rst_7), .in(pull_resistor_20_node[1]), .sel(Who));  // open: out0, out3
  DotMatrix #(.matrixcols(9), .matrixrows(15)) dotmatrix_1 (
    .col0(out_56), .col1(out_54), .col2(out_52), .col3(out_50), .col4(out_48), .col5(out_46), .col6(out_44),
    .col7(out_42), .col8(out_40));
  assign controlled_buffer_3_out = Who[0] ? Soh_prime : 1'bz;  // Controlled_Buffer controlled_buffer_3
  assign controlled_buffer_4_out = Who[1] ? Soh_prime : 1'bz;  // Controlled_Buffer controlled_buffer_4
  Pull_Resistor pull_resistor_10 (.node(pull_resistor_10_node[0]));
  Comparator #(.width(6)) comparator_3 (
    .a(multiplexer_4_out), .b({controlled_buffer_2_out, controlled_buffer_1_out}),
    .eq(pull_resistor_10_node[0]));  // open: gt, lt
  inc inc_3 (.in_1(xx_exit), .out_2(inc_3_out_2));
  // Probe on xx_exit
  Pull_Resistor pull_resistor_11 (.node(controlled_buffer_3_out));
  Pull_Resistor pull_resistor_12 (.node(controlled_buffer_4_out));
  Demultiplexer #(.select(2), .enable("false")) demultiplexer_3 (
    .out1(rst_3), .out2(rst_8), .in(pull_resistor_20_node[2]), .sel(Who));  // open: out0, out3
  and and_19 (pull_resistor_10_node[1], ~pull_resistor_10_node[0], comparator_4_eq);  // AND_Gate
  Multiplexer #(.select(2), .width(6), .enable("false")) multiplexer_5 (
    .in1(o_exzit_2), .in2(b_exzit_2), .out(multiplexer_5_out), .sel(Who));  // open: in0, in3
  Comparator #(.width(6)) comparator_4 (
    .a(multiplexer_5_out), .b({controlled_buffer_2_out, controlled_buffer_1_out}), .eq(comparator_4_eq));  // open: gt, lt
  Multiplier #(.width(3)) multiplier_1 (
    .a(controlled_buffer_1_out), .b(controlled_buffer_2_out), .out(multiplier_1_out), .cout(multiplier_1_cout));  // open: cin
  // Probe on multiplier_1_cout
  DotMatrix #(.matrixcols(9), .matrixrows(15)) dotmatrix_2 (
    .col0(out_57), .col1(out_55), .col2(out_53), .col3(out_51), .col4(out_49), .col5(out_47), .col6(out_45),
    .col7(out_43), .col8(out_41));
  Haight haight_1 (
    .new_task(gen_task), .out_4(out_57), .out_5(out_55), .out_6(out_53), .out_7(out_51), .out_8(out_49),
    .out_9(out_47), .out_10(out_45), .out_11(out_43), .out_12(out_41), .out_3(yy_exit), .in_1(d_ff_2_q));
  assign w_1o = controlled_buffer_3_out ? inc_3_out_2 : 3'bz;  // Controlled_Buffer controlled_buffer_5
  Demultiplexer #(.select(2), .enable("false")) demultiplexer_4 (
    .out1(rst_4), .out2(rst_9), .in(pull_resistor_20_node[3]), .sel(Who));  // open: out0, out3
  Pull_Resistor pull_resistor_13 (.node(comparator_4_eq));
  Pull_Resistor pull_resistor_14 (.node(w_1o));
  // Probe on yy_exit
  inc inc_4 (.in_1(yy_exit), .out_2(inc_4_out_2));
  assign w_1b = controlled_buffer_4_out ? inc_3_out_2 : 3'bz;  // Controlled_Buffer controlled_buffer_6
  and and_20 (pull_resistor_10_node[2], ~pull_resistor_10_node[0], ~comparator_4_eq, pull_resistor_15_node);  // AND_Gate
  Pull_Resistor pull_resistor_15 (.node(pull_resistor_15_node));
  Multiplexer #(.select(2), .width(6), .enable("false")) multiplexer_6 (
    .in1(o_exzit_3), .in2(b_exzit_3), .out(multiplexer_6_out), .sel(Who));  // open: in0, in3
  Comparator #(.width(6)) comparator_5 (
    .a(multiplexer_6_out), .b({controlled_buffer_2_out, controlled_buffer_1_out}), .eq(pull_resistor_15_node));  // open: gt, lt
  Pull_Resistor pull_resistor_16 (.node(h_1o));
  assign h_1o = controlled_buffer_3_out ? inc_4_out_2 : 3'bz;  // Controlled_Buffer controlled_buffer_7
  Demultiplexer #(.select(2), .enable("false")) demultiplexer_5 (
    .out1(rst_5), .out2(rst_10), .in(pull_resistor_20_node[4]), .sel(Who));  // open: out0, out3
  Multiplexer #(.select(2), .width(6), .enable("false")) multiplexer_7 (
    .in1(o_exzit_4), .in2(b_exzit_4), .out(multiplexer_7_out), .sel(Who));  // open: in0, in3
  // Probe on {4'b0000, multiplier_1_cout, multiplier_1_out}
  or or_9 (or_9_out, w_1o[0], w_1o[1], w_1o[2]);
  or or_10 (or_10_out, w_1b[0], w_1b[1], w_1b[2]);
  Pull_Resistor pull_resistor_17 (.node(w_1b));
  Pull_Resistor pull_resistor_18 (.node(h_1b));
  assign h_1b = controlled_buffer_4_out ? inc_4_out_2 : 3'bz;  // Controlled_Buffer controlled_buffer_8
  and and_21 (pull_resistor_10_node[3], ~pull_resistor_10_node[0], ~comparator_4_eq, ~pull_resistor_15_node, pull_resistor_19_node);  // AND_Gate
  Pull_Resistor pull_resistor_19 (.node(pull_resistor_19_node));
  Comparator #(.width(6)) comparator_6 (
    .a(multiplexer_7_out), .b({controlled_buffer_2_out, controlled_buffer_1_out}), .eq(pull_resistor_19_node));  // open: gt, lt
  Divider #(.width(10)) divider_1 (
    .a({4'b0000, multiplier_1_cout, multiplier_1_out}), .b(10'h4), .out(divider_1_out), .rem(divider_1_rem));  // open: upper
  // Probe on divider_1_rem
  not not_3 (not_3_out, or_9_out);
  not not_4 (not_4_out, or_10_out);
  Pull_Resistor pull_resistor_20 (.node(pull_resistor_20_node));
  assign pull_resistor_20_node = and_27_out ? pull_resistor_10_node : 5'bz;  // Controlled_Buffer controlled_buffer_9
  and and_22 (pull_resistor_10_node[4], ~pull_resistor_10_node[0], ~comparator_4_eq, ~pull_resistor_15_node, ~pull_resistor_19_node, comparator_7_eq);  // AND_Gate
  Multiplexer #(.select(2), .width(6), .enable("false")) multiplexer_8 (
    .in1(o_exzit_5), .in2(b_exzit_5), .out(multiplexer_8_out), .sel(Who));  // open: in0, in3
  Comparator #(.width(6)) comparator_7 (
    .a(multiplexer_8_out), .b({controlled_buffer_2_out, controlled_buffer_1_out}), .eq(comparator_7_eq));  // open: gt, lt
  Demultiplexer #(.select(2), .width(10), .enable("false")) demultiplexer_6 (
    .out1(demultiplexer_6_out1), .out2(demultiplexer_6_out2), .in(adder_1_out), .sel(Who));  // open: out0, out3
  Adder #(.width(10)) adder_1 (
    .a({4'b0000, multiplier_1_cout, multiplier_1_out}), .b({4'b0000, multiplier_1_cout, multiplier_1_out}),
    .out(adder_1_out));  // open: cin, cout
  Demultiplexer #(.select(2), .width(10), .enable("false")) demultiplexer_7 (
    .out1(demultiplexer_7_out1), .out2(demultiplexer_7_out2), .in(divider_1_out), .sel(Who));  // open: out0, out3
  Comparator #(.width(10)) comparator_8 (.a({10{1'b0}}), .b(divider_1_rem), .eq(comparator_8_eq));  // open: gt, lt
  and and_23 (kj, not_3_out, or_9_out);
  and and_24 (jk, not_4_out, or_10_out);
  and and_25 (and_25_out, kj, ~_1_o);  // AND_Gate
  or or_11 (or_11_out, rst, rst_1);
  and and_26 (and_26_out, jk, ~_1_b);  // AND_Gate
  or or_12 (or_12_out, rst, rst_6);
  not not_5 (not_5_out, in_3);
  Pull_Resistor pull_resistor_21 (.node(comparator_7_eq));
  not not_6 (not_6_out, comparator_8_eq);
  DotMatrix #(.matrixcols(7), .matrixrows(5)) dotmatrix_3 (
    .col0(out_35), .col1(out_30), .col2(out_25), .col3(out_20), .col4(out_15), .col5(out_10), .col6(out_5));
  numder_2 numder_2_1 (
    .in_1(w_1o), .out_5(out_35), .out_6(out_30), .out_7(out_25), .out_9(out_20), .out_11(out_15),
    .in_2(h_1o), .out_12(out_10), .out_13(out_5), .out_8(_1_o), .in_3(and_25_out), .rst(or_11_out),
    .out_10(o_exzit_1));
  DotMatrix #(.matrixcols(7), .matrixrows(5)) dotmatrix_4 (
    .col0(out_88), .col1(out_83), .col2(out_78), .col3(out_73), .col4(out_68), .col5(out_63), .col6(out_58));
  numder_2 numder_2_2 (
    .in_1(w_1b), .out_5(out_88), .out_6(out_83), .out_7(out_78), .out_9(out_73), .out_11(out_68),
    .in_2(h_1b), .out_12(out_63), .out_13(out_58), .out_8(_1_b), .in_3(and_26_out), .rst(or_12_out),
    .out_10(b_exzit_1));
  and and_27 (and_27_out, ~not_5_out, ~in_3);  // AND_Gate
  Demultiplexer #(.select(2), .enable("false")) demultiplexer_8 (
    .out1(demultiplexer_8_out1), .out2(demultiplexer_8_out2), .in(not_6_out), .sel(Who));  // open: out0, out3
  Subtractor #(.width(10)) subtractor_1 (.a(de_o), .b(dec), .out(subtractor_1_out), .bout(err_11));  // open: bin
  and and_28 (and_28_out, _1_o, ~_2_o, kj);  // AND_Gate
  and and_29 (and_29_out, ~err_11, dec_DE);  // AND_Gate
  Transistor #(.\type ("n"), .width(10)) transistor_9 (
    .in(subtractor_1_out), .out(transistor_9_out), .gate(and_29_out));
  Transistor #(.\type ("n"), .width(10)) transistor_10 (.in(transistor_9_out), .out(transistor_10_out), .gate(Who[0]));
  Register #(.width(10)) register_2 (.D(transistor_11_out), .Q(op_o), .clk(and_27_out), .clr(rst));  // open: en
  Transistor #(.\type ("n"), .width(10)) transistor_11 (.in(adder_2_out), .out(transistor_11_out), .gate(exit_OP));
  Adder #(.width(10)) adder_2 (
    .a(demultiplexer_7_out1), .b(op_o), .out(adder_2_out), .cin(demultiplexer_8_out1));  // open: cout
  Register #(.width(10)) register_3 (.D(transistor_13_out), .Q(op_b), .clk(and_27_out), .clr(rst));  // open: en
  Adder #(.width(10)) adder_3 (
    .a(demultiplexer_7_out2), .b(op_b), .out(adder_3_out), .cin(demultiplexer_8_out2));  // open: cout
  or or_13 (or_13_out, rst, rst_2);
  and and_30 (and_30_out, _1_b, ~_2_b, jk);  // AND_Gate
  or or_14 (or_14_out, rst, rst_7);
  Register #(.width(10)) register_4 (.D(transistor_10_out), .Q(de_o), .clk(and_27_out), .clr(rst));  // open: en
  Transistor #(.\type ("n"), .width(10)) transistor_12 (.in(adder_4_out), .out(transistor_10_out), .gate(exit_OP));
  Transistor #(.\type ("n"), .width(10)) transistor_13 (.in(adder_3_out), .out(transistor_13_out), .gate(exit_OP));
  DotMatrix #(.matrixcols(7), .matrixrows(5)) dotmatrix_5 (
    .col0(out_36), .col1(out_31), .col2(out_26), .col3(out_21), .col4(out_16), .col5(out_11), .col6(out_6));
  numder_2 numder_2_3 (
    .in_1(w_1o), .out_5(out_36), .out_6(out_31), .out_7(out_26), .out_9(out_21), .out_11(out_16),
    .in_2(h_1o), .out_12(out_11), .out_13(out_6), .out_8(_2_o), .in_3(and_28_out), .rst(or_13_out),
    .out_10(o_exzit_2));
  DotMatrix #(.matrixcols(7), .matrixrows(5)) dotmatrix_6 (
    .col0(out_89), .col1(out_84), .col2(out_79), .col3(out_74), .col4(out_69), .col5(out_64), .col6(out_59));
  numder_2 numder_2_4 (
    .in_1(w_1b), .out_5(out_89), .out_6(out_84), .out_7(out_79), .out_9(out_74), .out_11(out_69),
    .in_2(h_1b), .out_12(out_64), .out_13(out_59), .out_8(_2_b), .in_3(and_30_out), .rst(or_14_out),
    .out_10(b_exzit_2));
  Adder #(.width(10)) adder_4 (.a(de_o), .b(demultiplexer_6_out1), .out(adder_4_out));  // open: cin, cout
  Subtractor #(.width(10)) subtractor_2 (.a(op_o), .b(10'h1), .out(subtractor_2_out), .bout(err_01));  // open: bin
  Transistor #(.\type ("n"), .width(10)) transistor_14 (
    .in(subtractor_2_out), .out(transistor_14_out), .gate(and_31_out));
  Transistor #(.\type ("n"), .width(10)) transistor_15 (.in(transistor_14_out), .out(transistor_11_out), .gate(Who[0]));
  and and_31 (and_31_out, ~err_01, dec_OP);  // AND_Gate
  Subtractor #(.width(10)) subtractor_3 (.a(op_b), .b(10'h1), .out(subtractor_3_out), .bout(err_00));  // open: bin
  Transistor #(.\type ("n"), .width(10)) transistor_16 (
    .in(subtractor_3_out), .out(transistor_16_out), .gate(and_32_out));
  Transistor #(.\type ("n"), .width(10)) transistor_17 (.in(transistor_16_out), .out(transistor_13_out), .gate(Who[1]));
  and and_32 (and_32_out, ~err_00, dec_OP);  // AND_Gate
  DotMatrix #(.matrixcols(11), .matrixrows(5)) dotmatrix_7 (
    .col0(out_113), .col1(out_111), .col2(out_109), .col3(out_107), .col4(out_105), .col5(out_103),
    .col6(out_101), .col7(out_99), .col8(out_97), .col9(out_95), .col10(out_94));
  Numders numders_1 (
    .Energy(de_o), .in_2(1'b0), .out_3(out_113), .out_4(out_111), .out_5(out_109), .out_6(out_107),
    .out_7(out_105), .out_8(out_103), .out_9(out_101), .out_10(out_99), .out_11(out_97), .out_12(out_95),
    .out_13(out_94));
  DotMatrix #(.matrixcols(11), .matrixrows(5)) dotmatrix_8 (
    .col0(out_136), .col1(out_134), .col2(out_132), .col3(out_130), .col4(out_128), .col5(out_126),
    .col6(out_124), .col7(out_122), .col8(out_120), .col9(out_118), .col10(out_116));
  Numders numders_2 (
    .Energy(op_o), .in_2(1'b0), .out_3(out_136), .out_4(out_134), .out_5(out_132), .out_6(out_130),
    .out_7(out_128), .out_8(out_126), .out_9(out_124), .out_10(out_122), .out_11(out_120), .out_12(out_118),
    .out_13(out_116));
  Comparator #(.width(10)) comparator_9 (.a(op_o), .b({10{1'b0}}), .eq(dog_o));  // open: gt, lt
  and and_33 (and_33_out, _1_o, _2_o, ~_3_o, kj);  // AND_Gate
  and and_34 (and_34_out, _1_b, _2_b, ~_3_b, jk);  // AND_Gate
  Comparator #(.width(10)) comparator_10 (.a({10{1'b0}}), .b(de_o), .eq(god_b));  // open: gt, lt
  Register #(.width(10)) register_5 (.D(transistor_18_out), .Q(de_b), .clk(and_27_out), .clr(rst));  // open: en
  Adder #(.width(10)) adder_5 (.a(de_b), .b(demultiplexer_6_out2), .out(adder_5_out));  // open: cin, cout
  Comparator #(.width(10)) comparator_11 (.a({10{1'b0}}), .b(op_b), .eq(dog_b));  // open: gt, lt
  DotMatrix #(.matrixcols(7), .matrixrows(5)) dotmatrix_9 (
    .col0(out_37), .col1(out_32), .col2(out_27), .col3(out_22), .col4(out_17), .col5(out_12), .col6(out_7));
  numder_2 numder_2_5 (
    .in_1(w_1o), .out_5(out_37), .out_6(out_32), .out_7(out_27), .out_9(out_22), .out_11(out_17),
    .in_2(h_1o), .out_12(out_12), .out_13(out_7), .out_8(_3_o), .in_3(and_33_out), .rst(or_15_out),
    .out_10(o_exzit_3));
  or or_15 (or_15_out, rst, rst_3);
  DotMatrix #(.matrixcols(7), .matrixrows(5)) dotmatrix_10 (
    .col0(out_90), .col1(out_85), .col2(out_80), .col3(out_75), .col4(out_70), .col5(out_65), .col6(out_60));
  numder_2 numder_2_6 (
    .in_1(w_1b), .out_5(out_90), .out_6(out_85), .out_7(out_80), .out_9(out_75), .out_11(out_70),
    .in_2(h_1b), .out_12(out_65), .out_13(out_60), .out_8(_3_b), .in_3(and_34_out), .rst(or_16_out),
    .out_10(b_exzit_3));
  or or_16 (or_16_out, rst, rst_8);
  DotMatrix #(.matrixcols(11), .matrixrows(5)) dotmatrix_11 (
    .col0(out_115), .col1(out_114), .col2(out_112), .col3(out_110), .col4(out_108), .col5(out_106),
    .col6(out_104), .col7(out_102), .col8(out_100), .col9(out_98), .col10(out_96));
  Transistor #(.\type ("n"), .width(10)) transistor_18 (.in(adder_5_out), .out(transistor_18_out), .gate(exit_OP));
  DotMatrix #(.matrixcols(11), .matrixrows(5)) dotmatrix_12 (
    .col0(out_137), .col1(out_135), .col2(out_133), .col3(out_131), .col4(out_129), .col5(out_127),
    .col6(out_125), .col7(out_123), .col8(out_121), .col9(out_119), .col10(out_117));
  Numders numders_3 (
    .Energy(de_b), .in_2(1'b0), .out_3(out_115), .out_4(out_114), .out_5(out_112), .out_6(out_110),
    .out_7(out_108), .out_8(out_106), .out_9(out_104), .out_10(out_102), .out_11(out_100), .out_12(out_98),
    .out_13(out_96));
  Numders numders_4 (
    .Energy(op_b), .in_2(1'b0), .out_3(out_137), .out_4(out_135), .out_5(out_133), .out_6(out_131),
    .out_7(out_129), .out_8(out_127), .out_9(out_125), .out_10(out_123), .out_11(out_121), .out_12(out_119),
    .out_13(out_117));
  and and_35 (and_35_out, _1_o, _2_o, _3_o, ~_4_o, kj);  // AND_Gate
  and and_36 (and_36_out, _1_b, _2_b, _3_b, ~_4_b, jk);  // AND_Gate
  Comparator #(.width(10)) comparator_12 (.a(de_b), .b({10{1'b0}}), .eq(god_o));  // open: gt, lt
  and and_37 (and_37_out, ~err_10, dec_DE);  // AND_Gate
  or or_17 (or_17_out, rst, rst_9);
  Subtractor #(.width(10)) subtractor_4 (.a(de_b), .b(dec), .out(subtractor_4_out), .bout(err_10));  // open: bin
  Transistor #(.\type ("n"), .width(10)) transistor_19 (
    .in(subtractor_4_out), .out(transistor_19_out), .gate(and_37_out));
  Transistor #(.\type ("n"), .width(10)) transistor_20 (.in(transistor_19_out), .out(transistor_18_out), .gate(Who[1]));
  DotMatrix #(.matrixcols(7), .matrixrows(5)) dotmatrix_13 (
    .col0(out_38), .col1(out_33), .col2(out_28), .col3(out_23), .col4(out_18), .col5(out_13), .col6(out_8));
  numder_2 numder_2_7 (
    .in_1(w_1o), .out_5(out_38), .out_6(out_33), .out_7(out_28), .out_9(out_23), .out_11(out_18),
    .in_2(h_1o), .out_12(out_13), .out_13(out_8), .out_8(_4_o), .in_3(and_35_out), .rst(or_18_out),
    .out_10(o_exzit_4));
  or or_18 (or_18_out, rst, rst_4);
  DotMatrix #(.matrixcols(7), .matrixrows(5)) dotmatrix_14 (
    .col0(out_91), .col1(out_86), .col2(out_81), .col3(out_76), .col4(out_71), .col5(out_66), .col6(out_61));
  numder_2 numder_2_8 (
    .in_1(w_1b), .out_5(out_91), .out_6(out_86), .out_7(out_81), .out_9(out_76), .out_11(out_71),
    .in_2(h_1b), .out_12(out_66), .out_13(out_61), .out_8(_4_b), .in_3(and_36_out), .rst(or_17_out),
    .out_10(b_exzit_4));
  and and_38 (and_38_out, _1_b, _2_b, _3_b, _4_b, ~_5_b, jk);  // AND_Gate
  and and_39 (and_39_out, _1_o, _2_o, _3_o, _4_o, ~_5_o, kj);  // AND_Gate
  DotMatrix #(.matrixcols(7), .matrixrows(5)) dotmatrix_15 (
    .col0(out_92), .col1(out_87), .col2(out_82), .col3(out_77), .col4(out_72), .col5(out_67), .col6(out_62));
  numder_2 numder_2_9 (
    .in_1(w_1b), .out_5(out_92), .out_6(out_87), .out_7(out_82), .out_9(out_77), .out_11(out_72),
    .in_2(h_1b), .out_12(out_67), .out_13(out_62), .out_8(_5_b), .in_3(and_38_out), .rst(or_19_out),
    .out_10(b_exzit_5));
  or or_19 (or_19_out, rst, rst_10);
  DotMatrix #(.matrixcols(7), .matrixrows(5)) dotmatrix_16 (
    .col0(out_39), .col1(out_34), .col2(out_29), .col3(out_24), .col4(out_19), .col5(out_14), .col6(out_9));
  numder_2 numder_2_10 (
    .in_1(w_1o), .out_5(out_39), .out_6(out_34), .out_7(out_29), .out_9(out_24), .out_11(out_19),
    .in_2(h_1o), .out_12(out_14), .out_13(out_9), .out_8(_5_o), .in_3(and_39_out), .rst(or_20_out),
    .out_10(o_exzit_5));
  or or_20 (or_20_out, rst, rst_5);
  and and_40 (err_o, _1_o, _2_o, _3_o, _4_o, _5_o);
  and and_41 (err_b, _1_b, _2_b, _3_b, _4_b, _5_b);
  // NOT_Gate not_7 is placed but not wired

  // Other names for the same wires on the sheet: clk = in_3; clk_output = in_3; or = Who[0]; blue = Who[1]

  // Notes on the sheet:
  //   оп
  //   дэ
  //   оп
  //   дэ
  //   ОП
  //   ДЭ
endmodule

module Weight (
  input  in_1,
  input  new_task,
  output [1:0] out_3,
  output [14:0] out_4,
  output [14:0] out_5,
  output [14:0] out_6,
  output [14:0] out_7,
  output [14:0] out_8,
  output [14:0] out_9,
  output [14:0] out_10,
  output [14:0] out_11,
  output [14:0] out_12
);

  wire [2:0] inc_1_out_2;

  Random #(.width(2), .seed(1)) random_1 (.clk(new_task), .out(out_3));  // open: next, clr
  // Probe on inc_1_out_2
  display_controller_inc inc_1 (.in_1(out_3), .out_2(inc_1_out_2));
  DotMatrix #(.matrixcols(9), .matrixrows(15)) dotmatrix_1 (
    .col0(out_4), .col1(out_4), .col2(out_4), .col3(out_7), .col4(out_7), .col5(out_7), .col6(out_10),
    .col7(out_10), .col8(out_10));
  Big_col_1 big_col_1_1 (
    .Zero(in_1), .D(1'b0), .C(inc_1_out_2[2]), .B(inc_1_out_2[1]), .A(inc_1_out_2[0]), .out_7(out_4),
    .Inversion(1'b0));
  Big_col_2 big_col_2_1 (
    .Zero(in_1), .D(1'b0), .C(inc_1_out_2[2]), .B(inc_1_out_2[1]), .A(inc_1_out_2[0]), .out_7(out_7),
    .Inversion(1'b0));
  Big_col_3 big_col_3_1 (
    .Zero(in_1), .D(1'b0), .C(inc_1_out_2[2]), .B(inc_1_out_2[1]), .A(inc_1_out_2[0]), .out_7(out_10),
    .Inversion(1'b0));

  assign out_5 = out_4;
  assign out_6 = out_4;
  assign out_8 = out_7;
  assign out_9 = out_7;
  assign out_11 = out_10;
  assign out_12 = out_10;
endmodule

module Haight (
  input  in_1,
  input  new_task,
  output [1:0] out_3,
  output [14:0] out_4,
  output [14:0] out_5,
  output [14:0] out_6,
  output [14:0] out_7,
  output [14:0] out_8,
  output [14:0] out_9,
  output [14:0] out_10,
  output [14:0] out_11,
  output [14:0] out_12
);

  wire [2:0] inc_1_out_2;

  display_controller_inc inc_1 (.in_1(out_3), .out_2(inc_1_out_2));
  Random #(.width(2)) random_1 (.clk(new_task), .out(out_3));  // open: next, clr
  // Probe on inc_1_out_2
  DotMatrix #(.matrixcols(9), .matrixrows(15)) dotmatrix_1 (
    .col0(out_4), .col1(out_4), .col2(out_4), .col3(out_7), .col4(out_7), .col5(out_7), .col6(out_10),
    .col7(out_10), .col8(out_10));
  Big_col_1 big_col_1_1 (
    .Zero(in_1), .D(1'b0), .C(inc_1_out_2[2]), .B(inc_1_out_2[1]), .A(inc_1_out_2[0]), .out_7(out_4),
    .Inversion(1'b0));
  Big_col_2 big_col_2_1 (
    .Zero(in_1), .D(1'b0), .C(inc_1_out_2[2]), .B(inc_1_out_2[1]), .A(inc_1_out_2[0]), .out_7(out_7),
    .Inversion(1'b0));
  Big_col_3 big_col_3_1 (
    .Zero(in_1), .D(1'b0), .C(inc_1_out_2[2]), .B(inc_1_out_2[1]), .A(inc_1_out_2[0]), .out_7(out_10),
    .Inversion(1'b0));

  assign out_5 = out_4;
  assign out_6 = out_4;
  assign out_8 = out_7;
  assign out_9 = out_7;
  assign out_11 = out_10;
  assign out_12 = out_10;
endmodule

module numder_2 (
  input  [2:0] in_1,
  input  [2:0] in_2,
  input  in_3,
  input  rst,
  output [4:0] out_5,
  output [4:0] out_6,
  output [4:0] out_7,
  output out_8,
  output [4:0] out_9,
  output [5:0] out_10,
  output [4:0] out_11,
  output [4:0] out_12,
  output [4:0] out_13
);

  wire and_1_out, nor_1_out, nor_2_out;
  wire [4:0] col_1_1_e, col_1_2_e, col_2_1_e, col_2_2_e, col_3_1_e, col_3_2_e;

  // Probe on {in_1, in_2}
  and and_1 (and_1_out, in_3, ~out_8);  // AND_Gate
  Register #(.width(6)) register_1 (.D({in_1, in_2}), .Q(out_10), .clk(and_1_out), .clr(rst));  // open: en
  Comparator #(.width(6), .mode("unsigned")) comparator_1 (.a(out_10), .b({6{1'b0}}), .gt(out_8));  // open: eq, lt
  nor nor_1 (nor_1_out, out_10[3], out_10[4], out_10[5]);
  Col_1 col_1_1 (
    .D(1'b0), .C(out_10[5]), .B(out_10[4]), .A(out_10[3]), .e(col_1_1_e[0]), .d_2(col_1_1_e[1]),
    .c_2(col_1_1_e[2]), .b_2(col_1_1_e[3]), .a_2(col_1_1_e[4]));
  Col_2 col_2_1 (
    .D(1'b0), .C(out_10[5]), .B(out_10[4]), .A(out_10[3]), .e(col_2_1_e[0]), .d_2(col_2_1_e[1]),
    .c_2(col_2_1_e[2]), .b_2(col_2_1_e[3]), .a_2(col_2_1_e[4]));
  Col_3 col_3_1 (
    .D(1'b0), .C(out_10[5]), .B(out_10[4]), .A(out_10[3]), .e(col_3_1_e[0]), .d_2(col_3_1_e[1]),
    .c_2(col_3_1_e[2]), .b_2(col_3_1_e[3]), .a_2(col_3_1_e[4]));
  nor nor_2 (nor_2_out, out_10[0], out_10[1], out_10[2]);
  Transistor #(.\type ("n"), .width(5)) transistor_1 (.in({5{1'b0}}), .out(out_5), .gate(nor_1_out));
  Transistor #(.\type ("n"), .width(5)) transistor_2 (.in({5{1'b0}}), .out(out_6), .gate(nor_1_out));
  Transistor #(.\type ("n"), .width(5)) transistor_3 (.in({5{1'b0}}), .out(out_7), .gate(nor_1_out));
  Col_1 col_1_2 (
    .D(1'b0), .C(out_10[2]), .B(out_10[1]), .A(out_10[0]), .e(col_1_2_e[0]), .d_2(col_1_2_e[1]),
    .c_2(col_1_2_e[2]), .b_2(col_1_2_e[3]), .a_2(col_1_2_e[4]));
  Col_2 col_2_2 (
    .D(1'b0), .C(out_10[2]), .B(out_10[1]), .A(out_10[0]), .e(col_2_2_e[0]), .d_2(col_2_2_e[1]),
    .c_2(col_2_2_e[2]), .b_2(col_2_2_e[3]), .a_2(col_2_2_e[4]));
  Col_3 col_3_2 (
    .D(1'b0), .C(out_10[2]), .B(out_10[1]), .A(out_10[0]), .e(col_3_2_e[0]), .d_2(col_3_2_e[1]),
    .c_2(col_3_2_e[2]), .b_2(col_3_2_e[3]), .a_2(col_3_2_e[4]));
  DotMatrix #(.matrixcols(3), .matrixrows(5)) dotmatrix_1 (.col0(out_5), .col1(out_6), .col2(out_7));
  Transistor #(.width(5)) transistor_4 (.in(col_1_1_e), .out(out_5), .gate(nor_1_out));
  Transistor #(.width(5)) transistor_5 (.in(col_2_1_e), .out(out_6), .gate(nor_1_out));
  Transistor #(.width(5)) transistor_6 (.in(col_3_1_e), .out(out_7), .gate(nor_1_out));
  Transistor #(.\type ("n"), .width(5)) transistor_7 (.in({5{1'b0}}), .out(out_11), .gate(nor_2_out));
  Transistor #(.\type ("n"), .width(5)) transistor_8 (.in({5{1'b0}}), .out(out_12), .gate(nor_2_out));
  Transistor #(.\type ("n"), .width(5)) transistor_9 (.in({5{1'b0}}), .out(out_13), .gate(nor_2_out));
  DotMatrix #(.matrixcols(3), .matrixrows(5)) dotmatrix_2 (.col0(out_11), .col1(out_12), .col2(out_13));
  Transistor #(.width(5)) transistor_10 (.in(col_1_2_e), .out(out_11), .gate(nor_2_out));
  Transistor #(.width(5)) transistor_11 (.in(col_2_2_e), .out(out_12), .gate(nor_2_out));
  Transistor #(.width(5)) transistor_12 (.in(col_3_2_e), .out(out_13), .gate(nor_2_out));

  assign out_9 = {5{1'b0}};
endmodule

module inc (
  input  [1:0] in_1,
  output [2:0] out_2
);

  wire [0:0] and_1_out;

  assign {out_2[2], and_1_out[0]} = {and_1_out[0], 1'b1} & in_1;  // AND_Gate and_1, 2 bits wide
  assign out_2[1:0] = in_1 ^ {and_1_out[0], 1'b1};  // XOR_Gate xor_1, 2 bits wide
endmodule
